// Logisim project cpu24+4+IR_mul.circ as structural Verilog: 10 circuits, main circuit ◇单周期MIPS
module \单周期MIPS  (
);

  wire and_1_out, and_2_out, and_4_out, and_5_out, and_6_out, and_7_out, and_8_out, and_9_out, and_11_out,
       and_12_out, and_13_out, and_17_out, Clear1, Clear2, Clear3, CLK, comparator_1_eq, comparator_2_eq,
       comparator_2_lt, comparator_3_eq, decoder_1_out1, decoder_1_out2, decoder_1_out3, decoder_2_out1,
       decoder_2_out2, decoder_2_out3, decoder_3_out0, decoder_3_out1, decoder_3_out2, ERET,
       \ERET信号保留上升沿后的一个半周期_下降沿触发_q , FLAG1_q, FLAG2_q, FLAG3_q, Go, Has_Run, IE, IE_q, INT, INT_Level, IR1,
       IR2, IR3, MemWrite, MFC0, mips_alu_1_equal, MTC0, multiplexer_1_out, multiplexer_4_out,
       multiplexer_6_out, multiplexer_8_out, multiplexer_21_out, NEW_INT, not_1_out, not_2_out, not_3_out,
       not_4_out, not_5_out, not_6_out, not_7_out, not_8_out, not_9_out, not_10_out, not_11_out, not_12_out,
       not_13_out, not_14_out, not_15_out, or_1_out, or_2_out, or_6_out, or_7_out, or_8_out, or_9_out,
       or_10_out, or_11_out, or_12_out, or_13_out, or_15_out, or_16_out, or_17_out, or_18_out, or_19_out,
       priority_encoder_1_gs, register_2_q, register_3_q, register_5_q, register_6_q, register_7_q,
       register_8_q, register_9_q, register_10_q, register_11_q, RegWrite, RST, SignedExt, stop, Syscall, W1,
       W2, W3, xor_1_out, \单周期硬布线控制器_1_alu_src , \单周期硬布线控制器_1_beq , \单周期硬布线控制器_1_blez , \单周期硬布线控制器_1_bne ,
       \单周期硬布线控制器_1_jal , \单周期硬布线控制器_1_jr , \单周期硬布线控制器_1_memtoreg , \单周期硬布线控制器_1_regdst , \单周期硬布线控制器_1_sb ,
       \无条件分支 , \条件分支成功 ;
  wire [1:0] INT_NUM, multiplexer_18_out, OLD_INT_NUM_q, subtractor_1_out, Top;
  wire [3:0] \单周期硬布线控制器_1_alu_op ;
  wire [4:0] multiplexer_10_out, multiplexer_11_out, multiplexer_12_out, multiplexer_13_out;
  wire [15:0] \总周期数 , \无条件分支数 , \条件分支成功数 ;
  wire [31:0] a0, adder_1_out, adder_2_out, bit_extender_1_out, bit_extender_2_out, EPC0_q, EPC1_q, EPC2_q,
       INT_PC, IR, LedData, MDin, mips_alu_1_result, multiplexer_2_out, multiplexer_3_out, multiplexer_5_out,
       multiplexer_9_out, multiplexer_15_out, multiplexer_17_out, multiplexer_20_out, multiplexer_22_out,
       Next_PC, PC, ram_1_data, RDin, Ret_PC, shifter_1_out, v0;

  Button \u_总复位  (.out(RST));
  not not_1 (not_1_out, stop);
  // Probe on \总周期数 
  // Probe on \无条件分支数 
  // Probe on \条件分支成功数 
  Counter #(.width(16), .max('hffff), .ongoal("wrap"), .trigger("rising"), .behavior("old")) counter_1 (
    .count(1'b1), .Q(\总周期数 ), .clk(multiplexer_1_out), .clr(RST));  // open: load, D, carry, preset
  Multiplexer #(.select(1), .width(1), .disabled("Z"), .enable("false")) multiplexer_1 (
    .in0(and_1_out), .in1(1'b0), .out(multiplexer_1_out), .sel(not_2_out));
  not not_2 (not_2_out, not_3_out);
  and and_1 (and_1_out, not_1_out, CLK);
  Multiplexer #(.select(1), .width(32), .disabled("Z"), .enable("false")) multiplexer_2 (
    .in0({adder_1_out[31:28], IR[25:0], 2'b00}), .in1(v0), .out(multiplexer_2_out), .sel(\单周期硬布线控制器_1_jr ));
  Multiplexer #(.select(2), .width(32), .disabled("Z"), .enable("false")) multiplexer_3 (
    .in0(adder_1_out), .in1(adder_2_out), .in2(multiplexer_2_out), .out(multiplexer_3_out),
    .sel({\无条件分支 , \条件分支成功 }));  // open: in3
  Clock #(.highDuration(1), .lowDuration(1)) clock_1 (.out(CLK));
  Button _1 (.out(IR1));
  Button _2 (.out(IR2));
  Button _3 (.out(IR3));
  not not_3 (not_3_out, CLK);
  Button \u_继续运行  (.out(Go));
  LED #(.active("true")) led_1 (.in(W1));
  LED #(.active("true")) led_2 (.in(W2));
  LED #(.active("true")) led_3 (.in(W3));
  Multiplexer #(.select(1), .width(1), .disabled("Z"), .enable("false")) multiplexer_4 (
    .in0(and_2_out), .in1(1'b0), .out(multiplexer_4_out), .sel(not_4_out));
  and and_2 (and_2_out, \条件分支成功 , CLK);
  Comparator #(.width(32), .mode("twosComplement")) comparator_1 (
    .a(v0), .b(32'h22), .eq(comparator_1_eq));  // open: gt, lt
  xor xor_1 (xor_1_out, stop, register_3_q);
  Multiplexer #(.select(1), .width(32), .disabled("Z"), .enable("false")) multiplexer_5 (
    .in0(multiplexer_3_out), .in1(Ret_PC), .out(multiplexer_5_out), .sel(ERET));
  Register #(.width(1), .trigger("rising"), .Select("low")) register_1 (
    .D(1'b1), .Q(INT_Level), .clk(NEW_INT), .clr(or_1_out));  // open: en
  or or_1 (or_1_out, RST, register_2_q);
  Register #(.width(1), .trigger("rising"), .Select("low")) register_2 (
    .D(1'b1), .Q(register_2_q), .clk(multiplexer_6_out), .clr(or_2_out));  // open: en
  or or_2 (or_2_out, register_2_q, RST);
  Multiplexer #(.select(1), .width(1), .disabled("Z"), .enable("false")) multiplexer_6 (
    .in0(1'b1), .in1(CLK), .out(multiplexer_6_out), .sel(INT_Level));
  Hex_Digit_Display hex_digit_display_1 (.value(LedData[31:28]));  // open: dp
  Hex_Digit_Display hex_digit_display_2 (.value(LedData[27:24]));  // open: dp
  Counter #(.width(16), .max('hffff), .ongoal("wrap"), .trigger("rising"), .behavior("old")) counter_2 (
    .count(1'b1), .Q(\条件分支成功数 ), .clk(multiplexer_4_out), .clr(RST));  // open: load, D, carry, preset
  not not_4 (not_4_out, not_5_out);
  not not_5 (not_5_out, CLK);
  not not_6 (not_6_out, comparator_1_eq);
  and and_3 (stop, not_6_out, Syscall);
  Multiplexer #(.select(1), .width(32), .disabled("Z"), .enable("false")) multiplexer_7 (
    .in0(multiplexer_5_out), .in1(PC), .out(Next_PC), .sel(xor_1_out));
  Hex_Digit_Display hex_digit_display_3 (.value(LedData[19:16]));  // open: dp
  Hex_Digit_Display hex_digit_display_4 (.value(LedData[23:20]));  // open: dp
  and and_4 (and_4_out, Syscall, comparator_1_eq);
  and and_5 (and_5_out, stop, Go);
  Register #(.width(1), .trigger("rising"), .Select("low")) register_3 (
    .D(1'b0), .Q(register_3_q), .clk(CLK), .clr(RST), .preset(and_5_out));  // open: en, cs
  Register #(.width(32), .trigger("rising"), .Select("low")) u_PC (
    .D(Next_PC), .Q(PC), .clk(CLK), .clr(RST));  // open: en
  Hex_Digit_Display hex_digit_display_5 (.value(LedData[11:8]));  // open: dp
  Hex_Digit_Display hex_digit_display_6 (.value(LedData[15:12]));  // open: dp
  Multiplexer #(.select(1), .width(1), .disabled("Z"), .enable("false")) multiplexer_8 (
    .in0(and_6_out), .in1(1'b0), .out(multiplexer_8_out), .sel(not_7_out));
  and and_6 (and_6_out, \无条件分支 , CLK);
  Register #(.width(32), .trigger("rising"), .Select("low")) register_4 (
    .D(a0), .Q(LedData), .clk(and_4_out), .clr(RST));  // open: en
  Multiplexer #(.select(1), .width(32), .disabled("Z"), .enable("false")) multiplexer_9 (
    .in0(PC), .in1(INT_PC), .out(multiplexer_9_out), .sel(INT_Level));
  Hex_Digit_Display hex_digit_display_7 (.value(LedData[3:0]));  // open: dp
  Hex_Digit_Display hex_digit_display_8 (.value(LedData[7:4]));  // open: dp
  // Probe on \总周期数 
  Counter #(.width(16), .max('hffff), .ongoal("wrap"), .trigger("rising"), .behavior("old")) counter_3 (
    .count(1'b1), .Q(\无条件分支数 ), .clk(multiplexer_8_out), .clr(RST));  // open: load, D, carry, preset
  not not_7 (not_7_out, not_8_out);
  not not_8 (not_8_out, CLK);
  ROM #(.addrWidth(10), .dataWidth(32), .Select("high")) rom_1 (.addr(multiplexer_9_out[11:2]), .data(IR));
  Adder #(.width(32)) adder_1 (.a(multiplexer_9_out), .b(32'h4), .out(adder_1_out));  // open: cin, cout
  or or_3 (W1, register_8_q, register_5_q);
  or or_4 (W2, register_9_q, register_6_q);
  or or_5 (W3, register_10_q, register_7_q);
  Register #(.width(1), .trigger("rising"), .Select("low")) register_5 (
    .D(1'b1), .Q(register_5_q), .clk(IR1), .clr(or_6_out));  // open: en
  or or_6 (or_6_out, register_8_q, RST);
  Register #(.width(1), .trigger("rising"), .Select("low")) register_6 (
    .D(1'b1), .Q(register_6_q), .clk(IR2), .clr(or_7_out));  // open: en
  or or_7 (or_7_out, register_9_q, RST);
  Register #(.width(1), .trigger("rising"), .Select("low")) register_7 (
    .D(1'b1), .Q(register_7_q), .clk(IR3), .clr(or_8_out));  // open: en
  or or_8 (or_8_out, register_10_q, RST);
  or or_9 (or_9_out, register_5_q, register_8_q);
  or or_10 (or_10_out, register_6_q, register_9_q);
  or or_11 (or_11_out, register_7_q, register_10_q);
  \单周期硬布线控制器  \u_单周期硬布线控制器_1  (
    .Func(IR[5:0]), .OP(IR[31:26]), .ALU_OP(\单周期硬布线控制器_1_alu_op ), .MemToReg(\单周期硬布线控制器_1_memtoreg ),
    .MemWrite(MemWrite), .ALU_SRC(\单周期硬布线控制器_1_alu_src ), .RegWrite(RegWrite), .SysCALL(Syscall),
    .SignedExt(SignedExt), .RegDst(\单周期硬布线控制器_1_regdst ), .JR(\单周期硬布线控制器_1_jr ), .JMP(\无条件分支 ),
    .Beq(\单周期硬布线控制器_1_beq ), .JAL(\单周期硬布线控制器_1_jal ), .Bne(\单周期硬布线控制器_1_bne ), .BLEZ(\单周期硬布线控制器_1_blez ),
    .SB(\单周期硬布线控制器_1_sb ), .ERET(ERET), .MTC0(MTC0), .MFC0(MFC0), .MT(IR[25:21]));
  and and_7 (and_7_out, or_9_out, not_9_out);
  not not_9 (not_9_out, Clear1);
  and and_8 (and_8_out, or_10_out, not_10_out);
  not not_10 (not_10_out, Clear2);
  and and_9 (and_9_out, or_11_out, not_11_out);
  not not_11 (not_11_out, Clear3);
  Multiplexer #(.select(1), .width(5), .disabled("Z"), .enable("false")) multiplexer_10 (
    .in0(IR[20:16]), .in1(IR[15:11]), .out(multiplexer_10_out), .sel(\单周期硬布线控制器_1_regdst ));
  Register #(.width(1), .trigger("rising"), .Select("low")) register_8 (
    .D(and_7_out), .Q(register_8_q), .clk(CLK), .clr(RST));  // open: en
  Register #(.width(1), .trigger("rising"), .Select("low")) register_9 (
    .D(and_8_out), .Q(register_9_q), .clk(CLK), .clr(RST));  // open: en
  Register #(.width(1), .trigger("rising"), .Select("low")) register_10 (
    .D(and_9_out), .Q(register_10_q), .clk(CLK), .clr(RST));  // open: en
  Multiplexer #(.select(1), .width(5), .disabled("Z"), .enable("false")) multiplexer_11 (
    .in0(IR[25:21]), .in1(5'b00010), .out(multiplexer_11_out), .sel(Syscall));
  Multiplexer #(.select(1), .width(5), .disabled("Z"), .enable("false")) multiplexer_12 (
    .in0(IR[20:16]), .in1(5'b00100), .out(multiplexer_12_out), .sel(Syscall));
  Multiplexer #(.select(1), .width(5), .disabled("Z"), .enable("false")) multiplexer_13 (
    .in0(multiplexer_10_out), .in1({5{1'b1}}), .out(multiplexer_13_out), .sel(\单周期硬布线控制器_1_jal ));
  Multiplexer #(.select(1), .width(32), .disabled("Z"), .enable("false")) multiplexer_14 (
    .in0(multiplexer_22_out), .in1(adder_1_out), .out(RDin), .sel(\单周期硬布线控制器_1_jal ));
  assign bit_extender_1_out = {{16{1'b0}}, IR[15:0]};  // Bit_Extender bit_extender_1
  assign bit_extender_2_out = {{16{IR[15]}}, IR[15:0]};  // Bit_Extender bit_extender_2
  MIPS_Regifile mips_regifile_1 (
    .Din(RDin), .Clk(CLK), .R1(v0), .R2(a0), .WE(RegWrite), .W_num(multiplexer_13_out),
    .R1_num(multiplexer_11_out), .R2_num(multiplexer_12_out));
  Multiplexer #(.select(1), .width(32), .disabled("Z"), .enable("false")) multiplexer_15 (
    .in0(bit_extender_1_out), .in1(bit_extender_2_out), .out(multiplexer_15_out), .sel(SignedExt));
  // Probe on INT_NUM
  Priority_Encoder #(.select(2), .disabled("Z")) priority_encoder_1 (
    .in0(1'b1), .in1(register_8_q), .in2(register_9_q), .in3(register_10_q), .out(INT_NUM),
    .gs(priority_encoder_1_gs), .en_in(1'b1));  // open: en_out
  and and_10 (INT, priority_encoder_1_gs, IE);
  Multiplexer #(.select(2), .width(32), .disabled("Z"), .enable("false")) multiplexer_16 (
    .in1(32'h3488), .in2(32'h3534), .in3(32'h35e0), .out(INT_PC), .sel(INT_NUM));  // open: in0
  or or_12 (or_12_out, comparator_2_eq, comparator_2_lt);
  Comparator #(.width(32), .mode("twosComplement")) comparator_2 (
    .a(v0), .b({32{1'b0}}), .eq(comparator_2_eq), .lt(comparator_2_lt));  // open: gt
  Shifter #(.width(32), .shift("ll")) shifter_1 (.in(multiplexer_15_out), .\dist (5'b00010), .out(shifter_1_out));
  and and_11 (and_11_out, or_12_out, \单周期硬布线控制器_1_blez );
  Multiplexer #(.select(1), .width(32), .disabled("Z"), .enable("false")) multiplexer_17 (
    .in0(a0), .in1(multiplexer_15_out), .out(multiplexer_17_out), .sel(\单周期硬布线控制器_1_alu_src ));
  Adder #(.width(32)) adder_2 (.a(shifter_1_out), .b(adder_1_out), .out(adder_2_out));  // open: cin, cout
  Multiplexer #(.select(1), .width(2), .disabled("Z"), .enable("false")) multiplexer_18 (
    .in0(multiplexer_18_out), .in1(INT_NUM), .out(multiplexer_18_out), .sel(IE));
  MIPS_ALU mips_alu_1 (
    .X(v0), .Y(multiplexer_17_out), .AluOP(\单周期硬布线控制器_1_alu_op ), .Equal(mips_alu_1_equal),
    .Result(mips_alu_1_result), .shamt(IR[10:6]));  // open: Result_2
  Register #(.width(2), .trigger("rising"), .Select("low")) OLD_INT_NUM (
    .D(multiplexer_18_out), .Q(OLD_INT_NUM_q), .clk(CLK), .clr(RST));  // open: en
  and and_12 (and_12_out, mips_alu_1_equal, \单周期硬布线控制器_1_beq );
  Register #(.width(1), .trigger("falling"), .Select("low")) \ERET信号保留上升沿后的一个半周期_下降沿触发  (
    .D(1'b0), .Q(\ERET信号保留上升沿后的一个半周期_下降沿触发_q ), .clk(CLK), .clr(RST), .preset(ERET));  // open: en, cs
  not not_12 (not_12_out, mips_alu_1_equal);
  Multiplexer #(.select(1), .width(32), .disabled("Z"), .enable("false")) multiplexer_19 (
    .in0(a0), .in1(multiplexer_20_out), .out(MDin), .sel(\单周期硬布线控制器_1_sb ));
  Multiplexer #(.select(2), .width(32), .disabled("Z"), .enable("false")) multiplexer_20 (
    .in0({ram_1_data[31:8], a0[7:0]}), .in1({ram_1_data[31:16], a0[7:0], ram_1_data[7:0]}),
    .in2({ram_1_data[31:24], a0[7:0], ram_1_data[15:0]}), .in3({a0[7:0], ram_1_data[23:0]}),
    .out(multiplexer_20_out), .sel(mips_alu_1_result[1:0]));
  Decoder #(.select(2), .tristate("false"), .disabled("Z"), .enable("false")) decoder_1 (
    .out1(decoder_1_out1), .out2(decoder_1_out2), .out3(decoder_1_out3), .sel(OLD_INT_NUM_q));  // open: out0
  not not_13 (not_13_out, comparator_3_eq);
  Comparator #(.width(2), .mode("twosComplement")) comparator_3 (
    .a(OLD_INT_NUM_q), .b(multiplexer_18_out), .eq(comparator_3_eq));  // open: gt, lt
  Register #(.width(1), .trigger("falling"), .Select("low")) register_11 (
    .D(\ERET信号保留上升沿后的一个半周期_下降沿触发_q ), .Q(register_11_q), .clk(CLK), .clr(RST));  // open: en
  and and_13 (and_13_out, not_12_out, \单周期硬布线控制器_1_bne );
  and and_14 (Clear1, decoder_1_out1, ERET);
  and and_15 (Clear2, decoder_1_out2, ERET);
  and and_16 (Clear3, decoder_1_out3, ERET);
  Multiplexer #(.select(1), .width(1), .disabled("Z"), .enable("false")) multiplexer_21 (
    .in0(not_13_out), .in1(multiplexer_21_out), .out(multiplexer_21_out), .sel(or_13_out));
  or or_13 (or_13_out, register_11_q, \ERET信号保留上升沿后的一个半周期_下降沿触发_q );
  or or_14 (\条件分支成功 , and_11_out, and_13_out, and_12_out);
  RAM #(.addrWidth(10), .dataWidth(32), .bus("separate"), .Select("high")) ram_1 (
    .addr(mips_alu_1_result[11:2]), .din(MDin), .data(ram_1_data), .str(MemWrite), .clk(CLK));  // open: sel, ld, clr
  Multiplexer #(.select(1), .width(32), .disabled("Z"), .enable("false")) multiplexer_22 (
    .in0(mips_alu_1_result), .in1(ram_1_data), .out(multiplexer_22_out), .sel(\单周期硬布线控制器_1_memtoreg ));
  Multiplexer #(.select(1), .width(1), .disabled("Z"), .enable("false")) multiplexer_23 (
    .in0(not_13_out), .in1(multiplexer_21_out), .out(NEW_INT), .sel(Has_Run));
  not not_14 (not_14_out, ERET);
  not not_15 (not_15_out, MFC0);
  or or_15 (or_15_out, MTC0, INT_Level);
  Register #(.width(1), .trigger("rising"), .Select("low")) u_IE (
    .D(1'b0), .Q(IE_q), .clk(and_17_out), .clr(RST), .preset(or_15_out));  // open: en, cs
  and and_17 (and_17_out, not_14_out, not_15_out);
  not not_16 (IE, IE_q);
  Decoder #(.select(2), .tristate("false"), .disabled("Z"), .enable("false")) decoder_2 (
    .out1(decoder_2_out1), .out2(decoder_2_out2), .out3(decoder_2_out3), .sel(INT_NUM));  // open: out0
  or or_16 (or_16_out, INT_Level, ERET);
  Counter #(.width(2), .max('h3), .ongoal("wrap"), .trigger("rising"), .behavior("new")) u_Top (
    .count(or_16_out), .Q(Top), .clk(CLK), .clr(RST), .down(ERET));  // open: load, D, carry, preset
  Decoder #(.select(2), .tristate("false"), .disabled("Z"), .enable("false")) decoder_3 (
    .out0(decoder_3_out0), .out1(decoder_3_out1), .out2(decoder_3_out2), .sel(Top));  // open: out3
  Register #(.width(1), .trigger("rising"), .Select("low")) FLAG1 (
    .D(1'b1), .en(decoder_2_out1), .Q(FLAG1_q), .clk(INT_Level), .clr(or_17_out));
  or or_17 (or_17_out, Clear1, RST);
  Register #(.width(1), .trigger("rising"), .Select("low")) FLAG2 (
    .D(1'b1), .en(decoder_2_out2), .Q(FLAG2_q), .clk(INT_Level), .clr(or_18_out));
  or or_18 (or_18_out, Clear2, RST);
  Register #(.width(1), .trigger("rising"), .Select("low")) FLAG3 (
    .D(1'b1), .en(decoder_2_out3), .Q(FLAG3_q), .clk(INT_Level), .clr(or_19_out));
  or or_19 (or_19_out, Clear3, RST);
  Multiplexer #(.select(2), .width(1), .disabled("Z"), .enable("false")) multiplexer_24 (
    .in0(1'b1), .in1(FLAG1_q), .in2(FLAG2_q), .in3(FLAG3_q), .out(Has_Run), .sel(INT_NUM));
  Register #(.width(32), .trigger("rising"), .Select("low")) EPC2 (
    .D(PC), .en(decoder_3_out2), .Q(EPC2_q), .clk(CLK), .clr(RST));
  Register #(.width(32), .trigger("rising"), .Select("low")) EPC1 (
    .D(PC), .en(decoder_3_out1), .Q(EPC1_q), .clk(CLK), .clr(RST));
  Register #(.width(32), .trigger("rising"), .Select("low")) EPC0 (
    .D(PC), .en(decoder_3_out0), .Q(EPC0_q), .clk(CLK), .clr(RST));
  Subtractor #(.width(2)) subtractor_1 (.a(Top), .b(2'b01), .out(subtractor_1_out));  // open: bin, bout
  Multiplexer #(.select(2), .width(32), .disabled("Z"), .enable("false")) multiplexer_25 (
    .in0(EPC0_q), .in1(EPC1_q), .in2(EPC2_q), .out(Ret_PC), .sel(subtractor_1_out));  // open: in3

  // Notes on the sheet:
  //   总复位信号应将除ROM以外所有存储组件全部清零
  //   中断源
  //   中断等待指示
  //   数码管输出应该用寄存器锁存，否则显示数据只能一闪而过
  //   数码管输出
  //   指令存储器
  //   contents of rom_1 (hex, n*v repeats v):
  //   201d0100 20110200 20020022 112020 20020022 c 2231ffff 1620fffb 20020032 c 20110001 8000c0f 20110001
  //   20120002 20130003 8000c13 20110001 20120002 20130003 8000c17 20110001 20120002 20130003 8000c1b
  //   20110001 20120002 20130003 c000cff 20100001 20110001 118fc0 112020 20020022 c 118882 12200001
  //   8000c1f 112020 20020022 c 20110001 118880 112020 20020022 c 12200001 8000c29 20110001 118fc0 112020
  //   20020022 c 1188c3 112020 20020022 c 118903 112020 20020022 c 118903 112020 20020022 c 118903 112020
  //   20020022 c 118903 112020 20020022 c 118903 112020 20020022 c 118903 112020 20020022 c 118903 112020
  //   20020022 c 20100001 109fc0 139fc3 8021 2012000c 24160003 26100001 3210000f 20080008 20090001 139900
  //   2709825 132020 20020022 c 1094022 1500fff9 22100001 2018000f 2188024 108700 20080008 20090001 139902
  //   2709825 132021 20020022 c 1094022 1500fff9 108702 2c9b022 12c00001 8000c5a 4020 1084027 84400
  //   3508ffff 82021 20020022 c 2010ffff 20110000 ae300000 22100001 22310004 ae300000 22100001 22310004
  //   ae300000 22100001 22310004 ae300000 22100001 22310004 ae300000 22100001 22310004 ae300000 22100001
  //   22310004 ae300000 22100001 22310004 ae300000 22100001 22310004 ae300000 22100001 22310004 ae300000
  //   22100001 22310004 ae300000 22100001 22310004 ae300000 22100001 22310004 ae300000 22100001 22310004
  //   ae300000 22100001 22310004 ae300000 22100001 22310004 ae300000 22100001 22310004 22100001 8020
  //   2011003c 8e130000 8e340000 274402a 11000002 ae330000 ae140000 2231fffc 1611fff8 102020 20020022 c
  //   22100004 2011003c 1611fff2 20020032 c 20080001 20110010 112020 20020022 c 200b0020 2288823 112020
  //   20020022 c 216bffff 1560fffa 2002000a c 2008ffff 20117777 112020 20020022 c 200b0010 2288826 112020
  //   20020022 c 216bffff 1560fffa 2002000a c 20090000 200b0020 20110000 20120001 a1310000 112020 20020022
  //   c 2328820 21290001 216bffff 1560fff8 200b0008 20090000 8d310000 112020 20020022 c 21290004 216bffff
  //   1560fff9 2002000a c 2011fff1 112020 20020022 c 22310001 1a20fffb 2002000a c 2002000a c 20100000
  //   22100001 102020 20020022 c 22100002 102020 20020022 c 22100003 102020 20020022 c 22100004 102020
  //   20020022 c 22100005 102020 20020022 c 22100006 102020 20020022 c 22100007 102020 20020022 c 22100008
  //   102020 20020022 20020022 c 3e00008 afb00000 23bd0004 afb30000 23bd0004 afb40000 23bd0004 afb50000
  //   23bd0004 afb60000 23bd0004 afa40000 23bd0004 afa20000 23bd0004 40000000 20160001 20140006 20150001
  //   168020 108100 2149825 132020 20020022 c 1600fffa 295a022 1680fff7 40800000 23bdfffc 8fa20000
  //   23bdfffc 8fa40000 23bdfffc 8fb60000 23bdfffc 8fb50000 23bdfffc 8fb40000 23bdfffc 8fb30000 23bdfffc
  //   8fb00000 42000018 afb00000 23bd0004 afb30000 23bd0004 afb40000 23bd0004 afb50000 23bd0004 afb60000
  //   23bd0004 afa40000 23bd0004 afa20000 23bd0004 40000000 20160002 20140006 20150001 168020 108100
  //   2149825 132020 20020022 c 1600fffa 295a022 1680fff7 40800000 23bdfffc 8fa20000 23bdfffc 8fa40000
  //   23bdfffc 8fb60000 23bdfffc 8fb50000 23bdfffc 8fb40000 23bdfffc 8fb30000 23bdfffc 8fb00000 42000018
  //   afb00000 23bd0004 afb30000 23bd0004 afb40000 23bd0004 afb50000 23bd0004 afb60000 23bd0004 afa40000
  //   23bd0004 afa20000 23bd0004 40000000 20160003 20140006 20150001 168020 108100 2149825 132020 20020022
  //   c 1600fffa 295a022 1680fff7 40800000 23bdfffc 8fa20000 23bdfffc 8fa40000 23bdfffc 8fb60000 23bdfffc
  //   8fb50000 23bdfffc 8fb40000 23bdfffc 8fb30000 23bdfffc 8fb00000 42000018
  //   OP
  //   Func
  //   rs
  //   指令字
  //   rt
  //   rd
  //   JMP
  //   JR
  //   OP
  //   Func
  //   MT/MF
  //   BLEZ
  //   Beq
  //   Bne
  //   SB
  //   AluOP
  //   AluSrcB
  //   RegWrite
  //   JAL
  //   RegDst
  //   Syscall
  //   MemToReg
  //   MemWrite
  //   INT： 每个中断来临时，提供一个上升沿
  //   当返回被中断的程序时，需要屏蔽ERET信号带来的上升沿
endmodule

// 单周期硬布线控制器
module \单周期硬布线控制器  (
  input  [5:0] OP,
  input  [5:0] Func,
  input  [4:0] MT,
  output [3:0] ALU_OP,
  output MemToReg,
  output MemWrite,
  output ALU_SRC,
  output RegWrite,
  output SysCALL,
  output SignedExt,
  output RegDst,
  output Beq,
  output Bne,
  output JR,
  output JMP,
  output JAL,
  output BLEZ,
  output SB,
  output ERET,
  output MTC0,
  output MFC0
);

  \运算控制器自动生成  \u_运算控制器自动生成_1  (
    .OP0(OP[0]), .OP1(OP[1]), .OP2(OP[2]), .OP3(OP[3]), .OP4(OP[4]), .OP5(OP[5]), .F0(Func[0]), .F1(Func[1]),
    .F2(Func[2]), .F3(Func[3]), .F4(Func[4]), .F5(Func[5]), .S0(ALU_OP[0]), .S1(ALU_OP[1]), .S2(ALU_OP[2]),
    .S3(ALU_OP[3]));
  \控制信号自动生成  \u_控制信号自动生成_1  (
    .OP0(OP[0]), .MemToReg(MemToReg), .OP1(OP[1]), .OP2(OP[2]), .OP3(OP[3]), .OP4(OP[4]),
    .MemWrite(MemWrite), .OP5(OP[5]), .F0(Func[0]), .F1(Func[1]), .F2(Func[2]), .F3(Func[3]), .F4(Func[4]),
    .F5(Func[5]), .ALU_SRC(ALU_SRC), .ERET(ERET), .BLEZ(BLEZ), .SB(SB), .RegWrite(RegWrite),
    .SysCALL(SysCALL), .SignedExt(SignedExt), .RegDst(RegDst), .BEQ(Beq), .BNE(Bne), .JR(JR), .JUMP(JMP),
    .JAL(JAL), .MT_MF(MT), .MTC0(MTC0), .MFC0(MFC0));

  // Other names for the same wires on the sheet: MT_MF[4:0] = MT; OP_CODE[5:0] = OP

  // Notes on the sheet:
  //   判断是MTC0还是MFC0
  //   运算器控制器，根据指令生成运算器功能选择信号
  //   控制信号生成，产生数据通路需要的其他控制信号
endmodule

// 运算器控制器
module \运算控制器自动生成  (
  input  OP0,
  input  OP1,
  input  OP2,
  input  OP3,
  input  OP4,
  input  OP5,
  input  F0,
  input  F1,
  input  F2,
  input  F3,
  input  F4,
  input  F5,
  output S0,
  output S1,
  output S2,
  output S3
);

  wire and_1_out, and_2_out, and_3_out, and_4_out, and_5_out, and_6_out, and_7_out, and_8_out, and_9_out,
       and_10_out, and_11_out, and_12_out, and_13_out, and_14_out, and_15_out, and_16_out, and_17_out,
       and_18_out, and_19_out, and_20_out, and_21_out, and_22_out, and_23_out, and_24_out, and_25_out,
       and_26_out, and_27_out, and_28_out, and_29_out, not_1_out, not_2_out, not_3_out, not_4_out, not_5_out,
       not_6_out, not_7_out, not_8_out, not_9_out, not_10_out, not_11_out, not_12_out, not_13_out,
       not_14_out, not_15_out, not_16_out, not_17_out, not_18_out, not_19_out, not_20_out, not_21_out,
       not_22_out, not_23_out, not_24_out, not_25_out, not_26_out, not_27_out, not_28_out, not_29_out,
       not_30_out, not_31_out, not_32_out, not_33_out, not_34_out, not_35_out, not_36_out, not_37_out,
       not_38_out, not_39_out, not_40_out, not_41_out, not_42_out, not_43_out, not_44_out, not_45_out,
       not_46_out, not_47_out, not_48_out, not_49_out, not_50_out, not_51_out, not_52_out, not_53_out,
       not_54_out, not_55_out, not_56_out, not_57_out, not_58_out, not_59_out, not_60_out, not_61_out,
       not_62_out, not_63_out, not_64_out, not_65_out, not_66_out, not_67_out, not_68_out, not_69_out,
       not_70_out, not_71_out, not_72_out, not_73_out, not_74_out, not_75_out, not_76_out, not_77_out,
       not_78_out, not_79_out, not_80_out, not_81_out, not_82_out, not_83_out, not_84_out, not_85_out,
       not_86_out, not_87_out, not_88_out, not_89_out, not_90_out, not_91_out, not_92_out, not_93_out,
       not_94_out, not_95_out, not_96_out, not_97_out, not_98_out, not_99_out, not_100_out, not_101_out,
       not_102_out, not_103_out, not_104_out, not_105_out, not_106_out, not_107_out, not_108_out,
       not_109_out, not_110_out, not_111_out, not_112_out, not_113_out, not_114_out, not_115_out,
       not_116_out, not_117_out, not_118_out, not_119_out, not_120_out, not_121_out, not_122_out,
       not_123_out, not_124_out, not_125_out, not_126_out, not_127_out, not_128_out, not_129_out,
       not_130_out, not_131_out, not_132_out, not_133_out, not_134_out, not_135_out, not_136_out,
       not_137_out, not_138_out, not_139_out, not_140_out, not_141_out, not_142_out, not_143_out,
       not_144_out, not_145_out, not_146_out, not_147_out, not_148_out, not_149_out, not_150_out,
       not_151_out, not_152_out, not_153_out, not_154_out, not_155_out, not_156_out, not_157_out,
       not_158_out, not_159_out, not_160_out, not_161_out, not_162_out, not_163_out, not_164_out,
       not_165_out, not_166_out, not_167_out, not_168_out, not_169_out, not_170_out, not_171_out,
       not_172_out, not_173_out, not_174_out, not_175_out, not_176_out, not_177_out, not_178_out,
       not_179_out, not_180_out, not_181_out, not_182_out, not_183_out, not_184_out, not_185_out;

  not not_1 (not_1_out, OP0);
  not not_2 (not_2_out, OP1);
  not not_3 (not_3_out, OP2);
  not not_4 (not_4_out, OP4);
  not not_5 (not_5_out, OP5);
  not not_6 (not_6_out, F1);
  not not_7 (not_7_out, F2);
  not not_8 (not_8_out, F3);
  not not_9 (not_9_out, F4);
  not not_10 (not_10_out, OP0);
  not not_11 (not_11_out, OP1);
  not not_12 (not_12_out, OP2);
  not not_13 (not_13_out, OP4);
  not not_14 (not_14_out, OP5);
  not not_15 (not_15_out, F0);
  not not_16 (not_16_out, F3);
  not not_17 (not_17_out, F4);
  not not_18 (not_18_out, OP0);
  not not_19 (not_19_out, OP1);
  not not_20 (not_20_out, OP2);
  not not_21 (not_21_out, OP4);
  not not_22 (not_22_out, OP5);
  not not_23 (not_23_out, F0);
  not not_24 (not_24_out, F2);
  not not_25 (not_25_out, F4);
  not not_26 (not_26_out, OP0);
  not not_27 (not_27_out, OP1);
  not not_28 (not_28_out, OP2);
  not not_29 (not_29_out, OP4);
  not not_30 (not_30_out, OP5);
  not not_31 (not_31_out, F2);
  not not_32 (not_32_out, F3);
  not not_33 (not_33_out, F4);
  not not_34 (not_34_out, F5);
  not not_35 (not_35_out, OP0);
  not not_36 (not_36_out, OP1);
  not not_37 (not_37_out, OP2);
  not not_38 (not_38_out, OP4);
  not not_39 (not_39_out, OP0);
  not not_40 (not_40_out, OP1);
  not not_41 (not_41_out, OP4);
  not not_42 (not_42_out, OP5);
  not not_43 (not_43_out, OP0);
  not not_44 (not_44_out, OP2);
  not not_45 (not_45_out, OP4);
  not not_46 (not_46_out, OP5);
  not not_47 (not_47_out, OP1);
  not not_48 (not_48_out, OP2);
  not not_49 (not_49_out, OP4);
  not not_50 (not_50_out, OP5);
  not not_51 (not_51_out, OP2);
  not not_52 (not_52_out, OP4);
  not not_53 (not_53_out, OP0);
  not not_54 (not_54_out, OP1);
  not not_55 (not_55_out, OP2);
  not not_56 (not_56_out, OP3);
  not not_57 (not_57_out, OP4);
  not not_58 (not_58_out, OP5);
  not not_59 (not_59_out, F0);
  not not_60 (not_60_out, F1);
  not not_61 (not_61_out, F3);
  not not_62 (not_62_out, F4);
  not not_63 (not_63_out, OP0);
  not not_64 (not_64_out, OP1);
  not not_65 (not_65_out, OP2);
  not not_66 (not_66_out, OP3);
  not not_67 (not_67_out, OP4);
  not not_68 (not_68_out, OP5);
  not not_69 (not_69_out, F0);
  not not_70 (not_70_out, F2);
  not not_71 (not_71_out, F3);
  not not_72 (not_72_out, F4);
  not not_73 (not_73_out, OP0);
  not not_74 (not_74_out, OP1);
  not not_75 (not_75_out, OP2);
  not not_76 (not_76_out, OP3);
  not not_77 (not_77_out, OP4);
  not not_78 (not_78_out, OP5);
  not not_79 (not_79_out, F0);
  not not_80 (not_80_out, F2);
  not not_81 (not_81_out, F4);
  not not_82 (not_82_out, OP0);
  not not_83 (not_83_out, OP1);
  not not_84 (not_84_out, OP2);
  not not_85 (not_85_out, OP3);
  not not_86 (not_86_out, OP4);
  not not_87 (not_87_out, OP5);
  not not_88 (not_88_out, F3);
  not not_89 (not_89_out, F4);
  not not_90 (not_90_out, OP0);
  not not_91 (not_91_out, OP1);
  not not_92 (not_92_out, OP4);
  not not_93 (not_93_out, OP5);
  not not_94 (not_94_out, OP0);
  not not_95 (not_95_out, OP2);
  not not_96 (not_96_out, OP4);
  not not_97 (not_97_out, OP5);
  not not_98 (not_98_out, OP0);
  not not_99 (not_99_out, OP1);
  not not_100 (not_100_out, OP2);
  not not_101 (not_101_out, OP4);
  not not_102 (not_102_out, OP5);
  not not_103 (not_103_out, F0);
  not not_104 (not_104_out, F1);
  not not_105 (not_105_out, F3);
  not not_106 (not_106_out, F4);
  not not_107 (not_107_out, OP0);
  not not_108 (not_108_out, OP1);
  not not_109 (not_109_out, OP2);
  not not_110 (not_110_out, OP4);
  not not_111 (not_111_out, OP5);
  not not_112 (not_112_out, F2);
  not not_113 (not_113_out, F3);
  not not_114 (not_114_out, F4);
  not not_115 (not_115_out, OP0);
  not not_116 (not_116_out, OP1);
  not not_117 (not_117_out, OP2);
  not not_118 (not_118_out, OP4);
  not not_119 (not_119_out, OP5);
  not not_120 (not_120_out, F2);
  not not_121 (not_121_out, F4);
  not not_122 (not_122_out, OP0);
  not not_123 (not_123_out, OP1);
  not not_124 (not_124_out, OP2);
  not not_125 (not_125_out, OP4);
  not not_126 (not_126_out, OP0);
  not not_127 (not_127_out, OP1);
  not not_128 (not_128_out, OP4);
  not not_129 (not_129_out, OP5);
  not not_130 (not_130_out, OP1);
  not not_131 (not_131_out, OP2);
  not not_132 (not_132_out, OP4);
  not not_133 (not_133_out, OP5);
  not not_134 (not_134_out, OP2);
  not not_135 (not_135_out, OP4);
  not not_136 (not_136_out, OP5);
  not not_137 (not_137_out, OP4);
  not not_138 (not_138_out, OP3);
  not not_139 (not_139_out, OP2);
  not not_140 (not_140_out, OP1);
  not not_141 (not_141_out, OP0);
  not not_142 (not_142_out, F4);
  not not_143 (not_143_out, F3);
  not not_144 (not_144_out, F1);
  not not_145 (not_145_out, OP5);
  not not_146 (not_146_out, OP4);
  not not_147 (not_147_out, OP3);
  not not_148 (not_148_out, OP2);
  not not_149 (not_149_out, OP1);
  not not_150 (not_150_out, OP0);
  not not_151 (not_151_out, F4);
  not not_152 (not_152_out, F3);
  not not_153 (not_153_out, OP5);
  not not_154 (not_154_out, OP4);
  not not_155 (not_155_out, OP3);
  not not_156 (not_156_out, OP2);
  not not_157 (not_157_out, OP1);
  not not_158 (not_158_out, OP0);
  not not_159 (not_159_out, F4);
  not not_160 (not_160_out, F2);
  not not_161 (not_161_out, F0);
  not not_162 (not_162_out, OP5);
  not not_163 (not_163_out, OP4);
  not not_164 (not_164_out, OP3);
  not not_165 (not_165_out, OP2);
  not not_166 (not_166_out, OP1);
  not not_167 (not_167_out, OP0);
  not not_168 (not_168_out, F4);
  not not_169 (not_169_out, F2);
  not not_170 (not_170_out, OP5);
  not not_171 (not_171_out, OP4);
  not not_172 (not_172_out, OP2);
  not not_173 (not_173_out, OP0);
  not not_174 (not_174_out, OP5);
  not not_175 (not_175_out, OP4);
  not not_176 (not_176_out, OP1);
  not not_177 (not_177_out, OP5);
  not not_178 (not_178_out, OP4);
  not not_179 (not_179_out, OP3);
  not not_180 (not_180_out, OP2);
  not not_181 (not_181_out, OP1);
  not not_182 (not_182_out, OP0);
  not not_183 (not_183_out, F4);
  not not_184 (not_184_out, F3);
  not not_185 (not_185_out, F0);
  and and_1 (and_1_out, not_1_out, not_2_out, not_3_out, not_4_out, not_5_out, not_6_out, not_7_out, not_8_out, not_9_out, F5);
  and and_2 (and_2_out, not_10_out, not_11_out, not_12_out, not_13_out, not_14_out, not_15_out, F2, not_16_out, not_17_out, F5);
  and and_3 (and_3_out, not_18_out, not_19_out, not_20_out, not_21_out, not_22_out, not_23_out, F1, not_24_out, F3, not_25_out, F5);
  and and_4 (and_4_out, not_26_out, not_27_out, not_28_out, not_29_out, not_30_out, F0, F1, not_31_out, not_32_out, not_33_out, not_34_out);
  and and_5 (and_5_out, not_35_out, not_36_out, not_37_out, OP3, not_38_out);
  and and_6 (and_6_out, not_39_out, not_40_out, OP3, not_41_out, not_42_out);
  and and_7 (and_7_out, not_43_out, not_44_out, OP3, not_45_out, not_46_out);
  and and_8 (and_8_out, not_47_out, not_48_out, OP3, not_49_out, not_50_out);
  and and_9 (and_9_out, OP0, OP1, not_51_out, not_52_out, OP5);
  and and_10 (and_10_out, not_53_out, not_54_out, not_55_out, not_56_out, not_57_out, not_58_out, not_59_out, not_60_out, F2, not_61_out, not_62_out, F5);
  and and_11 (and_11_out, not_63_out, not_64_out, not_65_out, not_66_out, not_67_out, not_68_out, not_69_out, F1, not_70_out, not_71_out, not_72_out);
  and and_12 (and_12_out, not_73_out, not_74_out, not_75_out, not_76_out, not_77_out, not_78_out, not_79_out, F1, not_80_out, not_81_out, F5);
  and and_13 (and_13_out, not_82_out, not_83_out, not_84_out, not_85_out, not_86_out, not_87_out, F0, F1, not_88_out, not_89_out, F5);
  and and_14 (and_14_out, not_90_out, not_91_out, OP2, OP3, not_92_out, not_93_out);
  and and_15 (and_15_out, not_94_out, OP1, not_95_out, OP3, not_96_out, not_97_out);
  and and_16 (and_16_out, not_98_out, not_99_out, not_100_out, not_101_out, not_102_out, not_103_out, not_104_out, not_105_out, not_106_out, F5);
  and and_17 (and_17_out, not_107_out, not_108_out, not_109_out, not_110_out, not_111_out, not_112_out, not_113_out, not_114_out, F5);
  and and_18 (and_18_out, not_115_out, not_116_out, not_117_out, not_118_out, not_119_out, F0, F1, not_120_out, not_121_out, F5);
  and and_19 (and_19_out, not_122_out, not_123_out, not_124_out, OP3, not_125_out);
  and and_20 (and_20_out, not_126_out, not_127_out, OP3, not_128_out, not_129_out);
  and and_21 (and_21_out, not_130_out, not_131_out, OP3, not_132_out, not_133_out);
  and and_22 (and_22_out, OP0, OP1, not_134_out, not_135_out, OP5);
  and and_23 (and_23_out, not_136_out, not_137_out, not_138_out, not_139_out, not_140_out, not_141_out, F5, not_142_out, not_143_out, F2, not_144_out, F0);
  and and_24 (and_24_out, not_145_out, not_146_out, not_147_out, not_148_out, not_149_out, not_150_out, F5, not_151_out, not_152_out, F2, F1, F0);
  and and_25 (and_25_out, not_153_out, not_154_out, not_155_out, not_156_out, not_157_out, not_158_out, F5, not_159_out, F3, not_160_out, F1, not_161_out);
  and and_26 (and_26_out, not_162_out, not_163_out, not_164_out, not_165_out, not_166_out, not_167_out, F5, not_168_out, F3, not_169_out, F1, F0);
  and and_27 (and_27_out, not_170_out, not_171_out, OP3, not_172_out, OP1, not_173_out);
  and and_28 (and_28_out, not_174_out, not_175_out, OP3, OP2, not_176_out, OP0);
  and and_29 (and_29_out, not_177_out, not_178_out, not_179_out, not_180_out, not_181_out, not_182_out, F5, not_183_out, not_184_out, F2, F1, not_185_out);
  or or_1 (S0, and_1_out, and_2_out, and_3_out, and_4_out, and_5_out, and_6_out, and_7_out, and_8_out, and_9_out);
  or or_2 (S1, and_10_out, and_11_out, and_12_out, and_13_out, and_14_out, and_15_out);
  or or_3 (S2, and_16_out, and_17_out, and_18_out, and_19_out, and_20_out, and_21_out, and_22_out);
  or or_4 (S3, and_23_out, and_24_out, and_25_out, and_26_out, and_27_out, and_28_out, and_29_out);
endmodule

// 控制信号生成
module \控制信号自动生成  (
  input  OP0,
  input  OP1,
  input  OP2,
  input  OP3,
  input  OP4,
  input  OP5,
  input  F0,
  input  [4:0] MT_MF,
  input  F1,
  input  F2,
  input  F3,
  input  F4,
  input  F5,
  output MemToReg,
  output MTC0,
  output MemWrite,
  output MFC0,
  output ALU_SRC,
  output ERET,
  output BLEZ,
  output SB,
  output RegWrite,
  output SysCALL,
  output SignedExt,
  output RegDst,
  output BEQ,
  output BNE,
  output JR,
  output JUMP,
  output JAL
);

  wire and_1_out, and_2_out, and_3_out, and_4_out, and_5_out, and_6_out, and_7_out, and_8_out, and_9_out,
       and_10_out, and_12_out, and_13_out, and_17_out, and_18_out, and_19_out, and_20_out, and_21_out,
       and_22_out, and_23_out, and_25_out, and_26_out, and_27_out, and_28_out, and_32_out, and_33_out,
       and_35_out, and_36_out, and_37_out, and_38_out, not_1_out, not_2_out, not_3_out, not_4_out, not_5_out,
       not_6_out, not_7_out, not_8_out, not_9_out, not_10_out, not_11_out, not_12_out, not_13_out,
       not_14_out, not_15_out, not_16_out, not_17_out, not_18_out, not_19_out, not_20_out, not_21_out,
       not_22_out, not_23_out, not_24_out, not_25_out, not_26_out, not_27_out, not_28_out, not_29_out,
       not_30_out, not_31_out, not_32_out, not_33_out, not_34_out, not_35_out, not_36_out, not_37_out,
       not_38_out, not_39_out, not_40_out, not_41_out, not_42_out, not_43_out, not_44_out, not_45_out,
       not_46_out, not_47_out, not_48_out, not_49_out, not_50_out, not_51_out, not_52_out, not_53_out,
       not_54_out, not_55_out, not_56_out, not_57_out, not_58_out, not_59_out, not_60_out, not_61_out,
       not_62_out, not_63_out, not_64_out, not_65_out, not_66_out, not_67_out, not_68_out, not_69_out,
       not_70_out, not_71_out, not_72_out, not_73_out, not_74_out, not_75_out, not_76_out, not_77_out,
       not_78_out, not_79_out, not_80_out, not_81_out, not_82_out, not_83_out, not_84_out, not_85_out,
       not_86_out, not_87_out, not_88_out, not_89_out, not_90_out, not_91_out, not_92_out, not_93_out,
       not_94_out, not_95_out, not_96_out, not_97_out, not_98_out, not_99_out, not_100_out, not_101_out,
       not_102_out, not_103_out, not_104_out, not_105_out, not_106_out, not_107_out, not_108_out,
       not_109_out, not_110_out, not_111_out, not_112_out, not_113_out, not_114_out, not_115_out,
       not_116_out, not_117_out, not_118_out, not_119_out, not_120_out, not_121_out, not_122_out,
       not_123_out, not_124_out, not_125_out, not_126_out, not_127_out, not_128_out, not_129_out,
       not_130_out, not_131_out, not_132_out, not_133_out, not_134_out, not_135_out, not_136_out,
       not_137_out, not_138_out, not_139_out, not_140_out, not_141_out, not_142_out, not_143_out,
       not_144_out, not_145_out, not_146_out, not_147_out, not_148_out, not_149_out, not_150_out,
       not_151_out, not_152_out, not_153_out, not_154_out, not_155_out, not_156_out, not_157_out,
       not_158_out, not_159_out, not_160_out, not_161_out, not_162_out, not_163_out, not_164_out,
       not_165_out, not_166_out, not_167_out, not_168_out, not_169_out, not_170_out, not_171_out,
       not_172_out, not_173_out, not_174_out, not_175_out, not_176_out, not_177_out, not_178_out,
       not_179_out, not_180_out, not_181_out, not_182_out, not_183_out, not_184_out, not_185_out,
       not_186_out, not_187_out, not_188_out, not_189_out, not_190_out, not_191_out, not_192_out,
       not_193_out, not_194_out, not_195_out, not_196_out, not_197_out, not_198_out;

  not not_1 (not_1_out, OP2);
  not not_2 (not_2_out, OP3);
  not not_3 (not_3_out, OP4);
  not not_4 (not_4_out, OP0);
  not not_5 (not_5_out, OP1);
  not not_6 (not_6_out, OP2);
  not not_7 (not_7_out, OP4);
  not not_8 (not_8_out, OP2);
  not not_9 (not_9_out, OP4);
  not not_10 (not_10_out, OP0);
  not not_11 (not_11_out, OP1);
  not not_12 (not_12_out, OP2);
  not not_13 (not_13_out, OP4);
  not not_14 (not_14_out, OP0);
  not not_15 (not_15_out, OP2);
  not not_16 (not_16_out, OP4);
  not not_17 (not_17_out, OP5);
  not not_18 (not_18_out, OP1);
  not not_19 (not_19_out, OP4);
  not not_20 (not_20_out, OP5);
  not not_21 (not_21_out, OP2);
  not not_22 (not_22_out, OP4);
  not not_23 (not_23_out, OP5);
  not not_24 (not_24_out, OP3);
  not not_25 (not_25_out, OP2);
  not not_26 (not_26_out, OP1);
  not not_27 (not_27_out, OP0);
  not not_28 (not_28_out, F5);
  not not_29 (not_29_out, F2);
  not not_30 (not_30_out, F1);
  not not_31 (not_31_out, F0);
  not not_32 (not_32_out, OP0);
  not not_33 (not_33_out, OP3);
  not not_34 (not_34_out, OP4);
  not not_35 (not_35_out, OP5);
  not not_36 (not_36_out, OP0);
  not not_37 (not_37_out, OP1);
  not not_38 (not_38_out, OP2);
  not not_39 (not_39_out, OP4);
  not not_40 (not_40_out, OP0);
  not not_41 (not_41_out, OP1);
  not not_42 (not_42_out, OP2);
  not not_43 (not_43_out, OP4);
  not not_44 (not_44_out, OP5);
  not not_45 (not_45_out, F0);
  not not_46 (not_46_out, F2);
  not not_47 (not_47_out, F3);
  not not_48 (not_48_out, F4);
  not not_49 (not_49_out, OP0);
  not not_50 (not_50_out, OP1);
  not not_51 (not_51_out, OP2);
  not not_52 (not_52_out, OP4);
  not not_53 (not_53_out, OP5);
  not not_54 (not_54_out, F3);
  not not_55 (not_55_out, F4);
  not not_56 (not_56_out, OP0);
  not not_57 (not_57_out, OP1);
  not not_58 (not_58_out, OP2);
  not not_59 (not_59_out, OP4);
  not not_60 (not_60_out, OP5);
  not not_61 (not_61_out, F2);
  not not_62 (not_62_out, F3);
  not not_63 (not_63_out, F4);
  not not_64 (not_64_out, OP0);
  not not_65 (not_65_out, OP1);
  not not_66 (not_66_out, OP2);
  not not_67 (not_67_out, OP4);
  not not_68 (not_68_out, OP5);
  not not_69 (not_69_out, F2);
  not not_70 (not_70_out, F4);
  not not_71 (not_71_out, OP0);
  not not_72 (not_72_out, OP1);
  not not_73 (not_73_out, OP2);
  not not_74 (not_74_out, OP3);
  not not_75 (not_75_out, OP4);
  not not_76 (not_76_out, OP5);
  not not_77 (not_77_out, F0);
  not not_78 (not_78_out, F1);
  not not_79 (not_79_out, F4);
  not not_80 (not_80_out, F5);
  not not_81 (not_81_out, OP0);
  not not_82 (not_82_out, OP1);
  not not_83 (not_83_out, OP2);
  not not_84 (not_84_out, OP4);
  not not_85 (not_85_out, OP0);
  not not_86 (not_86_out, OP2);
  not not_87 (not_87_out, OP4);
  not not_88 (not_88_out, OP5);
  not not_89 (not_89_out, OP1);
  not not_90 (not_90_out, OP2);
  not not_91 (not_91_out, OP4);
  not not_92 (not_92_out, OP5);
  not not_93 (not_93_out, OP0);
  not not_94 (not_94_out, OP3);
  not not_95 (not_95_out, OP4);
  not not_96 (not_96_out, OP5);
  not not_97 (not_97_out, OP1);
  not not_98 (not_98_out, OP3);
  not not_99 (not_99_out, OP4);
  not not_100 (not_100_out, OP5);
  not not_101 (not_101_out, OP2);
  not not_102 (not_102_out, OP4);
  not not_103 (not_103_out, OP0);
  not not_104 (not_104_out, OP1);
  not not_105 (not_105_out, OP2);
  not not_106 (not_106_out, OP3);
  not not_107 (not_107_out, OP4);
  not not_108 (not_108_out, OP5);
  not not_109 (not_109_out, F0);
  not not_110 (not_110_out, F2);
  not not_111 (not_111_out, F3);
  not not_112 (not_112_out, F4);
  not not_113 (not_113_out, OP0);
  not not_114 (not_114_out, OP1);
  not not_115 (not_115_out, OP2);
  not not_116 (not_116_out, OP3);
  not not_117 (not_117_out, OP4);
  not not_118 (not_118_out, OP5);
  not not_119 (not_119_out, F2);
  not not_120 (not_120_out, F3);
  not not_121 (not_121_out, F4);
  not not_122 (not_122_out, OP0);
  not not_123 (not_123_out, OP1);
  not not_124 (not_124_out, OP2);
  not not_125 (not_125_out, OP3);
  not not_126 (not_126_out, OP4);
  not not_127 (not_127_out, OP5);
  not not_128 (not_128_out, F2);
  not not_129 (not_129_out, F4);
  not not_130 (not_130_out, OP0);
  not not_131 (not_131_out, OP1);
  not not_132 (not_132_out, OP3);
  not not_133 (not_133_out, OP4);
  not not_134 (not_134_out, OP5);
  not not_135 (not_135_out, OP1);
  not not_136 (not_136_out, OP3);
  not not_137 (not_137_out, OP4);
  not not_138 (not_138_out, OP5);
  not not_139 (not_139_out, OP0);
  not not_140 (not_140_out, OP1);
  not not_141 (not_141_out, OP2);
  not not_142 (not_142_out, OP3);
  not not_143 (not_143_out, OP4);
  not not_144 (not_144_out, OP5);
  not not_145 (not_145_out, F0);
  not not_146 (not_146_out, F1);
  not not_147 (not_147_out, F2);
  not not_148 (not_148_out, F4);
  not not_149 (not_149_out, F5);
  not not_150 (not_150_out, OP0);
  not not_151 (not_151_out, OP2);
  not not_152 (not_152_out, OP3);
  not not_153 (not_153_out, OP4);
  not not_154 (not_154_out, OP5);
  not not_155 (not_155_out, F0);
  not not_156 (not_156_out, F1);
  not not_157 (not_157_out, F2);
  not not_158 (not_158_out, F4);
  not not_159 (not_159_out, F5);
  not not_160 (not_160_out, OP2);
  not not_161 (not_161_out, OP3);
  not not_162 (not_162_out, OP4);
  not not_163 (not_163_out, OP5);
  and and_1 (and_1_out, not_10_out, not_11_out, not_12_out, OP3, not_13_out);
  and and_2 (and_2_out, not_14_out, not_15_out, OP3, not_16_out, not_17_out);
  and and_3 (and_3_out, not_18_out, OP3, not_19_out, not_20_out);
  and and_4 (and_4_out, OP0, OP1, not_21_out, not_22_out, OP5);
  not not_164 (not_164_out, OP0);
  not not_165 (not_165_out, OP2);
  not not_166 (not_166_out, OP4);
  not not_167 (not_167_out, OP5);
  not not_168 (not_168_out, OP1);
  not not_169 (not_169_out, OP4);
  not not_170 (not_170_out, OP5);
  not not_171 (not_171_out, OP2);
  not not_172 (not_172_out, OP3);
  not not_173 (not_173_out, OP4);
  and and_5 (and_5_out, not_81_out, not_82_out, not_83_out, OP3, not_84_out);
  and and_6 (and_6_out, not_85_out, not_86_out, OP3, not_87_out, not_88_out);
  and and_7 (and_7_out, not_89_out, not_90_out, OP3, not_91_out, not_92_out);
  and and_8 (and_8_out, not_93_out, OP2, not_94_out, not_95_out, not_96_out);
  and and_9 (and_9_out, not_97_out, OP2, not_98_out, not_99_out, not_100_out);
  and and_10 (and_10_out, OP0, OP1, not_101_out, not_102_out, OP5);
  not not_174 (not_174_out, OP0);
  not not_175 (not_175_out, OP1);
  not not_176 (not_176_out, OP2);
  not not_177 (not_177_out, OP3);
  not not_178 (not_178_out, OP4);
  not not_179 (not_179_out, OP5);
  not not_180 (not_180_out, F3);
  not not_181 (not_181_out, F4);
  not not_182 (not_182_out, OP2);
  not not_183 (not_183_out, OP3);
  not not_184 (not_184_out, OP4);
  not not_185 (not_185_out, OP5);
  and and_11 (MemToReg, OP0, OP1, not_1_out, not_2_out, not_3_out, OP5);
  and and_12 (and_12_out, not_4_out, not_5_out, not_6_out, OP3, not_7_out, OP5);
  or or_1 (MemWrite, and_12_out, and_13_out);
  and and_13 (and_13_out, OP0, OP1, not_8_out, OP3, not_9_out, OP5);
  or or_2 (ALU_SRC, and_1_out, and_2_out, and_3_out, and_4_out);
  and and_14 (ERET, not_23_out, OP4, not_24_out, not_25_out, not_26_out, not_27_out, not_28_out, F4, F3, not_29_out, not_30_out, not_31_out);
  and and_15 (BLEZ, not_32_out, OP1, OP2, not_33_out, not_34_out, not_35_out);
  and and_16 (SB, not_36_out, not_37_out, not_38_out, OP3, not_39_out, OP5);
  and and_17 (and_17_out, not_40_out, not_41_out, not_42_out, not_43_out, not_44_out, not_45_out, not_46_out, not_47_out, not_48_out);
  and and_18 (and_18_out, not_49_out, not_50_out, not_51_out, not_52_out, not_53_out, not_54_out, not_55_out, F5);
  and and_19 (and_19_out, not_56_out, not_57_out, not_58_out, not_59_out, not_60_out, F1, not_61_out, not_62_out, not_63_out);
  and and_20 (and_20_out, not_64_out, not_65_out, not_66_out, not_67_out, not_68_out, F1, not_69_out, not_70_out, F5);
  and and_21 (and_21_out, not_164_out, not_165_out, OP3, not_166_out, not_167_out);
  and and_22 (and_22_out, not_168_out, OP3, not_169_out, not_170_out);
  and and_23 (and_23_out, OP0, OP1, not_171_out, not_172_out, not_173_out);
  and and_24 (SysCALL, not_71_out, not_72_out, not_73_out, not_74_out, not_75_out, not_76_out, not_77_out, not_78_out, F2, F3, not_79_out, not_80_out);
  and and_25 (and_25_out, not_103_out, not_104_out, not_105_out, not_106_out, not_107_out, not_108_out, not_109_out, not_110_out, not_111_out, not_112_out);
  and and_26 (and_26_out, not_174_out, not_175_out, not_176_out, not_177_out, not_178_out, not_179_out, not_180_out, not_181_out, F5);
  and and_27 (and_27_out, not_113_out, not_114_out, not_115_out, not_116_out, not_117_out, not_118_out, F1, not_119_out, not_120_out, not_121_out);
  and and_28 (and_28_out, not_122_out, not_123_out, not_124_out, not_125_out, not_126_out, not_127_out, F1, not_128_out, not_129_out, F5);
  and and_29 (BEQ, not_130_out, not_131_out, OP2, not_132_out, not_133_out, not_134_out);
  and and_30 (BNE, OP0, not_135_out, OP2, not_136_out, not_137_out, not_138_out);
  and and_31 (JR, not_139_out, not_140_out, not_141_out, not_142_out, not_143_out, not_144_out, not_145_out, not_146_out, not_147_out, F3, not_148_out, not_149_out);
  and and_32 (and_32_out, not_150_out, not_151_out, not_152_out, not_153_out, not_154_out, not_155_out, not_156_out, not_157_out, F3, not_158_out, not_159_out);
  and and_33 (and_33_out, OP1, not_182_out, not_183_out, not_184_out, not_185_out);
  and and_34 (JAL, OP0, OP1, not_160_out, not_161_out, not_162_out, not_163_out);
  or or_3 (RegWrite, and_17_out, and_18_out, and_19_out, and_20_out, and_21_out, and_22_out, and_23_out);
  or or_4 (SignedExt, and_5_out, and_6_out, and_7_out, and_8_out, and_9_out, and_10_out);
  or or_5 (RegDst, and_25_out, and_26_out, and_27_out, and_28_out);
  or or_6 (JUMP, and_32_out, and_33_out);
  not not_186 (not_186_out, OP0);
  not not_187 (not_187_out, OP1);
  not not_188 (not_188_out, OP2);
  not not_189 (not_189_out, OP3);
  not not_190 (not_190_out, OP5);
  not not_191 (not_191_out, F3);
  not not_192 (not_192_out, F4);
  not not_193 (not_193_out, F5);
  and and_35 (and_35_out, not_186_out, not_187_out, not_188_out, not_189_out, OP4, not_190_out);
  and and_36 (and_36_out, not_191_out, not_192_out, not_193_out);
  and and_37 (and_37_out, and_35_out, and_36_out);
  not not_194 (not_194_out, MT_MF[0]);
  not not_195 (not_195_out, MT_MF[1]);
  not not_196 (not_196_out, MT_MF[3]);
  not not_197 (not_197_out, MT_MF[4]);
  and and_38 (and_38_out, not_194_out, not_195_out, MT_MF[2], not_196_out, not_197_out);
  not not_198 (not_198_out, and_38_out);
  and and_39 (MTC0, and_37_out, and_38_out);
  and and_40 (MFC0, and_37_out, not_198_out);

  // Notes on the sheet:
  //   MCT0 / MFC0 / ERET
  //   MCT0 / MFC0
endmodule

// ALU
module MIPS_ALU (
  input  [4:0] shamt,
  input  [31:0] X,
  input  [31:0] Y,
  input  [3:0] AluOP,
  output Equal,
  output [31:0] Result,
  output [31:0] Result_2
);

  wire [0:0] comparator_1_lt, comparator_2_lt;
  wire [31:0] adder_1_out, AND_out, divider_1_out, divider_1_rem, multiplier_1_cout, multiplier_1_out,
       NOR_out, OR_out, shifter_1_out, shifter_2_out, shifter_3_out, subtractor_1_out, XOR_out;

  assign AND_out = X & Y;  // AND_Gate AND, 32 bits wide
  assign OR_out = X | Y;  // OR_Gate OR, 32 bits wide
  Shifter #(.width(32), .shift("ll")) shifter_1 (.in(Y), .\dist (shamt), .out(shifter_1_out));
  Shifter #(.width(32), .shift("ar")) shifter_2 (.in(Y), .\dist (shamt), .out(shifter_2_out));
  Shifter #(.width(32), .shift("lr")) shifter_3 (.in(Y), .\dist (shamt), .out(shifter_3_out));
  Multiplier #(.width(32)) multiplier_1 (.a(X), .b(Y), .out(multiplier_1_out), .cout(multiplier_1_cout));  // open: cin
  Divider #(.width(32)) divider_1 (.a(X), .b(Y), .out(divider_1_out), .rem(divider_1_rem));  // open: upper
  Adder #(.width(32)) adder_1 (.a(X), .b(Y), .out(adder_1_out));  // open: cin, cout
  Subtractor #(.width(32)) subtractor_1 (.a(X), .b(Y), .out(subtractor_1_out));  // open: bin, bout
  assign XOR_out = X ^ Y;  // XOR_Gate XOR, 32 bits wide
  assign NOR_out = ~(X | Y);  // NOR_Gate NOR, 32 bits wide
  Comparator #(.width(32), .mode("twosComplement")) comparator_1 (
    .a(X), .b(Y), .eq(Equal), .lt(comparator_1_lt[0]));  // open: gt
  Comparator #(.width(32), .mode("unsigned")) comparator_2 (.a(X), .b(Y), .lt(comparator_2_lt[0]));  // open: gt, eq
  Multiplexer #(.select(4), .width(32), .disabled("Z"), .enable("false")) multiplexer_1 (
    .in0(shifter_1_out), .in1(shifter_2_out), .in2(shifter_3_out), .in3(multiplier_1_out),
    .in4(divider_1_out), .in5(adder_1_out), .in6(subtractor_1_out), .in7(AND_out), .in8(OR_out),
    .in9(XOR_out), .in10(NOR_out), .in11({{31{1'b0}}, comparator_1_lt[0]}),
    .in12({{31{1'b0}}, comparator_2_lt[0]}), .in13({32{1'b0}}), .in14({32{1'b0}}), .in15({32{1'b0}}),
    .out(Result), .sel(AluOP));
  Multiplexer #(.select(4), .width(32), .disabled("Z"), .enable("false")) multiplexer_2 (
    .in0({32{1'b0}}), .in1({32{1'b0}}), .in2({32{1'b0}}), .in3(multiplier_1_cout), .in4(divider_1_rem),
    .in5({32{1'b0}}), .in6({32{1'b0}}), .in7({32{1'b0}}), .in8({32{1'b0}}), .in9({32{1'b0}}),
    .in10({32{1'b0}}), .in11({32{1'b0}}), .in12({32{1'b0}}), .in13({32{1'b0}}), .in14({32{1'b0}}),
    .in15({32{1'b0}}), .out(Result_2), .sel(AluOP));

  // Other names for the same wires on the sheet: Result2[31:0] = Result_2; S[3:0] = AluOP

  // Notes on the sheet:
  //   不要改变此引脚区域内容，也不要改变ALU封装形式
  //   输入引脚
  //   输出引脚
endmodule

module MIPS_Regifile (
  input  [31:0] Din,
  input  Clk,
  input  WE,
  input  [4:0] R1_num,
  input  [4:0] W_num,
  input  [4:0] R2_num,
  output [31:0] R1,
  output [31:0] R2
);

  // RegisterFile registerfile_1: pin names not known; wires that end beside it: Din, Clk, WE, W_num, R1_num, R2_num, R1, R2
endmodule

module \理想流水线  (
);

  wire CLK, Go, IR1, IR2, IR3, RST, W1, W2, W3;
  wire [11:0] EX_PC, ID_PC, IF_PC, MEM_PC, WB_PC;
  wire [15:0] \LoadUse次数 , \总周期数 , \插入气泡数 , \无条件分支数 , \条件分支成功数 ;
  wire [31:0] LedData;

  Button \u_总复位  (.out(RST));
  Button _1 (.out(IR1));
  Button _2 (.out(IR2));
  Button _3 (.out(IR3));
  Button \u_继续运行  (.out(Go));
  LED #(.active("true")) led_1 (.in(W1));
  LED #(.active("true")) led_2 (.in(W2));
  LED #(.active("true")) led_3 (.in(W3));
  Hex_Digit_Display hex_digit_display_1 (.value(LedData[31:28]));  // open: dp
  Hex_Digit_Display hex_digit_display_2 (.value(LedData[23:20]));  // open: dp
  Hex_Digit_Display hex_digit_display_3 (.value(LedData[27:24]));  // open: dp
  Hex_Digit_Display hex_digit_display_4 (.value(LedData[19:16]));  // open: dp
  Hex_Digit_Display hex_digit_display_5 (.value(LedData[15:12]));  // open: dp
  Hex_Digit_Display hex_digit_display_6 (.value(LedData[11:8]));  // open: dp
  Hex_Digit_Display hex_digit_display_7 (.value(LedData[7:4]));  // open: dp
  Clock #(.highDuration(1), .lowDuration(1)) clock_1 (.out(CLK));
  Hex_Digit_Display hex_digit_display_8 (.value(LedData[3:0]));  // open: dp
  // Probe on \总周期数 
  // Probe on \无条件分支数 
  // Probe on \条件分支成功数 
  // Probe on \插入气泡数 
  // Probe on \LoadUse次数 
  // Probe on IF_PC
  // Probe on ID_PC
  // Probe on EX_PC
  // Probe on MEM_PC
  // Probe on WB_PC

  // Notes on the sheet:
  //   中断源
  //   中断等待指示
  //   数码管输出
  //   流水调试日志用
endmodule

module \气泡流水线  (
  output RegWrite,
  output MemWrite,
  output [31:0] PC,
  output [31:0] IR,
  output [31:0] RDin,
  output [31:0] MDin
);

  wire CLK, Go, IR1, IR2, IR3, W1, W2, W3;
  wire [15:0] \总周期数 ;
  wire [31:0] LedData;

  Clock #(.highDuration(1), .lowDuration(1)) clock_1 (.out(CLK));
  Button _1 (.out(IR1));
  Button _2 (.out(IR2));
  Button _3 (.out(IR3));
  Button \u_继续运行  (.out(Go));
  LED #(.active("true")) led_1 (.in(W1));
  LED #(.active("true")) led_2 (.in(W2));
  LED #(.active("true")) led_3 (.in(W3));
  Hex_Digit_Display hex_digit_display_1 (.value(LedData[31:28]));  // open: dp
  Hex_Digit_Display hex_digit_display_2 (.value(LedData[23:20]));  // open: dp
  Hex_Digit_Display hex_digit_display_3 (.value(LedData[27:24]));  // open: dp
  Hex_Digit_Display hex_digit_display_4 (.value(LedData[19:16]));  // open: dp
  Hex_Digit_Display hex_digit_display_5 (.value(LedData[15:12]));  // open: dp
  Hex_Digit_Display hex_digit_display_6 (.value(LedData[7:4]));  // open: dp
  Hex_Digit_Display hex_digit_display_7 (.value(LedData[11:8]));  // open: dp
  // Probe on \总周期数 
  Hex_Digit_Display hex_digit_display_8 (.value(LedData[3:0]));  // open: dp

  // Notes on the sheet:
  //   中断源
  //   中断等待指示
  //   总复位信号应将除ROM以外所有存储组件全部清零
  //   数码管输出
  //   数码管输出应该用寄存器锁存，否则显示数据只能一闪而过
  //   为方便自动评测，需要输出PC，IR，寄存器文件写入端口RDin，内存写入端口MDin等信号
endmodule

module \重定向流水线  (
  output RegWrite,
  output MemWrite,
  output [31:0] PC,
  output [31:0] IR,
  output [31:0] RDin,
  output [31:0] MDin
);

  wire CLK, Go, IR1, IR2, IR3, W1, W2, W3;
  wire [15:0] \总周期数 ;
  wire [31:0] LedData;

  Clock #(.highDuration(1), .lowDuration(1)) clock_1 (.out(CLK));
  Button _1 (.out(IR1));
  Button _2 (.out(IR2));
  Button _3 (.out(IR3));
  Button \u_继续运行  (.out(Go));
  LED #(.active("true")) led_1 (.in(W1));
  LED #(.active("true")) led_2 (.in(W2));
  LED #(.active("true")) led_3 (.in(W3));
  Hex_Digit_Display hex_digit_display_1 (.value(LedData[31:28]));  // open: dp
  Hex_Digit_Display hex_digit_display_2 (.value(LedData[27:24]));  // open: dp
  Hex_Digit_Display hex_digit_display_3 (.value(LedData[23:20]));  // open: dp
  Hex_Digit_Display hex_digit_display_4 (.value(LedData[15:12]));  // open: dp
  Hex_Digit_Display hex_digit_display_5 (.value(LedData[19:16]));  // open: dp
  Hex_Digit_Display hex_digit_display_6 (.value(LedData[11:8]));  // open: dp
  Hex_Digit_Display hex_digit_display_7 (.value(LedData[7:4]));  // open: dp
  // Probe on \总周期数 
  Hex_Digit_Display hex_digit_display_8 (.value(LedData[3:0]));  // open: dp

  // Notes on the sheet:
  //   中断源
  //   中断等待指示
  //   总复位信号应将除ROM以外所有存储组件全部清零
  //   数码管输出
  //   数码管输出应该用寄存器锁存，否则显示数据只能一闪而过
  //   为方便自动评测，需要输出PC，IR，寄存器文件写入端口RDin，内存写入端口MDin等信号
endmodule

module \中断按键参考电路  (
  input  \同步清零信号 ,
  output \与中断屏蔽位与 
);

  wire \_1号中断_out , and_1_out, clock_1_out, d_ff_1_q, or_1_out, or_2_out;

  Clock #(.highDuration(1), .lowDuration(1)) clock_1 (.out(clock_1_out));
  Button \_1号中断  (.out(\_1号中断_out ));
  LED #(.active("true")) \_1号中断等待指示灯  (.in(or_1_out));
  or or_1 (or_1_out, \与中断屏蔽位与 , d_ff_1_q);
  D_Flip_Flop #(.trigger("rising"), .Pre_Clr_Positions("LEGACY"), .NegatePresetClear("false"), .enable("true"), .NewFFLayout("false")) d_ff_1 (
    .clk(\_1号中断_out ), .D(1'b1), .Q(d_ff_1_q), .reset(\与中断屏蔽位与 ));  // open: Qn, preset, en
  or or_2 (or_2_out, d_ff_1_q, \与中断屏蔽位与 );
  and and_1 (and_1_out, or_2_out, ~\同步清零信号 );  // AND_Gate
  D_Flip_Flop #(.trigger("rising"), .Pre_Clr_Positions("LEGACY"), .NegatePresetClear("false"), .enable("true"), .NewFFLayout("false")) IR1 (
    .clk(clock_1_out), .D(and_1_out), .Q(\与中断屏蔽位与 ));  // open: Qn, preset, en, reset
  \单周期硬布线控制器  \u_单周期硬布线控制器_1  ();  // open: Func, OP, ALU_OP, MemToReg, MemWrite, ALU_SRC, RegWrite, SysCALL, SignedExt, RegDst, JR, JMP, Beq, JAL, Bne, BLEZ, SB, ERET, MTC0, MFC0, MT

  // Notes on the sheet:
  //   中断信号采样参考电路
  //   Reset 
endmodule
