// Logisim project cpu24+4+chongliu+dynamicPredict_8路全相联_默认不跳.circ as structural Verilog: 23 circuits, main circuit ◇单周期MIPS
module \单周期MIPS  (
  output RegWrite,
  output MemWrite,
  output [31:0] PC,
  output [31:0] IR,
  output [31:0] RDin,
  output [31:0] MDin
);

  wire and_1_out, and_3_out, and_4_out, and_5_out, and_6_out, and_7_out, and_8_out, and_9_out, CLK,
       comparator_1_eq, comparator_2_eq, comparator_2_lt, Go, IR1, IR2, IR3, mips_alu_1_equal,
       multiplexer_2_out, multiplexer_5_out, multiplexer_11_out, not_1_out, not_2_out, not_3_out, not_4_out,
       not_5_out, not_6_out, not_7_out, not_8_out, not_9_out, or_1_out, register_1_q, RST, SignedExt, stop,
       Syscall, W1, W2, W3, xor_1_out, \单周期硬布线控制器_1_alu_src , \单周期硬布线控制器_1_beq , \单周期硬布线控制器_1_blez ,
       \单周期硬布线控制器_1_bne , \单周期硬布线控制器_1_jal , \单周期硬布线控制器_1_jr , \单周期硬布线控制器_1_memtoreg , \单周期硬布线控制器_1_regdst ,
       \单周期硬布线控制器_1_sb , \无条件分支 , \条件分支成功 ;
  wire [3:0] \单周期硬布线控制器_1_alu_op ;
  wire [4:0] multiplexer_6_out, multiplexer_7_out, multiplexer_8_out, multiplexer_9_out;
  wire [15:0] \总周期数 , \无条件分支数 , \条件分支成功数 ;
  wire [31:0] a0, adder_1_out, adder_2_out, bit_extender_1_out, bit_extender_2_out, LedData,
       mips_alu_1_result, multiplexer_1_out, multiplexer_3_out, multiplexer_4_out, multiplexer_12_out,
       multiplexer_13_out, multiplexer_14_out, multiplexer_16_out, ram_1_data, shifter_1_out, v0;

  Button \u_总复位  (.out(RST));
  // Probe on \总周期数 
  // Probe on \无条件分支数 
  // Probe on \条件分支成功数 
  not not_1 (not_1_out, stop);
  Multiplexer #(.select(1), .width(32), .disabled("Z"), .enable("false")) multiplexer_1 (
    .in0({adder_1_out[31:28], IR[25:0], 2'b00}), .in1(v0), .out(multiplexer_1_out), .sel(\单周期硬布线控制器_1_jr ));
  Clock #(.highDuration(1), .lowDuration(1)) clock_1 (.out(CLK));
  Button _1 (.out(IR1));
  Button _2 (.out(IR2));
  Button _3 (.out(IR3));
  Counter #(.width(16), .max('hffff), .ongoal("wrap"), .trigger("rising"), .behavior("old")) counter_1 (
    .count(1'b1), .Q(\总周期数 ), .clk(multiplexer_2_out), .clr(RST));  // open: load, D, carry, preset
  Multiplexer #(.select(1), .width(1), .disabled("Z"), .enable("false")) multiplexer_2 (
    .in0(and_1_out), .in1(1'b0), .out(multiplexer_2_out), .sel(not_2_out));
  and and_1 (and_1_out, not_1_out, CLK);
  Multiplexer #(.select(2), .width(32), .disabled("Z"), .enable("false")) multiplexer_3 (
    .in0(adder_1_out), .in1(adder_2_out), .in2(multiplexer_1_out), .out(multiplexer_3_out),
    .sel({\无条件分支 , \条件分支成功 }));  // open: in3
  Button \u_继续运行  (.out(Go));
  LED #(.active("true")) led_1 (.in(W1));
  LED #(.active("true")) led_2 (.in(W2));
  LED #(.active("true")) led_3 (.in(W3));
  not not_2 (not_2_out, not_3_out);
  not not_3 (not_3_out, CLK);
  Comparator #(.width(32), .mode("twosComplement")) comparator_1 (
    .a(v0), .b(32'h22), .eq(comparator_1_eq));  // open: gt, lt
  Hex_Digit_Display hex_digit_display_1 (.value(LedData[27:24]));  // open: dp
  Hex_Digit_Display hex_digit_display_2 (.value(LedData[31:28]));  // open: dp
  not not_4 (not_4_out, comparator_1_eq);
  and and_2 (stop, not_4_out, Syscall);
  xor xor_1 (xor_1_out, stop, register_1_q);
  Hex_Digit_Display hex_digit_display_3 (.value(LedData[23:20]));  // open: dp
  Hex_Digit_Display hex_digit_display_4 (.value(LedData[19:16]));  // open: dp
  and and_3 (and_3_out, Syscall, comparator_1_eq);
  and and_4 (and_4_out, stop, Go);
  Register #(.width(1), .trigger("rising"), .Select("low")) register_1 (
    .D(1'b0), .Q(register_1_q), .clk(CLK), .clr(RST), .preset(and_4_out));  // open: en, cs
  Register #(.width(32), .trigger("rising"), .Select("low")) u_PC (
    .D(multiplexer_4_out), .Q(PC), .clk(CLK), .clr(RST));  // open: en
  Multiplexer #(.select(1), .width(32), .disabled("Z"), .enable("false")) multiplexer_4 (
    .in0(multiplexer_3_out), .in1(PC), .out(multiplexer_4_out), .sel(xor_1_out));
  Hex_Digit_Display hex_digit_display_5 (.value(LedData[11:8]));  // open: dp
  Hex_Digit_Display hex_digit_display_6 (.value(LedData[15:12]));  // open: dp
  Hex_Digit_Display hex_digit_display_7 (.value(LedData[3:0]));  // open: dp
  Hex_Digit_Display hex_digit_display_8 (.value(LedData[7:4]));  // open: dp
  // Probe on \总周期数 
  Register #(.width(32), .trigger("rising"), .Select("low")) register_2 (
    .D(a0), .Q(LedData), .clk(and_3_out), .clr(RST));  // open: en
  Adder #(.width(32)) adder_1 (.a(PC), .b(32'h4), .out(adder_1_out));  // open: cin, cout
  Counter #(.width(16), .max('hffff), .ongoal("wrap"), .trigger("rising"), .behavior("old")) counter_2 (
    .count(1'b1), .Q(\条件分支成功数 ), .clk(multiplexer_5_out), .clr(RST));  // open: load, D, carry, preset
  Multiplexer #(.select(1), .width(1), .disabled("Z"), .enable("false")) multiplexer_5 (
    .in0(and_5_out), .in1(1'b0), .out(multiplexer_5_out), .sel(not_5_out));
  not not_5 (not_5_out, not_6_out);
  and and_5 (and_5_out, \条件分支成功 , CLK);
  ROM #(.addrWidth(10), .dataWidth(32), .Select("high")) rom_1 (.addr(PC[11:2]), .data(IR));
  not not_6 (not_6_out, CLK);
  \单周期硬布线控制器  \u_单周期硬布线控制器_1  (
    .Func(IR[5:0]), .OP(IR[31:26]), .ALU_OP(\单周期硬布线控制器_1_alu_op ), .MemToReg(\单周期硬布线控制器_1_memtoreg ),
    .MemWrite(MemWrite), .ALU_SRC(\单周期硬布线控制器_1_alu_src ), .RegWrite(RegWrite), .SysCALL(Syscall),
    .SignedExt(SignedExt), .RegDst(\单周期硬布线控制器_1_regdst ), .JR(\单周期硬布线控制器_1_jr ), .JMP(\无条件分支 ),
    .Beq(\单周期硬布线控制器_1_beq ), .JAL(\单周期硬布线控制器_1_jal ), .Bne(\单周期硬布线控制器_1_bne ), .BLEZ(\单周期硬布线控制器_1_blez ),
    .SB(\单周期硬布线控制器_1_sb ));
  Multiplexer #(.select(1), .width(5), .disabled("Z"), .enable("false")) multiplexer_6 (
    .in0(IR[20:16]), .in1(IR[15:11]), .out(multiplexer_6_out), .sel(\单周期硬布线控制器_1_regdst ));
  Multiplexer #(.select(1), .width(5), .disabled("Z"), .enable("false")) multiplexer_7 (
    .in0(IR[25:21]), .in1(5'b00010), .out(multiplexer_7_out), .sel(Syscall));
  Multiplexer #(.select(1), .width(5), .disabled("Z"), .enable("false")) multiplexer_8 (
    .in0(IR[20:16]), .in1(5'b00100), .out(multiplexer_8_out), .sel(Syscall));
  Multiplexer #(.select(1), .width(5), .disabled("Z"), .enable("false")) multiplexer_9 (
    .in0(multiplexer_6_out), .in1({5{1'b1}}), .out(multiplexer_9_out), .sel(\单周期硬布线控制器_1_jal ));
  Multiplexer #(.select(1), .width(32), .disabled("Z"), .enable("false")) multiplexer_10 (
    .in0(multiplexer_16_out), .in1(adder_1_out), .out(RDin), .sel(\单周期硬布线控制器_1_jal ));
  assign bit_extender_1_out = {{16{1'b0}}, IR[15:0]};  // Bit_Extender bit_extender_1
  assign bit_extender_2_out = {{16{IR[15]}}, IR[15:0]};  // Bit_Extender bit_extender_2
  Counter #(.width(16), .max('hffff), .ongoal("wrap"), .trigger("rising"), .behavior("old")) counter_3 (
    .count(1'b1), .Q(\无条件分支数 ), .clk(multiplexer_11_out), .clr(RST));  // open: load, D, carry, preset
  Multiplexer #(.select(1), .width(1), .disabled("Z"), .enable("false")) multiplexer_11 (
    .in0(and_6_out), .in1(1'b0), .out(multiplexer_11_out), .sel(not_7_out));
  and and_6 (and_6_out, \无条件分支 , CLK);
  Multiplexer #(.select(1), .width(32), .disabled("Z"), .enable("false")) multiplexer_12 (
    .in0(bit_extender_1_out), .in1(bit_extender_2_out), .out(multiplexer_12_out), .sel(SignedExt));
  not not_7 (not_7_out, not_8_out);
  not not_8 (not_8_out, CLK);
  MIPS_Regifile mips_regifile_1 (
    .Din(RDin), .Clk(CLK), .R1(v0), .R2(a0), .WE(RegWrite), .W_num(multiplexer_9_out),
    .R1_num(multiplexer_7_out), .R2_num(multiplexer_8_out));
  Comparator #(.width(32), .mode("twosComplement")) comparator_2 (
    .a(v0), .b({32{1'b0}}), .eq(comparator_2_eq), .lt(comparator_2_lt));  // open: gt
  Shifter #(.width(32), .shift("ll")) shifter_1 (.in(multiplexer_12_out), .\dist (5'b00010), .out(shifter_1_out));
  and and_7 (and_7_out, or_1_out, \单周期硬布线控制器_1_blez );
  or or_1 (or_1_out, comparator_2_eq, comparator_2_lt);
  Multiplexer #(.select(1), .width(32), .disabled("Z"), .enable("false")) multiplexer_13 (
    .in0(a0), .in1(multiplexer_12_out), .out(multiplexer_13_out), .sel(\单周期硬布线控制器_1_alu_src ));
  Adder #(.width(32)) adder_2 (.a(shifter_1_out), .b(adder_1_out), .out(adder_2_out));  // open: cin, cout
  MIPS_ALU mips_alu_1 (
    .X(v0), .Y(multiplexer_13_out), .AluOP(\单周期硬布线控制器_1_alu_op ), .Equal(mips_alu_1_equal),
    .Result(mips_alu_1_result), .shamt(IR[10:6]));  // open: Result_2
  and and_8 (and_8_out, mips_alu_1_equal, \单周期硬布线控制器_1_beq );
  not not_9 (not_9_out, mips_alu_1_equal);
  Multiplexer #(.select(2), .width(32), .disabled("Z"), .enable("false")) multiplexer_14 (
    .in0({ram_1_data[31:8], a0[7:0]}), .in1({ram_1_data[31:16], a0[7:0], ram_1_data[7:0]}),
    .in2({ram_1_data[31:24], a0[7:0], ram_1_data[15:0]}), .in3({a0[7:0], ram_1_data[23:0]}),
    .out(multiplexer_14_out), .sel(mips_alu_1_result[1:0]));
  and and_9 (and_9_out, not_9_out, \单周期硬布线控制器_1_bne );
  Multiplexer #(.select(1), .width(32), .disabled("Z"), .enable("false")) multiplexer_15 (
    .in0(a0), .in1(multiplexer_14_out), .out(MDin), .sel(\单周期硬布线控制器_1_sb ));
  or or_2 (\条件分支成功 , and_7_out, and_9_out, and_8_out);
  RAM #(.addrWidth(10), .dataWidth(32), .bus("separate"), .Select("high")) ram_1 (
    .addr(mips_alu_1_result[11:2]), .din(MDin), .data(ram_1_data), .str(MemWrite), .clk(CLK));  // open: sel, ld, clr
  Multiplexer #(.select(1), .width(32), .disabled("Z"), .enable("false")) multiplexer_16 (
    .in0(mips_alu_1_result), .in1(ram_1_data), .out(multiplexer_16_out), .sel(\单周期硬布线控制器_1_memtoreg ));

  // Notes on the sheet:
  //   总复位信号应将除ROM以外所有存储组件全部清零
  //   中断源
  //   中断等待指示
  //   数码管输出应该用寄存器锁存，否则显示数据只能一闪而过
  //   数码管输出
  //   指令存储器
  //   指令字
  //   contents of rom_1 (hex, n*v repeats v):
  //   20110001 8000c05 20110001 20120002 20130003 8000c09 20110001 20120002 20130003 8000c0d 20110001
  //   20120002 20130003 8000c11 20110001 20120002 20130003 c000cf5 20100001 20110001 118fc0 112020
  //   20020022 c 118882 12200001 8000c15 112020 20020022 c 20110001 118880 112020 20020022 c 12200001
  //   8000c1f 20110001 118fc0 112020 20020022 c 1188c3 112020 20020022 c 118903 112020 20020022 c 118903
  //   112020 20020022 c 118903 112020 20020022 c 118903 112020 20020022 c 118903 112020 20020022 c 118903
  //   112020 20020022 c 118903 112020 20020022 c 20100001 109fc0 139fc3 8021 2012000c 24160003 26100001
  //   3210000f 20080008 20090001 139900 2709825 132020 20020022 c 1094022 1500fff9 22100001 2018000f
  //   2188024 108700 20080008 20090001 139902 2709825 132021 20020022 c 1094022 1500fff9 108702 2c9b022
  //   12c00001 8000c50 4020 1084027 84400 3508ffff 82021 20020022 c 2010ffff 20110000 ae300000 22100001
  //   22310004 ae300000 22100001 22310004 ae300000 22100001 22310004 ae300000 22100001 22310004 ae300000
  //   22100001 22310004 ae300000 22100001 22310004 ae300000 22100001 22310004 ae300000 22100001 22310004
  //   ae300000 22100001 22310004 ae300000 22100001 22310004 ae300000 22100001 22310004 ae300000 22100001
  //   22310004 ae300000 22100001 22310004 ae300000 22100001 22310004 ae300000 22100001 22310004 ae300000
  //   22100001 22310004 22100001 8020 2011003c 8e130000 8e340000 274402a 11000002 ae330000 ae140000
  //   2231fffc 1611fff8 102020 20020022 c 22100004 2011003c 1611fff2 20020032 c 20080001 20110010 112020
  //   20020022 c 200b0020 2288823 112020 20020022 c 216bffff 1560fffa 2002000a c 2008ffff 20117777 112020
  //   20020022 c 200b0010 2288826 112020 20020022 c 216bffff 1560fffa 2002000a c 20090000 200b0020
  //   20110000 20120001 a1310000 112020 20020022 c 2328820 21290001 216bffff 1560fff8 200b0008 20090000
  //   8d310000 112020 20020022 c 21290004 216bffff 1560fff9 2002000a c 2011fff1 112020 20020022 c 22310001
  //   1a20fffb 2002000a c 2002000a c 20100000 22100001 102020 20020022 c 22100002 102020 20020022 c
  //   22100003 102020 20020022 c 22100004 102020 20020022 c 22100005 102020 20020022 c 22100006 102020
  //   20020022 c 22100007 102020 20020022 c 22100008 102020 20020022 20020022 c 3e00008
  //   OP
  //   Func
  //   rs
  //   rt
  //   rd
  //   JMP
  //   JR
  //   OP
  //   Func
  //   Syscall
  //   BLEZ
  //   Beq
  //   Bne
  //   MemToReg
  //   MemWrite
  //   SB
  //   AluOP
  //   AluSrcB
  //   RegWrite
  //   JAL
  //   RegDst
  //   为方便自动评测，需要输出PC，IR，寄存器文件写入端口RDin，内存写入端口MDin等信号
endmodule

// 单周期硬布线控制器
module \单周期硬布线控制器  (
  input  [5:0] OP,
  input  [5:0] Func,
  output [3:0] ALU_OP,
  output MemToReg,
  output MemWrite,
  output ALU_SRC,
  output RegWrite,
  output SysCALL,
  output SignedExt,
  output RegDst,
  output Beq,
  output Bne,
  output JR,
  output JMP,
  output JAL,
  output BLEZ,
  output SB
);

  \运算控制器自动生成  \u_运算控制器自动生成_1  (
    .OP0(OP[0]), .OP1(OP[1]), .OP2(OP[2]), .OP3(OP[3]), .OP4(OP[4]), .OP5(OP[5]), .F0(Func[0]), .F1(Func[1]),
    .F2(Func[2]), .F3(Func[3]), .F4(Func[4]), .F5(Func[5]), .S0(ALU_OP[0]), .S1(ALU_OP[1]), .S2(ALU_OP[2]),
    .S3(ALU_OP[3]));
  \控制信号自动生成  \u_控制信号自动生成_1  (
    .OP0(OP[0]), .MemToReg(MemToReg), .OP1(OP[1]), .OP2(OP[2]), .OP3(OP[3]), .OP4(OP[4]),
    .MemWrite(MemWrite), .OP5(OP[5]), .F0(Func[0]), .F1(Func[1]), .F2(Func[2]), .F3(Func[3]), .F4(Func[4]),
    .F5(Func[5]), .ALU_SRC(ALU_SRC), .BLEZ(BLEZ), .SB(SB), .RegWrite(RegWrite), .SysCALL(SysCALL),
    .SignedExt(SignedExt), .RegDst(RegDst), .BEQ(Beq), .BNE(Bne), .JR(JR), .JUMP(JMP), .JAL(JAL));

  // Other names for the same wires on the sheet: OP_CODE[5:0] = OP

  // Notes on the sheet:
  //   运算器控制器，根据指令生成运算器功能选择信号
  //   控制信号生成，产生数据通路需要的其他控制信号
endmodule

// 运算器控制器
module \运算控制器自动生成  (
  input  OP0,
  input  OP1,
  input  OP2,
  input  OP3,
  input  OP4,
  input  OP5,
  input  F0,
  input  F1,
  input  F2,
  input  F3,
  input  F4,
  input  F5,
  output S0,
  output S1,
  output S2,
  output S3
);

  wire and_1_out, and_2_out, and_3_out, and_4_out, and_5_out, and_6_out, and_7_out, and_8_out, and_9_out,
       and_10_out, and_11_out, and_12_out, and_13_out, and_14_out, and_15_out, and_16_out, and_17_out,
       and_18_out, and_19_out, and_20_out, and_21_out, and_22_out, and_23_out, and_24_out, and_25_out,
       and_26_out, and_27_out, and_28_out, and_29_out, not_1_out, not_2_out, not_3_out, not_4_out, not_5_out,
       not_6_out, not_7_out, not_8_out, not_9_out, not_10_out, not_11_out, not_12_out, not_13_out,
       not_14_out, not_15_out, not_16_out, not_17_out, not_18_out, not_19_out, not_20_out, not_21_out,
       not_22_out, not_23_out, not_24_out, not_25_out, not_26_out, not_27_out, not_28_out, not_29_out,
       not_30_out, not_31_out, not_32_out, not_33_out, not_34_out, not_35_out, not_36_out, not_37_out,
       not_38_out, not_39_out, not_40_out, not_41_out, not_42_out, not_43_out, not_44_out, not_45_out,
       not_46_out, not_47_out, not_48_out, not_49_out, not_50_out, not_51_out, not_52_out, not_53_out,
       not_54_out, not_55_out, not_56_out, not_57_out, not_58_out, not_59_out, not_60_out, not_61_out,
       not_62_out, not_63_out, not_64_out, not_65_out, not_66_out, not_67_out, not_68_out, not_69_out,
       not_70_out, not_71_out, not_72_out, not_73_out, not_74_out, not_75_out, not_76_out, not_77_out,
       not_78_out, not_79_out, not_80_out, not_81_out, not_82_out, not_83_out, not_84_out, not_85_out,
       not_86_out, not_87_out, not_88_out, not_89_out, not_90_out, not_91_out, not_92_out, not_93_out,
       not_94_out, not_95_out, not_96_out, not_97_out, not_98_out, not_99_out, not_100_out, not_101_out,
       not_102_out, not_103_out, not_104_out, not_105_out, not_106_out, not_107_out, not_108_out,
       not_109_out, not_110_out, not_111_out, not_112_out, not_113_out, not_114_out, not_115_out,
       not_116_out, not_117_out, not_118_out, not_119_out, not_120_out, not_121_out, not_122_out,
       not_123_out, not_124_out, not_125_out, not_126_out, not_127_out, not_128_out, not_129_out,
       not_130_out, not_131_out, not_132_out, not_133_out, not_134_out, not_135_out, not_136_out,
       not_137_out, not_138_out, not_139_out, not_140_out, not_141_out, not_142_out, not_143_out,
       not_144_out, not_145_out, not_146_out, not_147_out, not_148_out, not_149_out, not_150_out,
       not_151_out, not_152_out, not_153_out, not_154_out, not_155_out, not_156_out, not_157_out,
       not_158_out, not_159_out, not_160_out, not_161_out, not_162_out, not_163_out, not_164_out,
       not_165_out, not_166_out, not_167_out, not_168_out, not_169_out, not_170_out, not_171_out,
       not_172_out, not_173_out, not_174_out, not_175_out, not_176_out, not_177_out, not_178_out,
       not_179_out, not_180_out, not_181_out, not_182_out, not_183_out, not_184_out, not_185_out;

  not not_1 (not_1_out, OP0);
  not not_2 (not_2_out, OP1);
  not not_3 (not_3_out, OP2);
  not not_4 (not_4_out, OP4);
  not not_5 (not_5_out, OP5);
  not not_6 (not_6_out, F1);
  not not_7 (not_7_out, F2);
  not not_8 (not_8_out, F3);
  not not_9 (not_9_out, F4);
  not not_10 (not_10_out, OP0);
  not not_11 (not_11_out, OP1);
  not not_12 (not_12_out, OP2);
  not not_13 (not_13_out, OP4);
  not not_14 (not_14_out, OP5);
  not not_15 (not_15_out, F0);
  not not_16 (not_16_out, F3);
  not not_17 (not_17_out, F4);
  not not_18 (not_18_out, OP0);
  not not_19 (not_19_out, OP1);
  not not_20 (not_20_out, OP2);
  not not_21 (not_21_out, OP4);
  not not_22 (not_22_out, OP5);
  not not_23 (not_23_out, F0);
  not not_24 (not_24_out, F2);
  not not_25 (not_25_out, F4);
  not not_26 (not_26_out, OP0);
  not not_27 (not_27_out, OP1);
  not not_28 (not_28_out, OP2);
  not not_29 (not_29_out, OP4);
  not not_30 (not_30_out, OP5);
  not not_31 (not_31_out, F2);
  not not_32 (not_32_out, F3);
  not not_33 (not_33_out, F4);
  not not_34 (not_34_out, F5);
  not not_35 (not_35_out, OP0);
  not not_36 (not_36_out, OP1);
  not not_37 (not_37_out, OP2);
  not not_38 (not_38_out, OP4);
  not not_39 (not_39_out, OP0);
  not not_40 (not_40_out, OP1);
  not not_41 (not_41_out, OP4);
  not not_42 (not_42_out, OP5);
  not not_43 (not_43_out, OP0);
  not not_44 (not_44_out, OP2);
  not not_45 (not_45_out, OP4);
  not not_46 (not_46_out, OP5);
  not not_47 (not_47_out, OP1);
  not not_48 (not_48_out, OP2);
  not not_49 (not_49_out, OP4);
  not not_50 (not_50_out, OP5);
  not not_51 (not_51_out, OP2);
  not not_52 (not_52_out, OP4);
  not not_53 (not_53_out, OP0);
  not not_54 (not_54_out, OP1);
  not not_55 (not_55_out, OP2);
  not not_56 (not_56_out, OP3);
  not not_57 (not_57_out, OP4);
  not not_58 (not_58_out, OP5);
  not not_59 (not_59_out, F0);
  not not_60 (not_60_out, F1);
  not not_61 (not_61_out, F3);
  not not_62 (not_62_out, F4);
  not not_63 (not_63_out, OP0);
  not not_64 (not_64_out, OP1);
  not not_65 (not_65_out, OP2);
  not not_66 (not_66_out, OP3);
  not not_67 (not_67_out, OP4);
  not not_68 (not_68_out, OP5);
  not not_69 (not_69_out, F0);
  not not_70 (not_70_out, F2);
  not not_71 (not_71_out, F3);
  not not_72 (not_72_out, F4);
  not not_73 (not_73_out, OP0);
  not not_74 (not_74_out, OP1);
  not not_75 (not_75_out, OP2);
  not not_76 (not_76_out, OP3);
  not not_77 (not_77_out, OP4);
  not not_78 (not_78_out, OP5);
  not not_79 (not_79_out, F0);
  not not_80 (not_80_out, F2);
  not not_81 (not_81_out, F4);
  not not_82 (not_82_out, OP0);
  not not_83 (not_83_out, OP1);
  not not_84 (not_84_out, OP2);
  not not_85 (not_85_out, OP3);
  not not_86 (not_86_out, OP4);
  not not_87 (not_87_out, OP5);
  not not_88 (not_88_out, F3);
  not not_89 (not_89_out, F4);
  not not_90 (not_90_out, OP0);
  not not_91 (not_91_out, OP1);
  not not_92 (not_92_out, OP4);
  not not_93 (not_93_out, OP5);
  not not_94 (not_94_out, OP0);
  not not_95 (not_95_out, OP2);
  not not_96 (not_96_out, OP4);
  not not_97 (not_97_out, OP5);
  not not_98 (not_98_out, OP0);
  not not_99 (not_99_out, OP1);
  not not_100 (not_100_out, OP2);
  not not_101 (not_101_out, OP4);
  not not_102 (not_102_out, OP5);
  not not_103 (not_103_out, F0);
  not not_104 (not_104_out, F1);
  not not_105 (not_105_out, F3);
  not not_106 (not_106_out, F4);
  not not_107 (not_107_out, OP0);
  not not_108 (not_108_out, OP1);
  not not_109 (not_109_out, OP2);
  not not_110 (not_110_out, OP4);
  not not_111 (not_111_out, OP5);
  not not_112 (not_112_out, F2);
  not not_113 (not_113_out, F3);
  not not_114 (not_114_out, F4);
  not not_115 (not_115_out, OP0);
  not not_116 (not_116_out, OP1);
  not not_117 (not_117_out, OP2);
  not not_118 (not_118_out, OP4);
  not not_119 (not_119_out, OP5);
  not not_120 (not_120_out, F2);
  not not_121 (not_121_out, F4);
  not not_122 (not_122_out, OP0);
  not not_123 (not_123_out, OP1);
  not not_124 (not_124_out, OP2);
  not not_125 (not_125_out, OP4);
  not not_126 (not_126_out, OP0);
  not not_127 (not_127_out, OP1);
  not not_128 (not_128_out, OP4);
  not not_129 (not_129_out, OP5);
  not not_130 (not_130_out, OP1);
  not not_131 (not_131_out, OP2);
  not not_132 (not_132_out, OP4);
  not not_133 (not_133_out, OP5);
  not not_134 (not_134_out, OP2);
  not not_135 (not_135_out, OP4);
  not not_136 (not_136_out, OP5);
  not not_137 (not_137_out, OP4);
  not not_138 (not_138_out, OP3);
  not not_139 (not_139_out, OP2);
  not not_140 (not_140_out, OP1);
  not not_141 (not_141_out, OP0);
  not not_142 (not_142_out, F4);
  not not_143 (not_143_out, F3);
  not not_144 (not_144_out, F1);
  not not_145 (not_145_out, OP5);
  not not_146 (not_146_out, OP4);
  not not_147 (not_147_out, OP3);
  not not_148 (not_148_out, OP2);
  not not_149 (not_149_out, OP1);
  not not_150 (not_150_out, OP0);
  not not_151 (not_151_out, F4);
  not not_152 (not_152_out, F3);
  not not_153 (not_153_out, OP5);
  not not_154 (not_154_out, OP4);
  not not_155 (not_155_out, OP3);
  not not_156 (not_156_out, OP2);
  not not_157 (not_157_out, OP1);
  not not_158 (not_158_out, OP0);
  not not_159 (not_159_out, F4);
  not not_160 (not_160_out, F2);
  not not_161 (not_161_out, F0);
  not not_162 (not_162_out, OP5);
  not not_163 (not_163_out, OP4);
  not not_164 (not_164_out, OP3);
  not not_165 (not_165_out, OP2);
  not not_166 (not_166_out, OP1);
  not not_167 (not_167_out, OP0);
  not not_168 (not_168_out, F4);
  not not_169 (not_169_out, F2);
  not not_170 (not_170_out, OP5);
  not not_171 (not_171_out, OP4);
  not not_172 (not_172_out, OP2);
  not not_173 (not_173_out, OP0);
  not not_174 (not_174_out, OP5);
  not not_175 (not_175_out, OP4);
  not not_176 (not_176_out, OP1);
  not not_177 (not_177_out, OP5);
  not not_178 (not_178_out, OP4);
  not not_179 (not_179_out, OP3);
  not not_180 (not_180_out, OP2);
  not not_181 (not_181_out, OP1);
  not not_182 (not_182_out, OP0);
  not not_183 (not_183_out, F4);
  not not_184 (not_184_out, F3);
  not not_185 (not_185_out, F0);
  and and_1 (and_1_out, not_1_out, not_2_out, not_3_out, not_4_out, not_5_out, not_6_out, not_7_out, not_8_out, not_9_out, F5);
  and and_2 (and_2_out, not_10_out, not_11_out, not_12_out, not_13_out, not_14_out, not_15_out, F2, not_16_out, not_17_out, F5);
  and and_3 (and_3_out, not_18_out, not_19_out, not_20_out, not_21_out, not_22_out, not_23_out, F1, not_24_out, F3, not_25_out, F5);
  and and_4 (and_4_out, not_26_out, not_27_out, not_28_out, not_29_out, not_30_out, F0, F1, not_31_out, not_32_out, not_33_out, not_34_out);
  and and_5 (and_5_out, not_35_out, not_36_out, not_37_out, OP3, not_38_out);
  and and_6 (and_6_out, not_39_out, not_40_out, OP3, not_41_out, not_42_out);
  and and_7 (and_7_out, not_43_out, not_44_out, OP3, not_45_out, not_46_out);
  and and_8 (and_8_out, not_47_out, not_48_out, OP3, not_49_out, not_50_out);
  and and_9 (and_9_out, OP0, OP1, not_51_out, not_52_out, OP5);
  and and_10 (and_10_out, not_53_out, not_54_out, not_55_out, not_56_out, not_57_out, not_58_out, not_59_out, not_60_out, F2, not_61_out, not_62_out, F5);
  and and_11 (and_11_out, not_63_out, not_64_out, not_65_out, not_66_out, not_67_out, not_68_out, not_69_out, F1, not_70_out, not_71_out, not_72_out);
  and and_12 (and_12_out, not_73_out, not_74_out, not_75_out, not_76_out, not_77_out, not_78_out, not_79_out, F1, not_80_out, not_81_out, F5);
  and and_13 (and_13_out, not_82_out, not_83_out, not_84_out, not_85_out, not_86_out, not_87_out, F0, F1, not_88_out, not_89_out, F5);
  and and_14 (and_14_out, not_90_out, not_91_out, OP2, OP3, not_92_out, not_93_out);
  and and_15 (and_15_out, not_94_out, OP1, not_95_out, OP3, not_96_out, not_97_out);
  and and_16 (and_16_out, not_98_out, not_99_out, not_100_out, not_101_out, not_102_out, not_103_out, not_104_out, not_105_out, not_106_out, F5);
  and and_17 (and_17_out, not_107_out, not_108_out, not_109_out, not_110_out, not_111_out, not_112_out, not_113_out, not_114_out, F5);
  and and_18 (and_18_out, not_115_out, not_116_out, not_117_out, not_118_out, not_119_out, F0, F1, not_120_out, not_121_out, F5);
  and and_19 (and_19_out, not_122_out, not_123_out, not_124_out, OP3, not_125_out);
  and and_20 (and_20_out, not_126_out, not_127_out, OP3, not_128_out, not_129_out);
  and and_21 (and_21_out, not_130_out, not_131_out, OP3, not_132_out, not_133_out);
  and and_22 (and_22_out, OP0, OP1, not_134_out, not_135_out, OP5);
  and and_23 (and_23_out, not_136_out, not_137_out, not_138_out, not_139_out, not_140_out, not_141_out, F5, not_142_out, not_143_out, F2, not_144_out, F0);
  and and_24 (and_24_out, not_145_out, not_146_out, not_147_out, not_148_out, not_149_out, not_150_out, F5, not_151_out, not_152_out, F2, F1, F0);
  and and_25 (and_25_out, not_153_out, not_154_out, not_155_out, not_156_out, not_157_out, not_158_out, F5, not_159_out, F3, not_160_out, F1, not_161_out);
  and and_26 (and_26_out, not_162_out, not_163_out, not_164_out, not_165_out, not_166_out, not_167_out, F5, not_168_out, F3, not_169_out, F1, F0);
  and and_27 (and_27_out, not_170_out, not_171_out, OP3, not_172_out, OP1, not_173_out);
  and and_28 (and_28_out, not_174_out, not_175_out, OP3, OP2, not_176_out, OP0);
  and and_29 (and_29_out, not_177_out, not_178_out, not_179_out, not_180_out, not_181_out, not_182_out, F5, not_183_out, not_184_out, F2, F1, not_185_out);
  or or_1 (S0, and_1_out, and_2_out, and_3_out, and_4_out, and_5_out, and_6_out, and_7_out, and_8_out, and_9_out);
  or or_2 (S1, and_10_out, and_11_out, and_12_out, and_13_out, and_14_out, and_15_out);
  or or_3 (S2, and_16_out, and_17_out, and_18_out, and_19_out, and_20_out, and_21_out, and_22_out);
  or or_4 (S3, and_23_out, and_24_out, and_25_out, and_26_out, and_27_out, and_28_out, and_29_out);
endmodule

// 控制信号生成
module \控制信号自动生成  (
  input  OP0,
  input  OP1,
  input  OP2,
  input  OP3,
  input  OP4,
  input  OP5,
  input  F0,
  input  F1,
  input  F2,
  input  F3,
  input  F4,
  input  F5,
  output MemToReg,
  output MemWrite,
  output ALU_SRC,
  output BLEZ,
  output SB,
  output RegWrite,
  output SysCALL,
  output SignedExt,
  output RegDst,
  output BEQ,
  output BNE,
  output JR,
  output JUMP,
  output JAL
);

  wire and_2_out, and_3_out, and_4_out, and_5_out, and_6_out, and_7_out, and_8_out, and_9_out, and_10_out,
       and_11_out, and_14_out, and_15_out, and_16_out, and_17_out, and_18_out, and_19_out, and_20_out,
       and_21_out, and_22_out, and_23_out, and_24_out, and_25_out, and_26_out, and_27_out, and_28_out,
       and_29_out, and_30_out, and_31_out, and_32_out, and_33_out, and_35_out, and_36_out, and_37_out,
       and_38_out, and_39_out, and_40_out, and_41_out, and_42_out, and_43_out, and_44_out, and_45_out,
       and_46_out, and_47_out, and_48_out, and_49_out, and_50_out, and_51_out, and_52_out, and_53_out,
       and_54_out, and_55_out, and_56_out, and_60_out, and_61_out, not_1_out, not_2_out, not_3_out,
       not_4_out, not_5_out, not_6_out, not_7_out, not_8_out, not_9_out, not_10_out, not_11_out, not_12_out,
       not_13_out, not_14_out, not_15_out, not_16_out, not_17_out, not_18_out, not_19_out, not_20_out,
       not_21_out, not_22_out, not_23_out, not_24_out, not_25_out, not_26_out, not_27_out, not_28_out,
       not_29_out, not_30_out, not_31_out, not_32_out, not_33_out, not_34_out, not_35_out, not_36_out,
       not_37_out, not_38_out, not_39_out, not_40_out, not_41_out, not_42_out, not_43_out, not_44_out,
       not_45_out, not_46_out, not_47_out, not_48_out, not_49_out, not_50_out, not_51_out, not_52_out,
       not_53_out, not_54_out, not_55_out, not_56_out, not_57_out, not_58_out, not_59_out, not_60_out,
       not_61_out, not_62_out, not_63_out, not_64_out, not_65_out, not_66_out, not_67_out, not_68_out,
       not_69_out, not_70_out, not_71_out, not_72_out, not_73_out, not_74_out, not_75_out, not_76_out,
       not_77_out, not_78_out, not_79_out, not_80_out, not_81_out, not_82_out, not_83_out, not_84_out,
       not_85_out, not_86_out, not_87_out, not_88_out, not_89_out, not_90_out, not_91_out, not_92_out,
       not_93_out, not_94_out, not_95_out, not_96_out, not_97_out, not_98_out, not_99_out, not_100_out,
       not_101_out, not_102_out, not_103_out, not_104_out, not_105_out, not_106_out, not_107_out,
       not_108_out, not_109_out, not_110_out, not_111_out, not_112_out, not_113_out, not_114_out,
       not_115_out, not_116_out, not_117_out, not_118_out, not_119_out, not_120_out, not_121_out,
       not_122_out, not_123_out, not_124_out, not_125_out, not_126_out, not_127_out, not_128_out,
       not_129_out, not_130_out, not_131_out, not_132_out, not_133_out, not_134_out, not_135_out,
       not_136_out, not_137_out, not_138_out, not_139_out, not_140_out, not_141_out, not_142_out,
       not_143_out, not_144_out, not_145_out, not_146_out, not_147_out, not_148_out, not_149_out,
       not_150_out, not_151_out, not_152_out, not_153_out, not_154_out, not_155_out, not_156_out,
       not_157_out, not_158_out, not_159_out, not_160_out, not_161_out, not_162_out, not_163_out,
       not_164_out, not_165_out, not_166_out, not_167_out, not_168_out, not_169_out, not_170_out,
       not_171_out, not_172_out, not_173_out, not_174_out, not_175_out, not_176_out, not_177_out,
       not_178_out, not_179_out, not_180_out, not_181_out, not_182_out, not_183_out, not_184_out,
       not_185_out, not_186_out, not_187_out, not_188_out, not_189_out, not_190_out, not_191_out,
       not_192_out, not_193_out, not_194_out, not_195_out, not_196_out, not_197_out, not_198_out,
       not_199_out, not_200_out, not_201_out, not_202_out, not_203_out, not_204_out, not_205_out,
       not_206_out, not_207_out, not_208_out, not_209_out, not_210_out, not_211_out, not_212_out,
       not_213_out, not_214_out, not_215_out, not_216_out, not_217_out, not_218_out, not_219_out,
       not_220_out, not_221_out, not_222_out, not_223_out, not_224_out, not_225_out, not_226_out,
       not_227_out, not_228_out, not_229_out, not_230_out, not_231_out, not_232_out, not_233_out,
       not_234_out, not_235_out, not_236_out, not_237_out, not_238_out, not_239_out, not_240_out,
       not_241_out, not_242_out, not_243_out, not_244_out, not_245_out, not_246_out, not_247_out,
       not_248_out, not_249_out, not_250_out, not_251_out, not_252_out, not_253_out, not_254_out,
       not_255_out, not_256_out, not_257_out, not_258_out, not_259_out, not_260_out, not_261_out,
       not_262_out, not_263_out, not_264_out, not_265_out, not_266_out, not_267_out, not_268_out,
       not_269_out, not_270_out, not_271_out, not_272_out, not_273_out, not_274_out, not_275_out,
       not_276_out, not_277_out, not_278_out, not_279_out, not_280_out, not_281_out, not_282_out,
       not_283_out, not_284_out, not_285_out, not_286_out, not_287_out, not_288_out, not_289_out,
       not_290_out, not_291_out, not_292_out, not_293_out, not_294_out, not_295_out, not_296_out,
       not_297_out, not_298_out, not_299_out, not_300_out, not_301_out, not_302_out, not_303_out,
       not_304_out, not_305_out, not_306_out, not_307_out, not_308_out, not_309_out, not_310_out,
       not_311_out, not_312_out, not_313_out, not_314_out, not_315_out, not_316_out, not_317_out,
       not_318_out, not_319_out, not_320_out, not_321_out, not_322_out, not_323_out, not_324_out,
       not_325_out, not_326_out, not_327_out, not_328_out, not_329_out, not_330_out, not_331_out,
       not_332_out, not_333_out, not_334_out, not_335_out, not_336_out, not_337_out, not_338_out,
       not_339_out, not_340_out, not_341_out, not_342_out, not_343_out, not_344_out, not_345_out,
       not_346_out, not_347_out, not_348_out, not_349_out, not_350_out, not_351_out, not_352_out,
       not_353_out, not_354_out, not_355_out, not_356_out, not_357_out, not_358_out, not_359_out,
       not_360_out, not_361_out, not_362_out, not_363_out, not_364_out, not_365_out, not_366_out,
       not_367_out, not_368_out, not_369_out, not_370_out, not_371_out, not_372_out, not_373_out,
       not_374_out, not_375_out, not_376_out, not_377_out, not_378_out, not_379_out, not_380_out,
       not_381_out, not_382_out, not_383_out, not_384_out, not_385_out, not_386_out, not_387_out,
       not_388_out, not_389_out, not_390_out, not_391_out, not_392_out, not_393_out, not_394_out,
       not_395_out, not_396_out, not_397_out, not_398_out, not_399_out, not_400_out, not_401_out,
       not_402_out, not_403_out, not_404_out, not_405_out, not_406_out, not_407_out, not_408_out;

  not not_1 (not_1_out, OP2);
  not not_2 (not_2_out, OP3);
  not not_3 (not_3_out, OP4);
  not not_4 (not_4_out, OP4);
  not not_5 (not_5_out, OP2);
  not not_6 (not_6_out, OP4);
  not not_7 (not_7_out, OP2);
  not not_8 (not_8_out, OP1);
  not not_9 (not_9_out, OP0);
  not not_10 (not_10_out, OP5);
  not not_11 (not_11_out, OP4);
  not not_12 (not_12_out, OP2);
  not not_13 (not_13_out, OP1);
  not not_14 (not_14_out, OP0);
  not not_15 (not_15_out, OP5);
  not not_16 (not_16_out, OP4);
  not not_17 (not_17_out, OP1);
  not not_18 (not_18_out, OP0);
  not not_19 (not_19_out, OP5);
  not not_20 (not_20_out, OP4);
  not not_21 (not_21_out, OP2);
  not not_22 (not_22_out, OP1);
  not not_23 (not_23_out, OP5);
  not not_24 (not_24_out, OP4);
  not not_25 (not_25_out, OP2);
  not not_26 (not_26_out, OP0);
  not not_27 (not_27_out, OP5);
  not not_28 (not_28_out, OP4);
  not not_29 (not_29_out, OP1);
  not not_30 (not_30_out, OP4);
  not not_31 (not_31_out, OP3);
  not not_32 (not_32_out, OP2);
  not not_33 (not_33_out, OP4);
  not not_34 (not_34_out, OP2);
  not not_35 (not_35_out, OP4);
  not not_36 (not_36_out, OP2);
  not not_37 (not_37_out, OP1);
  not not_38 (not_38_out, OP0);
  not not_39 (not_39_out, OP5);
  not not_40 (not_40_out, OP4);
  not not_41 (not_41_out, OP3);
  not not_42 (not_42_out, OP0);
  not not_43 (not_43_out, OP4);
  not not_44 (not_44_out, OP2);
  not not_45 (not_45_out, OP1);
  not not_46 (not_46_out, OP0);
  not not_47 (not_47_out, OP5);
  not not_48 (not_48_out, OP4);
  not not_49 (not_49_out, OP3);
  not not_50 (not_50_out, OP2);
  not not_51 (not_51_out, OP1);
  not not_52 (not_52_out, OP0);
  not not_53 (not_53_out, F5);
  not not_54 (not_54_out, F4);
  not not_55 (not_55_out, F3);
  not not_56 (not_56_out, F2);
  not not_57 (not_57_out, F1);
  not not_58 (not_58_out, F0);
  not not_59 (not_59_out, OP5);
  not not_60 (not_60_out, OP4);
  not not_61 (not_61_out, OP3);
  not not_62 (not_62_out, OP2);
  not not_63 (not_63_out, OP1);
  not not_64 (not_64_out, OP0);
  not not_65 (not_65_out, F5);
  not not_66 (not_66_out, F4);
  not not_67 (not_67_out, F3);
  not not_68 (not_68_out, F2);
  not not_69 (not_69_out, OP5);
  not not_70 (not_70_out, OP4);
  not not_71 (not_71_out, OP3);
  not not_72 (not_72_out, OP2);
  not not_73 (not_73_out, OP1);
  not not_74 (not_74_out, OP0);
  not not_75 (not_75_out, F5);
  not not_76 (not_76_out, F4);
  not not_77 (not_77_out, F3);
  not not_78 (not_78_out, F2);
  not not_79 (not_79_out, F0);
  not not_80 (not_80_out, OP5);
  not not_81 (not_81_out, OP4);
  not not_82 (not_82_out, OP3);
  not not_83 (not_83_out, OP2);
  not not_84 (not_84_out, OP1);
  not not_85 (not_85_out, OP0);
  not not_86 (not_86_out, F4);
  not not_87 (not_87_out, F3);
  not not_88 (not_88_out, F2);
  not not_89 (not_89_out, F1);
  not not_90 (not_90_out, F0);
  not not_91 (not_91_out, OP5);
  not not_92 (not_92_out, OP4);
  not not_93 (not_93_out, OP3);
  not not_94 (not_94_out, OP2);
  not not_95 (not_95_out, OP1);
  not not_96 (not_96_out, OP0);
  not not_97 (not_97_out, F4);
  not not_98 (not_98_out, F3);
  not not_99 (not_99_out, F2);
  not not_100 (not_100_out, F1);
  not not_101 (not_101_out, OP5);
  not not_102 (not_102_out, OP4);
  not not_103 (not_103_out, OP3);
  not not_104 (not_104_out, OP2);
  not not_105 (not_105_out, OP1);
  not not_106 (not_106_out, OP0);
  not not_107 (not_107_out, F4);
  not not_108 (not_108_out, F3);
  not not_109 (not_109_out, F2);
  not not_110 (not_110_out, F0);
  not not_111 (not_111_out, OP5);
  not not_112 (not_112_out, OP4);
  not not_113 (not_113_out, OP3);
  not not_114 (not_114_out, OP2);
  not not_115 (not_115_out, OP1);
  not not_116 (not_116_out, OP0);
  not not_117 (not_117_out, F4);
  not not_118 (not_118_out, F3);
  not not_119 (not_119_out, F1);
  not not_120 (not_120_out, F0);
  not not_121 (not_121_out, OP5);
  not not_122 (not_122_out, OP4);
  not not_123 (not_123_out, OP3);
  not not_124 (not_124_out, OP2);
  not not_125 (not_125_out, OP1);
  not not_126 (not_126_out, OP0);
  not not_127 (not_127_out, F4);
  not not_128 (not_128_out, F3);
  not not_129 (not_129_out, F1);
  not not_130 (not_130_out, OP5);
  not not_131 (not_131_out, OP4);
  not not_132 (not_132_out, OP3);
  not not_133 (not_133_out, OP2);
  not not_134 (not_134_out, OP1);
  not not_135 (not_135_out, OP0);
  not not_136 (not_136_out, F4);
  not not_137 (not_137_out, F3);
  not not_138 (not_138_out, OP5);
  not not_139 (not_139_out, OP4);
  not not_140 (not_140_out, OP3);
  not not_141 (not_141_out, OP2);
  not not_142 (not_142_out, OP1);
  not not_143 (not_143_out, OP0);
  not not_144 (not_144_out, F4);
  not not_145 (not_145_out, F2);
  not not_146 (not_146_out, F0);
  not not_147 (not_147_out, OP5);
  not not_148 (not_148_out, OP4);
  not not_149 (not_149_out, OP3);
  not not_150 (not_150_out, OP2);
  not not_151 (not_151_out, OP1);
  not not_152 (not_152_out, OP0);
  not not_153 (not_153_out, F4);
  not not_154 (not_154_out, F2);
  not not_155 (not_155_out, OP5);
  not not_156 (not_156_out, OP4);
  not not_157 (not_157_out, OP3);
  not not_158 (not_158_out, OP2);
  not not_159 (not_159_out, OP5);
  not not_160 (not_160_out, OP4);
  not not_161 (not_161_out, OP2);
  not not_162 (not_162_out, OP1);
  not not_163 (not_163_out, OP0);
  not not_164 (not_164_out, OP5);
  not not_165 (not_165_out, OP4);
  not not_166 (not_166_out, OP1);
  not not_167 (not_167_out, OP0);
  not not_168 (not_168_out, OP5);
  not not_169 (not_169_out, OP4);
  not not_170 (not_170_out, OP2);
  not not_171 (not_171_out, OP1);
  not not_172 (not_172_out, OP5);
  not not_173 (not_173_out, OP4);
  not not_174 (not_174_out, OP2);
  not not_175 (not_175_out, OP0);
  not not_176 (not_176_out, OP5);
  not not_177 (not_177_out, OP4);
  not not_178 (not_178_out, OP1);
  not not_179 (not_179_out, OP4);
  not not_180 (not_180_out, OP3);
  not not_181 (not_181_out, OP2);
  not not_182 (not_182_out, OP5);
  not not_183 (not_183_out, OP4);
  not not_184 (not_184_out, OP3);
  not not_185 (not_185_out, OP2);
  not not_186 (not_186_out, OP1);
  not not_187 (not_187_out, OP0);
  not not_188 (not_188_out, F4);
  not not_189 (not_189_out, F3);
  not not_190 (not_190_out, F2);
  not not_191 (not_191_out, OP5);
  not not_192 (not_192_out, OP4);
  not not_193 (not_193_out, OP3);
  not not_194 (not_194_out, OP2);
  not not_195 (not_195_out, OP1);
  not not_196 (not_196_out, OP0);
  not not_197 (not_197_out, F4);
  not not_198 (not_198_out, F3);
  not not_199 (not_199_out, F0);
  not not_200 (not_200_out, OP0);
  not not_201 (not_201_out, OP1);
  not not_202 (not_202_out, OP2);
  not not_203 (not_203_out, OP3);
  not not_204 (not_204_out, OP4);
  not not_205 (not_205_out, OP5);
  not not_206 (not_206_out, F0);
  not not_207 (not_207_out, F1);
  not not_208 (not_208_out, F4);
  not not_209 (not_209_out, F5);
  not not_210 (not_210_out, OP5);
  not not_211 (not_211_out, OP4);
  not not_212 (not_212_out, OP3);
  not not_213 (not_213_out, OP1);
  not not_214 (not_214_out, OP0);
  not not_215 (not_215_out, OP5);
  not not_216 (not_216_out, OP4);
  not not_217 (not_217_out, OP3);
  not not_218 (not_218_out, OP1);
  not not_219 (not_219_out, OP5);
  not not_220 (not_220_out, OP4);
  not not_221 (not_221_out, OP2);
  not not_222 (not_222_out, OP1);
  not not_223 (not_223_out, OP0);
  not not_224 (not_224_out, OP5);
  not not_225 (not_225_out, OP4);
  not not_226 (not_226_out, OP2);
  not not_227 (not_227_out, OP1);
  not not_228 (not_228_out, OP5);
  not not_229 (not_229_out, OP4);
  not not_230 (not_230_out, OP2);
  not not_231 (not_231_out, OP0);
  not not_232 (not_232_out, OP4);
  not not_233 (not_233_out, OP3);
  not not_234 (not_234_out, OP2);
  not not_235 (not_235_out, OP4);
  not not_236 (not_236_out, OP2);
  not not_237 (not_237_out, OP5);
  not not_238 (not_238_out, OP4);
  not not_239 (not_239_out, OP3);
  not not_240 (not_240_out, OP0);
  not not_241 (not_241_out, OP4);
  not not_242 (not_242_out, OP2);
  not not_243 (not_243_out, OP1);
  not not_244 (not_244_out, OP0);
  not not_245 (not_245_out, OP5);
  not not_246 (not_246_out, OP4);
  not not_247 (not_247_out, OP3);
  not not_248 (not_248_out, OP2);
  not not_249 (not_249_out, OP1);
  not not_250 (not_250_out, OP0);
  not not_251 (not_251_out, F5);
  not not_252 (not_252_out, F4);
  not not_253 (not_253_out, F3);
  not not_254 (not_254_out, F2);
  not not_255 (not_255_out, F1);
  not not_256 (not_256_out, F0);
  not not_257 (not_257_out, OP5);
  not not_258 (not_258_out, OP4);
  not not_259 (not_259_out, OP3);
  not not_260 (not_260_out, OP2);
  not not_261 (not_261_out, OP1);
  not not_262 (not_262_out, OP0);
  not not_263 (not_263_out, F5);
  not not_264 (not_264_out, F4);
  not not_265 (not_265_out, F3);
  not not_266 (not_266_out, F2);
  not not_267 (not_267_out, OP5);
  not not_268 (not_268_out, OP4);
  not not_269 (not_269_out, OP3);
  not not_270 (not_270_out, OP2);
  not not_271 (not_271_out, OP1);
  not not_272 (not_272_out, OP0);
  not not_273 (not_273_out, F5);
  not not_274 (not_274_out, F4);
  not not_275 (not_275_out, F3);
  not not_276 (not_276_out, F2);
  not not_277 (not_277_out, F0);
  not not_278 (not_278_out, OP5);
  not not_279 (not_279_out, OP4);
  not not_280 (not_280_out, OP3);
  not not_281 (not_281_out, OP2);
  not not_282 (not_282_out, OP1);
  not not_283 (not_283_out, OP0);
  not not_284 (not_284_out, F4);
  not not_285 (not_285_out, F3);
  not not_286 (not_286_out, F2);
  not not_287 (not_287_out, F1);
  not not_288 (not_288_out, F0);
  not not_289 (not_289_out, OP5);
  not not_290 (not_290_out, OP4);
  not not_291 (not_291_out, OP3);
  not not_292 (not_292_out, OP2);
  not not_293 (not_293_out, OP1);
  not not_294 (not_294_out, OP0);
  not not_295 (not_295_out, F4);
  not not_296 (not_296_out, F3);
  not not_297 (not_297_out, F2);
  not not_298 (not_298_out, F1);
  not not_299 (not_299_out, OP5);
  not not_300 (not_300_out, OP4);
  not not_301 (not_301_out, OP3);
  not not_302 (not_302_out, OP2);
  not not_303 (not_303_out, OP1);
  not not_304 (not_304_out, OP0);
  not not_305 (not_305_out, F4);
  not not_306 (not_306_out, F3);
  not not_307 (not_307_out, F2);
  not not_308 (not_308_out, F0);
  not not_309 (not_309_out, OP5);
  not not_310 (not_310_out, OP4);
  not not_311 (not_311_out, OP3);
  not not_312 (not_312_out, OP2);
  not not_313 (not_313_out, OP1);
  not not_314 (not_314_out, OP0);
  not not_315 (not_315_out, F4);
  not not_316 (not_316_out, F3);
  not not_317 (not_317_out, F1);
  not not_318 (not_318_out, F0);
  not not_319 (not_319_out, OP5);
  not not_320 (not_320_out, OP4);
  not not_321 (not_321_out, OP3);
  not not_322 (not_322_out, OP2);
  not not_323 (not_323_out, OP1);
  not not_324 (not_324_out, OP0);
  not not_325 (not_325_out, F4);
  not not_326 (not_326_out, F3);
  not not_327 (not_327_out, F1);
  not not_328 (not_328_out, OP5);
  not not_329 (not_329_out, OP4);
  not not_330 (not_330_out, OP3);
  not not_331 (not_331_out, OP2);
  not not_332 (not_332_out, OP1);
  not not_333 (not_333_out, OP0);
  not not_334 (not_334_out, F4);
  not not_335 (not_335_out, F3);
  not not_336 (not_336_out, OP5);
  not not_337 (not_337_out, OP4);
  not not_338 (not_338_out, OP3);
  not not_339 (not_339_out, OP2);
  not not_340 (not_340_out, OP1);
  not not_341 (not_341_out, OP0);
  not not_342 (not_342_out, F4);
  not not_343 (not_343_out, F2);
  not not_344 (not_344_out, F0);
  not not_345 (not_345_out, OP5);
  not not_346 (not_346_out, OP4);
  not not_347 (not_347_out, OP3);
  not not_348 (not_348_out, OP2);
  not not_349 (not_349_out, OP1);
  not not_350 (not_350_out, OP0);
  not not_351 (not_351_out, F4);
  not not_352 (not_352_out, F2);
  not not_353 (not_353_out, OP5);
  not not_354 (not_354_out, OP4);
  not not_355 (not_355_out, OP3);
  not not_356 (not_356_out, OP2);
  not not_357 (not_357_out, OP1);
  not not_358 (not_358_out, OP0);
  not not_359 (not_359_out, F4);
  not not_360 (not_360_out, F3);
  not not_361 (not_361_out, F2);
  not not_362 (not_362_out, OP5);
  not not_363 (not_363_out, OP4);
  not not_364 (not_364_out, OP3);
  not not_365 (not_365_out, OP2);
  not not_366 (not_366_out, OP1);
  not not_367 (not_367_out, OP0);
  not not_368 (not_368_out, F4);
  not not_369 (not_369_out, F3);
  not not_370 (not_370_out, F0);
  not not_371 (not_371_out, OP0);
  not not_372 (not_372_out, OP1);
  not not_373 (not_373_out, OP3);
  not not_374 (not_374_out, OP4);
  not not_375 (not_375_out, OP5);
  not not_376 (not_376_out, OP1);
  not not_377 (not_377_out, OP3);
  not not_378 (not_378_out, OP4);
  not not_379 (not_379_out, OP5);
  not not_380 (not_380_out, OP0);
  not not_381 (not_381_out, OP1);
  not not_382 (not_382_out, OP2);
  not not_383 (not_383_out, OP3);
  not not_384 (not_384_out, OP4);
  not not_385 (not_385_out, OP5);
  not not_386 (not_386_out, F0);
  not not_387 (not_387_out, F1);
  not not_388 (not_388_out, F2);
  not not_389 (not_389_out, F4);
  not not_390 (not_390_out, F5);
  not not_391 (not_391_out, OP0);
  not not_392 (not_392_out, OP2);
  not not_393 (not_393_out, OP3);
  not not_394 (not_394_out, OP4);
  not not_395 (not_395_out, OP5);
  not not_396 (not_396_out, F0);
  not not_397 (not_397_out, F1);
  not not_398 (not_398_out, F2);
  not not_399 (not_399_out, F4);
  not not_400 (not_400_out, F5);
  not not_401 (not_401_out, OP2);
  not not_402 (not_402_out, OP3);
  not not_403 (not_403_out, OP4);
  not not_404 (not_404_out, OP5);
  not not_405 (not_405_out, OP2);
  not not_406 (not_406_out, OP3);
  not not_407 (not_407_out, OP4);
  not not_408 (not_408_out, OP5);
  and and_1 (MemToReg, OP0, OP1, not_1_out, not_2_out, not_3_out, OP5);
  and and_2 (and_2_out, OP5, not_4_out, OP3, not_5_out, OP1, OP0);
  and and_3 (and_3_out, OP5, not_6_out, OP3, not_7_out, not_8_out, not_9_out);
  and and_4 (and_4_out, not_10_out, not_11_out, OP3, not_12_out, not_13_out, not_14_out);
  and and_5 (and_5_out, not_15_out, not_16_out, OP3, OP2, not_17_out, not_18_out);
  and and_6 (and_6_out, not_19_out, not_20_out, OP3, not_21_out, not_22_out, OP0);
  and and_7 (and_7_out, not_23_out, not_24_out, OP3, not_25_out, OP1, not_26_out);
  and and_8 (and_8_out, not_27_out, not_28_out, OP3, OP2, not_29_out, OP0);
  and and_9 (and_9_out, OP5, not_30_out, not_31_out, not_32_out, OP1, OP0);
  and and_10 (and_10_out, OP5, not_33_out, OP3, not_34_out, OP1, OP0);
  and and_11 (and_11_out, OP5, not_35_out, OP3, not_36_out, not_37_out, not_38_out);
  and and_12 (BLEZ, not_39_out, not_40_out, not_41_out, OP2, OP1, not_42_out);
  and and_13 (SB, OP5, not_43_out, OP3, not_44_out, not_45_out, not_46_out);
  and and_14 (and_14_out, not_47_out, not_48_out, not_49_out, not_50_out, not_51_out, not_52_out, not_53_out, not_54_out, not_55_out, not_56_out, not_57_out, not_58_out);
  and and_15 (and_15_out, not_59_out, not_60_out, not_61_out, not_62_out, not_63_out, not_64_out, not_65_out, not_66_out, not_67_out, not_68_out, F1, F0);
  and and_16 (and_16_out, not_69_out, not_70_out, not_71_out, not_72_out, not_73_out, not_74_out, not_75_out, not_76_out, not_77_out, not_78_out, F1, not_79_out);
  and and_17 (and_17_out, not_80_out, not_81_out, not_82_out, not_83_out, not_84_out, not_85_out, F5, not_86_out, not_87_out, not_88_out, not_89_out, not_90_out);
  and and_18 (and_18_out, not_91_out, not_92_out, not_93_out, not_94_out, not_95_out, not_96_out, F5, not_97_out, not_98_out, not_99_out, not_100_out, F0);
  and and_19 (and_19_out, not_101_out, not_102_out, not_103_out, not_104_out, not_105_out, not_106_out, F5, not_107_out, not_108_out, not_109_out, F1, not_110_out);
  and and_20 (and_20_out, not_111_out, not_112_out, not_113_out, not_114_out, not_115_out, not_116_out, F5, not_117_out, not_118_out, F2, not_119_out, not_120_out);
  and and_21 (and_21_out, not_121_out, not_122_out, not_123_out, not_124_out, not_125_out, not_126_out, F5, not_127_out, not_128_out, F2, not_129_out, F0);
  and and_22 (and_22_out, not_130_out, not_131_out, not_132_out, not_133_out, not_134_out, not_135_out, F5, not_136_out, not_137_out, F2, F1, F0);
  and and_23 (and_23_out, not_138_out, not_139_out, not_140_out, not_141_out, not_142_out, not_143_out, F5, not_144_out, F3, not_145_out, F1, not_146_out);
  and and_24 (and_24_out, not_147_out, not_148_out, not_149_out, not_150_out, not_151_out, not_152_out, F5, not_153_out, F3, not_154_out, F1, F0);
  and and_25 (and_25_out, not_155_out, not_156_out, not_157_out, not_158_out, OP1, OP0);
  and and_26 (and_26_out, not_159_out, not_160_out, OP3, not_161_out, not_162_out, not_163_out);
  and and_27 (and_27_out, not_164_out, not_165_out, OP3, OP2, not_166_out, not_167_out);
  and and_28 (and_28_out, not_168_out, not_169_out, OP3, not_170_out, not_171_out, OP0);
  and and_29 (and_29_out, not_172_out, not_173_out, OP3, not_174_out, OP1, not_175_out);
  and and_30 (and_30_out, not_176_out, not_177_out, OP3, OP2, not_178_out, OP0);
  and and_31 (and_31_out, OP5, not_179_out, not_180_out, not_181_out, OP1, OP0);
  and and_32 (and_32_out, not_182_out, not_183_out, not_184_out, not_185_out, not_186_out, not_187_out, F5, not_188_out, not_189_out, not_190_out, F1, F0);
  and and_33 (and_33_out, not_191_out, not_192_out, not_193_out, not_194_out, not_195_out, not_196_out, F5, not_197_out, not_198_out, F2, F1, not_199_out);
  and and_34 (SysCALL, not_200_out, not_201_out, not_202_out, not_203_out, not_204_out, not_205_out, not_206_out, not_207_out, F2, F3, not_208_out, not_209_out);
  and and_35 (and_35_out, not_210_out, not_211_out, not_212_out, OP2, not_213_out, not_214_out);
  and and_36 (and_36_out, not_215_out, not_216_out, not_217_out, OP2, not_218_out, OP0);
  and and_37 (and_37_out, not_219_out, not_220_out, OP3, not_221_out, not_222_out, not_223_out);
  and and_38 (and_38_out, not_224_out, not_225_out, OP3, not_226_out, not_227_out, OP0);
  and and_39 (and_39_out, not_228_out, not_229_out, OP3, not_230_out, OP1, not_231_out);
  and and_40 (and_40_out, OP5, not_232_out, not_233_out, not_234_out, OP1, OP0);
  and and_41 (and_41_out, OP5, not_235_out, OP3, not_236_out, OP1, OP0);
  and and_42 (and_42_out, not_237_out, not_238_out, not_239_out, OP2, OP1, not_240_out);
  and and_43 (and_43_out, OP5, not_241_out, OP3, not_242_out, not_243_out, not_244_out);
  and and_44 (and_44_out, not_245_out, not_246_out, not_247_out, not_248_out, not_249_out, not_250_out, not_251_out, not_252_out, not_253_out, not_254_out, not_255_out, not_256_out);
  and and_45 (and_45_out, not_257_out, not_258_out, not_259_out, not_260_out, not_261_out, not_262_out, not_263_out, not_264_out, not_265_out, not_266_out, F1, F0);
  and and_46 (and_46_out, not_267_out, not_268_out, not_269_out, not_270_out, not_271_out, not_272_out, not_273_out, not_274_out, not_275_out, not_276_out, F1, not_277_out);
  and and_47 (and_47_out, not_278_out, not_279_out, not_280_out, not_281_out, not_282_out, not_283_out, F5, not_284_out, not_285_out, not_286_out, not_287_out, not_288_out);
  and and_48 (and_48_out, not_289_out, not_290_out, not_291_out, not_292_out, not_293_out, not_294_out, F5, not_295_out, not_296_out, not_297_out, not_298_out, F0);
  and and_49 (and_49_out, not_299_out, not_300_out, not_301_out, not_302_out, not_303_out, not_304_out, F5, not_305_out, not_306_out, not_307_out, F1, not_308_out);
  and and_50 (and_50_out, not_309_out, not_310_out, not_311_out, not_312_out, not_313_out, not_314_out, F5, not_315_out, not_316_out, F2, not_317_out, not_318_out);
  and and_51 (and_51_out, not_319_out, not_320_out, not_321_out, not_322_out, not_323_out, not_324_out, F5, not_325_out, not_326_out, F2, not_327_out, F0);
  and and_52 (and_52_out, not_328_out, not_329_out, not_330_out, not_331_out, not_332_out, not_333_out, F5, not_334_out, not_335_out, F2, F1, F0);
  and and_53 (and_53_out, not_336_out, not_337_out, not_338_out, not_339_out, not_340_out, not_341_out, F5, not_342_out, F3, not_343_out, F1, not_344_out);
  and and_54 (and_54_out, not_345_out, not_346_out, not_347_out, not_348_out, not_349_out, not_350_out, F5, not_351_out, F3, not_352_out, F1, F0);
  and and_55 (and_55_out, not_353_out, not_354_out, not_355_out, not_356_out, not_357_out, not_358_out, F5, not_359_out, not_360_out, not_361_out, F1, F0);
  and and_56 (and_56_out, not_362_out, not_363_out, not_364_out, not_365_out, not_366_out, not_367_out, F5, not_368_out, not_369_out, F2, F1, not_370_out);
  and and_57 (BEQ, not_371_out, not_372_out, OP2, not_373_out, not_374_out, not_375_out);
  and and_58 (BNE, OP0, not_376_out, OP2, not_377_out, not_378_out, not_379_out);
  and and_59 (JR, not_380_out, not_381_out, not_382_out, not_383_out, not_384_out, not_385_out, not_386_out, not_387_out, not_388_out, F3, not_389_out, not_390_out);
  and and_60 (and_60_out, not_391_out, not_392_out, not_393_out, not_394_out, not_395_out, not_396_out, not_397_out, not_398_out, F3, not_399_out, not_400_out);
  and and_61 (and_61_out, OP1, not_401_out, not_402_out, not_403_out, not_404_out);
  and and_62 (JAL, OP0, OP1, not_405_out, not_406_out, not_407_out, not_408_out);
  or or_1 (MemWrite, and_2_out, and_3_out);
  or or_2 (ALU_SRC, and_4_out, and_5_out, and_6_out, and_7_out, and_8_out, and_9_out, and_10_out, and_11_out);
  or or_3 (SignedExt, and_35_out, and_36_out, and_37_out, and_38_out, and_39_out, and_40_out, and_41_out, and_42_out, and_43_out);
  or or_4 (JUMP, and_60_out, and_61_out);
  or or_5 (RegWrite, and_14_out, and_15_out, and_16_out, and_17_out, and_18_out, and_19_out, and_20_out, and_21_out, and_22_out, and_23_out, and_24_out, and_25_out, and_26_out, and_27_out, and_28_out, and_29_out, and_30_out, and_31_out, and_32_out, and_33_out);
  or or_6 (RegDst, and_44_out, and_45_out, and_46_out, and_47_out, and_48_out, and_49_out, and_50_out, and_51_out, and_52_out, and_53_out, and_54_out, and_55_out, and_56_out);
endmodule

// ALU
module MIPS_ALU (
  input  [4:0] shamt,
  input  [31:0] X,
  input  [31:0] Y,
  input  [3:0] AluOP,
  output Equal,
  output [31:0] Result,
  output [31:0] Result_2
);

  wire [0:0] comparator_1_lt, comparator_2_lt;
  wire [31:0] adder_1_out, AND_out, divider_1_out, divider_1_rem, multiplier_1_cout, multiplier_1_out,
       NOR_out, OR_out, shifter_1_out, shifter_2_out, shifter_3_out, subtractor_1_out, XOR_out;

  assign AND_out = X & Y;  // AND_Gate AND, 32 bits wide
  assign OR_out = X | Y;  // OR_Gate OR, 32 bits wide
  Shifter #(.width(32), .shift("ll")) shifter_1 (.in(Y), .\dist (shamt), .out(shifter_1_out));
  Shifter #(.width(32), .shift("ar")) shifter_2 (.in(Y), .\dist (shamt), .out(shifter_2_out));
  Shifter #(.width(32), .shift("lr")) shifter_3 (.in(Y), .\dist (shamt), .out(shifter_3_out));
  Multiplier #(.width(32)) multiplier_1 (.a(X), .b(Y), .out(multiplier_1_out), .cout(multiplier_1_cout));  // open: cin
  Divider #(.width(32)) divider_1 (.a(X), .b(Y), .out(divider_1_out), .rem(divider_1_rem));  // open: upper
  Adder #(.width(32)) adder_1 (.a(X), .b(Y), .out(adder_1_out));  // open: cin, cout
  Subtractor #(.width(32)) subtractor_1 (.a(X), .b(Y), .out(subtractor_1_out));  // open: bin, bout
  assign XOR_out = X ^ Y;  // XOR_Gate XOR, 32 bits wide
  assign NOR_out = ~(X | Y);  // NOR_Gate NOR, 32 bits wide
  Comparator #(.width(32), .mode("twosComplement")) comparator_1 (
    .a(X), .b(Y), .eq(Equal), .lt(comparator_1_lt[0]));  // open: gt
  Comparator #(.width(32), .mode("unsigned")) comparator_2 (.a(X), .b(Y), .lt(comparator_2_lt[0]));  // open: gt, eq
  Multiplexer #(.select(4), .width(32), .disabled("Z"), .enable("false")) multiplexer_1 (
    .in0(shifter_1_out), .in1(shifter_2_out), .in2(shifter_3_out), .in3(multiplier_1_out),
    .in4(divider_1_out), .in5(adder_1_out), .in6(subtractor_1_out), .in7(AND_out), .in8(OR_out),
    .in9(XOR_out), .in10(NOR_out), .in11({{31{1'b0}}, comparator_1_lt[0]}),
    .in12({{31{1'b0}}, comparator_2_lt[0]}), .in13({32{1'b0}}), .in14({32{1'b0}}), .in15({32{1'b0}}),
    .out(Result), .sel(AluOP));
  Multiplexer #(.select(4), .width(32), .disabled("Z"), .enable("false")) multiplexer_2 (
    .in0({32{1'b0}}), .in1({32{1'b0}}), .in2({32{1'b0}}), .in3(multiplier_1_cout), .in4(divider_1_rem),
    .in5({32{1'b0}}), .in6({32{1'b0}}), .in7({32{1'b0}}), .in8({32{1'b0}}), .in9({32{1'b0}}),
    .in10({32{1'b0}}), .in11({32{1'b0}}), .in12({32{1'b0}}), .in13({32{1'b0}}), .in14({32{1'b0}}),
    .in15({32{1'b0}}), .out(Result_2), .sel(AluOP));

  // Other names for the same wires on the sheet: Result2[31:0] = Result_2; S[3:0] = AluOP

  // Notes on the sheet:
  //   不要改变此引脚区域内容，也不要改变ALU封装形式
  //   输入引脚
  //   输出引脚
endmodule

module MIPS_Regifile (
  input  [31:0] Din,
  input  Clk,
  input  WE,
  input  [4:0] R1_num,
  input  [4:0] W_num,
  input  [4:0] R2_num,
  output [31:0] R1,
  output [31:0] R2
);

  // RegisterFile registerfile_1: pin names not known; wires that end beside it: Din, Clk, WE, W_num, R1_num, R2_num, R1, R2
endmodule

module \理想流水线  (
);

  wire and_2_out, and_3_out, and_4_out, and_5_out, and_6_out, and_7_out, CLK, comparator_1_eq,
       comparator_2_eq, comparator_2_lt, ex_mem_l_1_jal_2, ex_mem_l_1_memtoreg_2, ex_mem_l_1_memwrite_2,
       ex_mem_l_1_regdst_2, ex_mem_l_1_regwrite_2, ex_mem_l_1_sb_2, ex_mem_l_1_syscall_2, final_IsStop,
       final_IsStop_t, Go, id_ex_l_1_alusrcb_2, id_ex_l_1_beq_2, id_ex_l_1_blez_2, id_ex_l_1_bne_2,
       id_ex_l_1_jal_2, id_ex_l_1_jr_2, id_ex_l_1_memtoreg_2, id_ex_l_1_memwrite_2, id_ex_l_1_regdst_2,
       id_ex_l_1_regwrite_2, id_ex_l_1_sb_2, id_ex_l_1_syscall_2, IR1, IR2, IR3, IsStop, JAL,
       mem_wb_l_1_memtoreg_2, mips_alu_1_equal, multiplexer_4_out, multiplexer_11_out, not_1_out, not_2_out,
       not_3_out, not_4_out, not_5_out, or_1_out, or_2_out, or_3_out, or_5_out, or_6_out, RegDst,
       register_3_q, RegWrite, RST, RstFlow, SEL, SignedExt, stop, Syscall, W1, W2, W3,
       \单周期硬布线控制器_1_alu_src , \单周期硬布线控制器_1_beq , \单周期硬布线控制器_1_blez , \单周期硬布线控制器_1_bne , \单周期硬布线控制器_1_jal ,
       \单周期硬布线控制器_1_jmp , \单周期硬布线控制器_1_jr , \单周期硬布线控制器_1_memtoreg , \单周期硬布线控制器_1_memwrite ,
       \单周期硬布线控制器_1_regdst , \单周期硬布线控制器_1_regwrite , \单周期硬布线控制器_1_sb , \单周期硬布线控制器_1_signedext ,
       \点击此键_先设置同步清零信号_out ;
  wire [1:0] or_4_out;
  wire [3:0] id_ex_l_1_aluop_2, \单周期硬布线控制器_1_alu_op ;
  wire [4:0] multiplexer_6_out, multiplexer_7_out, multiplexer_8_out, multiplexer_9_out, WB_rd, WB_rt;
  wire [7:0] ram_1_data, ram_1_data_2, ram_1_data_3, ram_1_data_4;
  wire [11:0] EX_PC, ID_PC, IF_PC, MEM_PC, WB_PC;
  wire [15:0] \LoadUse次数 , \总周期数 , \插入气泡数 , \无条件分支数 , \条件分支成功数 ;
  wire [27:2] PC_no_condition;
  wire [31:0] a0, adder_1_out, bit_extender_1_out, bit_extender_2_out, ex_mem_l_1_alu_2, ex_mem_l_1_ir_2,
       ex_mem_l_1_pc_2, ex_mem_l_1_pc_4_2, ex_mem_l_1_r2_2, id_ex_l_1_ir_2, id_ex_l_1_pc_2, id_ex_l_1_r2_2,
       if_id_l_1_ir_2, if_id_l_1_pc_2, if_id_l_1_pc_4_2, Jal_PC_4, LedData, mem_wb_l_1_alu_2,
       mem_wb_l_1_ir_2, mem_wb_l_1_md_2, mips_alu_1_result, multiplexer_1_out, multiplexer_2_out,
       multiplexer_3_out, multiplexer_10_out, multiplexer_12_out, multiplexer_13_out, multiplexer_14_out,
       multiplexer_15_out, multiplexer_16_out, PC_4, PC_condition, PC_q, rom_1_data, RS, shifter_1_out, v0;

  Multiplexer #(.select(1), .width(32), .disabled("Z"), .enable("false")) multiplexer_1 (
    .in0({PC_4[31:28], PC_no_condition, 2'b00}), .in1(RS), .out(multiplexer_1_out), .sel(id_ex_l_1_jr_2));
  Button \u_点击此键_先设置同步清零信号  (.out(\点击此键_先设置同步清零信号_out ));
  Register #(.width(1), .trigger("falling"), .Select("low")) register_1 (
    .D(1'b0), .Q(RstFlow), .clk(RST), .preset(\点击此键_先设置同步清零信号_out ));  // open: en, clr, cs
  Multiplexer #(.select(2), .width(32), .disabled("Z"), .enable("false")) multiplexer_2 (
    .in0(adder_1_out), .in1(PC_condition), .in2(multiplexer_1_out), .out(multiplexer_2_out), .sel(or_4_out));  // open: in3
  Comparator #(.width(32), .mode("twosComplement")) comparator_1 (
    .a(v0), .b(32'h22), .eq(comparator_1_eq));  // open: gt, lt
  Multiplexer #(.select(1), .width(32), .disabled("Z"), .enable("false")) multiplexer_3 (
    .in0(multiplexer_2_out), .in1(PC_q), .out(multiplexer_3_out), .sel(stop));
  Register #(.width(32), .trigger("rising"), .Select("low")) PC (
    .D(multiplexer_3_out), .Q(PC_q), .clk(CLK), .clr(RST));  // open: en
  not not_1 (not_1_out, comparator_1_eq);
  and and_1 (IsStop, not_1_out, Syscall);
  xor xor_1 (stop, final_IsStop_t, register_3_q);
  Button \u_再总复位  (.out(RST));
  Button _1 (.out(IR1));
  Button _2 (.out(IR2));
  Button _3 (.out(IR3));
  Register #(.width(32), .trigger("rising"), .Select("low")) register_2 (
    .D(a0), .Q(LedData), .clk(and_2_out), .clr(RST));  // open: en
  and and_2 (and_2_out, Syscall, comparator_1_eq);
  and and_3 (and_3_out, final_IsStop_t, Go);
  Register #(.width(1), .trigger("rising"), .Select("low")) register_3 (
    .D(1'b0), .Q(register_3_q), .clk(CLK), .clr(RST), .preset(and_3_out));  // open: en, cs
  Button \u_继续运行  (.out(Go));
  LED #(.active("true")) led_1 (.in(W1));
  LED #(.active("true")) led_2 (.in(W2));
  LED #(.active("true")) led_3 (.in(W3));
  Multiplexer #(.select(1), .width(1), .disabled("Z"), .enable("false")) multiplexer_4 (
    .in0(final_IsStop_t), .in1(1'b0), .out(multiplexer_4_out), .sel(register_3_q));
  Hex_Digit_Display hex_digit_display_1 (.value(LedData[31:28]));  // open: dp
  Hex_Digit_Display hex_digit_display_2 (.value(LedData[27:24]));  // open: dp
  Adder #(.width(32)) adder_1 (.a(PC_q), .b(32'h4), .out(adder_1_out));  // open: cin, cout
  ROM #(.addrWidth(10), .dataWidth(32), .Select("high")) rom_1 (.addr(PC_q[11:2]), .data(rom_1_data));
  Multiplexer #(.select(1), .width(1), .disabled("Z"), .enable("false")) multiplexer_5 (
    .in0(multiplexer_4_out), .in1(1'b0), .out(SEL), .sel(RstFlow));
  Hex_Digit_Display hex_digit_display_3 (.value(LedData[19:16]));  // open: dp
  Hex_Digit_Display hex_digit_display_4 (.value(LedData[23:20]));  // open: dp
  or or_1 (or_1_out, RST, CLK);
  Hex_Digit_Display hex_digit_display_5 (.value(LedData[15:12]));  // open: dp
  Hex_Digit_Display hex_digit_display_6 (.value(LedData[11:8]));  // open: dp
  Clock #(.highDuration(1), .lowDuration(1)) clock_1 (.out(CLK));
  IF_ID_l if_id_l_1 (
    .CLK(or_1_out), .\同步清零_气泡_高电平有效 (RstFlow), .\使能端_低电平有效 (SEL), .PC(PC_q), .PC_2(if_id_l_1_pc_2),
    .IR(rom_1_data), .IR_2(if_id_l_1_ir_2), .PC_4(adder_1_out), .PC_4_2(if_id_l_1_pc_4_2));  // open: MISS, MISS_2, JMP_Pre, JMP_Pre_2, State_Now, State_Now_2, Row_Pre, Row_Pre_2
  Hex_Digit_Display hex_digit_display_7 (.value(LedData[3:0]));  // open: dp
  Hex_Digit_Display hex_digit_display_8 (.value(LedData[7:4]));  // open: dp
  Multiplexer #(.select(1), .width(5), .disabled("Z"), .enable("false")) multiplexer_6 (
    .in0(WB_rt), .in1(WB_rd), .out(multiplexer_6_out), .sel(RegDst));
  // Probe on \总周期数 
  // Probe on \无条件分支数 
  // Probe on \条件分支成功数 
  // Probe on \插入气泡数 
  // Probe on \LoadUse次数 
  \单周期硬布线控制器  \u_单周期硬布线控制器_1  (
    .Func(if_id_l_1_ir_2[5:0]), .OP(if_id_l_1_ir_2[31:26]), .ALU_OP(\单周期硬布线控制器_1_alu_op ),
    .MemToReg(\单周期硬布线控制器_1_memtoreg ), .MemWrite(\单周期硬布线控制器_1_memwrite ), .ALU_SRC(\单周期硬布线控制器_1_alu_src ),
    .RegWrite(\单周期硬布线控制器_1_regwrite ), .SysCALL(Syscall), .SignedExt(\单周期硬布线控制器_1_signedext ),
    .RegDst(\单周期硬布线控制器_1_regdst ), .JR(\单周期硬布线控制器_1_jr ), .JMP(\单周期硬布线控制器_1_jmp ), .Beq(\单周期硬布线控制器_1_beq ),
    .JAL(\单周期硬布线控制器_1_jal ), .Bne(\单周期硬布线控制器_1_bne ), .BLEZ(\单周期硬布线控制器_1_blez ), .SB(\单周期硬布线控制器_1_sb ));
  Multiplexer #(.select(1), .width(5), .disabled("Z"), .enable("false")) multiplexer_7 (
    .in0(if_id_l_1_ir_2[25:21]), .in1(5'b00010), .out(multiplexer_7_out), .sel(Syscall));
  Multiplexer #(.select(1), .width(5), .disabled("Z"), .enable("false")) multiplexer_8 (
    .in0(if_id_l_1_ir_2[20:16]), .in1(5'b00100), .out(multiplexer_8_out), .sel(Syscall));
  Multiplexer #(.select(1), .width(5), .disabled("Z"), .enable("false")) multiplexer_9 (
    .in0(multiplexer_6_out), .in1({5{1'b1}}), .out(multiplexer_9_out), .sel(JAL));
  Multiplexer #(.select(1), .width(32), .disabled("Z"), .enable("false")) multiplexer_10 (
    .in0(multiplexer_16_out), .in1(Jal_PC_4), .out(multiplexer_10_out), .sel(JAL));
  // Probe on IF_PC
  MIPS_Regifile mips_regifile_1 (
    .Din(multiplexer_10_out), .Clk(CLK), .R1(v0), .R2(a0), .WE(RegWrite), .W_num(multiplexer_9_out),
    .R1_num(multiplexer_7_out), .R2_num(multiplexer_8_out));
  // Probe on ID_PC
  // Probe on EX_PC
  // Probe on WB_PC
  // Probe on MEM_PC
  or or_2 (or_2_out, RST, CLK);
  ID_EX_l id_ex_l_1 (
    .CLK(or_2_out), .\同步清零_气泡_高电平有效 (RstFlow), .\使能端_低电平有效 (SEL), .PC(if_id_l_1_pc_2), .R1(v0),
    .BLEZ(\单周期硬布线控制器_1_blez ), .SignedExt(\单周期硬布线控制器_1_signedext ), .MemToReg(\单周期硬布线控制器_1_memtoreg ),
    .MemWrite(\单周期硬布线控制器_1_memwrite ), .BEQ(\单周期硬布线控制器_1_beq ), .Syscall(IsStop),
    .RegWrite(\单周期硬布线控制器_1_regwrite ), .SB(\单周期硬布线控制器_1_sb ), .BNE(\单周期硬布线控制器_1_bne ),
    .RegDst(\单周期硬布线控制器_1_regdst ), .IR(if_id_l_1_ir_2), .R2(a0), .AluSrcB(\单周期硬布线控制器_1_alu_src ),
    .JR(\单周期硬布线控制器_1_jr ), .JAL(\单周期硬布线控制器_1_jal ), .AluOP(\单周期硬布线控制器_1_alu_op ),
    .Imm26(if_id_l_1_ir_2[25:0]), .JMP(\单周期硬布线控制器_1_jmp ), .PC_2(id_ex_l_1_pc_2), .R1_2(RS),
    .BLEZ_2(id_ex_l_1_blez_2), .SignedExt_2(SignedExt), .MemToReg_2(id_ex_l_1_memtoreg_2),
    .MemWrite_2(id_ex_l_1_memwrite_2), .BEQ_2(id_ex_l_1_beq_2), .Syscall_2(id_ex_l_1_syscall_2),
    .RegWrite_2(id_ex_l_1_regwrite_2), .SB_2(id_ex_l_1_sb_2), .BNE_2(id_ex_l_1_bne_2),
    .RegDst_2(id_ex_l_1_regdst_2), .IR_2(id_ex_l_1_ir_2), .R2_2(id_ex_l_1_r2_2),
    .AluSrcB_2(id_ex_l_1_alusrcb_2), .JR_2(id_ex_l_1_jr_2), .JAL_2(id_ex_l_1_jal_2),
    .AluOP_2(id_ex_l_1_aluop_2), .Imm26_2(PC_no_condition), .JMP_2(or_4_out[1]), .PC_4(if_id_l_1_pc_4_2),
    .PC_4_2(PC_4));  // open: Forwarding_R1, Forwarding_R1_2, Forwarding_R2, Forwarding_R2_2, MISS, MISS_2, JMP_Pre, JMP_Pre_2, State_Now, State_Now_2, Row_Pre, Row_Pre_2
  and and_4 (and_4_out, not_2_out, CLK);
  not not_2 (not_2_out, stop);
  Counter #(.width(16), .max('hffff), .ongoal("wrap"), .trigger("rising"), .behavior("old")) counter_1 (
    .count(1'b1), .Q(\总周期数 ), .clk(multiplexer_11_out), .clr(RST));  // open: load, D, carry, preset
  Multiplexer #(.select(1), .width(1), .disabled("Z"), .enable("false")) multiplexer_11 (
    .in0(and_4_out), .in1(1'b0), .out(multiplexer_11_out), .sel(not_3_out));
  not not_3 (not_3_out, not_4_out);
  not not_4 (not_4_out, CLK);
  Comparator #(.width(32), .mode("twosComplement")) comparator_2 (
    .a(RS), .b({32{1'b0}}), .eq(comparator_2_eq), .lt(comparator_2_lt));  // open: gt
  assign bit_extender_1_out = {{16{1'b0}}, PC_no_condition[17:2]};  // Bit_Extender bit_extender_1
  assign bit_extender_2_out = {{16{PC_no_condition[17]}}, PC_no_condition[17:2]};  // Bit_Extender bit_extender_2
  or or_3 (or_3_out, comparator_2_eq, comparator_2_lt);
  Multiplexer #(.select(1), .width(32), .disabled("Z"), .enable("false")) multiplexer_12 (
    .in0(bit_extender_1_out), .in1(bit_extender_2_out), .out(multiplexer_12_out), .sel(SignedExt));
  and and_5 (and_5_out, or_3_out, id_ex_l_1_blez_2);
  Multiplexer #(.select(1), .width(32), .disabled("Z"), .enable("false")) multiplexer_13 (
    .in0(id_ex_l_1_r2_2), .in1(multiplexer_12_out), .out(multiplexer_13_out), .sel(id_ex_l_1_alusrcb_2));
  Shifter #(.width(32), .shift("ll")) shifter_1 (.in(multiplexer_12_out), .\dist (5'b00010), .out(shifter_1_out));
  Adder #(.width(32)) adder_2 (.a(shifter_1_out), .b(PC_4), .out(PC_condition));  // open: cin, cout
  not not_5 (not_5_out, mips_alu_1_equal);
  MIPS_ALU mips_alu_1 (
    .X(RS), .Y(multiplexer_13_out), .AluOP(id_ex_l_1_aluop_2), .Equal(mips_alu_1_equal),
    .Result(mips_alu_1_result), .shamt(PC_no_condition[12:8]));  // open: Result_2
  and and_6 (and_6_out, mips_alu_1_equal, id_ex_l_1_beq_2);
  and and_7 (and_7_out, id_ex_l_1_bne_2, not_5_out);
  or or_4 (or_4_out[0], and_5_out, and_7_out, and_6_out);
  or or_5 (or_5_out, RST, CLK);
  EX_MEM_l ex_mem_l_1 (
    .CLK(or_5_out), .\同步清零_气泡_高电平有效 (RstFlow), .\使能端_低电平有效 (SEL), .PC(id_ex_l_1_pc_2),
    .MemToReg(id_ex_l_1_memtoreg_2), .MemWrite(id_ex_l_1_memwrite_2), .RegWrite(id_ex_l_1_regwrite_2),
    .SB(id_ex_l_1_sb_2), .RegDst(id_ex_l_1_regdst_2), .IR(id_ex_l_1_ir_2), .R2(id_ex_l_1_r2_2),
    .JAL(id_ex_l_1_jal_2), .PC_2(ex_mem_l_1_pc_2), .MemToReg_2(ex_mem_l_1_memtoreg_2),
    .MemWrite_2(ex_mem_l_1_memwrite_2), .RegWrite_2(ex_mem_l_1_regwrite_2), .SB_2(ex_mem_l_1_sb_2),
    .RegDst_2(ex_mem_l_1_regdst_2), .IR_2(ex_mem_l_1_ir_2), .R2_2(ex_mem_l_1_r2_2), .JAL_2(ex_mem_l_1_jal_2),
    .ALU(mips_alu_1_result), .ALU_2(ex_mem_l_1_alu_2), .PC_4(PC_4), .PC_4_2(ex_mem_l_1_pc_4_2),
    .Syscall(id_ex_l_1_syscall_2), .Syscall_2(ex_mem_l_1_syscall_2));
  Multiplexer #(.select(2), .width(32), .disabled("Z"), .enable("false")) multiplexer_14 (
    .in0({ram_1_data, ram_1_data_4, ram_1_data_3, ex_mem_l_1_r2_2[7:0]}),
    .in1({ram_1_data, ram_1_data_4, ex_mem_l_1_r2_2[7:0], ram_1_data_2}),
    .in2({ram_1_data, ex_mem_l_1_r2_2[7:0], ram_1_data_3, ram_1_data_2}),
    .in3({ex_mem_l_1_r2_2[7:0], ram_1_data_4, ram_1_data_3, ram_1_data_2}), .out(multiplexer_14_out),
    .sel(ex_mem_l_1_alu_2[1:0]));
  Multiplexer #(.select(1), .width(32), .disabled("Z"), .enable("false")) multiplexer_15 (
    .in0(ex_mem_l_1_r2_2), .in1(multiplexer_14_out), .out(multiplexer_15_out), .sel(ex_mem_l_1_sb_2));
  RAM #(.addrWidth(10), .dataWidth(32), .bus("separate"), .Select("high")) ram_1 (
    .addr(ex_mem_l_1_alu_2[11:2]), .din(multiplexer_15_out),
    .data({ram_1_data, ram_1_data_4, ram_1_data_3, ram_1_data_2}), .str(ex_mem_l_1_memwrite_2), .clk(CLK),
    .clr(RST));  // open: sel, ld
  or or_6 (or_6_out, RST, CLK);
  MEM_WB_l mem_wb_l_1 (
    .CLK(or_6_out), .\同步清零_气泡_高电平有效 (RstFlow), .\使能端_低电平有效 (SEL), .PC(ex_mem_l_1_pc_2),
    .MemToReg(ex_mem_l_1_memtoreg_2), .MemToReg_2(mem_wb_l_1_memtoreg_2), .RegWrite(ex_mem_l_1_regwrite_2),
    .RegWrite_2(RegWrite), .RegDst(ex_mem_l_1_regdst_2), .IR(ex_mem_l_1_ir_2),
    .MD({ram_1_data, ram_1_data_4, ram_1_data_3, ram_1_data_2}), .RegDst_2(RegDst),
    .IR_2({mem_wb_l_1_ir_2[31:21], WB_rt, WB_rd, mem_wb_l_1_ir_2[10:0]}), .MD_2(mem_wb_l_1_md_2),
    .JAL(ex_mem_l_1_jal_2), .JAL_2(JAL), .ALU(ex_mem_l_1_alu_2), .ALU_2(mem_wb_l_1_alu_2),
    .PC_4(ex_mem_l_1_pc_4_2), .PC_4_2(Jal_PC_4), .Syscall(ex_mem_l_1_syscall_2), .Syscall_2(final_IsStop));  // open: PC_2
  Multiplexer #(.select(1), .width(32), .disabled("Z"), .enable("false")) multiplexer_16 (
    .in0(mem_wb_l_1_alu_2), .in1(mem_wb_l_1_md_2), .out(multiplexer_16_out), .sel(mem_wb_l_1_memtoreg_2));

  // Other names for the same wires on the sheet: PC_no_condition[31:28] = PC_4[31:28]

  // Notes on the sheet:
  //   中断源
  //   中断等待指示
  //   指令存储器
  //   contents of rom_1 (hex, n*v repeats v):
  //   20100000 20110000 20120000 20130000 36100000 36310001 36520002 36730003 ae100000 ae110004 ae120008
  //   ae13000c 2002000a 20110000 20120000 20130000 c
  //   数码管输出
  //   PC+4
  //   IR
  //   PC
  //   指令字
  //   OP
  //   Func
  //   rs
  //   rt
  //   rd
  //   Imm26
  //   流水调试日志用
  //   IR
  //   PC
  //   MemWrite
  //   SB
  //   IR
  //   PC
  //   R2
  //   ALU
  //   MemToReg
  //   rt
  //   rd
endmodule

module \气泡流水线  (
);

  wire and_1_out, and_3_out, and_4_out, and_5_out, and_6_out, and_7_out, and_8_out, and_9_out, and_10_out,
       and_11_out, Bubble, CLK, comparator_1_eq, comparator_2_eq, comparator_2_lt, ex_mem_l_1_jal_2,
       ex_mem_l_1_memtoreg_2, ex_mem_l_1_memwrite_2, ex_mem_l_1_regdst_2, ex_mem_l_1_sb_2,
       ex_mem_l_1_syscall_2, EX_RegWrite, final_IsStop, final_IsStop_t, Go, id_ex_l_1_alusrcb_2,
       id_ex_l_1_beq_2, id_ex_l_1_blez_2, id_ex_l_1_bne_2, id_ex_l_1_jal_2, id_ex_l_1_jr_2,
       id_ex_l_1_memtoreg_2, id_ex_l_1_memwrite_2, id_ex_l_1_regdst_2, id_ex_l_1_sb_2, id_ex_l_1_syscall_2,
       IR1, IR2, IR3, IsRelated, IsStop, JAL, MEM_RegWrite, mem_wb_l_1_memtoreg_2, mips_alu_1_equal,
       multiplexer_4_out, multiplexer_11_out, multiplexer_14_out, multiplexer_15_out, multiplexer_20_out,
       not_1_out, not_2_out, not_3_out, not_4_out, not_5_out, not_6_out, not_7_out, not_8_out, not_9_out,
       not_10_out, not_11_out, not_12_out, not_13_out, or_1_out, or_2_out, or_3_out, or_4_out, or_5_out,
       or_6_out, or_9_out, or_10_out, RegDst, register_3_q, RegWrite, RST, RstFlow, SEL, SignedExt, stop,
       Syscall, W1, W2, W3, \单周期硬布线控制器_1_alu_src , \单周期硬布线控制器_1_beq , \单周期硬布线控制器_1_blez , \单周期硬布线控制器_1_bne ,
       \单周期硬布线控制器_1_jal , \单周期硬布线控制器_1_jmp , \单周期硬布线控制器_1_jr , \单周期硬布线控制器_1_memtoreg ,
       \单周期硬布线控制器_1_memwrite , \单周期硬布线控制器_1_regdst , \单周期硬布线控制器_1_regwrite , \单周期硬布线控制器_1_sb ,
       \单周期硬布线控制器_1_signedext , \无条件分支 , \条件分支 , \源寄存器使用情况_1_r1_used , \源寄存器使用情况_1_r2_used ,
       \点击此键_先设置同步清零信号_out ;
  wire [3:0] id_ex_l_1_aluop_2, \单周期硬布线控制器_1_alu_op ;
  wire [4:0] EX_WriteReg_num, MEM_WriteReg_num, multiplexer_8_out, multiplexer_9_out, multiplexer_16_out,
       multiplexer_21_out, R1_Relate, R2_Relate, WB_rd, WB_rt;
  wire [5:0] Func, OP;
  wire [15:0] \LoadUse次数 , \总周期数 , \插入气泡数 , \无条件分支数 , \条件分支成功数 ;
  wire [25:6] if_id_l_1_ir_2;
  wire [27:2] PC_no_condition;
  wire [31:0] a0, adder_1_out, bit_extender_1_out, bit_extender_2_out, ex_mem_l_1_alu_2, ex_mem_l_1_ir_2,
       ex_mem_l_1_pc_4_2, ex_mem_l_1_r2_2, EX_PC, id_ex_l_1_ir_2, id_ex_l_1_r2_2, ID_PC, if_id_l_1_pc_4_2,
       IF_PC, Jal_PC_4, LedData, MEM_PC, mem_wb_l_1_alu_2, mem_wb_l_1_ir_2, mem_wb_l_1_md_2,
       mips_alu_1_result, multiplexer_1_out, multiplexer_2_out, multiplexer_3_out, multiplexer_10_out,
       multiplexer_12_out, multiplexer_13_out, multiplexer_18_out, multiplexer_19_out, multiplexer_23_out,
       PC_4, PC_condition, ram_1_data, rom_1_data, RS, shifter_1_out, v0, WB_PC;

  Multiplexer #(.select(1), .width(32), .disabled("Z"), .enable("false")) multiplexer_1 (
    .in0({PC_4[31:28], PC_no_condition, 2'b00}), .in1(RS), .out(multiplexer_1_out), .sel(id_ex_l_1_jr_2));
  Button \u_点击此键_先设置同步清零信号  (.out(\点击此键_先设置同步清零信号_out ));
  Register #(.width(1), .trigger("falling"), .Select("low")) register_1 (
    .D(1'b0), .Q(RstFlow), .clk(RST), .preset(\点击此键_先设置同步清零信号_out ));  // open: en, clr, cs
  Multiplexer #(.select(2), .width(32), .disabled("Z"), .enable("false")) multiplexer_2 (
    .in0(adder_1_out), .in1(PC_condition), .in2(multiplexer_1_out), .out(multiplexer_2_out),
    .sel({\无条件分支 , \条件分支 }));  // open: in3
  Comparator #(.width(32), .mode("twosComplement")) comparator_1 (
    .a(v0), .b(32'h22), .eq(comparator_1_eq));  // open: gt, lt
  not not_1 (not_1_out, comparator_1_eq);
  Register #(.width(32), .trigger("rising"), .Select("low")) PC (
    .D(multiplexer_3_out), .en(not_2_out), .Q(IF_PC), .clk(CLK), .clr(RST));
  Multiplexer #(.select(1), .width(32), .disabled("Z"), .enable("false")) multiplexer_3 (
    .in0(multiplexer_2_out), .in1(IF_PC), .out(multiplexer_3_out), .sel(stop));
  not not_2 (not_2_out, IsRelated);
  and and_1 (and_1_out, Syscall, comparator_1_eq);
  and and_2 (IsStop, not_1_out, Syscall);
  xor xor_1 (stop, final_IsStop_t, register_3_q);
  Button \u_再总复位  (.out(RST));
  Button _1 (.out(IR1));
  Button _2 (.out(IR2));
  Button _3 (.out(IR3));
  Register #(.width(32), .trigger("rising"), .Select("low")) register_2 (
    .D(a0), .Q(LedData), .clk(and_1_out), .clr(RST));  // open: en
  and and_3 (and_3_out, final_IsStop_t, Go);
  Register #(.width(1), .trigger("rising"), .Select("low")) register_3 (
    .D(1'b0), .Q(register_3_q), .clk(CLK), .clr(RST), .preset(and_3_out));  // open: en, cs
  Button \u_继续运行  (.out(Go));
  LED #(.active("true")) led_1 (.in(W1));
  LED #(.active("true")) led_2 (.in(W2));
  LED #(.active("true")) led_3 (.in(W3));
  Adder #(.width(32)) adder_1 (.a(IF_PC), .b(32'h4), .out(adder_1_out));  // open: cin, cout
  Multiplexer #(.select(1), .width(1), .disabled("Z"), .enable("false")) multiplexer_4 (
    .in0(final_IsStop_t), .in1(1'b0), .out(multiplexer_4_out), .sel(register_3_q));
  Multiplexer #(.select(1), .width(1), .disabled("Z"), .enable("false")) multiplexer_5 (
    .in0(multiplexer_4_out), .in1(1'b0), .out(SEL), .sel(or_1_out));
  Hex_Digit_Display hex_digit_display_1 (.value(LedData[31:28]));  // open: dp
  Hex_Digit_Display hex_digit_display_2 (.value(LedData[27:24]));  // open: dp
  ROM #(.addrWidth(10), .dataWidth(32), .Select("high")) rom_1 (.addr(IF_PC[11:2]), .data(rom_1_data));
  or or_1 (or_1_out, Bubble, RstFlow);
  or or_2 (or_2_out, SEL, IsRelated);
  Hex_Digit_Display hex_digit_display_3 (.value(LedData[23:20]));  // open: dp
  Hex_Digit_Display hex_digit_display_4 (.value(LedData[19:16]));  // open: dp
  IF_ID_l if_id_l_1 (
    .CLK(or_3_out), .\同步清零_气泡_高电平有效 (or_1_out), .\使能端_低电平有效 (or_2_out), .PC(IF_PC), .PC_2(ID_PC),
    .IR(rom_1_data), .IR_2({OP, if_id_l_1_ir_2, Func}), .PC_4(adder_1_out), .PC_4_2(if_id_l_1_pc_4_2));  // open: MISS, MISS_2, JMP_Pre, JMP_Pre_2, State_Now, State_Now_2, Row_Pre, Row_Pre_2
  or or_3 (or_3_out, RST, CLK);
  Hex_Digit_Display hex_digit_display_5 (.value(LedData[15:12]));  // open: dp
  Hex_Digit_Display hex_digit_display_6 (.value(LedData[11:8]));  // open: dp
  Clock #(.highDuration(1), .lowDuration(1)) clock_1 (.out(CLK));
  Hex_Digit_Display hex_digit_display_7 (.value(LedData[3:0]));  // open: dp
  Hex_Digit_Display hex_digit_display_8 (.value(LedData[7:4]));  // open: dp
  \源寄存器使用情况  \u_源寄存器使用情况_1  (.OP(OP), .FUN(Func), .R1_Used(\源寄存器使用情况_1_r1_used ), .R2_Used(\源寄存器使用情况_1_r2_used ));
  \数据相关检测  \u_数据相关检测_1  (
    .R1_Used(\源寄存器使用情况_1_r1_used ), .R2_Used(\源寄存器使用情况_1_r2_used ), .R1_num(R1_Relate), .R2_num(R2_Relate),
    .EX_WriteReg_num(EX_WriteReg_num), .EX_RegWrite(EX_RegWrite), .MEM_WriteReg_num(MEM_WriteReg_num),
    .MEM_RegWrite(MEM_RegWrite), .Relate(IsRelated));  // open: EX_OP, Load_Use, R1_EX_Relate, R2_EX_Relate, R1_MEM_Relate, R2_MEM_Relate
  \单周期硬布线控制器  \u_单周期硬布线控制器_1  (
    .Func(Func), .OP(OP), .ALU_OP(\单周期硬布线控制器_1_alu_op ), .MemToReg(\单周期硬布线控制器_1_memtoreg ),
    .MemWrite(\单周期硬布线控制器_1_memwrite ), .ALU_SRC(\单周期硬布线控制器_1_alu_src ), .RegWrite(\单周期硬布线控制器_1_regwrite ),
    .SysCALL(Syscall), .SignedExt(\单周期硬布线控制器_1_signedext ), .RegDst(\单周期硬布线控制器_1_regdst ),
    .JR(\单周期硬布线控制器_1_jr ), .JMP(\单周期硬布线控制器_1_jmp ), .Beq(\单周期硬布线控制器_1_beq ), .JAL(\单周期硬布线控制器_1_jal ),
    .Bne(\单周期硬布线控制器_1_bne ), .BLEZ(\单周期硬布线控制器_1_blez ), .SB(\单周期硬布线控制器_1_sb ));
  Multiplexer #(.select(1), .width(5), .disabled("Z"), .enable("false")) multiplexer_6 (
    .in0(if_id_l_1_ir_2[25:21]), .in1(5'b00010), .out(R1_Relate), .sel(Syscall));
  Multiplexer #(.select(1), .width(5), .disabled("Z"), .enable("false")) multiplexer_7 (
    .in0(if_id_l_1_ir_2[20:16]), .in1(5'b00100), .out(R2_Relate), .sel(Syscall));
  Multiplexer #(.select(1), .width(5), .disabled("Z"), .enable("false")) multiplexer_8 (
    .in0(WB_rt), .in1(WB_rd), .out(multiplexer_8_out), .sel(RegDst));
  Multiplexer #(.select(1), .width(5), .disabled("Z"), .enable("false")) multiplexer_9 (
    .in0(multiplexer_8_out), .in1({5{1'b1}}), .out(multiplexer_9_out), .sel(JAL));
  Multiplexer #(.select(1), .width(32), .disabled("Z"), .enable("false")) multiplexer_10 (
    .in0(multiplexer_23_out), .in1(Jal_PC_4), .out(multiplexer_10_out), .sel(JAL));
  // Probe on \总周期数 
  // Probe on \无条件分支数 
  // Probe on \条件分支成功数 
  // Probe on \插入气泡数 
  // Probe on \LoadUse次数 
  // Probe on IF_PC[11:0]
  MIPS_Regifile mips_regifile_1 (
    .Din(multiplexer_10_out), .Clk(CLK), .R1(v0), .R2(a0), .WE(RegWrite), .W_num(multiplexer_9_out),
    .R1_num(R1_Relate), .R2_num(R2_Relate));
  // Probe on EX_PC[11:0]
  // Probe on ID_PC[11:0]
  or or_4 (or_4_out, Bubble, IsRelated, RstFlow);
  // Probe on WB_PC[11:0]
  // Probe on MEM_PC[11:0]
  or or_5 (or_5_out, RST, CLK);
  ID_EX_l id_ex_l_1 (
    .CLK(or_5_out), .\同步清零_气泡_高电平有效 (or_4_out), .\使能端_低电平有效 (SEL), .PC(ID_PC), .R1(v0),
    .BLEZ(\单周期硬布线控制器_1_blez ), .SignedExt(\单周期硬布线控制器_1_signedext ), .MemToReg(\单周期硬布线控制器_1_memtoreg ),
    .MemWrite(\单周期硬布线控制器_1_memwrite ), .BEQ(\单周期硬布线控制器_1_beq ), .Syscall(IsStop),
    .RegWrite(\单周期硬布线控制器_1_regwrite ), .SB(\单周期硬布线控制器_1_sb ), .BNE(\单周期硬布线控制器_1_bne ),
    .RegDst(\单周期硬布线控制器_1_regdst ), .IR({OP, if_id_l_1_ir_2, Func}), .R2(a0), .AluSrcB(\单周期硬布线控制器_1_alu_src ),
    .JR(\单周期硬布线控制器_1_jr ), .JAL(\单周期硬布线控制器_1_jal ), .AluOP(\单周期硬布线控制器_1_alu_op ),
    .Imm26({if_id_l_1_ir_2, Func}), .JMP(\单周期硬布线控制器_1_jmp ), .PC_2(EX_PC), .R1_2(RS),
    .BLEZ_2(id_ex_l_1_blez_2), .SignedExt_2(SignedExt), .MemToReg_2(id_ex_l_1_memtoreg_2),
    .MemWrite_2(id_ex_l_1_memwrite_2), .BEQ_2(id_ex_l_1_beq_2), .Syscall_2(id_ex_l_1_syscall_2),
    .RegWrite_2(EX_RegWrite), .SB_2(id_ex_l_1_sb_2), .BNE_2(id_ex_l_1_bne_2), .RegDst_2(id_ex_l_1_regdst_2),
    .IR_2(id_ex_l_1_ir_2), .R2_2(id_ex_l_1_r2_2), .AluSrcB_2(id_ex_l_1_alusrcb_2), .JR_2(id_ex_l_1_jr_2),
    .JAL_2(id_ex_l_1_jal_2), .AluOP_2(id_ex_l_1_aluop_2), .Imm26_2(PC_no_condition), .JMP_2(\无条件分支 ),
    .PC_4(if_id_l_1_pc_4_2), .PC_4_2(PC_4));  // open: Forwarding_R1, Forwarding_R1_2, Forwarding_R2, Forwarding_R2_2, MISS, MISS_2, JMP_Pre, JMP_Pre_2, State_Now, State_Now_2, Row_Pre, Row_Pre_2
  and and_4 (and_4_out, not_3_out, CLK);
  not not_3 (not_3_out, stop);
  assign bit_extender_1_out = {{16{1'b0}}, PC_no_condition[17:2]};  // Bit_Extender bit_extender_1
  assign bit_extender_2_out = {{16{PC_no_condition[17]}}, PC_no_condition[17:2]};  // Bit_Extender bit_extender_2
  Counter #(.width(16), .max('hffff), .ongoal("wrap"), .trigger("rising"), .behavior("old")) counter_1 (
    .count(1'b1), .Q(\总周期数 ), .clk(multiplexer_11_out), .clr(RST));  // open: load, D, carry, preset
  Multiplexer #(.select(1), .width(1), .disabled("Z"), .enable("false")) multiplexer_11 (
    .in0(and_4_out), .in1(1'b0), .out(multiplexer_11_out), .sel(not_4_out));
  not not_4 (not_4_out, not_5_out);
  not not_5 (not_5_out, CLK);
  Comparator #(.width(32), .mode("twosComplement")) comparator_2 (
    .a(RS), .b({32{1'b0}}), .eq(comparator_2_eq), .lt(comparator_2_lt));  // open: gt
  Multiplexer #(.select(1), .width(32), .disabled("Z"), .enable("false")) multiplexer_12 (
    .in0(bit_extender_1_out), .in1(bit_extender_2_out), .out(multiplexer_12_out), .sel(SignedExt));
  or or_6 (or_6_out, comparator_2_eq, comparator_2_lt);
  Multiplexer #(.select(1), .width(32), .disabled("Z"), .enable("false")) multiplexer_13 (
    .in0(id_ex_l_1_r2_2), .in1(multiplexer_12_out), .out(multiplexer_13_out), .sel(id_ex_l_1_alusrcb_2));
  Shifter #(.width(32), .shift("ll")) shifter_1 (.in(multiplexer_12_out), .\dist (5'b00010), .out(shifter_1_out));
  and and_5 (and_5_out, or_6_out, id_ex_l_1_blez_2);
  MIPS_ALU mips_alu_1 (
    .X(RS), .Y(multiplexer_13_out), .AluOP(id_ex_l_1_aluop_2), .Equal(mips_alu_1_equal),
    .Result(mips_alu_1_result), .shamt(PC_no_condition[12:8]));  // open: Result_2
  Adder #(.width(32)) adder_2 (.a(shifter_1_out), .b(PC_4), .out(PC_condition));  // open: cin, cout
  Multiplexer #(.select(1), .width(1), .disabled("Z"), .enable("false")) multiplexer_14 (
    .in0(and_6_out), .in1(1'b0), .out(multiplexer_14_out), .sel(not_7_out));
  and and_6 (and_6_out, \无条件分支 , CLK);
  not not_6 (not_6_out, mips_alu_1_equal);
  Counter #(.width(16), .max('hffff), .ongoal("wrap"), .trigger("rising"), .behavior("old")) counter_2 (
    .count(1'b1), .Q(\无条件分支数 ), .clk(multiplexer_14_out), .clr(RST));  // open: load, D, carry, preset
  not not_7 (not_7_out, not_8_out);
  not not_8 (not_8_out, CLK);
  or or_7 (\条件分支 , and_5_out, and_8_out, and_7_out);
  and and_7 (and_7_out, mips_alu_1_equal, id_ex_l_1_beq_2);
  and and_8 (and_8_out, id_ex_l_1_bne_2, not_6_out);
  or or_8 (Bubble, \无条件分支 , \条件分支 );
  or or_9 (or_9_out, RST, CLK);
  Counter #(.width(16), .max('hffff), .ongoal("wrap"), .trigger("rising"), .behavior("old")) counter_3 (
    .count(1'b1), .Q(\条件分支成功数 ), .clk(multiplexer_15_out), .clr(RST));  // open: load, D, carry, preset
  Multiplexer #(.select(1), .width(1), .disabled("Z"), .enable("false")) multiplexer_15 (
    .in0(and_9_out), .in1(1'b0), .out(multiplexer_15_out), .sel(not_9_out));
  and and_9 (and_9_out, \条件分支 , CLK);
  Multiplexer #(.select(1), .width(5), .disabled("Z"), .enable("false")) multiplexer_16 (
    .in0(id_ex_l_1_ir_2[20:16]), .in1(id_ex_l_1_ir_2[15:11]), .out(multiplexer_16_out),
    .sel(id_ex_l_1_regdst_2));
  Multiplexer #(.select(1), .width(5), .disabled("Z"), .enable("false")) multiplexer_17 (
    .in0(multiplexer_16_out), .in1({5{1'b1}}), .out(EX_WriteReg_num), .sel(id_ex_l_1_jal_2));
  EX_MEM_l ex_mem_l_1 (
    .CLK(or_9_out), .\同步清零_气泡_高电平有效 (RstFlow), .\使能端_低电平有效 (SEL), .PC(EX_PC),
    .MemToReg(id_ex_l_1_memtoreg_2), .MemWrite(id_ex_l_1_memwrite_2), .RegWrite(EX_RegWrite),
    .SB(id_ex_l_1_sb_2), .RegDst(id_ex_l_1_regdst_2), .IR(id_ex_l_1_ir_2), .R2(id_ex_l_1_r2_2),
    .JAL(id_ex_l_1_jal_2), .PC_2(MEM_PC), .MemToReg_2(ex_mem_l_1_memtoreg_2),
    .MemWrite_2(ex_mem_l_1_memwrite_2), .RegWrite_2(MEM_RegWrite), .SB_2(ex_mem_l_1_sb_2),
    .RegDst_2(ex_mem_l_1_regdst_2), .IR_2(ex_mem_l_1_ir_2), .R2_2(ex_mem_l_1_r2_2), .JAL_2(ex_mem_l_1_jal_2),
    .ALU(mips_alu_1_result), .ALU_2(ex_mem_l_1_alu_2), .PC_4(PC_4), .PC_4_2(ex_mem_l_1_pc_4_2),
    .Syscall(id_ex_l_1_syscall_2), .Syscall_2(ex_mem_l_1_syscall_2));
  not not_9 (not_9_out, not_10_out);
  not not_10 (not_10_out, CLK);
  Multiplexer #(.select(1), .width(32), .disabled("Z"), .enable("false")) multiplexer_18 (
    .in0(ex_mem_l_1_r2_2), .in1(multiplexer_19_out), .out(multiplexer_18_out), .sel(ex_mem_l_1_sb_2));
  Multiplexer #(.select(2), .width(32), .disabled("Z"), .enable("false")) multiplexer_19 (
    .in0({ram_1_data[31:8], ex_mem_l_1_r2_2[7:0]}),
    .in1({ram_1_data[31:16], ex_mem_l_1_r2_2[7:0], ram_1_data[7:0]}),
    .in2({ram_1_data[31:24], ex_mem_l_1_r2_2[7:0], ram_1_data[15:0]}),
    .in3({ex_mem_l_1_r2_2[7:0], ram_1_data[23:0]}), .out(multiplexer_19_out), .sel(ex_mem_l_1_alu_2[1:0]));
  not not_11 (not_11_out, final_IsStop);
  Multiplexer #(.select(1), .width(1), .disabled("Z"), .enable("false")) multiplexer_20 (
    .in0(and_11_out), .in1(1'b0), .out(multiplexer_20_out), .sel(not_13_out));
  and and_10 (and_10_out, not_11_out, IsRelated);
  and and_11 (and_11_out, and_10_out, CLK);
  Multiplexer #(.select(1), .width(5), .disabled("Z"), .enable("false")) multiplexer_21 (
    .in0(ex_mem_l_1_ir_2[20:16]), .in1(ex_mem_l_1_ir_2[15:11]), .out(multiplexer_21_out),
    .sel(ex_mem_l_1_regdst_2));
  RAM #(.addrWidth(10), .dataWidth(32), .bus("separate"), .Select("high")) ram_1 (
    .addr(ex_mem_l_1_alu_2[11:2]), .din(multiplexer_18_out), .data(ram_1_data), .str(ex_mem_l_1_memwrite_2),
    .clk(CLK), .clr(RST));  // open: sel, ld
  Counter #(.width(16), .max('hffff), .ongoal("wrap"), .trigger("rising"), .behavior("old")) counter_4 (
    .count(1'b1), .Q(\插入气泡数 ), .clk(multiplexer_20_out), .clr(RST));  // open: load, D, carry, preset
  not not_12 (not_12_out, CLK);
  not not_13 (not_13_out, not_12_out);
  Multiplexer #(.select(1), .width(5), .disabled("Z"), .enable("false")) multiplexer_22 (
    .in0(multiplexer_21_out), .in1({5{1'b1}}), .out(MEM_WriteReg_num), .sel(ex_mem_l_1_jal_2));
  or or_10 (or_10_out, RST, CLK);
  MEM_WB_l mem_wb_l_1 (
    .CLK(or_10_out), .\同步清零_气泡_高电平有效 (RstFlow), .\使能端_低电平有效 (SEL), .PC(MEM_PC),
    .MemToReg(ex_mem_l_1_memtoreg_2), .PC_2(WB_PC), .MemToReg_2(mem_wb_l_1_memtoreg_2),
    .RegWrite(MEM_RegWrite), .RegWrite_2(RegWrite), .RegDst(ex_mem_l_1_regdst_2), .IR(ex_mem_l_1_ir_2),
    .MD(ram_1_data), .RegDst_2(RegDst), .IR_2({mem_wb_l_1_ir_2[31:21], WB_rt, WB_rd, mem_wb_l_1_ir_2[10:0]}),
    .MD_2(mem_wb_l_1_md_2), .JAL(ex_mem_l_1_jal_2), .JAL_2(JAL), .ALU(ex_mem_l_1_alu_2),
    .ALU_2(mem_wb_l_1_alu_2), .PC_4(ex_mem_l_1_pc_4_2), .PC_4_2(Jal_PC_4), .Syscall(ex_mem_l_1_syscall_2),
    .Syscall_2(final_IsStop));
  Multiplexer #(.select(1), .width(32), .disabled("Z"), .enable("false")) multiplexer_23 (
    .in0(mem_wb_l_1_alu_2), .in1(mem_wb_l_1_md_2), .out(multiplexer_23_out), .sel(mem_wb_l_1_memtoreg_2));

  // Other names for the same wires on the sheet: PC_no_condition[31:28] = PC_4[31:28]; stall = IsRelated

  // Notes on the sheet:
  //   中断源
  //   中断等待指示
  //   指令存储器
  //   contents of rom_1 (hex, n*v repeats v):
  //   20100001 109fc0 139fc3 8021 2012000c 24160003 26100001 3210000f 20080008 20090001 139900 2709825
  //   132020 20020022 c 1094022 1500fff9 22100001 2018000f 2188024 108700 20080008 20090001 139902 2709825
  //   132021 20020022 c 1094022 1500fff9 108702 2c9b022 12c00001 8000c06 4020 1084027 84400 3508ffff
  //   132021 20020022 c 2002000a c
  //   数码管输出
  //   PC+4
  //   IR
  //   PC
  //   指令字
  //   OP
  //   Func
  //   rs
  //   rt
  //   rd
  //   R1_Used
  //   R2_Used
  //   Imm26
  //   Bubble统计的是分支相关数，IsRelated统计的是数据相关数，即插入的气泡数
  //   流水调试日志用
  //   IR
  //   PC
  //   rt
  //   rd
  //   MemWrite
  //   SB
  //   IR
  //   PC
  //   R2
  //   ALU
  //   rt
  //   rd
  //   MemToReg
  //   rt
  //   rd
endmodule
module \重定向流水线  (
  output RegWrite,
  output MemWrite,
  output [31:0] IF_PC,
  output [31:0] ID_PC,
  output [31:0] EX_PC,
  output [31:0] MEM_PC,
  output [31:0] WB_PC,
  output [31:0] RDin,
  output [31:0] MDin
);

  wire and_1_out, and_3_out, and_4_out, and_5_out, and_6_out, and_7_out, and_8_out, and_9_out, and_10_out,
       and_11_out, and_12_out, Bubble, CLK, comparator_1_eq, comparator_2_eq, comparator_2_lt,
       ex_mem_l_1_jal_2, ex_mem_l_1_memtoreg_2, ex_mem_l_1_regdst_2, ex_mem_l_1_sb_2, ex_mem_l_1_syscall_2,
       EX_RegWrite, EX_Syscall, final_IsStop, final_IsStop_t, Go, id_ex_l_1_alusrcb_2, id_ex_l_1_beq_2,
       id_ex_l_1_blez_2, id_ex_l_1_bne_2, id_ex_l_1_jal_2, id_ex_l_1_jr_2, id_ex_l_1_memtoreg_2,
       id_ex_l_1_memwrite_2, id_ex_l_1_regdst_2, id_ex_l_1_sb_2, IR1, IR2, IR3, IsRelated, IsStop, JAL,
       Load_Use, MEM_RegWrite, mips_alu_1_equal, multiplexer_4_out, multiplexer_17_out, multiplexer_20_out,
       multiplexer_21_out, multiplexer_26_out, multiplexer_30_out, not_1_out, not_2_out, not_3_out,
       not_4_out, not_5_out, not_6_out, not_7_out, not_8_out, not_9_out, not_10_out, not_11_out, not_12_out,
       not_13_out, not_14_out, not_15_out, or_1_out, or_2_out, or_3_out, or_4_out, or_5_out, or_6_out,
       or_9_out, or_10_out, or_11_out, RegDst, register_3_q, RST, RstFlow, SEL, SignedExt, stop, Syscall, W1,
       W2, W3, WB_MemToReg, \单周期硬布线控制器_1_alu_src , \单周期硬布线控制器_1_beq , \单周期硬布线控制器_1_blez , \单周期硬布线控制器_1_bne ,
       \单周期硬布线控制器_1_jal , \单周期硬布线控制器_1_jmp , \单周期硬布线控制器_1_jr , \单周期硬布线控制器_1_memtoreg ,
       \单周期硬布线控制器_1_memwrite , \单周期硬布线控制器_1_regdst , \单周期硬布线控制器_1_regwrite , \单周期硬布线控制器_1_sb ,
       \单周期硬布线控制器_1_signedext , \无条件分支 , \条件分支 , \源寄存器使用情况_1_r1_used , \源寄存器使用情况_1_r2_used ,
       \点击此键_先设置同步清零信号_out ;
  wire [1:0] EX_Forward_R1, EX_Forward_R2, ID_Forward_R1, ID_Forward_R2, \数据相关检测_1_r1_ex_relate ,
       \数据相关检测_1_r2_ex_relate ;
  wire [3:0] id_ex_l_1_aluop_2, \单周期硬布线控制器_1_alu_op ;
  wire [4:0] EX_WriteReg_num, MEM_WriteReg_num, multiplexer_11_out, multiplexer_12_out, multiplexer_22_out,
       multiplexer_27_out, R1_Relate, R2_Relate, WB_rd, WB_rt;
  wire [5:0] EX_OP, Func, OP;
  wire [15:0] \LoadUse次数 , \总周期数 , \插入气泡数 , \无条件分支数 , \条件分支成功数 ;
  wire [25:0] id_ex_l_1_ir_2;
  wire [25:6] if_id_l_1_ir_2;
  wire [27:2] PC_no_condition;
  wire [31:0] a0, adder_1_out, bit_extender_1_out, bit_extender_2_out, ex_mem_l_1_ir_2, ex_mem_l_1_pc_4_2,
       ex_mem_l_1_r2_2, if_id_l_1_pc_4_2, Jal_PC_4, LedData, MEM_ALU, mem_wb_l_1_ir_2, mips_alu_1_result,
       multiplexer_1_out, multiplexer_2_out, multiplexer_3_out, multiplexer_6_out, multiplexer_15_out,
       multiplexer_18_out, multiplexer_19_out, multiplexer_25_out, multiplexer_29_out, PC_4, PC_condition,
       R1_Old, R1_Redirect, R2_Old, R2_Redirect, ram_1_data, rom_1_data, shifter_1_out, v0, WB_ALU,
       WB_ReadData;

  Multiplexer #(.select(1), .width(32), .disabled("Z"), .enable("false")) multiplexer_1 (
    .in0({PC_4[31:28], PC_no_condition, 2'b00}), .in1(R1_Redirect), .out(multiplexer_1_out),
    .sel(id_ex_l_1_jr_2));
  Button \u_点击此键_先设置同步清零信号  (.out(\点击此键_先设置同步清零信号_out ));
  Register #(.width(1), .trigger("falling"), .Select("low")) register_1 (
    .D(1'b0), .Q(RstFlow), .clk(RST), .preset(\点击此键_先设置同步清零信号_out ));  // open: en, clr, cs
  Multiplexer #(.select(2), .width(32), .disabled("Z"), .enable("false")) multiplexer_2 (
    .in0(adder_1_out), .in1(PC_condition), .in2(multiplexer_1_out), .out(multiplexer_2_out),
    .sel({\无条件分支 , \条件分支 }));  // open: in3
  Comparator #(.width(32), .mode("twosComplement")) comparator_1 (
    .a(R1_Redirect), .b(32'h22), .eq(comparator_1_eq));  // open: gt, lt
  not not_1 (not_1_out, comparator_1_eq);
  Register #(.width(32), .trigger("rising"), .Select("low")) PC (
    .D(multiplexer_3_out), .en(not_2_out), .Q(IF_PC), .clk(CLK), .clr(RST));
  Multiplexer #(.select(1), .width(32), .disabled("Z"), .enable("false")) multiplexer_3 (
    .in0(multiplexer_2_out), .in1(IF_PC), .out(multiplexer_3_out), .sel(stop));
  not not_2 (not_2_out, Load_Use);
  and and_1 (and_1_out, EX_Syscall, comparator_1_eq);
  and and_2 (IsStop, not_1_out, EX_Syscall);
  xor xor_1 (stop, final_IsStop_t, register_3_q);
  Button \u_再总复位  (.out(RST));
  Button _1 (.out(IR1));
  Button _2 (.out(IR2));
  Button _3 (.out(IR3));
  Register #(.width(32), .trigger("rising"), .Select("low")) register_2 (
    .D(R2_Redirect), .Q(LedData), .clk(and_1_out), .clr(RST));  // open: en
  and and_3 (and_3_out, final_IsStop_t, Go);
  Register #(.width(1), .trigger("rising"), .Select("low")) register_3 (
    .D(1'b0), .Q(register_3_q), .clk(CLK), .clr(RST), .preset(and_3_out));  // open: en, cs
  Button \u_继续运行  (.out(Go));
  LED #(.active("true")) led_1 (.in(W1));
  LED #(.active("true")) led_2 (.in(W2));
  LED #(.active("true")) led_3 (.in(W3));
  Adder #(.width(32)) adder_1 (.a(IF_PC), .b(32'h4), .out(adder_1_out));  // open: cin, cout
  Multiplexer #(.select(1), .width(1), .disabled("Z"), .enable("false")) multiplexer_4 (
    .in0(final_IsStop_t), .in1(1'b0), .out(multiplexer_4_out), .sel(register_3_q));
  Multiplexer #(.select(1), .width(1), .disabled("Z"), .enable("false")) multiplexer_5 (
    .in0(multiplexer_4_out), .in1(1'b0), .out(SEL), .sel(or_1_out));
  Hex_Digit_Display hex_digit_display_1 (.value(LedData[27:24]));  // open: dp
  Hex_Digit_Display hex_digit_display_2 (.value(LedData[31:28]));  // open: dp
  \源寄存器使用情况  \u_源寄存器使用情况_1  (.OP(OP), .FUN(Func), .R1_Used(\源寄存器使用情况_1_r1_used ), .R2_Used(\源寄存器使用情况_1_r2_used ));
  ROM #(.addrWidth(10), .dataWidth(32), .Select("high")) rom_1 (.addr(IF_PC[11:2]), .data(rom_1_data));
  or or_1 (or_1_out, Bubble, RstFlow);
  or or_2 (or_2_out, SEL, Load_Use);
  Hex_Digit_Display hex_digit_display_3 (.value(LedData[23:20]));  // open: dp
  Hex_Digit_Display hex_digit_display_4 (.value(LedData[19:16]));  // open: dp
  IF_ID_l if_id_l_1 (
    .CLK(or_3_out), .\同步清零_气泡_高电平有效 (or_1_out), .\使能端_低电平有效 (or_2_out), .PC(IF_PC), .PC_2(ID_PC),
    .IR(rom_1_data), .IR_2({OP, if_id_l_1_ir_2, Func}), .PC_4(adder_1_out), .PC_4_2(if_id_l_1_pc_4_2));  // open: MISS, MISS_2, JMP_Pre, JMP_Pre_2, State_Now, State_Now_2, Row_Pre, Row_Pre_2
  or or_3 (or_3_out, RST, CLK);
  Hex_Digit_Display hex_digit_display_5 (.value(LedData[15:12]));  // open: dp
  Hex_Digit_Display hex_digit_display_6 (.value(LedData[11:8]));  // open: dp
  Clock #(.highDuration(1), .lowDuration(1)) clock_1 (.out(CLK));
  \数据相关检测  \u_数据相关检测_1  (
    .R1_Used(\源寄存器使用情况_1_r1_used ), .R2_Used(\源寄存器使用情况_1_r2_used ), .R1_num(R1_Relate), .R2_num(R2_Relate),
    .EX_WriteReg_num(EX_WriteReg_num), .EX_RegWrite(EX_RegWrite), .MEM_WriteReg_num(MEM_WriteReg_num),
    .MEM_RegWrite(MEM_RegWrite), .Relate(IsRelated), .EX_OP(EX_OP), .Load_Use(Load_Use),
    .R1_EX_Relate(\数据相关检测_1_r1_ex_relate [0]), .R2_EX_Relate(\数据相关检测_1_r2_ex_relate [0]),
    .R1_MEM_Relate(\数据相关检测_1_r1_ex_relate [1]), .R2_MEM_Relate(\数据相关检测_1_r2_ex_relate [1]));
  Hex_Digit_Display hex_digit_display_7 (.value(LedData[3:0]));  // open: dp
  Hex_Digit_Display hex_digit_display_8 (.value(LedData[7:4]));  // open: dp
  Multiplexer #(.select(1), .width(32), .disabled("Z"), .enable("false")) multiplexer_6 (
    .in0(WB_ALU), .in1(WB_ReadData), .out(multiplexer_6_out), .sel(WB_MemToReg));
  Multiplexer #(.select(2), .width(32), .disabled("Z"), .enable("false")) multiplexer_7 (
    .in0(R1_Old), .in1(MEM_ALU), .in2(multiplexer_6_out), .in3(MEM_ALU), .out(R1_Redirect),
    .sel(EX_Forward_R1));
  Multiplexer #(.select(1), .width(2), .disabled("Z"), .enable("false")) multiplexer_8 (
    .in0(\数据相关检测_1_r2_ex_relate ), .in1(2'b00), .out(ID_Forward_R2), .sel(Load_Use));
  \单周期硬布线控制器  \u_单周期硬布线控制器_1  (
    .Func(Func), .OP(OP), .ALU_OP(\单周期硬布线控制器_1_alu_op ), .MemToReg(\单周期硬布线控制器_1_memtoreg ),
    .MemWrite(\单周期硬布线控制器_1_memwrite ), .ALU_SRC(\单周期硬布线控制器_1_alu_src ), .RegWrite(\单周期硬布线控制器_1_regwrite ),
    .SysCALL(Syscall), .SignedExt(\单周期硬布线控制器_1_signedext ), .RegDst(\单周期硬布线控制器_1_regdst ),
    .JR(\单周期硬布线控制器_1_jr ), .JMP(\单周期硬布线控制器_1_jmp ), .Beq(\单周期硬布线控制器_1_beq ), .JAL(\单周期硬布线控制器_1_jal ),
    .Bne(\单周期硬布线控制器_1_bne ), .BLEZ(\单周期硬布线控制器_1_blez ), .SB(\单周期硬布线控制器_1_sb ));
  Multiplexer #(.select(1), .width(5), .disabled("Z"), .enable("false")) multiplexer_9 (
    .in0(if_id_l_1_ir_2[25:21]), .in1(5'b00010), .out(R1_Relate), .sel(Syscall));
  Multiplexer #(.select(1), .width(5), .disabled("Z"), .enable("false")) multiplexer_10 (
    .in0(if_id_l_1_ir_2[20:16]), .in1(5'b00100), .out(R2_Relate), .sel(Syscall));
  Multiplexer #(.select(1), .width(5), .disabled("Z"), .enable("false")) multiplexer_11 (
    .in0(WB_rt), .in1(WB_rd), .out(multiplexer_11_out), .sel(RegDst));
  Multiplexer #(.select(1), .width(5), .disabled("Z"), .enable("false")) multiplexer_12 (
    .in0(multiplexer_11_out), .in1({5{1'b1}}), .out(multiplexer_12_out), .sel(JAL));
  Multiplexer #(.select(1), .width(32), .disabled("Z"), .enable("false")) multiplexer_13 (
    .in0(multiplexer_29_out), .in1(Jal_PC_4), .out(RDin), .sel(JAL));
  // Probe on \总周期数 
  // Probe on \无条件分支数 
  // Probe on \条件分支成功数 
  // Probe on \插入气泡数 
  // Probe on \LoadUse次数 
  // Probe on IF_PC[11:0]
  MIPS_Regifile mips_regifile_1 (
    .Din(RDin), .Clk(CLK), .R1(v0), .R2(a0), .WE(RegWrite), .W_num(multiplexer_12_out), .R1_num(R1_Relate),
    .R2_num(R2_Relate));
  // Probe on ID_PC[11:0]
  // Probe on EX_PC[11:0]
  Multiplexer #(.select(1), .width(2), .disabled("Z"), .enable("false")) multiplexer_14 (
    .in0(\数据相关检测_1_r1_ex_relate ), .in1(2'b00), .out(ID_Forward_R1), .sel(Load_Use));
  or or_4 (or_4_out, Bubble, Load_Use, RstFlow);
  // Probe on WB_PC[11:0]
  // Probe on MEM_PC[11:0]
  or or_5 (or_5_out, RST, CLK);
  Multiplexer #(.select(1), .width(32), .disabled("Z"), .enable("false")) multiplexer_15 (
    .in0(WB_ALU), .in1(WB_ReadData), .out(multiplexer_15_out), .sel(WB_MemToReg));
  ID_EX_l id_ex_l_1 (
    .CLK(or_5_out), .\同步清零_气泡_高电平有效 (or_4_out), .\使能端_低电平有效 (SEL), .PC(ID_PC), .R1(v0),
    .BLEZ(\单周期硬布线控制器_1_blez ), .SignedExt(\单周期硬布线控制器_1_signedext ), .MemToReg(\单周期硬布线控制器_1_memtoreg ),
    .MemWrite(\单周期硬布线控制器_1_memwrite ), .BEQ(\单周期硬布线控制器_1_beq ), .Syscall(Syscall),
    .RegWrite(\单周期硬布线控制器_1_regwrite ), .SB(\单周期硬布线控制器_1_sb ), .BNE(\单周期硬布线控制器_1_bne ),
    .RegDst(\单周期硬布线控制器_1_regdst ), .IR({OP, if_id_l_1_ir_2, Func}), .R2(a0), .AluSrcB(\单周期硬布线控制器_1_alu_src ),
    .JR(\单周期硬布线控制器_1_jr ), .JAL(\单周期硬布线控制器_1_jal ), .AluOP(\单周期硬布线控制器_1_alu_op ),
    .Imm26({if_id_l_1_ir_2, Func}), .JMP(\单周期硬布线控制器_1_jmp ), .PC_2(EX_PC), .R1_2(R1_Old),
    .BLEZ_2(id_ex_l_1_blez_2), .SignedExt_2(SignedExt), .MemToReg_2(id_ex_l_1_memtoreg_2),
    .MemWrite_2(id_ex_l_1_memwrite_2), .BEQ_2(id_ex_l_1_beq_2), .Syscall_2(EX_Syscall),
    .RegWrite_2(EX_RegWrite), .SB_2(id_ex_l_1_sb_2), .BNE_2(id_ex_l_1_bne_2), .RegDst_2(id_ex_l_1_regdst_2),
    .IR_2({EX_OP, id_ex_l_1_ir_2}), .R2_2(R2_Old), .AluSrcB_2(id_ex_l_1_alusrcb_2), .JR_2(id_ex_l_1_jr_2),
    .JAL_2(id_ex_l_1_jal_2), .AluOP_2(id_ex_l_1_aluop_2), .Imm26_2(PC_no_condition), .JMP_2(\无条件分支 ),
    .PC_4(if_id_l_1_pc_4_2), .PC_4_2(PC_4), .Forwarding_R1(ID_Forward_R1), .Forwarding_R1_2(EX_Forward_R1),
    .Forwarding_R2(ID_Forward_R2), .Forwarding_R2_2(EX_Forward_R2));  // open: MISS, MISS_2, JMP_Pre, JMP_Pre_2, State_Now, State_Now_2, Row_Pre, Row_Pre_2
  and and_4 (and_4_out, not_3_out, CLK);
  not not_3 (not_3_out, stop);
  Multiplexer #(.select(2), .width(32), .disabled("Z"), .enable("false")) multiplexer_16 (
    .in0(R2_Old), .in1(MEM_ALU), .in2(multiplexer_15_out), .in3(MEM_ALU), .out(R2_Redirect),
    .sel(EX_Forward_R2));
  assign bit_extender_1_out = {{16{1'b0}}, PC_no_condition[17:2]};  // Bit_Extender bit_extender_1
  assign bit_extender_2_out = {{16{PC_no_condition[17]}}, PC_no_condition[17:2]};  // Bit_Extender bit_extender_2
  Counter #(.width(16), .max('hffff), .ongoal("wrap"), .trigger("rising"), .behavior("old")) counter_1 (
    .count(1'b1), .Q(\总周期数 ), .clk(multiplexer_17_out), .clr(RST));  // open: load, D, carry, preset
  Multiplexer #(.select(1), .width(1), .disabled("Z"), .enable("false")) multiplexer_17 (
    .in0(and_4_out), .in1(1'b0), .out(multiplexer_17_out), .sel(not_4_out));
  not not_4 (not_4_out, not_5_out);
  not not_5 (not_5_out, CLK);
  Comparator #(.width(32), .mode("twosComplement")) comparator_2 (
    .a(R1_Redirect), .b({32{1'b0}}), .eq(comparator_2_eq), .lt(comparator_2_lt));  // open: gt
  Multiplexer #(.select(1), .width(32), .disabled("Z"), .enable("false")) multiplexer_18 (
    .in0(bit_extender_1_out), .in1(bit_extender_2_out), .out(multiplexer_18_out), .sel(SignedExt));
  or or_6 (or_6_out, comparator_2_eq, comparator_2_lt);
  Multiplexer #(.select(1), .width(32), .disabled("Z"), .enable("false")) multiplexer_19 (
    .in0(R2_Redirect), .in1(multiplexer_18_out), .out(multiplexer_19_out), .sel(id_ex_l_1_alusrcb_2));
  Shifter #(.width(32), .shift("ll")) shifter_1 (.in(multiplexer_18_out), .\dist (5'b00010), .out(shifter_1_out));
  and and_5 (and_5_out, or_6_out, id_ex_l_1_blez_2);
  MIPS_ALU mips_alu_1 (
    .X(R1_Redirect), .Y(multiplexer_19_out), .AluOP(id_ex_l_1_aluop_2), .Equal(mips_alu_1_equal),
    .Result(mips_alu_1_result), .shamt(PC_no_condition[12:8]));  // open: Result_2
  Adder #(.width(32)) adder_2 (.a(shifter_1_out), .b(PC_4), .out(PC_condition));  // open: cin, cout
  Multiplexer #(.select(1), .width(1), .disabled("Z"), .enable("false")) multiplexer_20 (
    .in0(and_6_out), .in1(1'b0), .out(multiplexer_20_out), .sel(not_7_out));
  and and_6 (and_6_out, \无条件分支 , CLK);
  not not_6 (not_6_out, mips_alu_1_equal);
  Counter #(.width(16), .max('hffff), .ongoal("wrap"), .trigger("rising"), .behavior("old")) counter_2 (
    .count(1'b1), .Q(\无条件分支数 ), .clk(multiplexer_20_out), .clr(RST));  // open: load, D, carry, preset
  not not_7 (not_7_out, not_8_out);
  not not_8 (not_8_out, CLK);
  or or_7 (\条件分支 , and_5_out, and_8_out, and_7_out);
  and and_7 (and_7_out, mips_alu_1_equal, id_ex_l_1_beq_2);
  and and_8 (and_8_out, id_ex_l_1_bne_2, not_6_out);
  or or_8 (Bubble, \无条件分支 , \条件分支 );
  or or_9 (or_9_out, RST, CLK);
  Counter #(.width(16), .max('hffff), .ongoal("wrap"), .trigger("rising"), .behavior("old")) counter_3 (
    .count(1'b1), .Q(\条件分支成功数 ), .clk(multiplexer_21_out), .clr(RST));  // open: load, D, carry, preset
  Multiplexer #(.select(1), .width(1), .disabled("Z"), .enable("false")) multiplexer_21 (
    .in0(and_9_out), .in1(1'b0), .out(multiplexer_21_out), .sel(not_9_out));
  and and_9 (and_9_out, \条件分支 , CLK);
  Multiplexer #(.select(1), .width(5), .disabled("Z"), .enable("false")) multiplexer_22 (
    .in0(id_ex_l_1_ir_2[20:16]), .in1(id_ex_l_1_ir_2[15:11]), .out(multiplexer_22_out),
    .sel(id_ex_l_1_regdst_2));
  Multiplexer #(.select(1), .width(5), .disabled("Z"), .enable("false")) multiplexer_23 (
    .in0(multiplexer_22_out), .in1({5{1'b1}}), .out(EX_WriteReg_num), .sel(id_ex_l_1_jal_2));
  EX_MEM_l ex_mem_l_1 (
    .CLK(or_9_out), .\同步清零_气泡_高电平有效 (RstFlow), .\使能端_低电平有效 (SEL), .PC(EX_PC),
    .MemToReg(id_ex_l_1_memtoreg_2), .MemWrite(id_ex_l_1_memwrite_2), .RegWrite(EX_RegWrite),
    .SB(id_ex_l_1_sb_2), .RegDst(id_ex_l_1_regdst_2), .IR({EX_OP, id_ex_l_1_ir_2}), .R2(R2_Redirect),
    .JAL(id_ex_l_1_jal_2), .PC_2(MEM_PC), .MemToReg_2(ex_mem_l_1_memtoreg_2), .MemWrite_2(MemWrite),
    .RegWrite_2(MEM_RegWrite), .SB_2(ex_mem_l_1_sb_2), .RegDst_2(ex_mem_l_1_regdst_2),
    .IR_2(ex_mem_l_1_ir_2), .R2_2(ex_mem_l_1_r2_2), .JAL_2(ex_mem_l_1_jal_2), .ALU(mips_alu_1_result),
    .ALU_2(MEM_ALU), .PC_4(PC_4), .PC_4_2(ex_mem_l_1_pc_4_2), .Syscall(IsStop),
    .Syscall_2(ex_mem_l_1_syscall_2));
  not not_9 (not_9_out, not_10_out);
  not not_10 (not_10_out, CLK);
  Multiplexer #(.select(1), .width(32), .disabled("Z"), .enable("false")) multiplexer_24 (
    .in0(ex_mem_l_1_r2_2), .in1(multiplexer_25_out), .out(MDin), .sel(ex_mem_l_1_sb_2));
  Multiplexer #(.select(2), .width(32), .disabled("Z"), .enable("false")) multiplexer_25 (
    .in0({ram_1_data[31:8], ex_mem_l_1_r2_2[7:0]}),
    .in1({ram_1_data[31:16], ex_mem_l_1_r2_2[7:0], ram_1_data[7:0]}),
    .in2({ram_1_data[31:24], ex_mem_l_1_r2_2[7:0], ram_1_data[15:0]}),
    .in3({ex_mem_l_1_r2_2[7:0], ram_1_data[23:0]}), .out(multiplexer_25_out), .sel(MEM_ALU[1:0]));
  not not_11 (not_11_out, final_IsStop);
  or or_10 (or_10_out, Bubble, Load_Use);
  Multiplexer #(.select(1), .width(1), .disabled("Z"), .enable("false")) multiplexer_26 (
    .in0(and_11_out), .in1(1'b0), .out(multiplexer_26_out), .sel(not_13_out));
  and and_10 (and_10_out, not_11_out, or_10_out);
  and and_11 (and_11_out, and_10_out, CLK);
  Multiplexer #(.select(1), .width(5), .disabled("Z"), .enable("false")) multiplexer_27 (
    .in0(ex_mem_l_1_ir_2[20:16]), .in1(ex_mem_l_1_ir_2[15:11]), .out(multiplexer_27_out),
    .sel(ex_mem_l_1_regdst_2));
  RAM #(.addrWidth(10), .dataWidth(32), .bus("separate"), .Select("high")) ram_1 (
    .addr(MEM_ALU[11:2]), .din(MDin), .data(ram_1_data), .str(MemWrite), .clk(CLK), .clr(RST));  // open: sel, ld
  Counter #(.width(16), .max('hffff), .ongoal("wrap"), .trigger("rising"), .behavior("old")) counter_4 (
    .count(1'b1), .Q(\插入气泡数 ), .clk(multiplexer_26_out), .clr(RST));  // open: load, D, carry, preset
  not not_12 (not_12_out, CLK);
  not not_13 (not_13_out, not_12_out);
  Multiplexer #(.select(1), .width(5), .disabled("Z"), .enable("false")) multiplexer_28 (
    .in0(multiplexer_27_out), .in1({5{1'b1}}), .out(MEM_WriteReg_num), .sel(ex_mem_l_1_jal_2));
  or or_11 (or_11_out, RST, CLK);
  MEM_WB_l mem_wb_l_1 (
    .CLK(or_11_out), .\同步清零_气泡_高电平有效 (RstFlow), .\使能端_低电平有效 (SEL), .PC(MEM_PC),
    .MemToReg(ex_mem_l_1_memtoreg_2), .PC_2(WB_PC), .MemToReg_2(WB_MemToReg), .RegWrite(MEM_RegWrite),
    .RegWrite_2(RegWrite), .RegDst(ex_mem_l_1_regdst_2), .IR(ex_mem_l_1_ir_2), .MD(ram_1_data),
    .RegDst_2(RegDst), .IR_2({mem_wb_l_1_ir_2[31:21], WB_rt, WB_rd, mem_wb_l_1_ir_2[10:0]}),
    .MD_2(WB_ReadData), .JAL(ex_mem_l_1_jal_2), .JAL_2(JAL), .ALU(MEM_ALU), .ALU_2(WB_ALU),
    .PC_4(ex_mem_l_1_pc_4_2), .PC_4_2(Jal_PC_4), .Syscall(ex_mem_l_1_syscall_2), .Syscall_2(final_IsStop));
  and and_12 (and_12_out, Load_Use, CLK);
  Multiplexer #(.select(1), .width(32), .disabled("Z"), .enable("false")) multiplexer_29 (
    .in0(WB_ALU), .in1(WB_ReadData), .out(multiplexer_29_out), .sel(WB_MemToReg));
  Counter #(.width(16), .max('hffff), .ongoal("wrap"), .trigger("rising"), .behavior("old")) counter_5 (
    .count(1'b1), .Q(\LoadUse次数 ), .clk(multiplexer_30_out), .clr(RST));  // open: load, D, carry, preset
  Multiplexer #(.select(1), .width(1), .disabled("Z"), .enable("false")) multiplexer_30 (
    .in0(and_12_out), .in1(1'b0), .out(multiplexer_30_out), .sel(not_14_out));
  not not_14 (not_14_out, not_15_out);
  not not_15 (not_15_out, CLK);

  // Other names for the same wires on the sheet: PC_no_condition[31:28] = PC_4[31:28]; RS[31:0] = R1_Redirect

  // Notes on the sheet:
  //   中断源
  //   中断等待指示
  //   指令存储器
  //   R1_Used
  //   R2_Used
  //   contents of rom_1 (hex, n*v repeats v):
  //   20110001 8000c05 20110001 20120002 20130003 8000c09 20110001 20120002 20130003 8000c0d 20110001
  //   20120002 20130003 8000c11 20110001 20120002 20130003 c000cb8 20100001 20110001 118fc0 112020
  //   20020022 c 118882 12200001 8000c15 112020 20020022 c 20110001 118880 112020 20020022 c 12200001
  //   8000c1f 20110001 118fc0 112020 20020022 c 1188c3 112020 20020022 c 118903 112020 20020022 c 118903
  //   112020 20020022 c 118903 112020 20020022 c 118903 112020 20020022 c 118903 112020 20020022 c 118903
  //   112020 20020022 c 118903 112020 20020022 c 20100001 109fc0 139fc3 8021 2012000c 24160003 26100001
  //   3210000f 20080008 20090001 139900 2709825 132020 20020022 c 1094022 1500fff9 22100001 2018000f
  //   2188024 108700 20080008 20090001 139902 2709825 132021 20020022 c 1094022 1500fff9 108702 2c9b022
  //   12c00001 8000c50 4020 1084027 84400 3508ffff 82021 20020022 c 2010ffff 20110000 ae300000 22100001
  //   22310004 ae300000 22100001 22310004 ae300000 22100001 22310004 ae300000 22100001 22310004 ae300000
  //   22100001 22310004 ae300000 22100001 22310004 ae300000 22100001 22310004 ae300000 22100001 22310004
  //   ae300000 22100001 22310004 ae300000 22100001 22310004 ae300000 22100001 22310004 ae300000 22100001
  //   22310004 ae300000 22100001 22310004 ae300000 22100001 22310004 ae300000 22100001 22310004 ae300000
  //   22100001 22310004 22100001 8020 2011003c 8e130000 8e340000 274402a 11000002 ae330000 ae140000
  //   2231fffc 1611fff8 102020 20020022 c 22100004 2011003c 1611fff2 20020032 c 20100000 22100001 102020
  //   20020022 c 22100002 102020 20020022 c 22100003 102020 20020022 c 22100004 102020 20020022 c 22100005
  //   102020 20020022 c 22100006 102020 20020022 c 22100007 102020 20020022 c 22100008 102020 20020022
  //   20020022 c 3e00008
  //   数码管输出
  //   PC+4
  //   IR
  //   PC
  //   指令字
  //   OP
  //   Func
  //   rs
  //   rt
  //   rd
  //   Imm26
  //   Bubble统计的是分支相关数，load_use是数据相关时处理的气泡数
  //   流水调试日志用
  //   IR
  //   PC
  //   rt
  //   rd
  //   MemWrite
  //   SB
  //   IR
  //   PC
  //   R2
  //   ALU
  //   rt
  //   rd
  //   MemToReg
  //   rt
  //   rd
endmodule

module \中断按键参考电路  (
  input  \同步清零信号 ,
  output \与中断屏蔽位与 
);

  wire \_1号中断_out , and_1_out, clock_1_out, d_ff_1_q, or_1_out, or_2_out;

  Clock #(.highDuration(1), .lowDuration(1)) clock_1 (.out(clock_1_out));
  Button \_1号中断  (.out(\_1号中断_out ));
  LED #(.active("true")) \_1号中断等待指示灯  (.in(or_1_out));
  or or_1 (or_1_out, \与中断屏蔽位与 , d_ff_1_q);
  D_Flip_Flop #(.trigger("rising"), .Pre_Clr_Positions("LEGACY"), .NegatePresetClear("false"), .enable("true"), .NewFFLayout("false")) d_ff_1 (
    .clk(\_1号中断_out ), .D(1'b1), .Q(d_ff_1_q), .reset(\与中断屏蔽位与 ));  // open: Qn, preset, en
  or or_2 (or_2_out, d_ff_1_q, \与中断屏蔽位与 );
  and and_1 (and_1_out, or_2_out, ~\同步清零信号 );  // AND_Gate
  D_Flip_Flop #(.trigger("rising"), .Pre_Clr_Positions("LEGACY"), .NegatePresetClear("false"), .enable("true"), .NewFFLayout("false")) IR1 (
    .clk(clock_1_out), .D(and_1_out), .Q(\与中断屏蔽位与 ));  // open: Qn, preset, en, reset
  \单周期硬布线控制器  \u_单周期硬布线控制器_1  ();  // open: Func, OP, ALU_OP, MemToReg, MemWrite, ALU_SRC, RegWrite, SysCALL, SignedExt, RegDst, JR, JMP, Beq, JAL, Bne, BLEZ, SB

  // Notes on the sheet:
  //   中断信号采样参考电路
  //   Reset 
endmodule

// ID/EX
module ID_EX_l (
  input  CLK,
  input  \同步清零_气泡_高电平有效 ,
  input  \使能端_低电平有效 ,
  input  [31:0] PC,
  input  [31:0] R1,
  input  BLEZ,
  input  SignedExt,
  input  MemToReg,
  input  MemWrite,
  input  BEQ,
  input  Syscall,
  input  RegWrite,
  input  SB,
  input  BNE,
  input  RegDst,
  input  [31:0] IR,
  input  [31:0] R2,
  input  AluSrcB,
  input  JR,
  input  JAL,
  input  [3:0] AluOP,
  input  [25:0] Imm26,
  input  JMP,
  input  [31:0] PC_4,
  input  MISS,
  input  [1:0] Forwarding_R1,
  input  JMP_Pre,
  input  [1:0] Forwarding_R2,
  input  [1:0] State_Now,
  input  [7:0] Row_Pre,
  output [31:0] PC_2,
  output [31:0] R1_2,
  output BLEZ_2,
  output SignedExt_2,
  output MemToReg_2,
  output MemWrite_2,
  output BEQ_2,
  output Syscall_2,
  output RegWrite_2,
  output SB_2,
  output BNE_2,
  output RegDst_2,
  output [31:0] IR_2,
  output [31:0] R2_2,
  output AluSrcB_2,
  output JR_2,
  output JAL_2,
  output [3:0] AluOP_2,
  output [25:0] Imm26_2,
  output JMP_2,
  output [31:0] PC_4_2,
  output MISS_2,
  output [1:0] Forwarding_R1_2,
  output JMP_Pre_2,
  output [1:0] Forwarding_R2_2,
  output [1:0] State_Now_2,
  output [7:0] Row_Pre_2
);

  wire multiplexer_9_out, multiplexer_10_out, multiplexer_11_out, multiplexer_12_out, multiplexer_13_out,
       multiplexer_14_out, multiplexer_15_out, multiplexer_18_out, multiplexer_19_out, multiplexer_20_out,
       multiplexer_21_out, multiplexer_22_out, multiplexer_23_out, multiplexer_24_out, multiplexer_25_out,
       multiplexer_26_out, not_1_out;
  wire [1:0] multiplexer_4_out, multiplexer_5_out, multiplexer_16_out;
  wire [3:0] multiplexer_27_out;
  wire [7:0] multiplexer_17_out;
  wire [25:0] multiplexer_8_out;
  wire [31:0] multiplexer_1_out, multiplexer_2_out, multiplexer_3_out, multiplexer_6_out, multiplexer_7_out;

  not not_1 (not_1_out, \使能端_低电平有效 );
  Multiplexer #(.select(1), .width(32), .disabled("Z"), .enable("false")) multiplexer_1 (
    .in0(PC), .in1({32{1'b0}}), .out(multiplexer_1_out), .sel(\同步清零_气泡_高电平有效 ));
  Multiplexer #(.select(1), .width(32), .disabled("Z"), .enable("false")) multiplexer_2 (
    .in0(IR), .in1({32{1'b0}}), .out(multiplexer_2_out), .sel(\同步清零_气泡_高电平有效 ));
  Multiplexer #(.select(1), .width(32), .disabled("Z"), .enable("false")) multiplexer_3 (
    .in0(PC_4), .in1({32{1'b0}}), .out(multiplexer_3_out), .sel(\同步清零_气泡_高电平有效 ));
  Multiplexer #(.select(1), .width(2), .disabled("Z"), .enable("false")) multiplexer_4 (
    .in0(Forwarding_R1), .in1(2'b00), .out(multiplexer_4_out), .sel(\同步清零_气泡_高电平有效 ));
  Multiplexer #(.select(1), .width(2), .disabled("Z"), .enable("false")) multiplexer_5 (
    .in0(Forwarding_R2), .in1(2'b00), .out(multiplexer_5_out), .sel(\同步清零_气泡_高电平有效 ));
  Register #(.width(32), .trigger("rising"), .Select("low")) u_PC (
    .D(multiplexer_1_out), .en(not_1_out), .Q(PC_2), .clk(CLK));  // open: clr
  Register #(.width(32), .trigger("rising"), .Select("low")) u_IR (
    .D(multiplexer_2_out), .en(not_1_out), .Q(IR_2), .clk(CLK));  // open: clr
  Register #(.width(32), .trigger("rising"), .Select("low")) u_PC_4 (
    .D(multiplexer_3_out), .en(not_1_out), .Q(PC_4_2), .clk(CLK));  // open: clr
  Register #(.width(2), .trigger("rising"), .Select("low")) u_Forwarding_R1 (
    .D(multiplexer_4_out), .en(not_1_out), .Q(Forwarding_R1_2), .clk(CLK));  // open: clr
  Register #(.width(2), .trigger("rising"), .Select("low")) u_Forwarding_R2 (
    .D(multiplexer_5_out), .en(not_1_out), .Q(Forwarding_R2_2), .clk(CLK));  // open: clr
  Pull_Resistor #(.pull(0)) pull_resistor_1 (.node(\同步清零_气泡_高电平有效 ));
  Pull_Resistor #(.pull(0)) pull_resistor_2 (.node(not_1_out));
  Multiplexer #(.select(1), .width(32), .disabled("Z"), .enable("false")) multiplexer_6 (
    .in0(R1), .in1({32{1'b0}}), .out(multiplexer_6_out), .sel(\同步清零_气泡_高电平有效 ));
  Multiplexer #(.select(1), .width(32), .disabled("Z"), .enable("false")) multiplexer_7 (
    .in0(R2), .in1({32{1'b0}}), .out(multiplexer_7_out), .sel(\同步清零_气泡_高电平有效 ));
  Multiplexer #(.select(1), .width(26), .disabled("Z"), .enable("false")) multiplexer_8 (
    .in0(Imm26), .in1({26{1'b0}}), .out(multiplexer_8_out), .sel(\同步清零_气泡_高电平有效 ));
  Register #(.width(32), .trigger("rising"), .Select("low")) u_R1 (
    .D(multiplexer_6_out), .en(not_1_out), .Q(R1_2), .clk(CLK));  // open: clr
  Register #(.width(32), .trigger("rising"), .Select("low")) u_R2 (
    .D(multiplexer_7_out), .en(not_1_out), .Q(R2_2), .clk(CLK));  // open: clr
  Register #(.width(26), .trigger("rising"), .Select("low")) u_Imm26 (
    .D(multiplexer_8_out), .en(not_1_out), .Q(Imm26_2), .clk(CLK));  // open: clr
  Multiplexer #(.select(1), .width(1), .disabled("Z"), .enable("false")) multiplexer_9 (
    .in0(BLEZ), .in1(1'b0), .out(multiplexer_9_out), .sel(\同步清零_气泡_高电平有效 ));
  Multiplexer #(.select(1), .width(1), .disabled("Z"), .enable("false")) multiplexer_10 (
    .in0(BEQ), .in1(1'b0), .out(multiplexer_10_out), .sel(\同步清零_气泡_高电平有效 ));
  Multiplexer #(.select(1), .width(1), .disabled("Z"), .enable("false")) multiplexer_11 (
    .in0(BNE), .in1(1'b0), .out(multiplexer_11_out), .sel(\同步清零_气泡_高电平有效 ));
  Multiplexer #(.select(1), .width(1), .disabled("Z"), .enable("false")) multiplexer_12 (
    .in0(JR), .in1(1'b0), .out(multiplexer_12_out), .sel(\同步清零_气泡_高电平有效 ));
  Multiplexer #(.select(1), .width(1), .disabled("Z"), .enable("false")) multiplexer_13 (
    .in0(JMP), .in1(1'b0), .out(multiplexer_13_out), .sel(\同步清零_气泡_高电平有效 ));
  Multiplexer #(.select(1), .width(1), .disabled("Z"), .enable("false")) multiplexer_14 (
    .in0(MISS), .in1(1'b0), .out(multiplexer_14_out), .sel(\同步清零_气泡_高电平有效 ));
  Multiplexer #(.select(1), .width(1), .disabled("Z"), .enable("false")) multiplexer_15 (
    .in0(JMP_Pre), .in1(1'b0), .out(multiplexer_15_out), .sel(\同步清零_气泡_高电平有效 ));
  Multiplexer #(.select(1), .width(2), .disabled("Z"), .enable("false")) multiplexer_16 (
    .in0(State_Now), .in1(2'b00), .out(multiplexer_16_out), .sel(\同步清零_气泡_高电平有效 ));
  Multiplexer #(.select(1), .width(8), .disabled("Z"), .enable("false")) multiplexer_17 (
    .in0(Row_Pre), .in1({8{1'b0}}), .out(multiplexer_17_out), .sel(\同步清零_气泡_高电平有效 ));
  Register #(.width(1), .trigger("rising"), .Select("low")) u_BLEZ (
    .D(multiplexer_9_out), .en(not_1_out), .Q(BLEZ_2), .clk(CLK));  // open: clr
  Register #(.width(1), .trigger("rising"), .Select("low")) u_BEQ (
    .D(multiplexer_10_out), .en(not_1_out), .Q(BEQ_2), .clk(CLK));  // open: clr
  Register #(.width(1), .trigger("rising"), .Select("low")) u_BNE (
    .D(multiplexer_11_out), .en(not_1_out), .Q(BNE_2), .clk(CLK));  // open: clr
  Register #(.width(1), .trigger("rising"), .Select("low")) u_JR (
    .D(multiplexer_12_out), .en(not_1_out), .Q(JR_2), .clk(CLK));  // open: clr
  Register #(.width(1), .trigger("rising"), .Select("low")) u_JMP (
    .D(multiplexer_13_out), .en(not_1_out), .Q(JMP_2), .clk(CLK));  // open: clr
  Register #(.width(1), .trigger("rising"), .Select("low")) u_MISS (
    .D(multiplexer_14_out), .en(not_1_out), .Q(MISS_2), .clk(CLK));  // open: clr
  Register #(.width(1), .trigger("rising"), .Select("low")) u_JMP_Pre (
    .D(multiplexer_15_out), .en(not_1_out), .Q(JMP_Pre_2), .clk(CLK));  // open: clr
  Register #(.width(2), .trigger("rising"), .Select("low")) u_State_Now (
    .D(multiplexer_16_out), .en(not_1_out), .Q(State_Now_2), .clk(CLK));  // open: clr
  Register #(.width(8), .trigger("rising"), .Select("low")) u_Row_Pre (
    .D(multiplexer_17_out), .en(not_1_out), .Q(Row_Pre_2), .clk(CLK));  // open: clr
  Multiplexer #(.select(1), .width(1), .disabled("Z"), .enable("false")) multiplexer_18 (
    .in0(SignedExt), .in1(1'b0), .out(multiplexer_18_out), .sel(\同步清零_气泡_高电平有效 ));
  Multiplexer #(.select(1), .width(1), .disabled("Z"), .enable("false")) multiplexer_19 (
    .in0(Syscall), .in1(1'b0), .out(multiplexer_19_out), .sel(\同步清零_气泡_高电平有效 ));
  Register #(.width(1), .trigger("rising"), .Select("low")) u_SignedExt (
    .D(multiplexer_18_out), .en(not_1_out), .Q(SignedExt_2), .clk(CLK));  // open: clr
  Register #(.width(1), .trigger("rising"), .Select("low")) u_Syscall (
    .D(multiplexer_19_out), .en(not_1_out), .Q(Syscall_2), .clk(CLK));  // open: clr
  Multiplexer #(.select(1), .width(1), .disabled("Z"), .enable("false")) multiplexer_20 (
    .in0(MemToReg), .in1(1'b0), .out(multiplexer_20_out), .sel(\同步清零_气泡_高电平有效 ));
  Multiplexer #(.select(1), .width(1), .disabled("Z"), .enable("false")) multiplexer_21 (
    .in0(RegWrite), .in1(1'b0), .out(multiplexer_21_out), .sel(\同步清零_气泡_高电平有效 ));
  Multiplexer #(.select(1), .width(1), .disabled("Z"), .enable("false")) multiplexer_22 (
    .in0(RegDst), .in1(1'b0), .out(multiplexer_22_out), .sel(\同步清零_气泡_高电平有效 ));
  Multiplexer #(.select(1), .width(1), .disabled("Z"), .enable("false")) multiplexer_23 (
    .in0(JAL), .in1(1'b0), .out(multiplexer_23_out), .sel(\同步清零_气泡_高电平有效 ));
  Register #(.width(1), .trigger("rising"), .Select("low")) u_MemToReg (
    .D(multiplexer_20_out), .en(not_1_out), .Q(MemToReg_2), .clk(CLK));  // open: clr
  Register #(.width(1), .trigger("rising"), .Select("low")) u_RegWrite (
    .D(multiplexer_21_out), .en(not_1_out), .Q(RegWrite_2), .clk(CLK));  // open: clr
  Register #(.width(1), .trigger("rising"), .Select("low")) u_RegDst (
    .D(multiplexer_22_out), .en(not_1_out), .Q(RegDst_2), .clk(CLK));  // open: clr
  Register #(.width(1), .trigger("rising"), .Select("low")) u_JAL (
    .D(multiplexer_23_out), .en(not_1_out), .Q(JAL_2), .clk(CLK));  // open: clr
  Multiplexer #(.select(1), .width(1), .disabled("Z"), .enable("false")) multiplexer_24 (
    .in0(MemWrite), .in1(1'b0), .out(multiplexer_24_out), .sel(\同步清零_气泡_高电平有效 ));
  Multiplexer #(.select(1), .width(1), .disabled("Z"), .enable("false")) multiplexer_25 (
    .in0(SB), .in1(1'b0), .out(multiplexer_25_out), .sel(\同步清零_气泡_高电平有效 ));
  Multiplexer #(.select(1), .width(1), .disabled("Z"), .enable("false")) multiplexer_26 (
    .in0(AluSrcB), .in1(1'b0), .out(multiplexer_26_out), .sel(\同步清零_气泡_高电平有效 ));
  Multiplexer #(.select(1), .width(4), .disabled("Z"), .enable("false")) multiplexer_27 (
    .in0(AluOP), .in1(4'b0000), .out(multiplexer_27_out), .sel(\同步清零_气泡_高电平有效 ));
  Register #(.width(1), .trigger("rising"), .Select("low")) u_MemWrite (
    .D(multiplexer_24_out), .en(not_1_out), .Q(MemWrite_2), .clk(CLK));  // open: clr
  Register #(.width(1), .trigger("rising"), .Select("low")) u_SB (
    .D(multiplexer_25_out), .en(not_1_out), .Q(SB_2), .clk(CLK));  // open: clr
  Register #(.width(1), .trigger("rising"), .Select("low")) u_AluSrcB (
    .D(multiplexer_26_out), .en(not_1_out), .Q(AluSrcB_2), .clk(CLK));  // open: clr
  Register #(.width(4), .trigger("rising"), .Select("low")) u_AluOP (
    .D(multiplexer_27_out), .en(not_1_out), .Q(AluOP_2), .clk(CLK));  // open: clr
endmodule

// EX/MEM
module EX_MEM_l (
  input  CLK,
  input  \同步清零_气泡_高电平有效 ,
  input  \使能端_低电平有效 ,
  input  [31:0] PC,
  input  MemToReg,
  input  MemWrite,
  input  Syscall,
  input  RegWrite,
  input  SB,
  input  RegDst,
  input  [31:0] IR,
  input  [31:0] R2,
  input  JAL,
  input  [31:0] ALU,
  input  [31:0] PC_4,
  output [31:0] PC_2,
  output MemToReg_2,
  output MemWrite_2,
  output Syscall_2,
  output RegWrite_2,
  output SB_2,
  output RegDst_2,
  output [31:0] IR_2,
  output [31:0] R2_2,
  output JAL_2,
  output [31:0] ALU_2,
  output [31:0] PC_4_2
);

  wire multiplexer_6_out, multiplexer_7_out, multiplexer_8_out, multiplexer_9_out, multiplexer_10_out,
       multiplexer_11_out, multiplexer_12_out, not_1_out;
  wire [31:0] multiplexer_1_out, multiplexer_2_out, multiplexer_3_out, multiplexer_4_out, multiplexer_5_out;

  not not_1 (not_1_out, \使能端_低电平有效 );
  Multiplexer #(.select(1), .width(32), .disabled("Z"), .enable("false")) multiplexer_1 (
    .in0(PC), .in1({32{1'b0}}), .out(multiplexer_1_out), .sel(\同步清零_气泡_高电平有效 ));
  Multiplexer #(.select(1), .width(32), .disabled("Z"), .enable("false")) multiplexer_2 (
    .in0(IR), .in1({32{1'b0}}), .out(multiplexer_2_out), .sel(\同步清零_气泡_高电平有效 ));
  Multiplexer #(.select(1), .width(32), .disabled("Z"), .enable("false")) multiplexer_3 (
    .in0(PC_4), .in1({32{1'b0}}), .out(multiplexer_3_out), .sel(\同步清零_气泡_高电平有效 ));
  Register #(.width(32), .trigger("rising"), .Select("low")) u_PC (
    .D(multiplexer_1_out), .en(not_1_out), .Q(PC_2), .clk(CLK));  // open: clr
  Register #(.width(32), .trigger("rising"), .Select("low")) u_IR (
    .D(multiplexer_2_out), .en(not_1_out), .Q(IR_2), .clk(CLK));  // open: clr
  Register #(.width(32), .trigger("rising"), .Select("low")) u_PC_4 (
    .D(multiplexer_3_out), .en(not_1_out), .Q(PC_4_2), .clk(CLK));  // open: clr
  Pull_Resistor #(.pull(0)) pull_resistor_1 (.node(\同步清零_气泡_高电平有效 ));
  Pull_Resistor #(.pull(0)) pull_resistor_2 (.node(not_1_out));
  Multiplexer #(.select(1), .width(32), .disabled("Z"), .enable("false")) multiplexer_4 (
    .in0(R2), .in1({32{1'b0}}), .out(multiplexer_4_out), .sel(\同步清零_气泡_高电平有效 ));
  Multiplexer #(.select(1), .width(32), .disabled("Z"), .enable("false")) multiplexer_5 (
    .in0(ALU), .in1({32{1'b0}}), .out(multiplexer_5_out), .sel(\同步清零_气泡_高电平有效 ));
  Register #(.width(32), .trigger("rising"), .Select("low")) u_R2 (
    .D(multiplexer_4_out), .en(not_1_out), .Q(R2_2), .clk(CLK));  // open: clr
  Register #(.width(32), .trigger("rising"), .Select("low")) u_ALU (
    .D(multiplexer_5_out), .en(not_1_out), .Q(ALU_2), .clk(CLK));  // open: clr
  Multiplexer #(.select(1), .width(1), .disabled("Z"), .enable("false")) multiplexer_6 (
    .in0(Syscall), .in1(1'b0), .out(multiplexer_6_out), .sel(\同步清零_气泡_高电平有效 ));
  Register #(.width(1), .trigger("rising"), .Select("low")) u_Syscall (
    .D(multiplexer_6_out), .en(not_1_out), .Q(Syscall_2), .clk(CLK));  // open: clr
  Multiplexer #(.select(1), .width(1), .disabled("Z"), .enable("false")) multiplexer_7 (
    .in0(MemToReg), .in1(1'b0), .out(multiplexer_7_out), .sel(\同步清零_气泡_高电平有效 ));
  Multiplexer #(.select(1), .width(1), .disabled("Z"), .enable("false")) multiplexer_8 (
    .in0(RegWrite), .in1(1'b0), .out(multiplexer_8_out), .sel(\同步清零_气泡_高电平有效 ));
  Multiplexer #(.select(1), .width(1), .disabled("Z"), .enable("false")) multiplexer_9 (
    .in0(RegDst), .in1(1'b0), .out(multiplexer_9_out), .sel(\同步清零_气泡_高电平有效 ));
  Multiplexer #(.select(1), .width(1), .disabled("Z"), .enable("false")) multiplexer_10 (
    .in0(JAL), .in1(1'b0), .out(multiplexer_10_out), .sel(\同步清零_气泡_高电平有效 ));
  Register #(.width(1), .trigger("rising"), .Select("low")) u_MemToReg (
    .D(multiplexer_7_out), .en(not_1_out), .Q(MemToReg_2), .clk(CLK));  // open: clr
  Register #(.width(1), .trigger("rising"), .Select("low")) u_RegWrite (
    .D(multiplexer_8_out), .en(not_1_out), .Q(RegWrite_2), .clk(CLK));  // open: clr
  Register #(.width(1), .trigger("rising"), .Select("low")) u_RegDst (
    .D(multiplexer_9_out), .en(not_1_out), .Q(RegDst_2), .clk(CLK));  // open: clr
  Register #(.width(1), .trigger("rising"), .Select("low")) u_JAL (
    .D(multiplexer_10_out), .en(not_1_out), .Q(JAL_2), .clk(CLK));  // open: clr
  Multiplexer #(.select(1), .width(1), .disabled("Z"), .enable("false")) multiplexer_11 (
    .in0(MemWrite), .in1(1'b0), .out(multiplexer_11_out), .sel(\同步清零_气泡_高电平有效 ));
  Multiplexer #(.select(1), .width(1), .disabled("Z"), .enable("false")) multiplexer_12 (
    .in0(SB), .in1(1'b0), .out(multiplexer_12_out), .sel(\同步清零_气泡_高电平有效 ));
  Register #(.width(1), .trigger("rising"), .Select("low")) u_MemWrite (
    .D(multiplexer_11_out), .en(not_1_out), .Q(MemWrite_2), .clk(CLK));  // open: clr
  Register #(.width(1), .trigger("rising"), .Select("low")) u_SB (
    .D(multiplexer_12_out), .en(not_1_out), .Q(SB_2), .clk(CLK));  // open: clr
endmodule

// MEM/WB
module MEM_WB_l (
  input  CLK,
  input  \同步清零_气泡_高电平有效 ,
  input  \使能端_低电平有效 ,
  input  [31:0] PC,
  input  MemToReg,
  input  Syscall,
  input  RegWrite,
  input  RegDst,
  input  [31:0] IR,
  input  [31:0] MD,
  input  JAL,
  input  [31:0] ALU,
  input  [31:0] PC_4,
  output [31:0] PC_2,
  output MemToReg_2,
  output Syscall_2,
  output RegWrite_2,
  output RegDst_2,
  output [31:0] IR_2,
  output [31:0] MD_2,
  output JAL_2,
  output [31:0] ALU_2,
  output [31:0] PC_4_2
);

  wire multiplexer_6_out, multiplexer_7_out, multiplexer_8_out, multiplexer_9_out, multiplexer_10_out,
       not_1_out;
  wire [31:0] multiplexer_1_out, multiplexer_2_out, multiplexer_3_out, multiplexer_4_out, multiplexer_5_out;

  not not_1 (not_1_out, \使能端_低电平有效 );
  Multiplexer #(.select(1), .width(32), .disabled("Z"), .enable("false")) multiplexer_1 (
    .in0(PC), .in1({32{1'b0}}), .out(multiplexer_1_out), .sel(\同步清零_气泡_高电平有效 ));
  Multiplexer #(.select(1), .width(32), .disabled("Z"), .enable("false")) multiplexer_2 (
    .in0(IR), .in1({32{1'b0}}), .out(multiplexer_2_out), .sel(\同步清零_气泡_高电平有效 ));
  Multiplexer #(.select(1), .width(32), .disabled("Z"), .enable("false")) multiplexer_3 (
    .in0(PC_4), .in1({32{1'b0}}), .out(multiplexer_3_out), .sel(\同步清零_气泡_高电平有效 ));
  Register #(.width(32), .trigger("rising"), .Select("low")) u_PC (
    .D(multiplexer_1_out), .en(not_1_out), .Q(PC_2), .clk(CLK));  // open: clr
  Register #(.width(32), .trigger("rising"), .Select("low")) u_IR (
    .D(multiplexer_2_out), .en(not_1_out), .Q(IR_2), .clk(CLK));  // open: clr
  Register #(.width(32), .trigger("rising"), .Select("low")) u_PC_4 (
    .D(multiplexer_3_out), .en(not_1_out), .Q(PC_4_2), .clk(CLK));  // open: clr
  Pull_Resistor #(.pull(0)) pull_resistor_1 (.node(\同步清零_气泡_高电平有效 ));
  Pull_Resistor #(.pull(0)) pull_resistor_2 (.node(not_1_out));
  Multiplexer #(.select(1), .width(32), .disabled("Z"), .enable("false")) multiplexer_4 (
    .in0(MD), .in1({32{1'b0}}), .out(multiplexer_4_out), .sel(\同步清零_气泡_高电平有效 ));
  Multiplexer #(.select(1), .width(32), .disabled("Z"), .enable("false")) multiplexer_5 (
    .in0(ALU), .in1({32{1'b0}}), .out(multiplexer_5_out), .sel(\同步清零_气泡_高电平有效 ));
  Register #(.width(32), .trigger("rising"), .Select("low")) u_MD (
    .D(multiplexer_4_out), .en(not_1_out), .Q(MD_2), .clk(CLK));  // open: clr
  Register #(.width(32), .trigger("rising"), .Select("low")) u_ALU (
    .D(multiplexer_5_out), .en(not_1_out), .Q(ALU_2), .clk(CLK));  // open: clr
  Multiplexer #(.select(1), .width(1), .disabled("Z"), .enable("false")) multiplexer_6 (
    .in0(Syscall), .in1(1'b0), .out(multiplexer_6_out), .sel(\同步清零_气泡_高电平有效 ));
  Register #(.width(1), .trigger("rising"), .Select("low")) u_Syscall (
    .D(multiplexer_6_out), .en(not_1_out), .Q(Syscall_2), .clk(CLK));  // open: clr
  Multiplexer #(.select(1), .width(1), .disabled("Z"), .enable("false")) multiplexer_7 (
    .in0(MemToReg), .in1(1'b0), .out(multiplexer_7_out), .sel(\同步清零_气泡_高电平有效 ));
  Multiplexer #(.select(1), .width(1), .disabled("Z"), .enable("false")) multiplexer_8 (
    .in0(RegWrite), .in1(1'b0), .out(multiplexer_8_out), .sel(\同步清零_气泡_高电平有效 ));
  Multiplexer #(.select(1), .width(1), .disabled("Z"), .enable("false")) multiplexer_9 (
    .in0(RegDst), .in1(1'b0), .out(multiplexer_9_out), .sel(\同步清零_气泡_高电平有效 ));
  Multiplexer #(.select(1), .width(1), .disabled("Z"), .enable("false")) multiplexer_10 (
    .in0(JAL), .in1(1'b0), .out(multiplexer_10_out), .sel(\同步清零_气泡_高电平有效 ));
  Register #(.width(1), .trigger("rising"), .Select("low")) u_MemToReg (
    .D(multiplexer_7_out), .en(not_1_out), .Q(MemToReg_2), .clk(CLK));  // open: clr
  Register #(.width(1), .trigger("rising"), .Select("low")) u_RegWrite (
    .D(multiplexer_8_out), .en(not_1_out), .Q(RegWrite_2), .clk(CLK));  // open: clr
  Register #(.width(1), .trigger("rising"), .Select("low")) u_RegDst (
    .D(multiplexer_9_out), .en(not_1_out), .Q(RegDst_2), .clk(CLK));  // open: clr
  Register #(.width(1), .trigger("rising"), .Select("low")) u_JAL (
    .D(multiplexer_10_out), .en(not_1_out), .Q(JAL_2), .clk(CLK));  // open: clr
endmodule

// IF/ID
module IF_ID_l (
  input  CLK,
  input  \同步清零_气泡_高电平有效 ,
  input  \使能端_低电平有效 ,
  input  [31:0] PC,
  input  MISS,
  input  JMP_Pre,
  input  [31:0] IR,
  input  [1:0] State_Now,
  input  [7:0] Row_Pre,
  input  [31:0] PC_4,
  output [31:0] PC_2,
  output MISS_2,
  output JMP_Pre_2,
  output [31:0] IR_2,
  output [1:0] State_Now_2,
  output [7:0] Row_Pre_2,
  output [31:0] PC_4_2
);

  wire multiplexer_4_out, multiplexer_5_out, not_1_out;
  wire [1:0] multiplexer_6_out;
  wire [7:0] multiplexer_7_out;
  wire [31:0] multiplexer_1_out, multiplexer_2_out, multiplexer_3_out;

  not not_1 (not_1_out, \使能端_低电平有效 );
  Multiplexer #(.select(1), .width(32), .disabled("Z"), .enable("false")) multiplexer_1 (
    .in0(PC), .in1({32{1'b0}}), .out(multiplexer_1_out), .sel(\同步清零_气泡_高电平有效 ));
  Multiplexer #(.select(1), .width(32), .disabled("Z"), .enable("false")) multiplexer_2 (
    .in0(IR), .in1({32{1'b0}}), .out(multiplexer_2_out), .sel(\同步清零_气泡_高电平有效 ));
  Multiplexer #(.select(1), .width(32), .disabled("Z"), .enable("false")) multiplexer_3 (
    .in0(PC_4), .in1({32{1'b0}}), .out(multiplexer_3_out), .sel(\同步清零_气泡_高电平有效 ));
  Register #(.width(32), .trigger("rising"), .Select("low")) u_PC (
    .D(multiplexer_1_out), .en(not_1_out), .Q(PC_2), .clk(CLK));  // open: clr
  Register #(.width(32), .trigger("rising"), .Select("low")) u_IR (
    .D(multiplexer_2_out), .en(not_1_out), .Q(IR_2), .clk(CLK));  // open: clr
  Register #(.width(32), .trigger("rising"), .Select("low")) u_PC_4 (
    .D(multiplexer_3_out), .en(not_1_out), .Q(PC_4_2), .clk(CLK));  // open: clr
  Pull_Resistor #(.pull(0)) pull_resistor_1 (.node(\同步清零_气泡_高电平有效 ));
  Pull_Resistor #(.pull(0)) pull_resistor_2 (.node(not_1_out));
  Multiplexer #(.select(1), .width(1), .disabled("Z"), .enable("false")) multiplexer_4 (
    .in0(MISS), .in1(1'b0), .out(multiplexer_4_out), .sel(\同步清零_气泡_高电平有效 ));
  Multiplexer #(.select(1), .width(1), .disabled("Z"), .enable("false")) multiplexer_5 (
    .in0(JMP_Pre), .in1(1'b0), .out(multiplexer_5_out), .sel(\同步清零_气泡_高电平有效 ));
  Multiplexer #(.select(1), .width(2), .disabled("Z"), .enable("false")) multiplexer_6 (
    .in0(State_Now), .in1(2'b00), .out(multiplexer_6_out), .sel(\同步清零_气泡_高电平有效 ));
  Multiplexer #(.select(1), .width(8), .disabled("Z"), .enable("false")) multiplexer_7 (
    .in0(Row_Pre), .in1({8{1'b0}}), .out(multiplexer_7_out), .sel(\同步清零_气泡_高电平有效 ));
  Register #(.width(1), .trigger("rising"), .Select("low")) u_MISS (
    .D(multiplexer_4_out), .en(not_1_out), .Q(MISS_2), .clk(CLK));  // open: clr
  Register #(.width(1), .trigger("rising"), .Select("low")) u_JMP_Pre (
    .D(multiplexer_5_out), .en(not_1_out), .Q(JMP_Pre_2), .clk(CLK));  // open: clr
  Register #(.width(2), .trigger("rising"), .Select("low")) u_State_Now (
    .D(multiplexer_6_out), .en(not_1_out), .Q(State_Now_2), .clk(CLK));  // open: clr
  Register #(.width(8), .trigger("rising"), .Select("low")) u_Row_Pre (
    .D(multiplexer_7_out), .en(not_1_out), .Q(Row_Pre_2), .clk(CLK));  // open: clr
endmodule

module \分支相关流水线  (
);

  wire and_2_out, and_3_out, and_4_out, and_5_out, and_6_out, and_7_out, and_8_out, and_9_out, and_10_out,
       Bubble, CLK, comparator_1_eq, comparator_2_eq, comparator_2_lt, ex_mem_l_1_jal_2,
       ex_mem_l_1_memtoreg_2, ex_mem_l_1_memwrite_2, ex_mem_l_1_regdst_2, ex_mem_l_1_regwrite_2,
       ex_mem_l_1_sb_2, ex_mem_l_1_syscall_2, final_IsStop, final_IsStop_t, Go, id_ex_l_1_alusrcb_2,
       id_ex_l_1_beq_2, id_ex_l_1_blez_2, id_ex_l_1_bne_2, id_ex_l_1_jal_2, id_ex_l_1_jr_2,
       id_ex_l_1_memtoreg_2, id_ex_l_1_memwrite_2, id_ex_l_1_regdst_2, id_ex_l_1_regwrite_2, id_ex_l_1_sb_2,
       id_ex_l_1_syscall_2, IR1, IR2, IR3, IsStop, JAL, mem_wb_l_1_memtoreg_2, mips_alu_1_equal,
       multiplexer_4_out, multiplexer_11_out, multiplexer_14_out, multiplexer_15_out, multiplexer_17_out,
       not_1_out, not_2_out, not_3_out, not_4_out, not_5_out, not_6_out, not_7_out, not_8_out, not_9_out,
       not_10_out, not_11_out, or_1_out, or_2_out, or_3_out, or_4_out, or_5_out, or_8_out, or_9_out, RegDst,
       register_3_q, RegWrite, RST, RstFlow, SEL, SignedExt, stop, Syscall, W1, W2, W3,
       \单周期硬布线控制器_1_alu_src , \单周期硬布线控制器_1_beq , \单周期硬布线控制器_1_blez , \单周期硬布线控制器_1_bne , \单周期硬布线控制器_1_jal ,
       \单周期硬布线控制器_1_jmp , \单周期硬布线控制器_1_jr , \单周期硬布线控制器_1_memtoreg , \单周期硬布线控制器_1_memwrite ,
       \单周期硬布线控制器_1_regdst , \单周期硬布线控制器_1_regwrite , \单周期硬布线控制器_1_sb , \单周期硬布线控制器_1_signedext , \无条件分支 ,
       \条件分支 , \点击此键_先设置同步清零信号_out ;
  wire [3:0] id_ex_l_1_aluop_2, \单周期硬布线控制器_1_alu_op ;
  wire [4:0] multiplexer_6_out, multiplexer_7_out, multiplexer_8_out, multiplexer_9_out, WB_rd, WB_rt;
  wire [7:0] ram_1_data, ram_1_data_2, ram_1_data_3, ram_1_data_4;
  wire [11:0] EX_PC, ID_PC, IF_PC, MEM_PC, WB_PC;
  wire [15:0] \LoadUse次数 , \总周期数 , \插入气泡数 , \无条件分支数 , \条件分支成功数 ;
  wire [27:2] PC_no_condition;
  wire [31:0] a0, adder_1_out, bit_extender_1_out, bit_extender_2_out, ex_mem_l_1_alu_2, ex_mem_l_1_ir_2,
       ex_mem_l_1_pc_2, ex_mem_l_1_pc_4_2, ex_mem_l_1_r2_2, id_ex_l_1_ir_2, id_ex_l_1_pc_2, id_ex_l_1_r2_2,
       if_id_l_1_ir_2, if_id_l_1_pc_2, if_id_l_1_pc_4_2, Jal_PC_4, LedData, mem_wb_l_1_alu_2,
       mem_wb_l_1_ir_2, mem_wb_l_1_md_2, mips_alu_1_result, multiplexer_1_out, multiplexer_2_out,
       multiplexer_3_out, multiplexer_10_out, multiplexer_12_out, multiplexer_13_out, multiplexer_16_out,
       multiplexer_18_out, multiplexer_19_out, PC_4, PC_condition, PC_q, rom_1_data, RS, shifter_1_out, v0;

  Multiplexer #(.select(1), .width(32), .disabled("Z"), .enable("false")) multiplexer_1 (
    .in0({PC_4[31:28], PC_no_condition, 2'b00}), .in1(RS), .out(multiplexer_1_out), .sel(id_ex_l_1_jr_2));
  Button \u_点击此键_先设置同步清零信号  (.out(\点击此键_先设置同步清零信号_out ));
  Register #(.width(1), .trigger("falling"), .Select("low")) register_1 (
    .D(1'b0), .Q(RstFlow), .clk(RST), .preset(\点击此键_先设置同步清零信号_out ));  // open: en, clr, cs
  Multiplexer #(.select(2), .width(32), .disabled("Z"), .enable("false")) multiplexer_2 (
    .in0(adder_1_out), .in1(PC_condition), .in2(multiplexer_1_out), .out(multiplexer_2_out),
    .sel({\无条件分支 , \条件分支 }));  // open: in3
  Comparator #(.width(32), .mode("twosComplement")) comparator_1 (
    .a(v0), .b(32'h22), .eq(comparator_1_eq));  // open: gt, lt
  Register #(.width(32), .trigger("rising"), .Select("low")) PC (
    .D(multiplexer_3_out), .Q(PC_q), .clk(CLK), .clr(RST));  // open: en
  Multiplexer #(.select(1), .width(32), .disabled("Z"), .enable("false")) multiplexer_3 (
    .in0(multiplexer_2_out), .in1(PC_q), .out(multiplexer_3_out), .sel(stop));
  not not_1 (not_1_out, comparator_1_eq);
  and and_1 (IsStop, not_1_out, Syscall);
  xor xor_1 (stop, final_IsStop_t, register_3_q);
  Button \u_再总复位  (.out(RST));
  Button _1 (.out(IR1));
  Button _2 (.out(IR2));
  Button _3 (.out(IR3));
  Register #(.width(32), .trigger("rising"), .Select("low")) register_2 (
    .D(a0), .Q(LedData), .clk(and_2_out), .clr(RST));  // open: en
  and and_2 (and_2_out, Syscall, comparator_1_eq);
  and and_3 (and_3_out, final_IsStop_t, Go);
  Register #(.width(1), .trigger("rising"), .Select("low")) register_3 (
    .D(1'b0), .Q(register_3_q), .clk(CLK), .clr(RST), .preset(and_3_out));  // open: en, cs
  Button \u_继续运行  (.out(Go));
  LED #(.active("true")) led_1 (.in(W1));
  LED #(.active("true")) led_2 (.in(W2));
  LED #(.active("true")) led_3 (.in(W3));
  Multiplexer #(.select(1), .width(1), .disabled("Z"), .enable("false")) multiplexer_4 (
    .in0(final_IsStop_t), .in1(1'b0), .out(multiplexer_4_out), .sel(register_3_q));
  Hex_Digit_Display hex_digit_display_1 (.value(LedData[27:24]));  // open: dp
  Hex_Digit_Display hex_digit_display_2 (.value(LedData[31:28]));  // open: dp
  Adder #(.width(32)) adder_1 (.a(PC_q), .b(32'h4), .out(adder_1_out));  // open: cin, cout
  ROM #(.addrWidth(10), .dataWidth(32), .Select("high")) rom_1 (.addr(PC_q[11:2]), .data(rom_1_data));
  or or_1 (or_1_out, Bubble, RstFlow);
  Multiplexer #(.select(1), .width(1), .disabled("Z"), .enable("false")) multiplexer_5 (
    .in0(multiplexer_4_out), .in1(1'b0), .out(SEL), .sel(or_1_out));
  Hex_Digit_Display hex_digit_display_3 (.value(LedData[19:16]));  // open: dp
  Hex_Digit_Display hex_digit_display_4 (.value(LedData[23:20]));  // open: dp
  or or_2 (or_2_out, RST, CLK);
  Hex_Digit_Display hex_digit_display_5 (.value(LedData[11:8]));  // open: dp
  Hex_Digit_Display hex_digit_display_6 (.value(LedData[15:12]));  // open: dp
  Clock #(.highDuration(1), .lowDuration(1)) clock_1 (.out(CLK));
  IF_ID_l if_id_l_1 (
    .CLK(or_2_out), .\同步清零_气泡_高电平有效 (or_1_out), .\使能端_低电平有效 (SEL), .PC(PC_q), .PC_2(if_id_l_1_pc_2),
    .IR(rom_1_data), .IR_2(if_id_l_1_ir_2), .PC_4(adder_1_out), .PC_4_2(if_id_l_1_pc_4_2));  // open: MISS, MISS_2, JMP_Pre, JMP_Pre_2, State_Now, State_Now_2, Row_Pre, Row_Pre_2
  Hex_Digit_Display hex_digit_display_7 (.value(LedData[3:0]));  // open: dp
  Hex_Digit_Display hex_digit_display_8 (.value(LedData[7:4]));  // open: dp
  Multiplexer #(.select(1), .width(5), .disabled("Z"), .enable("false")) multiplexer_6 (
    .in0(WB_rt), .in1(WB_rd), .out(multiplexer_6_out), .sel(RegDst));
  // Probe on \总周期数 
  // Probe on \无条件分支数 
  // Probe on \条件分支成功数 
  // Probe on \插入气泡数 
  // Probe on \LoadUse次数 
  \单周期硬布线控制器  \u_单周期硬布线控制器_1  (
    .Func(if_id_l_1_ir_2[5:0]), .OP(if_id_l_1_ir_2[31:26]), .ALU_OP(\单周期硬布线控制器_1_alu_op ),
    .MemToReg(\单周期硬布线控制器_1_memtoreg ), .MemWrite(\单周期硬布线控制器_1_memwrite ), .ALU_SRC(\单周期硬布线控制器_1_alu_src ),
    .RegWrite(\单周期硬布线控制器_1_regwrite ), .SysCALL(Syscall), .SignedExt(\单周期硬布线控制器_1_signedext ),
    .RegDst(\单周期硬布线控制器_1_regdst ), .JR(\单周期硬布线控制器_1_jr ), .JMP(\单周期硬布线控制器_1_jmp ), .Beq(\单周期硬布线控制器_1_beq ),
    .JAL(\单周期硬布线控制器_1_jal ), .Bne(\单周期硬布线控制器_1_bne ), .BLEZ(\单周期硬布线控制器_1_blez ), .SB(\单周期硬布线控制器_1_sb ));
  Multiplexer #(.select(1), .width(5), .disabled("Z"), .enable("false")) multiplexer_7 (
    .in0(if_id_l_1_ir_2[25:21]), .in1(5'b00010), .out(multiplexer_7_out), .sel(Syscall));
  Multiplexer #(.select(1), .width(5), .disabled("Z"), .enable("false")) multiplexer_8 (
    .in0(if_id_l_1_ir_2[20:16]), .in1(5'b00100), .out(multiplexer_8_out), .sel(Syscall));
  Multiplexer #(.select(1), .width(5), .disabled("Z"), .enable("false")) multiplexer_9 (
    .in0(multiplexer_6_out), .in1({5{1'b1}}), .out(multiplexer_9_out), .sel(JAL));
  Multiplexer #(.select(1), .width(32), .disabled("Z"), .enable("false")) multiplexer_10 (
    .in0(multiplexer_19_out), .in1(Jal_PC_4), .out(multiplexer_10_out), .sel(JAL));
  // Probe on IF_PC
  MIPS_Regifile mips_regifile_1 (
    .Din(multiplexer_10_out), .Clk(CLK), .R1(v0), .R2(a0), .WE(RegWrite), .W_num(multiplexer_9_out),
    .R1_num(multiplexer_7_out), .R2_num(multiplexer_8_out));
  // Probe on ID_PC
  // Probe on EX_PC
  // Probe on WB_PC
  // Probe on MEM_PC
  or or_3 (or_3_out, Bubble, RstFlow);
  or or_4 (or_4_out, RST, CLK);
  ID_EX_l id_ex_l_1 (
    .CLK(or_4_out), .\同步清零_气泡_高电平有效 (or_3_out), .\使能端_低电平有效 (SEL), .PC(if_id_l_1_pc_2), .R1(v0),
    .BLEZ(\单周期硬布线控制器_1_blez ), .SignedExt(\单周期硬布线控制器_1_signedext ), .MemToReg(\单周期硬布线控制器_1_memtoreg ),
    .MemWrite(\单周期硬布线控制器_1_memwrite ), .BEQ(\单周期硬布线控制器_1_beq ), .Syscall(IsStop),
    .RegWrite(\单周期硬布线控制器_1_regwrite ), .SB(\单周期硬布线控制器_1_sb ), .BNE(\单周期硬布线控制器_1_bne ),
    .RegDst(\单周期硬布线控制器_1_regdst ), .IR(if_id_l_1_ir_2), .R2(a0), .AluSrcB(\单周期硬布线控制器_1_alu_src ),
    .JR(\单周期硬布线控制器_1_jr ), .JAL(\单周期硬布线控制器_1_jal ), .AluOP(\单周期硬布线控制器_1_alu_op ),
    .Imm26(if_id_l_1_ir_2[25:0]), .JMP(\单周期硬布线控制器_1_jmp ), .PC_2(id_ex_l_1_pc_2), .R1_2(RS),
    .BLEZ_2(id_ex_l_1_blez_2), .SignedExt_2(SignedExt), .MemToReg_2(id_ex_l_1_memtoreg_2),
    .MemWrite_2(id_ex_l_1_memwrite_2), .BEQ_2(id_ex_l_1_beq_2), .Syscall_2(id_ex_l_1_syscall_2),
    .RegWrite_2(id_ex_l_1_regwrite_2), .SB_2(id_ex_l_1_sb_2), .BNE_2(id_ex_l_1_bne_2),
    .RegDst_2(id_ex_l_1_regdst_2), .IR_2(id_ex_l_1_ir_2), .R2_2(id_ex_l_1_r2_2),
    .AluSrcB_2(id_ex_l_1_alusrcb_2), .JR_2(id_ex_l_1_jr_2), .JAL_2(id_ex_l_1_jal_2),
    .AluOP_2(id_ex_l_1_aluop_2), .Imm26_2(PC_no_condition), .JMP_2(\无条件分支 ), .PC_4(if_id_l_1_pc_4_2),
    .PC_4_2(PC_4));  // open: Forwarding_R1, Forwarding_R1_2, Forwarding_R2, Forwarding_R2_2, MISS, MISS_2, JMP_Pre, JMP_Pre_2, State_Now, State_Now_2, Row_Pre, Row_Pre_2
  and and_4 (and_4_out, not_2_out, CLK);
  not not_2 (not_2_out, stop);
  Counter #(.width(16), .max('hffff), .ongoal("wrap"), .trigger("rising"), .behavior("old")) counter_1 (
    .count(1'b1), .Q(\总周期数 ), .clk(multiplexer_11_out), .clr(RST));  // open: load, D, carry, preset
  Multiplexer #(.select(1), .width(1), .disabled("Z"), .enable("false")) multiplexer_11 (
    .in0(and_4_out), .in1(1'b0), .out(multiplexer_11_out), .sel(not_4_out));
  not not_3 (not_3_out, CLK);
  not not_4 (not_4_out, not_3_out);
  Comparator #(.width(32), .mode("twosComplement")) comparator_2 (
    .a(RS), .b({32{1'b0}}), .eq(comparator_2_eq), .lt(comparator_2_lt));  // open: gt
  assign bit_extender_1_out = {{16{1'b0}}, PC_no_condition[17:2]};  // Bit_Extender bit_extender_1
  assign bit_extender_2_out = {{16{PC_no_condition[17]}}, PC_no_condition[17:2]};  // Bit_Extender bit_extender_2
  or or_5 (or_5_out, comparator_2_eq, comparator_2_lt);
  Multiplexer #(.select(1), .width(32), .disabled("Z"), .enable("false")) multiplexer_12 (
    .in0(bit_extender_1_out), .in1(bit_extender_2_out), .out(multiplexer_12_out), .sel(SignedExt));
  and and_5 (and_5_out, or_5_out, id_ex_l_1_blez_2);
  Multiplexer #(.select(1), .width(32), .disabled("Z"), .enable("false")) multiplexer_13 (
    .in0(id_ex_l_1_r2_2), .in1(multiplexer_12_out), .out(multiplexer_13_out), .sel(id_ex_l_1_alusrcb_2));
  Shifter #(.width(32), .shift("ll")) shifter_1 (.in(multiplexer_12_out), .\dist (5'b00010), .out(shifter_1_out));
  Adder #(.width(32)) adder_2 (.a(shifter_1_out), .b(PC_4), .out(PC_condition));  // open: cin, cout
  Multiplexer #(.select(1), .width(1), .disabled("Z"), .enable("false")) multiplexer_14 (
    .in0(and_6_out), .in1(1'b0), .out(multiplexer_14_out), .sel(not_7_out));
  and and_6 (and_6_out, \无条件分支 , CLK);
  not not_5 (not_5_out, mips_alu_1_equal);
  MIPS_ALU mips_alu_1 (
    .X(RS), .Y(multiplexer_13_out), .AluOP(id_ex_l_1_aluop_2), .Equal(mips_alu_1_equal),
    .Result(mips_alu_1_result), .shamt(PC_no_condition[12:8]));  // open: Result_2
  Counter #(.width(16), .max('hffff), .ongoal("wrap"), .trigger("rising"), .behavior("old")) counter_2 (
    .count(1'b1), .Q(\无条件分支数 ), .clk(multiplexer_14_out), .clr(RST));  // open: load, D, carry, preset
  not not_6 (not_6_out, CLK);
  not not_7 (not_7_out, not_6_out);
  and and_7 (and_7_out, mips_alu_1_equal, id_ex_l_1_beq_2);
  and and_8 (and_8_out, id_ex_l_1_bne_2, not_5_out);
  or or_6 (\条件分支 , and_5_out, and_8_out, and_7_out);
  or or_7 (Bubble, \无条件分支 , \条件分支 );
  or or_8 (or_8_out, RST, CLK);
  Counter #(.width(16), .max('hffff), .ongoal("wrap"), .trigger("rising"), .behavior("old")) counter_3 (
    .count(1'b1), .Q(\条件分支成功数 ), .clk(multiplexer_15_out), .clr(RST));  // open: load, D, carry, preset
  Multiplexer #(.select(1), .width(1), .disabled("Z"), .enable("false")) multiplexer_15 (
    .in0(and_9_out), .in1(1'b0), .out(multiplexer_15_out), .sel(not_9_out));
  and and_9 (and_9_out, \条件分支 , CLK);
  EX_MEM_l ex_mem_l_1 (
    .CLK(or_8_out), .\同步清零_气泡_高电平有效 (RstFlow), .\使能端_低电平有效 (SEL), .PC(id_ex_l_1_pc_2),
    .MemToReg(id_ex_l_1_memtoreg_2), .MemWrite(id_ex_l_1_memwrite_2), .RegWrite(id_ex_l_1_regwrite_2),
    .SB(id_ex_l_1_sb_2), .RegDst(id_ex_l_1_regdst_2), .IR(id_ex_l_1_ir_2), .R2(id_ex_l_1_r2_2),
    .JAL(id_ex_l_1_jal_2), .PC_2(ex_mem_l_1_pc_2), .MemToReg_2(ex_mem_l_1_memtoreg_2),
    .MemWrite_2(ex_mem_l_1_memwrite_2), .RegWrite_2(ex_mem_l_1_regwrite_2), .SB_2(ex_mem_l_1_sb_2),
    .RegDst_2(ex_mem_l_1_regdst_2), .IR_2(ex_mem_l_1_ir_2), .R2_2(ex_mem_l_1_r2_2), .JAL_2(ex_mem_l_1_jal_2),
    .ALU(mips_alu_1_result), .ALU_2(ex_mem_l_1_alu_2), .PC_4(PC_4), .PC_4_2(ex_mem_l_1_pc_4_2),
    .Syscall(id_ex_l_1_syscall_2), .Syscall_2(ex_mem_l_1_syscall_2));
  not not_8 (not_8_out, CLK);
  not not_9 (not_9_out, not_8_out);
  Multiplexer #(.select(2), .width(32), .disabled("Z"), .enable("false")) multiplexer_16 (
    .in0({ram_1_data, ram_1_data_4, ram_1_data_3, ex_mem_l_1_r2_2[7:0]}),
    .in1({ram_1_data, ram_1_data_4, ex_mem_l_1_r2_2[7:0], ram_1_data_2}),
    .in2({ram_1_data, ex_mem_l_1_r2_2[7:0], ram_1_data_3, ram_1_data_2}),
    .in3({ex_mem_l_1_r2_2[7:0], ram_1_data_4, ram_1_data_3, ram_1_data_2}), .out(multiplexer_16_out),
    .sel(ex_mem_l_1_alu_2[1:0]));
  Counter #(.width(16), .max('hffff), .ongoal("wrap"), .trigger("rising"), .behavior("old")) counter_4 (
    .count(1'b1), .Q(\插入气泡数 ), .clk(multiplexer_17_out), .clr(RST));  // open: load, D, carry, preset
  Multiplexer #(.select(1), .width(1), .disabled("Z"), .enable("false")) multiplexer_17 (
    .in0(and_10_out), .in1(1'b0), .out(multiplexer_17_out), .sel(not_11_out));
  and and_10 (and_10_out, Bubble, CLK);
  Multiplexer #(.select(1), .width(32), .disabled("Z"), .enable("false")) multiplexer_18 (
    .in0(ex_mem_l_1_r2_2), .in1(multiplexer_16_out), .out(multiplexer_18_out), .sel(ex_mem_l_1_sb_2));
  not not_10 (not_10_out, CLK);
  not not_11 (not_11_out, not_10_out);
  RAM #(.addrWidth(10), .dataWidth(32), .bus("separate"), .Select("high")) ram_1 (
    .addr(ex_mem_l_1_alu_2[11:2]), .din(multiplexer_18_out),
    .data({ram_1_data, ram_1_data_4, ram_1_data_3, ram_1_data_2}), .str(ex_mem_l_1_memwrite_2), .clk(CLK),
    .clr(RST));  // open: sel, ld
  or or_9 (or_9_out, RST, CLK);
  MEM_WB_l mem_wb_l_1 (
    .CLK(or_9_out), .\同步清零_气泡_高电平有效 (RstFlow), .\使能端_低电平有效 (SEL), .PC(ex_mem_l_1_pc_2),
    .MemToReg(ex_mem_l_1_memtoreg_2), .MemToReg_2(mem_wb_l_1_memtoreg_2), .RegWrite(ex_mem_l_1_regwrite_2),
    .RegWrite_2(RegWrite), .RegDst(ex_mem_l_1_regdst_2), .IR(ex_mem_l_1_ir_2),
    .MD({ram_1_data, ram_1_data_4, ram_1_data_3, ram_1_data_2}), .RegDst_2(RegDst),
    .IR_2({mem_wb_l_1_ir_2[31:21], WB_rt, WB_rd, mem_wb_l_1_ir_2[10:0]}), .MD_2(mem_wb_l_1_md_2),
    .JAL(ex_mem_l_1_jal_2), .JAL_2(JAL), .ALU(ex_mem_l_1_alu_2), .ALU_2(mem_wb_l_1_alu_2),
    .PC_4(ex_mem_l_1_pc_4_2), .PC_4_2(Jal_PC_4), .Syscall(ex_mem_l_1_syscall_2), .Syscall_2(final_IsStop));  // open: PC_2
  Multiplexer #(.select(1), .width(32), .disabled("Z"), .enable("false")) multiplexer_19 (
    .in0(mem_wb_l_1_alu_2), .in1(mem_wb_l_1_md_2), .out(multiplexer_19_out), .sel(mem_wb_l_1_memtoreg_2));

  // Other names for the same wires on the sheet: PC_no_condition[31:28] = PC_4[31:28]

  // Notes on the sheet:
  //   中断源
  //   中断等待指示
  //   指令存储器
  //   contents of rom_1 (hex, n*v repeats v):
  //   20110001 8000c05 20110001 20120002 20130003 8000c09 20110001 20120002 20130003 8000c0d 20110001
  //   20120002 20130003 8000c11 20110001 20120002 20130003 c000cf5 20100001 20110001 118fc0 112020
  //   20020022 c 118882 12200001 8000c15 112020 20020022 c 20110001 118880 112020 20020022 c 12200001
  //   8000c1f 20110001 118fc0 112020 20020022 c 1188c3 112020 20020022 c 118903 112020 20020022 c 118903
  //   112020 20020022 c 118903 112020 20020022 c 118903 112020 20020022 c 118903 112020 20020022 c 118903
  //   112020 20020022 c 118903 112020 20020022 c 20100001 109fc0 139fc3 8021 2012000c 24160003 26100001
  //   3210000f 20080008 20090001 139900 2709825 132020 20020022 c 1094022 1500fff9 22100001 2018000f
  //   2188024 108700 20080008 20090001 139902 2709825 132021 20020022 c 1094022 1500fff9 108702 2c9b022
  //   12c00001 8000c50 4020 1084027 84400 3508ffff 82021 20020022 c 2010ffff 20110000 ae300000 22100001
  //   22310004 ae300000 22100001 22310004 ae300000 22100001 22310004 ae300000 22100001 22310004 ae300000
  //   22100001 22310004 ae300000 22100001 22310004 ae300000 22100001 22310004 ae300000 22100001 22310004
  //   ae300000 22100001 22310004 ae300000 22100001 22310004 ae300000 22100001 22310004 ae300000 22100001
  //   22310004 ae300000 22100001 22310004 ae300000 22100001 22310004 ae300000 22100001 22310004 ae300000
  //   22100001 22310004 22100001 8020 2011003c 8e130000 8e340000 274402a 11000002 ae330000 ae140000
  //   2231fffc 1611fff8 102020 20020022 c 22100004 2011003c 1611fff2 20020032 c 20080001 20110010 112020
  //   20020022 c 200b0020 2288823 112020 20020022 c 216bffff 1560fffa 2002000a c 2008ffff 20117777 112020
  //   20020022 c 200b0010 2288826 112020 20020022 c 216bffff 1560fffa 2002000a c 20090000 200b0020
  //   20110000 20120001 a1310000 112020 20020022 c 2328820 21290001 216bffff 1560fff8 200b0008 20090000
  //   8d310000 112020 20020022 c 21290004 216bffff 1560fff9 2002000a c 2011fff1 112020 20020022 c 22310001
  //   1a20fffb 2002000a c 2002000a c 20100000 22100001 102020 20020022 c 22100002 102020 20020022 c
  //   22100003 102020 20020022 c 22100004 102020 20020022 c 22100005 102020 20020022 c 22100006 102020
  //   20020022 c 22100007 102020 20020022 c 22100008 102020 20020022 20020022 c 3e00008
  //   数码管输出
  //   PC+4
  //   IR
  //   PC
  //   指令字
  //   OP
  //   Func
  //   rs
  //   rt
  //   rd
  //   Imm26
  //   流水调试日志用
  //   IR
  //   PC
  //   MemWrite
  //   SB
  //   IR
  //   PC
  //   R2
  //   ALU
  //   MemToReg
  //   rt
  //   rd
endmodule

// 寄
module \源寄存器使用情况  (
  input  [5:0] OP,
  input  [5:0] FUN,
  output R1_Used,
  output R2_Used
);

  wire and_1_out, and_2_out, and_3_out, and_4_out, and_5_out, and_6_out, and_7_out, and_8_out, and_9_out,
       and_10_out, and_11_out, and_12_out, and_13_out, and_14_out, and_15_out, and_16_out, and_17_out,
       and_18_out, and_19_out, and_20_out, and_21_out, and_22_out, and_23_out, and_24_out, and_25_out,
       and_26_out, and_27_out, and_28_out, and_29_out, and_30_out, and_31_out, and_32_out, and_33_out,
       and_34_out, and_35_out, and_36_out, and_37_out, and_38_out, and_39_out, and_40_out, and_41_out,
       and_42_out, and_43_out, and_44_out, not_1_out, not_2_out, not_3_out, not_4_out, not_5_out, not_6_out,
       not_7_out, not_8_out, not_9_out, not_10_out, not_11_out, not_12_out, not_13_out, not_14_out,
       not_15_out, not_16_out, not_17_out, not_18_out, not_19_out, not_20_out, not_21_out, not_22_out,
       not_23_out, not_24_out, not_25_out, not_26_out, not_27_out, not_28_out, not_29_out, not_30_out,
       not_31_out, not_32_out, not_33_out, not_34_out, not_35_out, not_36_out, not_37_out, not_38_out,
       not_39_out, not_40_out, not_41_out, not_42_out, not_43_out, not_44_out, not_45_out, not_46_out,
       not_47_out, not_48_out, not_49_out, not_50_out, not_51_out, not_52_out, not_53_out, not_54_out,
       not_55_out, not_56_out, not_57_out, not_58_out, not_59_out, not_60_out, not_61_out, not_62_out,
       not_63_out, not_64_out, not_65_out, not_66_out, not_67_out, not_68_out, not_69_out, not_70_out,
       not_71_out, not_72_out, not_73_out, not_74_out, not_75_out, not_76_out, not_77_out, not_78_out,
       not_79_out, not_80_out, not_81_out, not_82_out, not_83_out, not_84_out, not_85_out, not_86_out,
       not_87_out, not_88_out, not_89_out, not_90_out, not_91_out, not_92_out, not_93_out, not_94_out,
       not_95_out, not_96_out, not_97_out, not_98_out, not_99_out, not_100_out, not_101_out, not_102_out,
       not_103_out, not_104_out, not_105_out, not_106_out, not_107_out, not_108_out, not_109_out,
       not_110_out, not_111_out, not_112_out, not_113_out, not_114_out, not_115_out, not_116_out,
       not_117_out, not_118_out, not_119_out, not_120_out, not_121_out, not_122_out, not_123_out,
       not_124_out, not_125_out, not_126_out, not_127_out, not_128_out, not_129_out, not_130_out,
       not_131_out, not_132_out, not_133_out, not_134_out, not_135_out, not_136_out, not_137_out,
       not_138_out, not_139_out, not_140_out, not_141_out, not_142_out, not_143_out, not_144_out,
       not_145_out, not_146_out, not_147_out, not_148_out, not_149_out, not_150_out, not_151_out,
       not_152_out, not_153_out, not_154_out, not_155_out, not_156_out, not_157_out, not_158_out,
       not_159_out, not_160_out, not_161_out, not_162_out, not_163_out, not_164_out, not_165_out,
       not_166_out, not_167_out, not_168_out, not_169_out, not_170_out, not_171_out, not_172_out,
       not_173_out, not_174_out, not_175_out, not_176_out, not_177_out, not_178_out, not_179_out,
       not_180_out, not_181_out, not_182_out, not_183_out, not_184_out, not_185_out, not_186_out,
       not_187_out, not_188_out, not_189_out, not_190_out, not_191_out, not_192_out, not_193_out,
       not_194_out, not_195_out, not_196_out, not_197_out, not_198_out, not_199_out, not_200_out,
       not_201_out, not_202_out, not_203_out, not_204_out, not_205_out, not_206_out, not_207_out,
       not_208_out, not_209_out, not_210_out, not_211_out, not_212_out, not_213_out, not_214_out,
       not_215_out, not_216_out, not_217_out, not_218_out, not_219_out, not_220_out, not_221_out,
       not_222_out, not_223_out, not_224_out, not_225_out, not_226_out, not_227_out, not_228_out,
       not_229_out, not_230_out, not_231_out, not_232_out, not_233_out, not_234_out, not_235_out,
       not_236_out, not_237_out, not_238_out, not_239_out, not_240_out, not_241_out, not_242_out,
       not_243_out, not_244_out, not_245_out, not_246_out, not_247_out, not_248_out, not_249_out,
       not_250_out, not_251_out, not_252_out, not_253_out, not_254_out, not_255_out, not_256_out,
       not_257_out, not_258_out, not_259_out, not_260_out, not_261_out, not_262_out, not_263_out,
       not_264_out, not_265_out, not_266_out, not_267_out, not_268_out, not_269_out, not_270_out,
       not_271_out, not_272_out, not_273_out, not_274_out, not_275_out, not_276_out, not_277_out,
       not_278_out, not_279_out, not_280_out, not_281_out, not_282_out, not_283_out, not_284_out,
       not_285_out, not_286_out, not_287_out, not_288_out, not_289_out, not_290_out, not_291_out,
       not_292_out, not_293_out, not_294_out, not_295_out, not_296_out, not_297_out, not_298_out,
       not_299_out, not_300_out, not_301_out, not_302_out, not_303_out, not_304_out, not_305_out,
       not_306_out, not_307_out, not_308_out, not_309_out, not_310_out, not_311_out, not_312_out,
       not_313_out, not_314_out, not_315_out, not_316_out, not_317_out, not_318_out, not_319_out,
       not_320_out, not_321_out, not_322_out, not_323_out, not_324_out, not_325_out, not_326_out,
       not_327_out, not_328_out, not_329_out, not_330_out, not_331_out, not_332_out, not_333_out,
       not_334_out, not_335_out, not_336_out, not_337_out, not_338_out, not_339_out, not_340_out;

  not not_1 (not_1_out, OP[5]);
  not not_2 (not_2_out, OP[4]);
  not not_3 (not_3_out, OP[3]);
  not not_4 (not_4_out, OP[2]);
  not not_5 (not_5_out, OP[1]);
  not not_6 (not_6_out, OP[0]);
  not not_7 (not_7_out, FUN[5]);
  not not_8 (not_8_out, FUN[4]);
  not not_9 (not_9_out, FUN[3]);
  not not_10 (not_10_out, FUN[2]);
  not not_11 (not_11_out, FUN[1]);
  not not_12 (not_12_out, FUN[0]);
  not not_13 (not_13_out, OP[5]);
  not not_14 (not_14_out, OP[4]);
  not not_15 (not_15_out, OP[3]);
  not not_16 (not_16_out, OP[2]);
  not not_17 (not_17_out, OP[1]);
  not not_18 (not_18_out, OP[0]);
  not not_19 (not_19_out, FUN[5]);
  not not_20 (not_20_out, FUN[4]);
  not not_21 (not_21_out, FUN[3]);
  not not_22 (not_22_out, FUN[2]);
  not not_23 (not_23_out, OP[5]);
  not not_24 (not_24_out, OP[4]);
  not not_25 (not_25_out, OP[3]);
  not not_26 (not_26_out, OP[2]);
  not not_27 (not_27_out, OP[1]);
  not not_28 (not_28_out, OP[0]);
  not not_29 (not_29_out, FUN[5]);
  not not_30 (not_30_out, FUN[4]);
  not not_31 (not_31_out, FUN[3]);
  not not_32 (not_32_out, FUN[2]);
  not not_33 (not_33_out, FUN[0]);
  not not_34 (not_34_out, OP[5]);
  not not_35 (not_35_out, OP[4]);
  not not_36 (not_36_out, OP[3]);
  not not_37 (not_37_out, OP[2]);
  not not_38 (not_38_out, OP[1]);
  not not_39 (not_39_out, OP[0]);
  not not_40 (not_40_out, FUN[4]);
  not not_41 (not_41_out, FUN[3]);
  not not_42 (not_42_out, FUN[2]);
  not not_43 (not_43_out, FUN[1]);
  not not_44 (not_44_out, FUN[0]);
  not not_45 (not_45_out, OP[5]);
  not not_46 (not_46_out, OP[4]);
  not not_47 (not_47_out, OP[3]);
  not not_48 (not_48_out, OP[2]);
  not not_49 (not_49_out, OP[1]);
  not not_50 (not_50_out, OP[0]);
  not not_51 (not_51_out, FUN[4]);
  not not_52 (not_52_out, FUN[3]);
  not not_53 (not_53_out, FUN[2]);
  not not_54 (not_54_out, FUN[1]);
  not not_55 (not_55_out, OP[5]);
  not not_56 (not_56_out, OP[4]);
  not not_57 (not_57_out, OP[3]);
  not not_58 (not_58_out, OP[2]);
  not not_59 (not_59_out, OP[1]);
  not not_60 (not_60_out, OP[0]);
  not not_61 (not_61_out, FUN[4]);
  not not_62 (not_62_out, FUN[3]);
  not not_63 (not_63_out, FUN[2]);
  not not_64 (not_64_out, FUN[0]);
  not not_65 (not_65_out, OP[5]);
  not not_66 (not_66_out, OP[4]);
  not not_67 (not_67_out, OP[3]);
  not not_68 (not_68_out, OP[2]);
  not not_69 (not_69_out, OP[1]);
  not not_70 (not_70_out, OP[0]);
  not not_71 (not_71_out, FUN[4]);
  not not_72 (not_72_out, FUN[3]);
  not not_73 (not_73_out, FUN[1]);
  not not_74 (not_74_out, FUN[0]);
  not not_75 (not_75_out, OP[5]);
  not not_76 (not_76_out, OP[4]);
  not not_77 (not_77_out, OP[3]);
  not not_78 (not_78_out, OP[2]);
  not not_79 (not_79_out, OP[1]);
  not not_80 (not_80_out, OP[0]);
  not not_81 (not_81_out, FUN[4]);
  not not_82 (not_82_out, FUN[3]);
  not not_83 (not_83_out, FUN[1]);
  not not_84 (not_84_out, OP[5]);
  not not_85 (not_85_out, OP[4]);
  not not_86 (not_86_out, OP[3]);
  not not_87 (not_87_out, OP[2]);
  not not_88 (not_88_out, OP[1]);
  not not_89 (not_89_out, OP[0]);
  not not_90 (not_90_out, FUN[4]);
  not not_91 (not_91_out, FUN[3]);
  not not_92 (not_92_out, OP[5]);
  not not_93 (not_93_out, OP[4]);
  not not_94 (not_94_out, OP[3]);
  not not_95 (not_95_out, OP[2]);
  not not_96 (not_96_out, OP[1]);
  not not_97 (not_97_out, OP[0]);
  not not_98 (not_98_out, FUN[4]);
  not not_99 (not_99_out, FUN[2]);
  not not_100 (not_100_out, FUN[0]);
  not not_101 (not_101_out, OP[5]);
  not not_102 (not_102_out, OP[4]);
  not not_103 (not_103_out, OP[3]);
  not not_104 (not_104_out, OP[2]);
  not not_105 (not_105_out, OP[1]);
  not not_106 (not_106_out, OP[0]);
  not not_107 (not_107_out, FUN[4]);
  not not_108 (not_108_out, FUN[2]);
  not not_109 (not_109_out, OP[5]);
  not not_110 (not_110_out, OP[4]);
  not not_111 (not_111_out, OP[3]);
  not not_112 (not_112_out, OP[2]);
  not not_113 (not_113_out, OP[1]);
  not not_114 (not_114_out, OP[0]);
  not not_115 (not_115_out, FUN[5]);
  not not_116 (not_116_out, FUN[4]);
  not not_117 (not_117_out, FUN[2]);
  not not_118 (not_118_out, FUN[1]);
  not not_119 (not_119_out, FUN[0]);
  not not_120 (not_120_out, OP[5]);
  not not_121 (not_121_out, OP[4]);
  not not_122 (not_122_out, OP[3]);
  not not_123 (not_123_out, OP[2]);
  not not_124 (not_124_out, OP[1]);
  not not_125 (not_125_out, OP[0]);
  not not_126 (not_126_out, FUN[5]);
  not not_127 (not_127_out, FUN[4]);
  not not_128 (not_128_out, FUN[1]);
  not not_129 (not_129_out, FUN[0]);
  not not_130 (not_130_out, OP[5]);
  not not_131 (not_131_out, OP[4]);
  not not_132 (not_132_out, OP[3]);
  not not_133 (not_133_out, OP[1]);
  not not_134 (not_134_out, OP[0]);
  not not_135 (not_135_out, OP[5]);
  not not_136 (not_136_out, OP[4]);
  not not_137 (not_137_out, OP[3]);
  not not_138 (not_138_out, OP[1]);
  not not_139 (not_139_out, OP[5]);
  not not_140 (not_140_out, OP[4]);
  not not_141 (not_141_out, OP[2]);
  not not_142 (not_142_out, OP[1]);
  not not_143 (not_143_out, OP[0]);
  not not_144 (not_144_out, OP[5]);
  not not_145 (not_145_out, OP[4]);
  not not_146 (not_146_out, OP[1]);
  not not_147 (not_147_out, OP[0]);
  not not_148 (not_148_out, OP[5]);
  not not_149 (not_149_out, OP[4]);
  not not_150 (not_150_out, OP[2]);
  not not_151 (not_151_out, OP[1]);
  not not_152 (not_152_out, OP[5]);
  not not_153 (not_153_out, OP[4]);
  not not_154 (not_154_out, OP[2]);
  not not_155 (not_155_out, OP[0]);
  not not_156 (not_156_out, OP[5]);
  not not_157 (not_157_out, OP[4]);
  not not_158 (not_158_out, OP[1]);
  not not_159 (not_159_out, OP[4]);
  not not_160 (not_160_out, OP[3]);
  not not_161 (not_161_out, OP[2]);
  not not_162 (not_162_out, OP[4]);
  not not_163 (not_163_out, OP[2]);
  not not_164 (not_164_out, OP[5]);
  not not_165 (not_165_out, OP[4]);
  not not_166 (not_166_out, OP[3]);
  not not_167 (not_167_out, OP[0]);
  not not_168 (not_168_out, OP[4]);
  not not_169 (not_169_out, OP[2]);
  not not_170 (not_170_out, OP[1]);
  not not_171 (not_171_out, OP[0]);
  not not_172 (not_172_out, OP[5]);
  not not_173 (not_173_out, OP[4]);
  not not_174 (not_174_out, OP[3]);
  not not_175 (not_175_out, OP[2]);
  not not_176 (not_176_out, OP[1]);
  not not_177 (not_177_out, OP[0]);
  not not_178 (not_178_out, FUN[4]);
  not not_179 (not_179_out, FUN[3]);
  not not_180 (not_180_out, FUN[2]);
  not not_181 (not_181_out, OP[5]);
  not not_182 (not_182_out, OP[4]);
  not not_183 (not_183_out, OP[3]);
  not not_184 (not_184_out, OP[2]);
  not not_185 (not_185_out, OP[1]);
  not not_186 (not_186_out, OP[0]);
  not not_187 (not_187_out, FUN[4]);
  not not_188 (not_188_out, FUN[3]);
  not not_189 (not_189_out, FUN[0]);
  not not_190 (not_190_out, OP[5]);
  not not_191 (not_191_out, OP[4]);
  not not_192 (not_192_out, OP[3]);
  not not_193 (not_193_out, OP[2]);
  not not_194 (not_194_out, OP[1]);
  not not_195 (not_195_out, OP[0]);
  not not_196 (not_196_out, FUN[5]);
  not not_197 (not_197_out, FUN[4]);
  not not_198 (not_198_out, FUN[3]);
  not not_199 (not_199_out, FUN[2]);
  not not_200 (not_200_out, FUN[1]);
  not not_201 (not_201_out, FUN[0]);
  not not_202 (not_202_out, OP[5]);
  not not_203 (not_203_out, OP[4]);
  not not_204 (not_204_out, OP[3]);
  not not_205 (not_205_out, OP[2]);
  not not_206 (not_206_out, OP[1]);
  not not_207 (not_207_out, OP[0]);
  not not_208 (not_208_out, FUN[5]);
  not not_209 (not_209_out, FUN[4]);
  not not_210 (not_210_out, FUN[3]);
  not not_211 (not_211_out, FUN[2]);
  not not_212 (not_212_out, OP[5]);
  not not_213 (not_213_out, OP[4]);
  not not_214 (not_214_out, OP[3]);
  not not_215 (not_215_out, OP[2]);
  not not_216 (not_216_out, OP[1]);
  not not_217 (not_217_out, OP[0]);
  not not_218 (not_218_out, FUN[5]);
  not not_219 (not_219_out, FUN[4]);
  not not_220 (not_220_out, FUN[3]);
  not not_221 (not_221_out, FUN[2]);
  not not_222 (not_222_out, FUN[0]);
  not not_223 (not_223_out, OP[5]);
  not not_224 (not_224_out, OP[4]);
  not not_225 (not_225_out, OP[3]);
  not not_226 (not_226_out, OP[2]);
  not not_227 (not_227_out, OP[1]);
  not not_228 (not_228_out, OP[0]);
  not not_229 (not_229_out, FUN[4]);
  not not_230 (not_230_out, FUN[3]);
  not not_231 (not_231_out, FUN[2]);
  not not_232 (not_232_out, FUN[1]);
  not not_233 (not_233_out, FUN[0]);
  not not_234 (not_234_out, OP[5]);
  not not_235 (not_235_out, OP[4]);
  not not_236 (not_236_out, OP[3]);
  not not_237 (not_237_out, OP[2]);
  not not_238 (not_238_out, OP[1]);
  not not_239 (not_239_out, OP[0]);
  not not_240 (not_240_out, FUN[4]);
  not not_241 (not_241_out, FUN[3]);
  not not_242 (not_242_out, FUN[2]);
  not not_243 (not_243_out, FUN[1]);
  not not_244 (not_244_out, OP[5]);
  not not_245 (not_245_out, OP[4]);
  not not_246 (not_246_out, OP[3]);
  not not_247 (not_247_out, OP[2]);
  not not_248 (not_248_out, OP[1]);
  not not_249 (not_249_out, OP[0]);
  not not_250 (not_250_out, FUN[4]);
  not not_251 (not_251_out, FUN[3]);
  not not_252 (not_252_out, FUN[2]);
  not not_253 (not_253_out, FUN[0]);
  not not_254 (not_254_out, OP[5]);
  not not_255 (not_255_out, OP[4]);
  not not_256 (not_256_out, OP[3]);
  not not_257 (not_257_out, OP[2]);
  not not_258 (not_258_out, OP[1]);
  not not_259 (not_259_out, OP[0]);
  not not_260 (not_260_out, FUN[4]);
  not not_261 (not_261_out, FUN[3]);
  not not_262 (not_262_out, FUN[1]);
  not not_263 (not_263_out, FUN[0]);
  not not_264 (not_264_out, OP[5]);
  not not_265 (not_265_out, OP[4]);
  not not_266 (not_266_out, OP[3]);
  not not_267 (not_267_out, OP[2]);
  not not_268 (not_268_out, OP[1]);
  not not_269 (not_269_out, OP[0]);
  not not_270 (not_270_out, FUN[4]);
  not not_271 (not_271_out, FUN[3]);
  not not_272 (not_272_out, FUN[1]);
  not not_273 (not_273_out, OP[5]);
  not not_274 (not_274_out, OP[4]);
  not not_275 (not_275_out, OP[3]);
  not not_276 (not_276_out, OP[2]);
  not not_277 (not_277_out, OP[1]);
  not not_278 (not_278_out, OP[0]);
  not not_279 (not_279_out, FUN[4]);
  not not_280 (not_280_out, FUN[3]);
  not not_281 (not_281_out, OP[5]);
  not not_282 (not_282_out, OP[4]);
  not not_283 (not_283_out, OP[3]);
  not not_284 (not_284_out, OP[2]);
  not not_285 (not_285_out, OP[1]);
  not not_286 (not_286_out, OP[0]);
  not not_287 (not_287_out, FUN[4]);
  not not_288 (not_288_out, FUN[2]);
  not not_289 (not_289_out, FUN[0]);
  not not_290 (not_290_out, OP[5]);
  not not_291 (not_291_out, OP[4]);
  not not_292 (not_292_out, OP[3]);
  not not_293 (not_293_out, OP[2]);
  not not_294 (not_294_out, OP[1]);
  not not_295 (not_295_out, OP[0]);
  not not_296 (not_296_out, FUN[4]);
  not not_297 (not_297_out, FUN[2]);
  not not_298 (not_298_out, OP[5]);
  not not_299 (not_299_out, OP[4]);
  not not_300 (not_300_out, OP[3]);
  not not_301 (not_301_out, OP[2]);
  not not_302 (not_302_out, OP[1]);
  not not_303 (not_303_out, OP[0]);
  not not_304 (not_304_out, FUN[5]);
  not not_305 (not_305_out, FUN[4]);
  not not_306 (not_306_out, FUN[1]);
  not not_307 (not_307_out, FUN[0]);
  not not_308 (not_308_out, OP[5]);
  not not_309 (not_309_out, OP[4]);
  not not_310 (not_310_out, OP[3]);
  not not_311 (not_311_out, OP[1]);
  not not_312 (not_312_out, OP[0]);
  not not_313 (not_313_out, OP[5]);
  not not_314 (not_314_out, OP[4]);
  not not_315 (not_315_out, OP[3]);
  not not_316 (not_316_out, OP[1]);
  not not_317 (not_317_out, OP[4]);
  not not_318 (not_318_out, OP[2]);
  not not_319 (not_319_out, OP[4]);
  not not_320 (not_320_out, OP[2]);
  not not_321 (not_321_out, OP[1]);
  not not_322 (not_322_out, OP[0]);
  not not_323 (not_323_out, OP[5]);
  not not_324 (not_324_out, OP[4]);
  not not_325 (not_325_out, OP[3]);
  not not_326 (not_326_out, OP[2]);
  not not_327 (not_327_out, OP[1]);
  not not_328 (not_328_out, OP[0]);
  not not_329 (not_329_out, FUN[4]);
  not not_330 (not_330_out, FUN[3]);
  not not_331 (not_331_out, FUN[2]);
  not not_332 (not_332_out, OP[5]);
  not not_333 (not_333_out, OP[4]);
  not not_334 (not_334_out, OP[3]);
  not not_335 (not_335_out, OP[2]);
  not not_336 (not_336_out, OP[1]);
  not not_337 (not_337_out, OP[0]);
  not not_338 (not_338_out, FUN[4]);
  not not_339 (not_339_out, FUN[3]);
  not not_340 (not_340_out, FUN[0]);
  and and_1 (and_1_out, not_1_out, not_2_out, not_3_out, not_4_out, not_5_out, not_6_out, not_7_out, not_8_out, not_9_out, not_10_out, not_11_out, not_12_out);
  and and_2 (and_2_out, not_13_out, not_14_out, not_15_out, not_16_out, not_17_out, not_18_out, not_19_out, not_20_out, not_21_out, not_22_out, FUN[1], FUN[0]);
  and and_3 (and_3_out, not_23_out, not_24_out, not_25_out, not_26_out, not_27_out, not_28_out, not_29_out, not_30_out, not_31_out, not_32_out, FUN[1], not_33_out);
  and and_4 (and_4_out, not_34_out, not_35_out, not_36_out, not_37_out, not_38_out, not_39_out, FUN[5], not_40_out, not_41_out, not_42_out, not_43_out, not_44_out);
  and and_5 (and_5_out, not_45_out, not_46_out, not_47_out, not_48_out, not_49_out, not_50_out, FUN[5], not_51_out, not_52_out, not_53_out, not_54_out, FUN[0]);
  and and_6 (and_6_out, not_55_out, not_56_out, not_57_out, not_58_out, not_59_out, not_60_out, FUN[5], not_61_out, not_62_out, not_63_out, FUN[1], not_64_out);
  and and_7 (and_7_out, not_65_out, not_66_out, not_67_out, not_68_out, not_69_out, not_70_out, FUN[5], not_71_out, not_72_out, FUN[2], not_73_out, not_74_out);
  and and_8 (and_8_out, not_75_out, not_76_out, not_77_out, not_78_out, not_79_out, not_80_out, FUN[5], not_81_out, not_82_out, FUN[2], not_83_out, FUN[0]);
  and and_9 (and_9_out, not_84_out, not_85_out, not_86_out, not_87_out, not_88_out, not_89_out, FUN[5], not_90_out, not_91_out, FUN[2], FUN[1], FUN[0]);
  and and_10 (and_10_out, not_92_out, not_93_out, not_94_out, not_95_out, not_96_out, not_97_out, FUN[5], not_98_out, FUN[3], not_99_out, FUN[1], not_100_out);
  and and_11 (and_11_out, not_101_out, not_102_out, not_103_out, not_104_out, not_105_out, not_106_out, FUN[5], not_107_out, FUN[3], not_108_out, FUN[1], FUN[0]);
  and and_12 (and_12_out, not_109_out, not_110_out, not_111_out, not_112_out, not_113_out, not_114_out, not_115_out, not_116_out, FUN[3], not_117_out, not_118_out, not_119_out);
  and and_13 (and_13_out, not_120_out, not_121_out, not_122_out, not_123_out, not_124_out, not_125_out, not_126_out, not_127_out, FUN[3], FUN[2], not_128_out, not_129_out);
  and and_14 (and_14_out, not_130_out, not_131_out, not_132_out, OP[2], not_133_out, not_134_out);
  and and_15 (and_15_out, not_135_out, not_136_out, not_137_out, OP[2], not_138_out, OP[0]);
  and and_16 (and_16_out, not_139_out, not_140_out, OP[3], not_141_out, not_142_out, not_143_out);
  and and_17 (and_17_out, not_144_out, not_145_out, OP[3], OP[2], not_146_out, not_147_out);
  and and_18 (and_18_out, not_148_out, not_149_out, OP[3], not_150_out, not_151_out, OP[0]);
  and and_19 (and_19_out, not_152_out, not_153_out, OP[3], not_154_out, OP[1], not_155_out);
  and and_20 (and_20_out, not_156_out, not_157_out, OP[3], OP[2], not_158_out, OP[0]);
  and and_21 (and_21_out, OP[5], not_159_out, not_160_out, not_161_out, OP[1], OP[0]);
  and and_22 (and_22_out, OP[5], not_162_out, OP[3], not_163_out, OP[1], OP[0]);
  and and_23 (and_23_out, not_164_out, not_165_out, not_166_out, OP[2], OP[1], not_167_out);
  and and_24 (and_24_out, OP[5], not_168_out, OP[3], not_169_out, not_170_out, not_171_out);
  and and_25 (and_25_out, not_172_out, not_173_out, not_174_out, not_175_out, not_176_out, not_177_out, FUN[5], not_178_out, not_179_out, not_180_out, FUN[1], FUN[0]);
  and and_26 (and_26_out, not_181_out, not_182_out, not_183_out, not_184_out, not_185_out, not_186_out, FUN[5], not_187_out, not_188_out, FUN[2], FUN[1], not_189_out);
  and and_27 (and_27_out, not_190_out, not_191_out, not_192_out, not_193_out, not_194_out, not_195_out, not_196_out, not_197_out, not_198_out, not_199_out, not_200_out, not_201_out);
  and and_28 (and_28_out, not_202_out, not_203_out, not_204_out, not_205_out, not_206_out, not_207_out, not_208_out, not_209_out, not_210_out, not_211_out, FUN[1], FUN[0]);
  and and_29 (and_29_out, not_212_out, not_213_out, not_214_out, not_215_out, not_216_out, not_217_out, not_218_out, not_219_out, not_220_out, not_221_out, FUN[1], not_222_out);
  and and_30 (and_30_out, not_223_out, not_224_out, not_225_out, not_226_out, not_227_out, not_228_out, FUN[5], not_229_out, not_230_out, not_231_out, not_232_out, not_233_out);
  and and_31 (and_31_out, not_234_out, not_235_out, not_236_out, not_237_out, not_238_out, not_239_out, FUN[5], not_240_out, not_241_out, not_242_out, not_243_out, FUN[0]);
  and and_32 (and_32_out, not_244_out, not_245_out, not_246_out, not_247_out, not_248_out, not_249_out, FUN[5], not_250_out, not_251_out, not_252_out, FUN[1], not_253_out);
  and and_33 (and_33_out, not_254_out, not_255_out, not_256_out, not_257_out, not_258_out, not_259_out, FUN[5], not_260_out, not_261_out, FUN[2], not_262_out, not_263_out);
  and and_34 (and_34_out, not_264_out, not_265_out, not_266_out, not_267_out, not_268_out, not_269_out, FUN[5], not_270_out, not_271_out, FUN[2], not_272_out, FUN[0]);
  and and_35 (and_35_out, not_273_out, not_274_out, not_275_out, not_276_out, not_277_out, not_278_out, FUN[5], not_279_out, not_280_out, FUN[2], FUN[1], FUN[0]);
  and and_36 (and_36_out, not_281_out, not_282_out, not_283_out, not_284_out, not_285_out, not_286_out, FUN[5], not_287_out, FUN[3], not_288_out, FUN[1], not_289_out);
  and and_37 (and_37_out, not_290_out, not_291_out, not_292_out, not_293_out, not_294_out, not_295_out, FUN[5], not_296_out, FUN[3], not_297_out, FUN[1], FUN[0]);
  and and_38 (and_38_out, not_298_out, not_299_out, not_300_out, not_301_out, not_302_out, not_303_out, not_304_out, not_305_out, FUN[3], FUN[2], not_306_out, not_307_out);
  and and_39 (and_39_out, not_308_out, not_309_out, not_310_out, OP[2], not_311_out, not_312_out);
  and and_40 (and_40_out, not_313_out, not_314_out, not_315_out, OP[2], not_316_out, OP[0]);
  and and_41 (and_41_out, OP[5], not_317_out, OP[3], not_318_out, OP[1], OP[0]);
  and and_42 (and_42_out, OP[5], not_319_out, OP[3], not_320_out, not_321_out, not_322_out);
  and and_43 (and_43_out, not_323_out, not_324_out, not_325_out, not_326_out, not_327_out, not_328_out, FUN[5], not_329_out, not_330_out, not_331_out, FUN[1], FUN[0]);
  and and_44 (and_44_out, not_332_out, not_333_out, not_334_out, not_335_out, not_336_out, not_337_out, FUN[5], not_338_out, not_339_out, FUN[2], FUN[1], not_340_out);
  or or_1 (R2_Used, and_27_out, and_28_out, and_29_out, and_30_out, and_31_out, and_32_out, and_33_out, and_34_out, and_35_out, and_36_out, and_37_out, and_38_out, and_39_out, and_40_out, and_41_out, and_42_out, and_43_out, and_44_out);
  or or_2 (R1_Used, and_1_out, and_2_out, and_3_out, and_4_out, and_5_out, and_6_out, and_7_out, and_8_out, and_9_out, and_10_out, and_11_out, and_12_out, and_13_out, and_14_out, and_15_out, and_16_out, and_17_out, and_18_out, and_19_out, and_20_out, and_21_out, and_22_out, and_23_out, and_24_out, and_25_out, and_26_out);
endmodule

module \数据相关检测  (
  input  R1_Used,
  input  R2_Used,
  input  [4:0] R1_num,
  input  [4:0] R2_num,
  input  [5:0] EX_OP,
  input  [4:0] EX_WriteReg_num,
  input  EX_RegWrite,
  input  [4:0] MEM_WriteReg_num,
  input  MEM_RegWrite,
  output Relate,
  output Load_Use,
  output R1_EX_Relate,
  output R2_EX_Relate,
  output R1_MEM_Relate,
  output R2_MEM_Relate
);

  wire and_1_out, and_2_out, and_3_out, and_4_out, comparator_1_eq, comparator_2_eq, comparator_3_eq,
       comparator_4_eq, comparator_5_eq, comparator_6_eq, comparator_7_eq, not_1_out, not_2_out, or_1_out,
       or_2_out, or_3_out, or_4_out;

  Comparator #(.width(5), .mode("twosComplement")) comparator_1 (
    .a(R1_num), .b({5{1'b0}}), .eq(comparator_1_eq));  // open: gt, lt
  Comparator #(.width(5), .mode("twosComplement")) comparator_2 (
    .a(R2_num), .b({5{1'b0}}), .eq(comparator_2_eq));  // open: gt, lt
  Comparator #(.width(5), .mode("twosComplement")) comparator_3 (
    .a(R1_num), .b(EX_WriteReg_num), .eq(comparator_3_eq));  // open: gt, lt
  Comparator #(.width(5), .mode("twosComplement")) comparator_4 (
    .a(EX_WriteReg_num), .b(R2_num), .eq(comparator_4_eq));  // open: gt, lt
  Comparator #(.width(5), .mode("twosComplement")) comparator_5 (
    .a(R1_num), .b(MEM_WriteReg_num), .eq(comparator_5_eq));  // open: gt, lt
  Comparator #(.width(5), .mode("twosComplement")) comparator_6 (
    .a(MEM_WriteReg_num), .b(R2_num), .eq(comparator_6_eq));  // open: gt, lt
  not not_1 (not_1_out, comparator_1_eq);
  not not_2 (not_2_out, comparator_2_eq);
  and and_1 (and_1_out, not_1_out, comparator_3_eq, EX_RegWrite);
  and and_2 (and_2_out, EX_RegWrite, not_2_out, comparator_4_eq);
  and and_3 (and_3_out, not_1_out, comparator_5_eq, MEM_RegWrite);
  and and_4 (and_4_out, MEM_RegWrite, not_2_out, comparator_6_eq);
  and and_5 (R1_EX_Relate, and_1_out, R1_Used);
  and and_6 (R2_EX_Relate, and_2_out, R2_Used);
  and and_7 (R1_MEM_Relate, and_3_out, R1_Used);
  and and_8 (R2_MEM_Relate, and_4_out, R2_Used);
  or or_1 (or_1_out, and_1_out, and_3_out);
  // Probe on 6'b100011
  or or_2 (or_2_out, and_2_out, and_4_out);
  Comparator #(.width(6), .mode("twosComplement")) comparator_7 (
    .a(EX_OP), .b(6'b100011), .eq(comparator_7_eq));  // open: gt, lt
  or or_3 (or_3_out, R1_EX_Relate, R2_EX_Relate);
  and and_9 (Load_Use, comparator_7_eq, or_3_out);
  or or_4 (or_4_out, or_2_out, or_1_out);
  Multiplexer #(.select(2), .width(1), .disabled("Z"), .enable("false")) multiplexer_1 (
    .in0(1'b0), .in1(or_1_out), .in2(or_2_out), .in3(or_4_out), .out(Relate), .sel({R2_Used, R1_Used}));

  // Notes on the sheet:
  //   EX_Write_R1
  //   EX_Write_R2
  //   MEM_Write_R1
  //   MEM_Write_R2
  //   R1_EX_Relate
  //   R2_EX_Relate
  //   R1_MEM_Relate
  //   R2_MEM_Relate
  //   Only_R1_Used
  //   Only_R2_Used
  //   R1_R2_Used
endmodule
module \重定向流水动态分支预测  (
  input  [1:0] \设置为11或者10 ,
  input  [1:0] \设置为11 ,
  output RegWrite,
  output MemWrite,
  output [31:0] IF_PC,
  output [31:0] ID_PC,
  output [31:0] EX_PC,
  output [31:0] MEM_PC,
  output [31:0] WB_PC,
  output [31:0] RDin,
  output [31:0] MDin
);

  wire and_1_out, and_3_out, and_4_out, and_5_out, and_6_out, and_7_out, and_8_out, and_10_out, and_13_out,
       and_14_out, and_15_out, Bubble, CLK, comparator_1_eq, comparator_2_eq, comparator_3_eq,
       comparator_4_eq, comparator_4_lt, EX_Branch_Pre, EX_Load, ex_mem_l_1_jal_2, ex_mem_l_1_memtoreg_2,
       ex_mem_l_1_regdst_2, ex_mem_l_1_sb_2, ex_mem_l_1_syscall_2, EX_MISS, EX_RegWrite, EX_Syscall,
       final_IsStop, final_IsStop_t, Go, id_ex_l_1_alusrcb_2, id_ex_l_1_beq_2, id_ex_l_1_blez_2,
       id_ex_l_1_bne_2, id_ex_l_1_jal_2, id_ex_l_1_memtoreg_2, id_ex_l_1_memwrite_2, id_ex_l_1_regdst_2,
       id_ex_l_1_sb_2, IF_Branch_Pre, if_id_l_1_jmp_pre_2, if_id_l_1_miss_2, IF_MISS, Insert_Bubble, IR1,
       IR2, IR3, IsBranchIR_con, IsBranchIR_nocon, IsIR_JR, IsRelated, IsStop, JAL, Load_Use, MEM_RegWrite,
       mips_alu_1_equal, multiplexer_6_out, multiplexer_20_out, multiplexer_25_out, multiplexer_28_out,
       multiplexer_34_out, multiplexer_37_out, not_1_out, not_2_out, not_3_out, not_4_out, not_5_out,
       not_6_out, not_7_out, not_8_out, not_9_out, not_10_out, not_11_out, not_12_out, not_13_out,
       not_14_out, not_15_out, not_16_out, or_2_out, or_3_out, or_4_out, or_5_out, or_6_out, or_8_out,
       or_9_out, or_12_out, or_13_out, or_14_out, Predict_Success, RegDst, register_3_q, RST, RstFlow, SEL,
       SignedExt, stop, Syscall, W1, W2, W3, WB_MemToReg, xnor_1_out, \单周期硬布线控制器_1_alu_src ,
       \单周期硬布线控制器_1_beq , \单周期硬布线控制器_1_blez , \单周期硬布线控制器_1_bne , \单周期硬布线控制器_1_jal , \单周期硬布线控制器_1_jmp ,
       \单周期硬布线控制器_1_jr , \单周期硬布线控制器_1_memtoreg , \单周期硬布线控制器_1_memwrite , \单周期硬布线控制器_1_regdst ,
       \单周期硬布线控制器_1_regwrite , \单周期硬布线控制器_1_sb , \单周期硬布线控制器_1_signedext , \条件分支 , \源寄存器使用情况_1_r1_used ,
       \源寄存器使用情况_1_r2_used , \点击此键_先设置同步清零信号_out ;
  wire [1:0] EX_Forward_R1, EX_Forward_R2, EX_Next_State_Pre, EX_Now_State_Pre, ID_Forward_R1, ID_Forward_R2,
       if_id_l_1_state_now_2, IF_Now_State_Pre, multiplexer_23_out, multiplexer_26_out,
       \双位预测状态机_1_next_state , \数据相关检测_1_r1_ex_relate , \数据相关检测_1_r2_ex_relate ;
  wire [3:0] id_ex_l_1_aluop_2, \单周期硬布线控制器_1_alu_op ;
  wire [4:0] EX_WriteReg_num, MEM_WriteReg_num, multiplexer_12_out, multiplexer_13_out, multiplexer_29_out,
       multiplexer_33_out, R1_Relate, R2_Relate, WB_rd, WB_rt;
  wire [5:0] EX_OP, Func, OP;
  wire [7:0] EX_Row_Pre, if_id_l_1_row_pre_2, IF_Row_Pre, ram_1_data, ram_1_data_2, ram_1_data_3,
       ram_1_data_4;
  wire [15:0] \LoadUse次数 , \总周期数 , \插入气泡数 , \无条件分支数 , \条件分支成功数 ;
  wire [25:0] id_ex_l_1_ir_2;
  wire [25:6] if_id_l_1_ir_2;
  wire [27:2] PC_no_condition;
  wire [31:0] a0, adder_1_out, bit_extender_1_out, bit_extender_2_out, ex_mem_l_1_ir_2, ex_mem_l_1_pc_4_2,
       ex_mem_l_1_r2_2, EX_Next_PC_Pre, if_id_l_1_pc_4_2, IF_Next_PC_Pre, Jal_PC_4, LedData, MEM_ALU,
       mem_wb_l_1_ir_2, mips_alu_1_result, multiplexer_1_out, multiplexer_2_out, multiplexer_3_out,
       multiplexer_4_out, multiplexer_5_out, multiplexer_9_out, multiplexer_18_out, multiplexer_19_out,
       multiplexer_21_out, multiplexer_22_out, multiplexer_31_out, multiplexer_36_out, PC_4, PC_condition,
       R1_Old, R1_Redirect, R2_Old, R2_Redirect, rom_1_data, shifter_1_out, v0, WB_ALU, WB_ReadData;

  Multiplexer #(.select(1), .width(32), .disabled("Z"), .enable("false")) multiplexer_1 (
    .in0({PC_4[31:28], PC_no_condition, 2'b00}), .in1(R1_Redirect), .out(multiplexer_1_out), .sel(IsIR_JR));
  Multiplexer #(.select(2), .width(32), .disabled("Z"), .enable("false")) multiplexer_2 (
    .in0(multiplexer_5_out), .in1(PC_condition), .in2(multiplexer_1_out), .out(multiplexer_2_out),
    .sel({IsBranchIR_nocon, \条件分支 }));  // open: in3
  Button \u_点击此键_先设置同步清零信号  (.out(\点击此键_先设置同步清零信号_out ));
  Multiplexer #(.select(2), .width(32), .disabled("Z"), .enable("false")) multiplexer_3 (
    .in0(multiplexer_5_out), .in1(multiplexer_2_out), .in2(multiplexer_5_out), .in3(PC_4),
    .out(multiplexer_3_out), .sel({EX_Branch_Pre, Insert_Bubble}));
  Comparator #(.width(32), .mode("twosComplement")) comparator_1 (
    .a(R1_Redirect), .b(32'h22), .eq(comparator_1_eq));  // open: gt, lt
  Register #(.width(1), .trigger("falling"), .Select("low")) register_1 (
    .D(1'b0), .Q(RstFlow), .clk(RST), .preset(\点击此键_先设置同步清零信号_out ));  // open: en, clr, cs
  Register #(.width(32), .trigger("rising"), .Select("low")) PC (
    .D(multiplexer_4_out), .en(not_1_out), .Q(IF_PC), .clk(CLK), .clr(RST));
  Multiplexer #(.select(1), .width(32), .disabled("Z"), .enable("false")) multiplexer_4 (
    .in0(multiplexer_3_out), .in1(IF_PC), .out(multiplexer_4_out), .sel(stop));
  not not_1 (not_1_out, Load_Use);
  and and_1 (and_1_out, EX_Syscall, comparator_1_eq);
  not not_2 (not_2_out, comparator_1_eq);
  and and_2 (IsStop, not_2_out, EX_Syscall);
  xor xor_1 (stop, final_IsStop_t, register_3_q);
  BHT bht_1 (
    .CLK(CLK), .\读_分支指令地址 (IF_PC), .\欲写标志 (EX_Load), .\写_分支指令地址 (EX_PC), .\写_分支目标地址 (EX_Next_PC_Pre),
    .\写_更新_预测历史 (EX_Next_State_Pre), .MISS(IF_MISS), .\分支目标地址 (IF_Next_PC_Pre), .\预测历史 (IF_Now_State_Pre),
    .\IF_Row_选中的哪一行 (IF_Row_Pre), .\EX_Row_选中的哪一行_更新预测历史 (EX_Row_Pre));
  Comparator #(.width(2), .mode("twosComplement")) comparator_2 (
    .a(IF_Now_State_Pre), .b(2'b10), .eq(comparator_2_eq));  // open: gt, lt
  Comparator #(.width(2), .mode("twosComplement")) comparator_3 (
    .a(IF_Now_State_Pre), .b(2'b11), .eq(comparator_3_eq));  // open: gt, lt
  Button \u_再总复位  (.out(RST));
  Button _1 (.out(IR1));
  Button _2 (.out(IR2));
  Button _3 (.out(IR3));
  Multiplexer #(.select(1), .width(32), .disabled("Z"), .enable("false")) multiplexer_5 (
    .in0(adder_1_out), .in1(IF_Next_PC_Pre), .out(multiplexer_5_out), .sel(IF_Branch_Pre));
  Register #(.width(32), .trigger("rising"), .Select("low")) register_2 (
    .D(R2_Redirect), .Q(LedData), .clk(and_1_out), .clr(RST));  // open: en
  and and_3 (and_3_out, final_IsStop_t, Go);
  Register #(.width(1), .trigger("rising"), .Select("low")) register_3 (
    .D(1'b0), .Q(register_3_q), .clk(CLK), .clr(RST), .preset(and_3_out));  // open: en, cs
  or or_1 (IF_Branch_Pre, comparator_2_eq, comparator_3_eq);
  Button \u_继续运行  (.out(Go));
  LED #(.active("true")) led_1 (.in(W1));
  LED #(.active("true")) led_2 (.in(W2));
  LED #(.active("true")) led_3 (.in(W3));
  Adder #(.width(32)) adder_1 (.a(IF_PC), .b(32'h4), .out(adder_1_out));  // open: cin, cout
  Multiplexer #(.select(1), .width(1), .disabled("Z"), .enable("false")) multiplexer_6 (
    .in0(final_IsStop_t), .in1(1'b0), .out(multiplexer_6_out), .sel(register_3_q));
  Hex_Digit_Display hex_digit_display_1 (.value(LedData[27:24]));  // open: dp
  Hex_Digit_Display hex_digit_display_2 (.value(LedData[31:28]));  // open: dp
  \源寄存器使用情况  \u_源寄存器使用情况_1  (.OP(OP), .FUN(Func), .R1_Used(\源寄存器使用情况_1_r1_used ), .R2_Used(\源寄存器使用情况_1_r2_used ));
  ROM #(.addrWidth(10), .dataWidth(32), .Select("high")) rom_1 (.addr(IF_PC[11:2]), .data(rom_1_data));
  or or_2 (or_2_out, Insert_Bubble, RstFlow);
  Multiplexer #(.select(1), .width(1), .disabled("Z"), .enable("false")) multiplexer_7 (
    .in0(multiplexer_6_out), .in1(1'b0), .out(SEL), .sel(or_2_out));
  or or_3 (or_3_out, SEL, Load_Use);
  Hex_Digit_Display hex_digit_display_3 (.value(LedData[23:20]));  // open: dp
  Hex_Digit_Display hex_digit_display_4 (.value(LedData[19:16]));  // open: dp
  or or_4 (or_4_out, RST, CLK);
  Hex_Digit_Display hex_digit_display_5 (.value(LedData[11:8]));  // open: dp
  Hex_Digit_Display hex_digit_display_6 (.value(LedData[15:12]));  // open: dp
  \数据相关检测  \u_数据相关检测_1  (
    .R1_Used(\源寄存器使用情况_1_r1_used ), .R2_Used(\源寄存器使用情况_1_r2_used ), .R1_num(R1_Relate), .R2_num(R2_Relate),
    .EX_WriteReg_num(EX_WriteReg_num), .EX_RegWrite(EX_RegWrite), .MEM_WriteReg_num(MEM_WriteReg_num),
    .MEM_RegWrite(MEM_RegWrite), .Relate(IsRelated), .EX_OP(EX_OP), .Load_Use(Load_Use),
    .R1_EX_Relate(\数据相关检测_1_r1_ex_relate [0]), .R2_EX_Relate(\数据相关检测_1_r2_ex_relate [0]),
    .R1_MEM_Relate(\数据相关检测_1_r1_ex_relate [1]), .R2_MEM_Relate(\数据相关检测_1_r2_ex_relate [1]));
  IF_ID_l if_id_l_1 (
    .CLK(or_4_out), .\同步清零_气泡_高电平有效 (or_2_out), .\使能端_低电平有效 (or_3_out), .PC(IF_PC), .PC_2(ID_PC),
    .IR(rom_1_data), .IR_2({OP, if_id_l_1_ir_2, Func}), .PC_4(adder_1_out), .PC_4_2(if_id_l_1_pc_4_2),
    .MISS(IF_MISS), .MISS_2(if_id_l_1_miss_2), .JMP_Pre(IF_Branch_Pre), .JMP_Pre_2(if_id_l_1_jmp_pre_2),
    .State_Now(IF_Now_State_Pre), .State_Now_2(if_id_l_1_state_now_2), .Row_Pre(IF_Row_Pre),
    .Row_Pre_2(if_id_l_1_row_pre_2));
  Hex_Digit_Display hex_digit_display_7 (.value(LedData[3:0]));  // open: dp
  Hex_Digit_Display hex_digit_display_8 (.value(LedData[7:4]));  // open: dp
  Clock #(.highDuration(1), .lowDuration(1)) clock_1 (.out(CLK));
  Multiplexer #(.select(2), .width(32), .disabled("Z"), .enable("false")) multiplexer_8 (
    .in0(R1_Old), .in1(MEM_ALU), .in2(multiplexer_9_out), .in3(MEM_ALU), .out(R1_Redirect),
    .sel(EX_Forward_R1));
  Multiplexer #(.select(1), .width(32), .disabled("Z"), .enable("false")) multiplexer_9 (
    .in0(WB_ALU), .in1(WB_ReadData), .out(multiplexer_9_out), .sel(WB_MemToReg));
  \单周期硬布线控制器  \u_单周期硬布线控制器_1  (
    .Func(Func), .OP(OP), .ALU_OP(\单周期硬布线控制器_1_alu_op ), .MemToReg(\单周期硬布线控制器_1_memtoreg ),
    .MemWrite(\单周期硬布线控制器_1_memwrite ), .ALU_SRC(\单周期硬布线控制器_1_alu_src ), .RegWrite(\单周期硬布线控制器_1_regwrite ),
    .SysCALL(Syscall), .SignedExt(\单周期硬布线控制器_1_signedext ), .RegDst(\单周期硬布线控制器_1_regdst ),
    .JR(\单周期硬布线控制器_1_jr ), .JMP(\单周期硬布线控制器_1_jmp ), .Beq(\单周期硬布线控制器_1_beq ), .JAL(\单周期硬布线控制器_1_jal ),
    .Bne(\单周期硬布线控制器_1_bne ), .BLEZ(\单周期硬布线控制器_1_blez ), .SB(\单周期硬布线控制器_1_sb ));
  Multiplexer #(.select(1), .width(5), .disabled("Z"), .enable("false")) multiplexer_10 (
    .in0(if_id_l_1_ir_2[25:21]), .in1(5'b00010), .out(R1_Relate), .sel(Syscall));
  Multiplexer #(.select(1), .width(5), .disabled("Z"), .enable("false")) multiplexer_11 (
    .in0(if_id_l_1_ir_2[20:16]), .in1(5'b00100), .out(R2_Relate), .sel(Syscall));
  Multiplexer #(.select(1), .width(5), .disabled("Z"), .enable("false")) multiplexer_12 (
    .in0(WB_rt), .in1(WB_rd), .out(multiplexer_12_out), .sel(RegDst));
  Multiplexer #(.select(1), .width(5), .disabled("Z"), .enable("false")) multiplexer_13 (
    .in0(multiplexer_12_out), .in1({5{1'b1}}), .out(multiplexer_13_out), .sel(JAL));
  Multiplexer #(.select(1), .width(32), .disabled("Z"), .enable("false")) multiplexer_14 (
    .in0(multiplexer_36_out), .in1(Jal_PC_4), .out(RDin), .sel(JAL));
  // Probe on \总周期数 
  // Probe on \无条件分支数 
  // Probe on \条件分支成功数 
  // Probe on \插入气泡数 
  // Probe on \LoadUse次数 
  Multiplexer #(.select(1), .width(2), .disabled("Z"), .enable("false")) multiplexer_15 (
    .in0(\数据相关检测_1_r2_ex_relate ), .in1(2'b00), .out(ID_Forward_R2), .sel(Load_Use));
  // Probe on IF_PC[11:0]
  // Probe on ID_PC[11:0]
  // Probe on EX_PC[11:0]
  Multiplexer #(.select(1), .width(2), .disabled("Z"), .enable("false")) multiplexer_16 (
    .in0(\数据相关检测_1_r1_ex_relate ), .in1(2'b00), .out(ID_Forward_R1), .sel(Load_Use));
  MIPS_Regifile mips_regifile_1 (
    .Din(RDin), .Clk(CLK), .R1(v0), .R2(a0), .WE(RegWrite), .W_num(multiplexer_13_out), .R1_num(R1_Relate),
    .R2_num(R2_Relate));
  or or_5 (or_5_out, Insert_Bubble, Load_Use, RstFlow);
  // Probe on MEM_PC[11:0]
  or or_6 (or_6_out, RST, CLK);
  // Probe on WB_PC[11:0]
  ID_EX_l id_ex_l_1 (
    .CLK(or_6_out), .\同步清零_气泡_高电平有效 (or_5_out), .\使能端_低电平有效 (SEL), .PC(ID_PC), .R1(v0),
    .BLEZ(\单周期硬布线控制器_1_blez ), .SignedExt(\单周期硬布线控制器_1_signedext ), .MemToReg(\单周期硬布线控制器_1_memtoreg ),
    .MemWrite(\单周期硬布线控制器_1_memwrite ), .BEQ(\单周期硬布线控制器_1_beq ), .Syscall(Syscall),
    .RegWrite(\单周期硬布线控制器_1_regwrite ), .SB(\单周期硬布线控制器_1_sb ), .BNE(\单周期硬布线控制器_1_bne ),
    .RegDst(\单周期硬布线控制器_1_regdst ), .IR({OP, if_id_l_1_ir_2, Func}), .R2(a0), .AluSrcB(\单周期硬布线控制器_1_alu_src ),
    .JR(\单周期硬布线控制器_1_jr ), .JAL(\单周期硬布线控制器_1_jal ), .AluOP(\单周期硬布线控制器_1_alu_op ),
    .Imm26({if_id_l_1_ir_2, Func}), .JMP(\单周期硬布线控制器_1_jmp ), .PC_2(EX_PC), .R1_2(R1_Old),
    .BLEZ_2(id_ex_l_1_blez_2), .SignedExt_2(SignedExt), .MemToReg_2(id_ex_l_1_memtoreg_2),
    .MemWrite_2(id_ex_l_1_memwrite_2), .BEQ_2(id_ex_l_1_beq_2), .Syscall_2(EX_Syscall),
    .RegWrite_2(EX_RegWrite), .SB_2(id_ex_l_1_sb_2), .BNE_2(id_ex_l_1_bne_2), .RegDst_2(id_ex_l_1_regdst_2),
    .IR_2({EX_OP, id_ex_l_1_ir_2}), .R2_2(R2_Old), .AluSrcB_2(id_ex_l_1_alusrcb_2), .JR_2(IsIR_JR),
    .JAL_2(id_ex_l_1_jal_2), .AluOP_2(id_ex_l_1_aluop_2), .Imm26_2(PC_no_condition),
    .JMP_2(IsBranchIR_nocon), .PC_4(if_id_l_1_pc_4_2), .PC_4_2(PC_4), .Forwarding_R1(ID_Forward_R1),
    .Forwarding_R1_2(EX_Forward_R1), .Forwarding_R2(ID_Forward_R2), .Forwarding_R2_2(EX_Forward_R2),
    .MISS(if_id_l_1_miss_2), .MISS_2(EX_MISS), .JMP_Pre(if_id_l_1_jmp_pre_2), .JMP_Pre_2(EX_Branch_Pre),
    .State_Now(if_id_l_1_state_now_2), .State_Now_2(EX_Now_State_Pre), .Row_Pre(if_id_l_1_row_pre_2),
    .Row_Pre_2(EX_Row_Pre));
  not not_3 (not_3_out, stop);
  Multiplexer #(.select(2), .width(32), .disabled("Z"), .enable("false")) multiplexer_17 (
    .in0(R2_Old), .in1(MEM_ALU), .in2(multiplexer_18_out), .in3(MEM_ALU), .out(R2_Redirect),
    .sel(EX_Forward_R2));
  Multiplexer #(.select(1), .width(32), .disabled("Z"), .enable("false")) multiplexer_18 (
    .in0(WB_ALU), .in1(WB_ReadData), .out(multiplexer_18_out), .sel(WB_MemToReg));
  or or_7 (IsBranchIR_con, id_ex_l_1_blez_2, id_ex_l_1_beq_2, id_ex_l_1_bne_2);
  assign bit_extender_1_out = {{16{1'b0}}, PC_no_condition[17:2]};  // Bit_Extender bit_extender_1
  assign bit_extender_2_out = {{16{PC_no_condition[17]}}, PC_no_condition[17:2]};  // Bit_Extender bit_extender_2
  Multiplexer #(.select(1), .width(32), .disabled("Z"), .enable("false")) multiplexer_19 (
    .in0({PC_4[31:28], PC_no_condition, 2'b00}), .in1(R1_Redirect), .out(multiplexer_19_out), .sel(IsIR_JR));
  Counter #(.width(16), .max('hffff), .ongoal("wrap"), .trigger("rising"), .behavior("old")) counter_1 (
    .count(1'b1), .Q(\总周期数 ), .clk(multiplexer_20_out), .clr(RST));  // open: load, D, carry, preset
  Multiplexer #(.select(1), .width(1), .disabled("Z"), .enable("false")) multiplexer_20 (
    .in0(and_4_out), .in1(1'b0), .out(multiplexer_20_out), .sel(not_4_out));
  not not_4 (not_4_out, not_5_out);
  and and_4 (and_4_out, not_3_out, CLK);
  Comparator #(.width(32), .mode("twosComplement")) comparator_4 (
    .a(R1_Redirect), .b({32{1'b0}}), .eq(comparator_4_eq), .lt(comparator_4_lt));  // open: gt
  not not_5 (not_5_out, CLK);
  or or_8 (or_8_out, comparator_4_eq, comparator_4_lt);
  Multiplexer #(.select(1), .width(32), .disabled("Z"), .enable("false")) multiplexer_21 (
    .in0(R2_Redirect), .in1(multiplexer_22_out), .out(multiplexer_21_out), .sel(id_ex_l_1_alusrcb_2));
  Multiplexer #(.select(1), .width(32), .disabled("Z"), .enable("false")) multiplexer_22 (
    .in0(bit_extender_1_out), .in1(bit_extender_2_out), .out(multiplexer_22_out), .sel(SignedExt));
  Shifter #(.width(32), .shift("ll")) shifter_1 (.in(multiplexer_22_out), .\dist (5'b00010), .out(shifter_1_out));
  and and_5 (and_5_out, or_8_out, id_ex_l_1_blez_2);
  Adder #(.width(32)) adder_2 (.a(shifter_1_out), .b(PC_4), .out(PC_condition));  // open: cin, cout
  \双位预测状态机  \u_双位预测状态机_1  (.Now_State(EX_Now_State_Pre), .Branch(Bubble), .Next_State(\双位预测状态机_1_next_state ));
  Multiplexer #(.select(1), .width(2), .disabled("Z"), .enable("false")) multiplexer_23 (
    .in0(\设置为11或者10 ), .in1(\设置为11 ), .out(multiplexer_23_out), .sel(IsBranchIR_con));
  Multiplexer #(.select(1), .width(32), .disabled("Z"), .enable("false")) multiplexer_24 (
    .in0(multiplexer_19_out), .in1(PC_condition), .out(EX_Next_PC_Pre), .sel(IsBranchIR_con));
  Multiplexer #(.select(1), .width(1), .disabled("Z"), .enable("false")) multiplexer_25 (
    .in0(and_6_out), .in1(1'b0), .out(multiplexer_25_out), .sel(not_8_out));
  and and_6 (and_6_out, IsBranchIR_nocon, CLK);
  not not_6 (not_6_out, mips_alu_1_equal);
  MIPS_ALU mips_alu_1 (
    .X(R1_Redirect), .Y(multiplexer_21_out), .AluOP(id_ex_l_1_aluop_2), .Equal(mips_alu_1_equal),
    .Result(mips_alu_1_result), .shamt(PC_no_condition[12:8]));  // open: Result_2
  or or_9 (or_9_out, IsBranchIR_con, IsBranchIR_nocon);
  Multiplexer #(.select(1), .width(2), .disabled("Z"), .enable("false")) multiplexer_26 (
    .in1(multiplexer_23_out), .out(multiplexer_26_out), .sel(or_9_out));  // open: in0
  Counter #(.width(16), .max('hffff), .ongoal("wrap"), .trigger("rising"), .behavior("old")) counter_2 (
    .count(1'b1), .Q(\无条件分支数 ), .clk(multiplexer_25_out), .clr(RST));  // open: load, D, carry, preset
  not not_7 (not_7_out, CLK);
  not not_8 (not_8_out, not_7_out);
  and and_7 (and_7_out, mips_alu_1_equal, id_ex_l_1_beq_2);
  and and_8 (and_8_out, id_ex_l_1_bne_2, not_6_out);
  or or_10 (\条件分支 , and_5_out, and_8_out, and_7_out);
  or or_11 (Bubble, IsBranchIR_nocon, \条件分支 );
  Multiplexer #(.select(1), .width(2), .disabled("Z"), .enable("false")) multiplexer_27 (
    .in0(\双位预测状态机_1_next_state ), .in1(multiplexer_26_out), .out(EX_Next_State_Pre), .sel(EX_MISS));
  xnor xnor_1 (xnor_1_out, Bubble, EX_Branch_Pre);
  or or_12 (or_12_out, RST, CLK);
  and and_9 (Predict_Success, xnor_1_out, or_9_out);
  Multiplexer #(.select(1), .width(1), .disabled("Z"), .enable("false")) multiplexer_28 (
    .in0(and_10_out), .in1(1'b0), .out(multiplexer_28_out), .sel(not_10_out));
  and and_10 (and_10_out, \条件分支 , CLK);
  Multiplexer #(.select(1), .width(5), .disabled("Z"), .enable("false")) multiplexer_29 (
    .in0(id_ex_l_1_ir_2[20:16]), .in1(id_ex_l_1_ir_2[15:11]), .out(multiplexer_29_out),
    .sel(id_ex_l_1_regdst_2));
  EX_MEM_l ex_mem_l_1 (
    .CLK(or_12_out), .\同步清零_气泡_高电平有效 (RstFlow), .\使能端_低电平有效 (SEL), .PC(EX_PC),
    .MemToReg(id_ex_l_1_memtoreg_2), .MemWrite(id_ex_l_1_memwrite_2), .RegWrite(EX_RegWrite),
    .SB(id_ex_l_1_sb_2), .RegDst(id_ex_l_1_regdst_2), .IR({EX_OP, id_ex_l_1_ir_2}), .R2(R2_Redirect),
    .JAL(id_ex_l_1_jal_2), .PC_2(MEM_PC), .MemToReg_2(ex_mem_l_1_memtoreg_2), .MemWrite_2(MemWrite),
    .RegWrite_2(MEM_RegWrite), .SB_2(ex_mem_l_1_sb_2), .RegDst_2(ex_mem_l_1_regdst_2),
    .IR_2(ex_mem_l_1_ir_2), .R2_2(ex_mem_l_1_r2_2), .JAL_2(ex_mem_l_1_jal_2), .ALU(mips_alu_1_result),
    .ALU_2(MEM_ALU), .PC_4(PC_4), .PC_4_2(ex_mem_l_1_pc_4_2), .Syscall(IsStop),
    .Syscall_2(ex_mem_l_1_syscall_2));
  // Probe on Predict_Success
  Counter #(.width(16), .max('hffff), .ongoal("wrap"), .trigger("rising"), .behavior("old")) counter_3 (
    .count(1'b1), .Q(\条件分支成功数 ), .clk(multiplexer_28_out), .clr(RST));  // open: load, D, carry, preset
  not not_9 (not_9_out, CLK);
  not not_10 (not_10_out, not_9_out);
  Multiplexer #(.select(1), .width(5), .disabled("Z"), .enable("false")) multiplexer_30 (
    .in0(multiplexer_29_out), .in1({5{1'b1}}), .out(EX_WriteReg_num), .sel(id_ex_l_1_jal_2));
  not not_11 (not_11_out, Predict_Success);
  and and_11 (EX_Load, EX_MISS, or_9_out);
  and and_12 (Insert_Bubble, or_9_out, not_11_out);
  Multiplexer #(.select(2), .width(32), .disabled("Z"), .enable("false")) multiplexer_31 (
    .in0({ram_1_data, ram_1_data_4, ram_1_data_3, ex_mem_l_1_r2_2[7:0]}),
    .in1({ram_1_data, ram_1_data_4, ex_mem_l_1_r2_2[7:0], ram_1_data_2}),
    .in2({ram_1_data, ex_mem_l_1_r2_2[7:0], ram_1_data_3, ram_1_data_2}),
    .in3({ex_mem_l_1_r2_2[7:0], ram_1_data_4, ram_1_data_3, ram_1_data_2}), .out(multiplexer_31_out),
    .sel(MEM_ALU[1:0]));
  not not_12 (not_12_out, final_IsStop);
  or or_13 (or_13_out, Bubble, Load_Use);
  Multiplexer #(.select(1), .width(32), .disabled("Z"), .enable("false")) multiplexer_32 (
    .in0(ex_mem_l_1_r2_2), .in1(multiplexer_31_out), .out(MDin), .sel(ex_mem_l_1_sb_2));
  and and_13 (and_13_out, not_12_out, or_13_out);
  and and_14 (and_14_out, and_13_out, CLK);
  Multiplexer #(.select(1), .width(5), .disabled("Z"), .enable("false")) multiplexer_33 (
    .in0(ex_mem_l_1_ir_2[20:16]), .in1(ex_mem_l_1_ir_2[15:11]), .out(multiplexer_33_out),
    .sel(ex_mem_l_1_regdst_2));
  Counter #(.width(16), .max('hffff), .ongoal("wrap"), .trigger("rising"), .behavior("old")) counter_4 (
    .count(1'b1), .Q(\插入气泡数 ), .clk(multiplexer_34_out), .clr(RST));  // open: load, D, carry, preset
  Multiplexer #(.select(1), .width(1), .disabled("Z"), .enable("false")) multiplexer_34 (
    .in0(and_14_out), .in1(1'b0), .out(multiplexer_34_out), .sel(not_13_out));
  not not_13 (not_13_out, not_14_out);
  Multiplexer #(.select(1), .width(5), .disabled("Z"), .enable("false")) multiplexer_35 (
    .in0(multiplexer_33_out), .in1({5{1'b1}}), .out(MEM_WriteReg_num), .sel(ex_mem_l_1_jal_2));
  RAM #(.addrWidth(10), .dataWidth(32), .bus("separate"), .Select("high")) ram_1 (
    .addr(MEM_ALU[11:2]), .din(MDin), .data({ram_1_data, ram_1_data_4, ram_1_data_3, ram_1_data_2}),
    .str(MemWrite), .clk(CLK), .clr(RST));  // open: sel, ld
  not not_14 (not_14_out, CLK);
  or or_14 (or_14_out, RST, CLK);
  MEM_WB_l mem_wb_l_1 (
    .CLK(or_14_out), .\同步清零_气泡_高电平有效 (RstFlow), .\使能端_低电平有效 (SEL), .PC(MEM_PC),
    .MemToReg(ex_mem_l_1_memtoreg_2), .PC_2(WB_PC), .MemToReg_2(WB_MemToReg), .RegWrite(MEM_RegWrite),
    .RegWrite_2(RegWrite), .RegDst(ex_mem_l_1_regdst_2), .IR(ex_mem_l_1_ir_2),
    .MD({ram_1_data, ram_1_data_4, ram_1_data_3, ram_1_data_2}), .RegDst_2(RegDst),
    .IR_2({mem_wb_l_1_ir_2[31:21], WB_rt, WB_rd, mem_wb_l_1_ir_2[10:0]}), .MD_2(WB_ReadData),
    .JAL(ex_mem_l_1_jal_2), .JAL_2(JAL), .ALU(MEM_ALU), .ALU_2(WB_ALU), .PC_4(ex_mem_l_1_pc_4_2),
    .PC_4_2(Jal_PC_4), .Syscall(ex_mem_l_1_syscall_2), .Syscall_2(final_IsStop));
  Multiplexer #(.select(1), .width(32), .disabled("Z"), .enable("false")) multiplexer_36 (
    .in0(WB_ALU), .in1(WB_ReadData), .out(multiplexer_36_out), .sel(WB_MemToReg));
  Counter #(.width(16), .max('hffff), .ongoal("wrap"), .trigger("rising"), .behavior("old")) counter_5 (
    .count(1'b1), .Q(\LoadUse次数 ), .clk(multiplexer_37_out), .clr(RST));  // open: load, D, carry, preset
  Multiplexer #(.select(1), .width(1), .disabled("Z"), .enable("false")) multiplexer_37 (
    .in0(and_15_out), .in1(1'b0), .out(multiplexer_37_out), .sel(not_15_out));
  not not_15 (not_15_out, not_16_out);
  and and_15 (and_15_out, Load_Use, CLK);
  not not_16 (not_16_out, CLK);

  // Other names for the same wires on the sheet: 无条件分支 = IsBranchIR_nocon; B_condition_init[1:0] = \设置为11 ;
  //   B_Nocondition_init[1:0] = \设置为11或者10 ; PC_no_condition[31:28] = PC_4[31:28]; RS[31:0] = R1_Redirect

  // Notes on the sheet:
  //   设置重定向的预测初值
  //   若不命中，该值默认为0
  //   中断源
  //   缺失时，默认为0，即选择PC+4
  //   中断等待指示
  //   指令存储器
  //   R1_Used
  //   R2_Used
  //   contents of rom_1 (hex, n*v repeats v):
  //   20110001 8000c05 20110001 20120002 20130003 8000c09 20110001 20120002 20130003 8000c0d 20110001
  //   20120002 20130003 8000c11 20110001 20120002 20130003 c000cf5 20100001 20110001 118fc0 112020
  //   20020022 c 118882 12200001 8000c15 112020 20020022 c 20110001 118880 112020 20020022 c 12200001
  //   8000c1f 20110001 118fc0 112020 20020022 c 1188c3 112020 20020022 c 118903 112020 20020022 c 118903
  //   112020 20020022 c 118903 112020 20020022 c 118903 112020 20020022 c 118903 112020 20020022 c 118903
  //   112020 20020022 c 118903 112020 20020022 c 20100001 109fc0 139fc3 8021 2012000c 24160003 26100001
  //   3210000f 20080008 20090001 139900 2709825 132020 20020022 c 1094022 1500fff9 22100001 2018000f
  //   2188024 108700 20080008 20090001 139902 2709825 132021 20020022 c 1094022 1500fff9 108702 2c9b022
  //   12c00001 8000c50 4020 1084027 84400 3508ffff 82021 20020022 c 2010ffff 20110000 ae300000 22100001
  //   22310004 ae300000 22100001 22310004 ae300000 22100001 22310004 ae300000 22100001 22310004 ae300000
  //   22100001 22310004 ae300000 22100001 22310004 ae300000 22100001 22310004 ae300000 22100001 22310004
  //   ae300000 22100001 22310004 ae300000 22100001 22310004 ae300000 22100001 22310004 ae300000 22100001
  //   22310004 ae300000 22100001 22310004 ae300000 22100001 22310004 ae300000 22100001 22310004 ae300000
  //   22100001 22310004 22100001 8020 2011003c 8e130000 8e340000 274402a 11000002 ae330000 ae140000
  //   2231fffc 1611fff8 102020 20020022 c 22100004 2011003c 1611fff2 20020032 c 20080001 20110010 112020
  //   20020022 c 200b0020 2288823 112020 20020022 c 216bffff 1560fffa 2002000a c 2008ffff 20117777 112020
  //   20020022 c 200b0010 2288826 112020 20020022 c 216bffff 1560fffa 2002000a c 20090000 200b0020
  //   20110000 20120001 a1310000 112020 20020022 c 2328820 21290001 216bffff 1560fff8 200b0008 20090000
  //   8d310000 112020 20020022 c 21290004 216bffff 1560fff9 2002000a c 2011fff1 112020 20020022 c 22310001
  //   1a20fffb 2002000a c 2002000a c 20100000 22100001 102020 20020022 c 22100002 102020 20020022 c
  //   22100003 102020 20020022 c 22100004 102020 20020022 c 22100005 102020 20020022 c 22100006 102020
  //   20020022 c 22100007 102020 20020022 c 22100008 102020 20020022 20020022 c 3e00008
  //   数码管输出
  //   PC+4
  //   IR
  //   PC
  //   指令字
  //   OP
  //   Func
  //   rs
  //   rt
  //   rd
  //   Imm26
  //   Bubble统计的是分支相关数，load_use是数据相关时处理的气泡数
  //   流水调试日志用
  //   IR
  //   PC
  //   初值
  //   rt
  //   rd
  //   MemWrite
  //   SB
  //   IR
  //   PC
  //   R2
  //   ALU
  //   rt
  //   rd
  //   MemToReg
  //   rt
  //   rd
endmodule

// 状
module \双位预测状态机  (
  input  [1:0] Now_State,
  input  Branch,
  output [1:0] Next_State
);

  wire and_1_out, and_2_out, and_3_out, and_4_out, not_1_out, not_2_out, not_3_out, not_4_out, not_5_out;

  not not_1 (not_1_out, Now_State[0]);
  not not_2 (not_2_out, Now_State[1]);
  not not_3 (not_3_out, Now_State[0]);
  not not_4 (not_4_out, Now_State[0]);
  not not_5 (not_5_out, Branch);
  and and_1 (and_1_out, Now_State[0], Branch);
  and and_2 (and_2_out, Now_State[1], not_1_out);
  and and_3 (and_3_out, not_2_out, not_3_out, Branch);
  and and_4 (and_4_out, Now_State[1], not_4_out, not_5_out);
  or or_1 (Next_State[1], and_1_out, and_2_out);
  or or_2 (Next_State[0], and_3_out, and_4_out);
endmodule

module BHT (
  input  [31:0] \读_分支指令地址 ,
  input  [7:0] \EX_Row_选中的哪一行_更新预测历史 ,
  input  [1:0] \写_更新_预测历史 ,
  input  \欲写标志 ,
  input  [31:0] \写_分支目标地址 ,
  input  [31:0] \写_分支指令地址 ,
  input  CLK,
  output [1:0] \预测历史 ,
  output [7:0] \IF_Row_选中的哪一行 ,
  output [31:0] \分支目标地址 ,
  output MISS
);

  wire and_9_out, and_10_out, and_11_out, and_12_out, and_13_out, and_14_out, and_15_out, and_16_out,
       not_1_out, not_2_out, not_3_out, not_4_out, not_5_out, not_6_out, not_7_out, not_8_out, or_1_out,
       or_2_out, or_3_out, or_4_out, or_5_out, or_6_out, or_7_out, or_8_out, ToWriteW0, ToWriteW1, ToWriteW2,
       ToWriteW3, ToWriteW4, ToWriteW5, ToWriteW6, ToWriteW7, V0, V1, V2, V3, V4, V5, V6, V7, W0, W1, W2, W3,
       W4, W5, W6, W7;
  wire [1:0] controlled_buffer_9_out, \预测历史_2_q , \预测历史_3_q , \预测历史_4_q , \预测历史_5_q , \预测历史_6_q , \预测历史_7_q ,
       \预测历史_8_q , \预测历史_q ;
  wire [2:0] \bht写控制_1_towritre_num ;
  wire [15:0] Count0, Count1, Count2, Count3, Count4, Count5, Count6, Count7;
  wire [31:0] controlled_buffer_1_out, \分支指令地址_2_q , \分支指令地址_3_q , \分支指令地址_4_q , \分支指令地址_5_q , \分支指令地址_6_q ,
       \分支指令地址_7_q , \分支指令地址_8_q , \分支指令地址_q , \分支目标地址_2_q , \分支目标地址_3_q , \分支目标地址_4_q , \分支目标地址_5_q ,
       \分支目标地址_6_q , \分支目标地址_7_q , \分支目标地址_8_q , \分支目标地址_q ;

  Register #(.width(1), .trigger("rising"), .Select("low")) VALID (
    .D(1'b1), .en(ToWriteW0), .Q(V0), .clk(CLK));  // open: clr
  and and_1 (ToWriteW0, \欲写标志 , W0);
  Register #(.width(1), .trigger("rising"), .Select("low")) VALID_2 (
    .D(1'b1), .en(ToWriteW1), .Q(V1), .clk(CLK));  // open: clr
  and and_2 (ToWriteW1, \欲写标志 , W1);
  Register #(.width(1), .trigger("rising"), .Select("low")) VALID_3 (
    .D(1'b1), .en(ToWriteW2), .Q(V2), .clk(CLK));  // open: clr
  and and_3 (ToWriteW2, \欲写标志 , W2);
  Register #(.width(1), .trigger("rising"), .Select("low")) VALID_4 (
    .D(1'b1), .en(ToWriteW3), .Q(V3), .clk(CLK));  // open: clr
  and and_4 (ToWriteW3, \欲写标志 , W3);
  Register #(.width(1), .trigger("rising"), .Select("low")) VALID_5 (
    .D(1'b1), .en(ToWriteW4), .Q(V4), .clk(CLK));  // open: clr
  and and_5 (ToWriteW4, \欲写标志 , W4);
  Register #(.width(1), .trigger("rising"), .Select("low")) VALID_6 (
    .D(1'b1), .en(ToWriteW5), .Q(V5), .clk(CLK));  // open: clr
  and and_6 (ToWriteW5, \欲写标志 , W5);
  Register #(.width(1), .trigger("rising"), .Select("low")) VALID_7 (
    .D(1'b1), .en(ToWriteW6), .Q(V6), .clk(CLK));  // open: clr
  and and_7 (ToWriteW6, \欲写标志 , W6);
  Register #(.width(1), .trigger("rising"), .Select("low")) VALID_8 (
    .D(1'b1), .en(ToWriteW7), .Q(V7), .clk(CLK));  // open: clr
  and and_8 (ToWriteW7, \欲写标志 , W7);
  Register #(.width(32), .trigger("rising"), .Select("low")) \u_分支指令地址  (
    .D(\写_分支指令地址 ), .en(ToWriteW0), .Q(\分支指令地址_q ), .clk(CLK));  // open: clr
  Register #(.width(32), .trigger("rising"), .Select("low")) \u_分支指令地址_2  (
    .D(\写_分支指令地址 ), .en(ToWriteW1), .Q(\分支指令地址_2_q ), .clk(CLK));  // open: clr
  Register #(.width(32), .trigger("rising"), .Select("low")) \u_分支指令地址_3  (
    .D(\写_分支指令地址 ), .en(ToWriteW2), .Q(\分支指令地址_3_q ), .clk(CLK));  // open: clr
  Register #(.width(32), .trigger("rising"), .Select("low")) \u_分支指令地址_4  (
    .D(\写_分支指令地址 ), .en(ToWriteW3), .Q(\分支指令地址_4_q ), .clk(CLK));  // open: clr
  Register #(.width(32), .trigger("rising"), .Select("low")) \u_分支指令地址_5  (
    .D(\写_分支指令地址 ), .en(ToWriteW4), .Q(\分支指令地址_5_q ), .clk(CLK));  // open: clr
  Register #(.width(32), .trigger("rising"), .Select("low")) \u_分支指令地址_6  (
    .D(\写_分支指令地址 ), .en(ToWriteW5), .Q(\分支指令地址_6_q ), .clk(CLK));  // open: clr
  Register #(.width(32), .trigger("rising"), .Select("low")) \u_分支指令地址_7  (
    .D(\写_分支指令地址 ), .en(ToWriteW6), .Q(\分支指令地址_7_q ), .clk(CLK));  // open: clr
  Register #(.width(32), .trigger("rising"), .Select("low")) \u_分支指令地址_8  (
    .D(\写_分支指令地址 ), .en(ToWriteW7), .Q(\分支指令地址_8_q ), .clk(CLK));  // open: clr
  \BHT写控制  \bht写控制_1  (
    .V0(V0), .V1(V1), .V2(V2), .V3(V3), .V4(V4), .V5(V5), .V6(V6), .V7(V7), .LRUCount0(Count0),
    .LRUCount1(Count1), .LRUCount2(Count2), .LRUCount3(Count3), .LRUCount4(Count4), .LRUCount5(Count5),
    .LRUCount6(Count6), .LRUCount7(Count7), .ToWritre_num(\bht写控制_1_towritre_num ));
  \八路并发比较  \u_八路并发比较_1  (
    .in_3(\分支指令地址_q ), .in_4(V0), .in_5(\分支指令地址_2_q ), .in_6(V1), .in_7(\分支指令地址_3_q ), .in_8(V2),
    .in_9(\分支指令地址_4_q ), .in_10(V3), .in_11(\分支指令地址_5_q ), .in_12(V4), .in_13(\分支指令地址_6_q ), .in_14(V5),
    .in_15(\分支指令地址_7_q ), .in_16(V6), .in_17(\分支指令地址_8_q ), .in_18(V7), .K0(\IF_Row_选中的哪一行 [0]),
    .K1(\IF_Row_选中的哪一行 [1]), .K2(\IF_Row_选中的哪一行 [2]), .K3(\IF_Row_选中的哪一行 [3]), .K4(\IF_Row_选中的哪一行 [4]),
    .K5(\IF_Row_选中的哪一行 [5]), .K6(\IF_Row_选中的哪一行 [6]), .K7(\IF_Row_选中的哪一行 [7]), .V(1'b1),
    .\分支指令地址 (\读_分支指令地址 ), .Miss(MISS));
  Decoder #(.select(3), .tristate("false"), .disabled("Z"), .enable("false")) decoder_1 (
    .out0(W0), .out1(W1), .out2(W2), .out3(W3), .out4(W4), .out5(W5), .out6(W6), .out7(W7),
    .sel(\bht写控制_1_towritre_num ));
  not not_1 (not_1_out, ToWriteW0);
  and and_9 (and_9_out, not_1_out, V0);
  not not_2 (not_2_out, ToWriteW1);
  and and_10 (and_10_out, not_2_out, V1);
  not not_3 (not_3_out, ToWriteW2);
  and and_11 (and_11_out, not_3_out, V2);
  not not_4 (not_4_out, ToWriteW3);
  and and_12 (and_12_out, not_4_out, V3);
  not not_5 (not_5_out, ToWriteW4);
  and and_13 (and_13_out, not_5_out, V4);
  not not_6 (not_6_out, ToWriteW5);
  and and_14 (and_14_out, not_6_out, V5);
  not not_7 (not_7_out, ToWriteW6);
  and and_15 (and_15_out, not_7_out, V6);
  not not_8 (not_8_out, ToWriteW7);
  and and_16 (and_16_out, not_8_out, V7);
  Counter #(.width(16), .max('hffff), .ongoal("wrap"), .trigger("rising"), .behavior("old")) LRUCount (
    .load(ToWriteW0), .D({16{1'b0}}), .count(and_9_out), .Q(Count0), .clk(CLK), .clr(\IF_Row_选中的哪一行 [0]));  // open: carry, preset
  Counter #(.width(16), .max('hffff), .ongoal("wrap"), .trigger("rising"), .behavior("old")) LRUCount_2 (
    .load(ToWriteW1), .D({16{1'b0}}), .count(and_10_out), .Q(Count1), .clk(CLK), .clr(\IF_Row_选中的哪一行 [1]));  // open: carry, preset
  Counter #(.width(16), .max('hffff), .ongoal("wrap"), .trigger("rising"), .behavior("old")) LRUCount_3 (
    .load(ToWriteW2), .D({16{1'b0}}), .count(and_11_out), .Q(Count2), .clk(CLK), .clr(\IF_Row_选中的哪一行 [2]));  // open: carry, preset
  Counter #(.width(16), .max('hffff), .ongoal("wrap"), .trigger("rising"), .behavior("old")) LRUCount_4 (
    .load(ToWriteW3), .D({16{1'b0}}), .count(and_12_out), .Q(Count3), .clk(CLK), .clr(\IF_Row_选中的哪一行 [3]));  // open: carry, preset
  Counter #(.width(16), .max('hffff), .ongoal("wrap"), .trigger("rising"), .behavior("old")) LRUCount_5 (
    .load(ToWriteW4), .D({16{1'b0}}), .count(and_13_out), .Q(Count4), .clk(CLK), .clr(\IF_Row_选中的哪一行 [4]));  // open: carry, preset
  Counter #(.width(16), .max('hffff), .ongoal("wrap"), .trigger("rising"), .behavior("old")) LRUCount_6 (
    .load(ToWriteW5), .D({16{1'b0}}), .count(and_14_out), .Q(Count5), .clk(CLK), .clr(\IF_Row_选中的哪一行 [5]));  // open: carry, preset
  Counter #(.width(16), .max('hffff), .ongoal("wrap"), .trigger("rising"), .behavior("old")) LRUCount_7 (
    .load(ToWriteW6), .D({16{1'b0}}), .count(and_15_out), .Q(Count6), .clk(CLK), .clr(\IF_Row_选中的哪一行 [6]));  // open: carry, preset
  Counter #(.width(16), .max('hffff), .ongoal("wrap"), .trigger("rising"), .behavior("old")) LRUCount_8 (
    .load(ToWriteW7), .D({16{1'b0}}), .count(and_16_out), .Q(Count7), .clk(CLK), .clr(\IF_Row_选中的哪一行 [7]));  // open: carry, preset
  assign controlled_buffer_1_out = \IF_Row_选中的哪一行 [0] ? \分支目标地址_q  : 32'bz;  // Controlled_Buffer controlled_buffer_1
  Register #(.width(32), .trigger("rising"), .Select("low")) \u_分支目标地址  (
    .D(\写_分支目标地址 ), .en(ToWriteW0), .Q(\分支目标地址_q ), .clk(CLK));  // open: clr
  assign controlled_buffer_1_out = \IF_Row_选中的哪一行 [1] ? \分支目标地址_2_q  : 32'bz;  // Controlled_Buffer controlled_buffer_2
  Register #(.width(32), .trigger("rising"), .Select("low")) \u_分支目标地址_2  (
    .D(\写_分支目标地址 ), .en(ToWriteW1), .Q(\分支目标地址_2_q ), .clk(CLK));  // open: clr
  Register #(.width(32), .trigger("rising"), .Select("low")) \u_分支目标地址_3  (
    .D(\写_分支目标地址 ), .en(ToWriteW2), .Q(\分支目标地址_3_q ), .clk(CLK));  // open: clr
  assign controlled_buffer_1_out = \IF_Row_选中的哪一行 [2] ? \分支目标地址_3_q  : 32'bz;  // Controlled_Buffer controlled_buffer_3
  assign controlled_buffer_1_out = \IF_Row_选中的哪一行 [3] ? \分支目标地址_4_q  : 32'bz;  // Controlled_Buffer controlled_buffer_4
  Register #(.width(32), .trigger("rising"), .Select("low")) \u_分支目标地址_4  (
    .D(\写_分支目标地址 ), .en(ToWriteW3), .Q(\分支目标地址_4_q ), .clk(CLK));  // open: clr
  assign controlled_buffer_1_out = \IF_Row_选中的哪一行 [4] ? \分支目标地址_5_q  : 32'bz;  // Controlled_Buffer controlled_buffer_5
  Register #(.width(32), .trigger("rising"), .Select("low")) \u_分支目标地址_5  (
    .D(\写_分支目标地址 ), .en(ToWriteW4), .Q(\分支目标地址_5_q ), .clk(CLK));  // open: clr
  assign controlled_buffer_1_out = \IF_Row_选中的哪一行 [5] ? \分支目标地址_6_q  : 32'bz;  // Controlled_Buffer controlled_buffer_6
  Register #(.width(32), .trigger("rising"), .Select("low")) \u_分支目标地址_6  (
    .D(\写_分支目标地址 ), .en(ToWriteW5), .Q(\分支目标地址_6_q ), .clk(CLK));  // open: clr
  Register #(.width(32), .trigger("rising"), .Select("low")) \u_分支目标地址_7  (
    .D(\写_分支目标地址 ), .en(ToWriteW6), .Q(\分支目标地址_7_q ), .clk(CLK));  // open: clr
  assign controlled_buffer_1_out = \IF_Row_选中的哪一行 [6] ? \分支目标地址_7_q  : 32'bz;  // Controlled_Buffer controlled_buffer_7
  assign controlled_buffer_1_out = \IF_Row_选中的哪一行 [7] ? \分支目标地址_8_q  : 32'bz;  // Controlled_Buffer controlled_buffer_8
  Register #(.width(32), .trigger("rising"), .Select("low")) \u_分支目标地址_8  (
    .D(\写_分支目标地址 ), .en(ToWriteW7), .Q(\分支目标地址_8_q ), .clk(CLK));  // open: clr
  Multiplexer #(.select(1), .width(32), .disabled("Z"), .enable("false")) multiplexer_1 (
    .in0(controlled_buffer_1_out), .in1({32{1'b0}}), .out(\分支目标地址 ), .sel(MISS));
  or or_1 (or_1_out, \EX_Row_选中的哪一行_更新预测历史 [0], ToWriteW0);
  or or_2 (or_2_out, \EX_Row_选中的哪一行_更新预测历史 [1], ToWriteW1);
  or or_3 (or_3_out, \EX_Row_选中的哪一行_更新预测历史 [2], ToWriteW2);
  or or_4 (or_4_out, \EX_Row_选中的哪一行_更新预测历史 [3], ToWriteW3);
  or or_5 (or_5_out, \EX_Row_选中的哪一行_更新预测历史 [4], ToWriteW4);
  or or_6 (or_6_out, \EX_Row_选中的哪一行_更新预测历史 [5], ToWriteW5);
  or or_7 (or_7_out, \EX_Row_选中的哪一行_更新预测历史 [6], ToWriteW6);
  or or_8 (or_8_out, \EX_Row_选中的哪一行_更新预测历史 [7], ToWriteW7);
  Register #(.width(2), .trigger("rising"), .Select("low")) \u_预测历史  (
    .D(\写_更新_预测历史 ), .en(or_1_out), .Q(\预测历史_q ), .clk(CLK));  // open: clr
  Register #(.width(2), .trigger("rising"), .Select("low")) \u_预测历史_2  (
    .D(\写_更新_预测历史 ), .en(or_2_out), .Q(\预测历史_2_q ), .clk(CLK));  // open: clr
  Register #(.width(2), .trigger("rising"), .Select("low")) \u_预测历史_3  (
    .D(\写_更新_预测历史 ), .en(or_3_out), .Q(\预测历史_3_q ), .clk(CLK));  // open: clr
  Register #(.width(2), .trigger("rising"), .Select("low")) \u_预测历史_4  (
    .D(\写_更新_预测历史 ), .en(or_4_out), .Q(\预测历史_4_q ), .clk(CLK));  // open: clr
  Register #(.width(2), .trigger("rising"), .Select("low")) \u_预测历史_5  (
    .D(\写_更新_预测历史 ), .en(or_5_out), .Q(\预测历史_5_q ), .clk(CLK));  // open: clr
  Register #(.width(2), .trigger("rising"), .Select("low")) \u_预测历史_6  (
    .D(\写_更新_预测历史 ), .en(or_6_out), .Q(\预测历史_6_q ), .clk(CLK));  // open: clr
  Register #(.width(2), .trigger("rising"), .Select("low")) \u_预测历史_7  (
    .D(\写_更新_预测历史 ), .en(or_7_out), .Q(\预测历史_7_q ), .clk(CLK));  // open: clr
  Register #(.width(2), .trigger("rising"), .Select("low")) \u_预测历史_8  (
    .D(\写_更新_预测历史 ), .en(or_8_out), .Q(\预测历史_8_q ), .clk(CLK));  // open: clr
  assign controlled_buffer_9_out = \IF_Row_选中的哪一行 [0] ? \预测历史_q  : 2'bz;  // Controlled_Buffer controlled_buffer_9
  assign controlled_buffer_9_out = \IF_Row_选中的哪一行 [1] ? \预测历史_2_q  : 2'bz;  // Controlled_Buffer controlled_buffer_10
  assign controlled_buffer_9_out = \IF_Row_选中的哪一行 [2] ? \预测历史_3_q  : 2'bz;  // Controlled_Buffer controlled_buffer_11
  assign controlled_buffer_9_out = \IF_Row_选中的哪一行 [3] ? \预测历史_4_q  : 2'bz;  // Controlled_Buffer controlled_buffer_12
  assign controlled_buffer_9_out = \IF_Row_选中的哪一行 [4] ? \预测历史_5_q  : 2'bz;  // Controlled_Buffer controlled_buffer_13
  assign controlled_buffer_9_out = \IF_Row_选中的哪一行 [5] ? \预测历史_6_q  : 2'bz;  // Controlled_Buffer controlled_buffer_14
  assign controlled_buffer_9_out = \IF_Row_选中的哪一行 [6] ? \预测历史_7_q  : 2'bz;  // Controlled_Buffer controlled_buffer_15
  assign controlled_buffer_9_out = \IF_Row_选中的哪一行 [7] ? \预测历史_8_q  : 2'bz;  // Controlled_Buffer controlled_buffer_16
  Multiplexer #(.select(1), .width(2), .disabled("Z"), .enable("false")) multiplexer_2 (
    .in0(controlled_buffer_9_out), .in1(2'b00), .out(\预测历史 ), .sel(MISS));

  // Other names for the same wires on the sheet: L0 = \IF_Row_选中的哪一行 [0]; L1 = \IF_Row_选中的哪一行 [1];
  //   L2 = \IF_Row_选中的哪一行 [2]; L3 = \IF_Row_选中的哪一行 [3]; L4 = \IF_Row_选中的哪一行 [4]; L5 = \IF_Row_选中的哪一行 [5];
  //   L6 = \IF_Row_选中的哪一行 [6]; L7 = \IF_Row_选中的哪一行 [7]; RowToUpdate[7:0] = \EX_Row_选中的哪一行_更新预测历史 ;
  //   Update_L0 = \EX_Row_选中的哪一行_更新预测历史 [0]; Update_L1 = \EX_Row_选中的哪一行_更新预测历史 [1];
  //   Update_L2 = \EX_Row_选中的哪一行_更新预测历史 [2]; Update_L3 = \EX_Row_选中的哪一行_更新预测历史 [3];
  //   Update_L4 = \EX_Row_选中的哪一行_更新预测历史 [4]; Update_L5 = \EX_Row_选中的哪一行_更新预测历史 [5];
  //   Update_L6 = \EX_Row_选中的哪一行_更新预测历史 [6]; Update_L7 = \EX_Row_选中的哪一行_更新预测历史 [7]; ToWrite = \欲写标志 
endmodule

module \八路并发比较  (
  input  V,
  input  [31:0] \分支指令地址 ,
  input  [31:0] in_3,
  input  in_4,
  input  [31:0] in_5,
  input  in_6,
  input  [31:0] in_7,
  input  in_8,
  input  [31:0] in_9,
  input  in_10,
  input  [31:0] in_11,
  input  in_12,
  input  [31:0] in_13,
  input  in_14,
  input  [31:0] in_15,
  input  in_16,
  input  [31:0] in_17,
  input  in_18,
  output K0,
  output K1,
  output K2,
  output K3,
  output K4,
  output K5,
  output K6,
  output K7,
  output Miss
);

  wire and_1_out, and_2_out, and_3_out, and_4_out, and_5_out, and_6_out, and_7_out, and_8_out,
       comparator_1_eq, comparator_2_eq, comparator_3_eq, comparator_4_eq, comparator_5_eq, comparator_6_eq,
       comparator_7_eq, comparator_8_eq;

  Comparator #(.width(32), .mode("twosComplement")) comparator_1 (
    .a(\分支指令地址 ), .b(in_3), .eq(comparator_1_eq));  // open: gt, lt
  and and_1 (and_1_out, V, in_4);
  Comparator #(.width(32), .mode("twosComplement")) comparator_2 (
    .a(\分支指令地址 ), .b(in_5), .eq(comparator_2_eq));  // open: gt, lt
  and and_2 (and_2_out, V, in_6);
  Comparator #(.width(32), .mode("twosComplement")) comparator_3 (
    .a(\分支指令地址 ), .b(in_7), .eq(comparator_3_eq));  // open: gt, lt
  and and_3 (and_3_out, V, in_8);
  Comparator #(.width(32), .mode("twosComplement")) comparator_4 (
    .a(\分支指令地址 ), .b(in_9), .eq(comparator_4_eq));  // open: gt, lt
  and and_4 (and_4_out, V, in_10);
  Comparator #(.width(32), .mode("twosComplement")) comparator_5 (
    .a(\分支指令地址 ), .b(in_11), .eq(comparator_5_eq));  // open: gt, lt
  and and_5 (and_5_out, V, in_12);
  Comparator #(.width(32), .mode("twosComplement")) comparator_6 (
    .a(\分支指令地址 ), .b(in_13), .eq(comparator_6_eq));  // open: gt, lt
  and and_6 (and_6_out, V, in_14);
  Comparator #(.width(32), .mode("twosComplement")) comparator_7 (
    .a(\分支指令地址 ), .b(in_15), .eq(comparator_7_eq));  // open: gt, lt
  and and_7 (and_7_out, V, in_16);
  Comparator #(.width(32), .mode("twosComplement")) comparator_8 (
    .a(\分支指令地址 ), .b(in_17), .eq(comparator_8_eq));  // open: gt, lt
  and and_8 (and_8_out, V, in_18);
  and and_9 (K0, comparator_1_eq, and_1_out);
  and and_10 (K1, comparator_2_eq, and_2_out);
  and and_11 (K2, comparator_3_eq, and_3_out);
  and and_12 (K3, comparator_4_eq, and_4_out);
  and and_13 (K4, comparator_5_eq, and_5_out);
  and and_14 (K5, comparator_6_eq, and_6_out);
  and and_15 (K6, comparator_7_eq, and_7_out);
  and and_16 (K7, comparator_8_eq, and_8_out);
  nor nor_1 (Miss, K0, K1, K2, K3, K4, K5, K6, K7);

  // Notes on the sheet:
  //   增加Valid位一起比较
  //   初始时刻Miss为1
endmodule

// 写控制
module \BHT写控制  (
  input  V0,
  input  V1,
  input  V2,
  input  V3,
  input  V4,
  input  V5,
  input  V6,
  input  V7,
  input  [15:0] LRUCount0,
  input  [15:0] LRUCount1,
  input  [15:0] LRUCount2,
  input  [15:0] LRUCount3,
  input  [15:0] LRUCount4,
  input  [15:0] LRUCount5,
  input  [15:0] LRUCount6,
  input  [15:0] LRUCount7,
  output [2:0] ToWritre_num
);

  wire and_1_out;
  wire [2:0] \max3_归并比较_1_max_num , \max3_归并比较_2_max_num , \max3_归并比较_3_max_num , \max3_归并比较_4_max_num ,
       \max3_归并比较_5_max_num , \max3_归并比较_6_max_num , \max3_归并比较_7_max_num , multiplexer_1_out,
       multiplexer_2_out, multiplexer_3_out, multiplexer_4_out, multiplexer_5_out, multiplexer_6_out,
       multiplexer_7_out, multiplexer_8_out;
  wire [15:0] \max3_归并比较_1_max , \max3_归并比较_2_max , \max3_归并比较_3_max , \max3_归并比较_4_max , \max3_归并比较_5_max ,
       \max3_归并比较_6_max ;

  \MAX3_归并比较  \max3_归并比较_1  (
    .Y(LRUCount0), .X(LRUCount1), .X_num(3'b001), .MAX(\max3_归并比较_1_max ), .Max_num(\max3_归并比较_1_max_num ),
    .Y_num(3'b000));
  Multiplexer #(.select(1), .width(3), .disabled("Z"), .enable("false")) multiplexer_1 (
    .in0(3'b110), .in1(multiplexer_2_out), .out(multiplexer_1_out), .sel(V6));
  Multiplexer #(.select(1), .width(3), .disabled("Z"), .enable("false")) multiplexer_2 (
    .in0(3'b111), .out(multiplexer_2_out), .sel(V7));  // open: in1
  \MAX3_归并比较  \max3_归并比较_2  (
    .Y(\max3_归并比较_1_max ), .X(LRUCount2), .X_num(3'b010), .MAX(\max3_归并比较_2_max ),
    .Max_num(\max3_归并比较_2_max_num ), .Y_num(\max3_归并比较_1_max_num ));
  Multiplexer #(.select(1), .width(3), .disabled("Z"), .enable("false")) multiplexer_3 (
    .in0(3'b101), .in1(multiplexer_1_out), .out(multiplexer_3_out), .sel(V5));
  \MAX3_归并比较  \max3_归并比较_3  (
    .Y(\max3_归并比较_2_max ), .X(LRUCount3), .X_num(3'b011), .MAX(\max3_归并比较_3_max ),
    .Max_num(\max3_归并比较_3_max_num ), .Y_num(\max3_归并比较_2_max_num ));
  Multiplexer #(.select(1), .width(3), .disabled("Z"), .enable("false")) multiplexer_4 (
    .in0(3'b011), .in1(multiplexer_5_out), .out(multiplexer_4_out), .sel(V3));
  Multiplexer #(.select(1), .width(3), .disabled("Z"), .enable("false")) multiplexer_5 (
    .in0(3'b100), .in1(multiplexer_3_out), .out(multiplexer_5_out), .sel(V4));
  \MAX3_归并比较  \max3_归并比较_4  (
    .Y(\max3_归并比较_3_max ), .X(LRUCount4), .X_num(3'b100), .MAX(\max3_归并比较_4_max ),
    .Max_num(\max3_归并比较_4_max_num ), .Y_num(\max3_归并比较_3_max_num ));
  Multiplexer #(.select(1), .width(3), .disabled("Z"), .enable("false")) multiplexer_6 (
    .in0(3'b010), .in1(multiplexer_4_out), .out(multiplexer_6_out), .sel(V2));
  \MAX3_归并比较  \max3_归并比较_5  (
    .Y(\max3_归并比较_4_max ), .X(LRUCount5), .X_num(3'b101), .MAX(\max3_归并比较_5_max ),
    .Max_num(\max3_归并比较_5_max_num ), .Y_num(\max3_归并比较_4_max_num ));
  Multiplexer #(.select(1), .width(3), .disabled("Z"), .enable("false")) multiplexer_7 (
    .in0(3'b000), .in1(multiplexer_8_out), .out(multiplexer_7_out), .sel(V0));
  Multiplexer #(.select(1), .width(3), .disabled("Z"), .enable("false")) multiplexer_8 (
    .in0(3'b001), .in1(multiplexer_6_out), .out(multiplexer_8_out), .sel(V1));
  \MAX3_归并比较  \max3_归并比较_6  (
    .Y(\max3_归并比较_5_max ), .X(LRUCount6), .X_num(3'b110), .MAX(\max3_归并比较_6_max ),
    .Max_num(\max3_归并比较_6_max_num ), .Y_num(\max3_归并比较_5_max_num ));
  and and_1 (and_1_out, V0, V1, V2, V3, V4, V5, V6, V7);
  \MAX3_归并比较  \max3_归并比较_7  (
    .Y(\max3_归并比较_6_max ), .X(LRUCount7), .X_num(3'b111), .Max_num(\max3_归并比较_7_max_num ),
    .Y_num(\max3_归并比较_6_max_num ));  // open: MAX
  Multiplexer #(.select(1), .width(3), .disabled("Z"), .enable("false")) multiplexer_9 (
    .in0(multiplexer_7_out), .in1(\max3_归并比较_7_max_num ), .out(ToWritre_num), .sel(and_1_out));

  // Notes on the sheet:
  //   首先找V为0的行（从未被写入）
  //   判断哪一行应该被写入（初始写入或被替换）
  //   再通过LRU算法找Count的最大值得那一行（最久未使用）
  //   当BHT充满时，减少时延
endmodule

// MAX3
module \MAX3_归并比较  (
  input  [15:0] Y,
  input  [15:0] X,
  input  [2:0] Y_num,
  input  [2:0] X_num,
  output [15:0] MAX,
  output [2:0] Max_num
);

  wire comparator_1_eq, comparator_1_gt, or_1_out;

  Multiplexer #(.select(1), .width(16), .disabled("Z"), .enable("false")) multiplexer_1 (
    .in0(Y), .in1(X), .out(MAX), .sel(or_1_out));
  Comparator #(.width(16), .mode("unsigned")) comparator_1 (
    .a(X), .b(Y), .gt(comparator_1_gt), .eq(comparator_1_eq));  // open: lt
  or or_1 (or_1_out, comparator_1_gt, comparator_1_eq);
  Multiplexer #(.select(1), .width(3), .disabled("Z"), .enable("false")) multiplexer_2 (
    .in0(Y_num), .in1(X_num), .out(Max_num), .sel(or_1_out));

  // Notes on the sheet:
  //   输出两个输入中的较大值，并输出较大值的3位编号
endmodule
