// Logisim project cpu24+4+chongliu+IR.circ as structural Verilog
module \单周期MIPS  (
  output RegWrite,
  output MemWrite,
  output [31:0] PC,
  output [31:0] IR,
  output [31:0] RDin,
  output [31:0] MDin
);

  wire and_1_out, and_3_out, and_4_out, and_5_out, and_6_out, and_7_out, and_8_out, and_9_out, CLK,
       comparator_1_eq, comparator_2_eq, comparator_2_lt, Go, IR1, IR2, IR3, mips_alu_1_equal,
       multiplexer_2_out, multiplexer_5_out, multiplexer_11_out, not_1_out, not_2_out, not_3_out, not_4_out,
       not_5_out, not_6_out, not_7_out, not_8_out, not_9_out, or_1_out, register_1_q, RST, SignedExt, stop,
       Syscall, W1, W2, W3, xor_1_out, \单周期硬布线控制器_1_alu_src , \单周期硬布线控制器_1_beq , \单周期硬布线控制器_1_blez ,
       \单周期硬布线控制器_1_bne , \单周期硬布线控制器_1_jal , \单周期硬布线控制器_1_jr , \单周期硬布线控制器_1_memtoreg , \单周期硬布线控制器_1_regdst ,
       \单周期硬布线控制器_1_sb , \无条件分支 , \条件分支成功 ;
  wire [3:0] \单周期硬布线控制器_1_alu_op ;
  wire [4:0] multiplexer_6_out, multiplexer_7_out, multiplexer_8_out, multiplexer_9_out;
  wire [15:0] \总周期数 , \无条件分支数 , \条件分支成功数 ;
  wire [31:0] a0, adder_1_out, adder_2_out, bit_extender_1_out, bit_extender_2_out, LedData,
       mips_alu_1_result, multiplexer_1_out, multiplexer_3_out, multiplexer_4_out, multiplexer_12_out,
       multiplexer_13_out, multiplexer_14_out, multiplexer_16_out, ram_1_data, shifter_1_out, v0;

  Button \u_总复位  (.out(RST));
  // Probe on \总周期数 
  // Probe on \无条件分支数 
  // Probe on \条件分支成功数 
  not not_1 (not_1_out, stop);
  Multiplexer #(.select(1), .width(32), .disabled("Z"), .enable("false")) multiplexer_1 (
    .in0({adder_1_out[31:28], IR[25:0], 2'b00}), .in1(v0), .out(multiplexer_1_out), .sel(\单周期硬布线控制器_1_jr ));
  Clock #(.highDuration(1), .lowDuration(1)) clock_1 (.out(CLK));
  Button _1 (.out(IR1));
  Button _2 (.out(IR2));
  Button _3 (.out(IR3));
  Counter #(.width(16), .max('hffff), .ongoal("wrap"), .trigger("rising"), .behavior("old")) counter_1 (
    .count(1'b1), .Q(\总周期数 ), .clk(multiplexer_2_out), .clr(RST));  // open: load, D, carry, preset
  Multiplexer #(.select(1), .width(1), .disabled("Z"), .enable("false")) multiplexer_2 (
    .in0(and_1_out), .in1(1'b0), .out(multiplexer_2_out), .sel(not_3_out));
  and and_1 (and_1_out, not_1_out, CLK);
  Multiplexer #(.select(2), .width(32), .disabled("Z"), .enable("false")) multiplexer_3 (
    .in0(adder_1_out), .in1(adder_2_out), .in2(multiplexer_1_out), .out(multiplexer_3_out),
    .sel({\无条件分支 , \条件分支成功 }));  // open: in3
  Button \u_继续运行  (.out(Go));
  LED #(.active("true")) led_1 (.in(W1));
  LED #(.active("true")) led_2 (.in(W2));
  LED #(.active("true")) led_3 (.in(W3));
  not not_2 (not_2_out, CLK);
  not not_3 (not_3_out, not_2_out);
  Comparator #(.width(32), .mode("twosComplement")) comparator_1 (
    .a(v0), .b(32'h22), .eq(comparator_1_eq));  // open: gt, lt
  Hex_Digit_Display hex_digit_display_1 (.value(LedData[31:28]));  // open: dp
  Hex_Digit_Display hex_digit_display_2 (.value(LedData[27:24]));  // open: dp
  not not_4 (not_4_out, comparator_1_eq);
  and and_2 (stop, not_4_out, Syscall);
  xor xor_1 (xor_1_out, stop, register_1_q);
  Hex_Digit_Display hex_digit_display_3 (.value(LedData[19:16]));  // open: dp
  Hex_Digit_Display hex_digit_display_4 (.value(LedData[23:20]));  // open: dp
  and and_3 (and_3_out, Syscall, comparator_1_eq);
  and and_4 (and_4_out, stop, Go);
  Register #(.width(1), .trigger("rising"), .Select("low")) register_1 (
    .D(1'b0), .Q(register_1_q), .clk(CLK), .clr(RST), .preset(and_4_out));  // open: en, cs
  Multiplexer #(.select(1), .width(32), .disabled("Z"), .enable("false")) multiplexer_4 (
    .in0(multiplexer_3_out), .in1(PC), .out(multiplexer_4_out), .sel(xor_1_out));
  Register #(.width(32), .trigger("rising"), .Select("low")) u_PC (
    .D(multiplexer_4_out), .Q(PC), .clk(CLK), .clr(RST));  // open: en
  Hex_Digit_Display hex_digit_display_5 (.value(LedData[15:12]));  // open: dp
  Hex_Digit_Display hex_digit_display_6 (.value(LedData[11:8]));  // open: dp
  Hex_Digit_Display hex_digit_display_7 (.value(LedData[3:0]));  // open: dp
  Hex_Digit_Display hex_digit_display_8 (.value(LedData[7:4]));  // open: dp
  // Probe on \总周期数 
  Register #(.width(32), .trigger("rising"), .Select("low")) register_2 (
    .D(a0), .Q(LedData), .clk(and_3_out), .clr(RST));  // open: en
  Adder #(.width(32)) adder_1 (.a(PC), .b(32'h4), .out(adder_1_out));  // open: cin, cout
  Counter #(.width(16), .max('hffff), .ongoal("wrap"), .trigger("rising"), .behavior("old")) counter_2 (
    .count(1'b1), .Q(\条件分支成功数 ), .clk(multiplexer_5_out), .clr(RST));  // open: load, D, carry, preset
  Multiplexer #(.select(1), .width(1), .disabled("Z"), .enable("false")) multiplexer_5 (
    .in0(and_5_out), .in1(1'b0), .out(multiplexer_5_out), .sel(not_5_out));
  not not_5 (not_5_out, not_6_out);
  and and_5 (and_5_out, \条件分支成功 , CLK);
  ROM #(.addrWidth(10), .dataWidth(32), .Select("high")) rom_1 (.addr(PC[11:2]), .data(IR));
  not not_6 (not_6_out, CLK);
  \单周期硬布线控制器  \u_单周期硬布线控制器_1  (
    .OP(IR[31:26]), .Func(IR[5:0]), .ALU_OP(\单周期硬布线控制器_1_alu_op ), .MemToReg(\单周期硬布线控制器_1_memtoreg ),
    .MemWrite(MemWrite), .ALU_SRC(\单周期硬布线控制器_1_alu_src ), .RegWrite(RegWrite), .SysCALL(Syscall),
    .SignedExt(SignedExt), .RegDst(\单周期硬布线控制器_1_regdst ), .Beq(\单周期硬布线控制器_1_beq ), .Bne(\单周期硬布线控制器_1_bne ),
    .JR(\单周期硬布线控制器_1_jr ), .JMP(\无条件分支 ), .JAL(\单周期硬布线控制器_1_jal ), .BLEZ(\单周期硬布线控制器_1_blez ),
    .SB(\单周期硬布线控制器_1_sb ));  // open: ERET
  Multiplexer #(.select(1), .width(5), .disabled("Z"), .enable("false")) multiplexer_6 (
    .in0(IR[20:16]), .in1(IR[15:11]), .out(multiplexer_6_out), .sel(\单周期硬布线控制器_1_regdst ));
  Multiplexer #(.select(1), .width(5), .disabled("Z"), .enable("false")) multiplexer_7 (
    .in0(IR[25:21]), .in1(5'b00010), .out(multiplexer_7_out), .sel(Syscall));
  Multiplexer #(.select(1), .width(5), .disabled("Z"), .enable("false")) multiplexer_8 (
    .in0(IR[20:16]), .in1(5'b00100), .out(multiplexer_8_out), .sel(Syscall));
  Multiplexer #(.select(1), .width(5), .disabled("Z"), .enable("false")) multiplexer_9 (
    .in0(multiplexer_6_out), .in1({5{1'b1}}), .out(multiplexer_9_out), .sel(\单周期硬布线控制器_1_jal ));
  Multiplexer #(.select(1), .width(32), .disabled("Z"), .enable("false")) multiplexer_10 (
    .in0(multiplexer_16_out), .in1(adder_1_out), .out(RDin), .sel(\单周期硬布线控制器_1_jal ));
  assign bit_extender_1_out = {{16{1'b0}}, IR[15:0]};  // Bit_Extender bit_extender_1
  assign bit_extender_2_out = {{16{IR[15]}}, IR[15:0]};  // Bit_Extender bit_extender_2
  Counter #(.width(16), .max('hffff), .ongoal("wrap"), .trigger("rising"), .behavior("old")) counter_3 (
    .count(1'b1), .Q(\无条件分支数 ), .clk(multiplexer_11_out), .clr(RST));  // open: load, D, carry, preset
  Multiplexer #(.select(1), .width(1), .disabled("Z"), .enable("false")) multiplexer_11 (
    .in0(and_6_out), .in1(1'b0), .out(multiplexer_11_out), .sel(not_7_out));
  and and_6 (and_6_out, \无条件分支 , CLK);
  Multiplexer #(.select(1), .width(32), .disabled("Z"), .enable("false")) multiplexer_12 (
    .in0(bit_extender_1_out), .in1(bit_extender_2_out), .out(multiplexer_12_out), .sel(SignedExt));
  not not_7 (not_7_out, not_8_out);
  not not_8 (not_8_out, CLK);
  MIPS_Regifile mips_regifile_1 (
    .Din(RDin), .Clk(CLK), .R1(v0), .R2(a0), .WE(RegWrite), .W_num(multiplexer_9_out),
    .R1_num(multiplexer_7_out), .R2_num(multiplexer_8_out));
  Comparator #(.width(32), .mode("twosComplement")) comparator_2 (
    .a(v0), .b({32{1'b0}}), .eq(comparator_2_eq), .lt(comparator_2_lt));  // open: gt
  Shifter #(.width(32), .shift("ll")) shifter_1 (.in(multiplexer_12_out), .\dist (5'b00010), .out(shifter_1_out));
  and and_7 (and_7_out, or_1_out, \单周期硬布线控制器_1_blez );
  or or_1 (or_1_out, comparator_2_eq, comparator_2_lt);
  Multiplexer #(.select(1), .width(32), .disabled("Z"), .enable("false")) multiplexer_13 (
    .in0(a0), .in1(multiplexer_12_out), .out(multiplexer_13_out), .sel(\单周期硬布线控制器_1_alu_src ));
  Adder #(.width(32)) adder_2 (.a(shifter_1_out), .b(adder_1_out), .out(adder_2_out));  // open: cin, cout
  MIPS_ALU mips_alu_1 (
    .X(v0), .Y(multiplexer_13_out), .AluOP(\单周期硬布线控制器_1_alu_op ), .Equal(mips_alu_1_equal),
    .Result(mips_alu_1_result), .shamt(IR[10:6]));  // open: Result_2
  and and_8 (and_8_out, mips_alu_1_equal, \单周期硬布线控制器_1_beq );
  not not_9 (not_9_out, mips_alu_1_equal);
  Multiplexer #(.select(2), .width(32), .disabled("Z"), .enable("false")) multiplexer_14 (
    .in0({ram_1_data[31:8], a0[7:0]}), .in1({ram_1_data[31:16], a0[7:0], ram_1_data[7:0]}),
    .in2({ram_1_data[31:24], a0[7:0], ram_1_data[15:0]}), .in3({a0[7:0], ram_1_data[23:0]}),
    .out(multiplexer_14_out), .sel(mips_alu_1_result[1:0]));
  and and_9 (and_9_out, not_9_out, \单周期硬布线控制器_1_bne );
  Multiplexer #(.select(1), .width(32), .disabled("Z"), .enable("false")) multiplexer_15 (
    .in0(a0), .in1(multiplexer_14_out), .out(MDin), .sel(\单周期硬布线控制器_1_sb ));
  or or_2 (\条件分支成功 , and_7_out, and_9_out, and_8_out);
  RAM #(.addrWidth(10), .dataWidth(32), .bus("separate"), .Select("high")) ram_1 (
    .addr(mips_alu_1_result[11:2]), .din(MDin), .data(ram_1_data), .str(MemWrite), .clk(CLK));  // open: sel, ld, clr
  Multiplexer #(.select(1), .width(32), .disabled("Z"), .enable("false")) multiplexer_16 (
    .in0(mips_alu_1_result), .in1(ram_1_data), .out(multiplexer_16_out), .sel(\单周期硬布线控制器_1_memtoreg ));

  // Notes on the sheet:
  //   总复位信号应将除ROM以外所有存储组件全部清零
  //   中断源
  //   中断等待指示
  //   数码管输出应该用寄存器锁存，否则显示数据只能一闪而过
  //   数码管输出
  //   指令存储器
  //   指令字
  //   contents of rom_1 (hex, n*v repeats v):
  //   20110001 8000c05 20110001 20120002 20130003 8000c09 20110001 20120002 20130003 8000c0d 20110001
  //   20120002 20130003 8000c11 20110001 20120002 20130003 c000cf5 20100001 20110001 118fc0 112020
  //   20020022 c 118882 12200001 8000c15 112020 20020022 c 20110001 118880 112020 20020022 c 12200001
  //   8000c1f 20110001 118fc0 112020 20020022 c 1188c3 112020 20020022 c 118903 112020 20020022 c 118903
  //   112020 20020022 c 118903 112020 20020022 c 118903 112020 20020022 c 118903 112020 20020022 c 118903
  //   112020 20020022 c 118903 112020 20020022 c 20100001 109fc0 139fc3 8021 2012000c 24160003 26100001
  //   3210000f 20080008 20090001 139900 2709825 132020 20020022 c 1094022 1500fff9 22100001 2018000f
  //   2188024 108700 20080008 20090001 139902 2709825 132021 20020022 c 1094022 1500fff9 108702 2c9b022
  //   12c00001 8000c50 4020 1084027 84400 3508ffff 82021 20020022 c 2010ffff 20110000 ae300000 22100001
  //   22310004 ae300000 22100001 22310004 ae300000 22100001 22310004 ae300000 22100001 22310004 ae300000
  //   22100001 22310004 ae300000 22100001 22310004 ae300000 22100001 22310004 ae300000 22100001 22310004
  //   ae300000 22100001 22310004 ae300000 22100001 22310004 ae300000 22100001 22310004 ae300000 22100001
  //   22310004 ae300000 22100001 22310004 ae300000 22100001 22310004 ae300000 22100001 22310004 ae300000
  //   22100001 22310004 22100001 8020 2011003c 8e130000 8e340000 274402a 11000002 ae330000 ae140000
  //   2231fffc 1611fff8 102020 20020022 c 22100004 2011003c 1611fff2 20020032 c 20080001 20110010 112020
  //   20020022 c 200b0020 2288823 112020 20020022 c 216bffff 1560fffa 2002000a c 2008ffff 20117777 112020
  //   20020022 c 200b0010 2288826 112020 20020022 c 216bffff 1560fffa 2002000a c 20090000 200b0020
  //   20110000 20120001 a1310000 112020 20020022 c 2328820 21290001 216bffff 1560fff8 200b0008 20090000
  //   8d310000 112020 20020022 c 21290004 216bffff 1560fff9 2002000a c 2011fff1 112020 20020022 c 22310001
  //   1a20fffb 2002000a c 2002000a c 20100000 22100001 102020 20020022 c 22100002 102020 20020022 c
  //   22100003 102020 20020022 c 22100004 102020 20020022 c 22100005 102020 20020022 c 22100006 102020
  //   20020022 c 22100007 102020 20020022 c 22100008 102020 20020022 20020022 c 3e00008
  //   OP
  //   Func
  //   rs
  //   rt
  //   rd
  //   JMP
  //   JR
  //   OP
  //   Func
  //   Syscall
  //   BLEZ
  //   Beq
  //   Bne
  //   MemToReg
  //   MemWrite
  //   SB
  //   AluOP
  //   AluSrcB
  //   RegWrite
  //   JAL
  //   RegDst
  //   为方便自动评测，需要输出PC，IR，寄存器文件写入端口RDin，内存写入端口MDin等信号
endmodule

// 单周期硬布线控制器
module \单周期硬布线控制器  (
  input  [5:0] OP,
  input  [5:0] Func,
  output [3:0] ALU_OP,
  output MemToReg,
  output MemWrite,
  output ALU_SRC,
  output RegWrite,
  output SysCALL,
  output SignedExt,
  output RegDst,
  output Beq,
  output Bne,
  output JR,
  output JMP,
  output JAL,
  output BLEZ,
  output SB,
  output ERET
);

  \运算控制器自动生成  \u_运算控制器自动生成_1  (
    .OP0(OP[0]), .OP1(OP[1]), .OP2(OP[2]), .OP3(OP[3]), .OP4(OP[4]), .OP5(OP[5]), .F0(Func[0]), .F1(Func[1]),
    .F2(Func[2]), .F3(Func[3]), .F4(Func[4]), .F5(Func[5]), .S0(ALU_OP[0]), .S1(ALU_OP[1]), .S2(ALU_OP[2]),
    .S3(ALU_OP[3]));
  \控制信号自动生成  \u_控制信号自动生成_1  (
    .OP0(OP[0]), .MemToReg(MemToReg), .OP1(OP[1]), .OP2(OP[2]), .OP3(OP[3]), .OP4(OP[4]),
    .MemWrite(MemWrite), .OP5(OP[5]), .F0(Func[0]), .F1(Func[1]), .F2(Func[2]), .F3(Func[3]), .F4(Func[4]),
    .F5(Func[5]), .ALU_SRC(ALU_SRC), .ERET(ERET), .BLEZ(BLEZ), .SB(SB), .RegWrite(RegWrite),
    .SysCALL(SysCALL), .SignedExt(SignedExt), .RegDst(RegDst), .BEQ(Beq), .BNE(Bne), .JR(JR), .JUMP(JMP),
    .JAL(JAL));

  // Other names for the same wires on the sheet: OP_CODE[5:0] = OP

  // Notes on the sheet:
  //   运算器控制器，根据指令生成运算器功能选择信号
  //   控制信号生成，产生数据通路需要的其他控制信号
endmodule

// 运算器控制器
module \运算控制器自动生成  (
  input  OP0,
  input  OP1,
  input  OP2,
  input  OP3,
  input  OP4,
  input  OP5,
  input  F0,
  input  F1,
  input  F2,
  input  F3,
  input  F4,
  input  F5,
  output S0,
  output S1,
  output S2,
  output S3
);

  wire and_1_out, and_2_out, and_3_out, and_4_out, and_5_out, and_6_out, and_7_out, and_8_out, and_9_out,
       and_10_out, and_11_out, and_12_out, and_13_out, and_14_out, and_15_out, and_16_out, and_17_out,
       and_18_out, and_19_out, and_20_out, and_21_out, and_22_out, and_23_out, and_24_out, and_25_out,
       and_26_out, and_27_out, and_28_out, and_29_out, not_1_out, not_2_out, not_3_out, not_4_out, not_5_out,
       not_6_out, not_7_out, not_8_out, not_9_out, not_10_out, not_11_out, not_12_out, not_13_out,
       not_14_out, not_15_out, not_16_out, not_17_out, not_18_out, not_19_out, not_20_out, not_21_out,
       not_22_out, not_23_out, not_24_out, not_25_out, not_26_out, not_27_out, not_28_out, not_29_out,
       not_30_out, not_31_out, not_32_out, not_33_out, not_34_out, not_35_out, not_36_out, not_37_out,
       not_38_out, not_39_out, not_40_out, not_41_out, not_42_out, not_43_out, not_44_out, not_45_out,
       not_46_out, not_47_out, not_48_out, not_49_out, not_50_out, not_51_out, not_52_out, not_53_out,
       not_54_out, not_55_out, not_56_out, not_57_out, not_58_out, not_59_out, not_60_out, not_61_out,
       not_62_out, not_63_out, not_64_out, not_65_out, not_66_out, not_67_out, not_68_out, not_69_out,
       not_70_out, not_71_out, not_72_out, not_73_out, not_74_out, not_75_out, not_76_out, not_77_out,
       not_78_out, not_79_out, not_80_out, not_81_out, not_82_out, not_83_out, not_84_out, not_85_out,
       not_86_out, not_87_out, not_88_out, not_89_out, not_90_out, not_91_out, not_92_out, not_93_out,
       not_94_out, not_95_out, not_96_out, not_97_out, not_98_out, not_99_out, not_100_out, not_101_out,
       not_102_out, not_103_out, not_104_out, not_105_out, not_106_out, not_107_out, not_108_out,
       not_109_out, not_110_out, not_111_out, not_112_out, not_113_out, not_114_out, not_115_out,
       not_116_out, not_117_out, not_118_out, not_119_out, not_120_out, not_121_out, not_122_out,
       not_123_out, not_124_out, not_125_out, not_126_out, not_127_out, not_128_out, not_129_out,
       not_130_out, not_131_out, not_132_out, not_133_out, not_134_out, not_135_out, not_136_out,
       not_137_out, not_138_out, not_139_out, not_140_out, not_141_out, not_142_out, not_143_out,
       not_144_out, not_145_out, not_146_out, not_147_out, not_148_out, not_149_out, not_150_out,
       not_151_out, not_152_out, not_153_out, not_154_out, not_155_out, not_156_out, not_157_out,
       not_158_out, not_159_out, not_160_out, not_161_out, not_162_out, not_163_out, not_164_out,
       not_165_out, not_166_out, not_167_out, not_168_out, not_169_out, not_170_out, not_171_out,
       not_172_out, not_173_out, not_174_out, not_175_out, not_176_out, not_177_out, not_178_out,
       not_179_out, not_180_out, not_181_out, not_182_out, not_183_out, not_184_out, not_185_out;

  not not_1 (not_1_out, OP0);
  not not_2 (not_2_out, OP1);
  not not_3 (not_3_out, OP2);
  not not_4 (not_4_out, OP4);
  not not_5 (not_5_out, OP5);
  not not_6 (not_6_out, F1);
  not not_7 (not_7_out, F2);
  not not_8 (not_8_out, F3);
  not not_9 (not_9_out, F4);
  not not_10 (not_10_out, OP0);
  not not_11 (not_11_out, OP1);
  not not_12 (not_12_out, OP2);
  not not_13 (not_13_out, OP4);
  not not_14 (not_14_out, OP5);
  not not_15 (not_15_out, F0);
  not not_16 (not_16_out, F3);
  not not_17 (not_17_out, F4);
  not not_18 (not_18_out, OP0);
  not not_19 (not_19_out, OP1);
  not not_20 (not_20_out, OP2);
  not not_21 (not_21_out, OP4);
  not not_22 (not_22_out, OP5);
  not not_23 (not_23_out, F0);
  not not_24 (not_24_out, F2);
  not not_25 (not_25_out, F4);
  not not_26 (not_26_out, OP0);
  not not_27 (not_27_out, OP1);
  not not_28 (not_28_out, OP2);
  not not_29 (not_29_out, OP4);
  not not_30 (not_30_out, OP5);
  not not_31 (not_31_out, F2);
  not not_32 (not_32_out, F3);
  not not_33 (not_33_out, F4);
  not not_34 (not_34_out, F5);
  not not_35 (not_35_out, OP0);
  not not_36 (not_36_out, OP1);
  not not_37 (not_37_out, OP2);
  not not_38 (not_38_out, OP4);
  not not_39 (not_39_out, OP0);
  not not_40 (not_40_out, OP1);
  not not_41 (not_41_out, OP4);
  not not_42 (not_42_out, OP5);
  not not_43 (not_43_out, OP0);
  not not_44 (not_44_out, OP2);
  not not_45 (not_45_out, OP4);
  not not_46 (not_46_out, OP5);
  not not_47 (not_47_out, OP1);
  not not_48 (not_48_out, OP2);
  not not_49 (not_49_out, OP4);
  not not_50 (not_50_out, OP5);
  not not_51 (not_51_out, OP2);
  not not_52 (not_52_out, OP4);
  not not_53 (not_53_out, OP0);
  not not_54 (not_54_out, OP1);
  not not_55 (not_55_out, OP2);
  not not_56 (not_56_out, OP3);
  not not_57 (not_57_out, OP4);
  not not_58 (not_58_out, OP5);
  not not_59 (not_59_out, F0);
  not not_60 (not_60_out, F1);
  not not_61 (not_61_out, F3);
  not not_62 (not_62_out, F4);
  not not_63 (not_63_out, OP0);
  not not_64 (not_64_out, OP1);
  not not_65 (not_65_out, OP2);
  not not_66 (not_66_out, OP3);
  not not_67 (not_67_out, OP4);
  not not_68 (not_68_out, OP5);
  not not_69 (not_69_out, F0);
  not not_70 (not_70_out, F2);
  not not_71 (not_71_out, F3);
  not not_72 (not_72_out, F4);
  not not_73 (not_73_out, OP0);
  not not_74 (not_74_out, OP1);
  not not_75 (not_75_out, OP2);
  not not_76 (not_76_out, OP3);
  not not_77 (not_77_out, OP4);
  not not_78 (not_78_out, OP5);
  not not_79 (not_79_out, F0);
  not not_80 (not_80_out, F2);
  not not_81 (not_81_out, F4);
  not not_82 (not_82_out, OP0);
  not not_83 (not_83_out, OP1);
  not not_84 (not_84_out, OP2);
  not not_85 (not_85_out, OP3);
  not not_86 (not_86_out, OP4);
  not not_87 (not_87_out, OP5);
  not not_88 (not_88_out, F3);
  not not_89 (not_89_out, F4);
  not not_90 (not_90_out, OP0);
  not not_91 (not_91_out, OP1);
  not not_92 (not_92_out, OP4);
  not not_93 (not_93_out, OP5);
  not not_94 (not_94_out, OP0);
  not not_95 (not_95_out, OP2);
  not not_96 (not_96_out, OP4);
  not not_97 (not_97_out, OP5);
  not not_98 (not_98_out, OP0);
  not not_99 (not_99_out, OP1);
  not not_100 (not_100_out, OP2);
  not not_101 (not_101_out, OP4);
  not not_102 (not_102_out, OP5);
  not not_103 (not_103_out, F0);
  not not_104 (not_104_out, F1);
  not not_105 (not_105_out, F3);
  not not_106 (not_106_out, F4);
  not not_107 (not_107_out, OP0);
  not not_108 (not_108_out, OP1);
  not not_109 (not_109_out, OP2);
  not not_110 (not_110_out, OP4);
  not not_111 (not_111_out, OP5);
  not not_112 (not_112_out, F2);
  not not_113 (not_113_out, F3);
  not not_114 (not_114_out, F4);
  not not_115 (not_115_out, OP0);
  not not_116 (not_116_out, OP1);
  not not_117 (not_117_out, OP2);
  not not_118 (not_118_out, OP4);
  not not_119 (not_119_out, OP5);
  not not_120 (not_120_out, F2);
  not not_121 (not_121_out, F4);
  not not_122 (not_122_out, OP0);
  not not_123 (not_123_out, OP1);
  not not_124 (not_124_out, OP2);
  not not_125 (not_125_out, OP4);
  not not_126 (not_126_out, OP0);
  not not_127 (not_127_out, OP1);
  not not_128 (not_128_out, OP4);
  not not_129 (not_129_out, OP5);
  not not_130 (not_130_out, OP1);
  not not_131 (not_131_out, OP2);
  not not_132 (not_132_out, OP4);
  not not_133 (not_133_out, OP5);
  not not_134 (not_134_out, OP2);
  not not_135 (not_135_out, OP4);
  not not_136 (not_136_out, OP5);
  not not_137 (not_137_out, OP4);
  not not_138 (not_138_out, OP3);
  not not_139 (not_139_out, OP2);
  not not_140 (not_140_out, OP1);
  not not_141 (not_141_out, OP0);
  not not_142 (not_142_out, F4);
  not not_143 (not_143_out, F3);
  not not_144 (not_144_out, F1);
  not not_145 (not_145_out, OP5);
  not not_146 (not_146_out, OP4);
  not not_147 (not_147_out, OP3);
  not not_148 (not_148_out, OP2);
  not not_149 (not_149_out, OP1);
  not not_150 (not_150_out, OP0);
  not not_151 (not_151_out, F4);
  not not_152 (not_152_out, F3);
  not not_153 (not_153_out, OP5);
  not not_154 (not_154_out, OP4);
  not not_155 (not_155_out, OP3);
  not not_156 (not_156_out, OP2);
  not not_157 (not_157_out, OP1);
  not not_158 (not_158_out, OP0);
  not not_159 (not_159_out, F4);
  not not_160 (not_160_out, F2);
  not not_161 (not_161_out, F0);
  not not_162 (not_162_out, OP5);
  not not_163 (not_163_out, OP4);
  not not_164 (not_164_out, OP3);
  not not_165 (not_165_out, OP2);
  not not_166 (not_166_out, OP1);
  not not_167 (not_167_out, OP0);
  not not_168 (not_168_out, F4);
  not not_169 (not_169_out, F2);
  not not_170 (not_170_out, OP5);
  not not_171 (not_171_out, OP4);
  not not_172 (not_172_out, OP2);
  not not_173 (not_173_out, OP0);
  not not_174 (not_174_out, OP5);
  not not_175 (not_175_out, OP4);
  not not_176 (not_176_out, OP1);
  not not_177 (not_177_out, OP5);
  not not_178 (not_178_out, OP4);
  not not_179 (not_179_out, OP3);
  not not_180 (not_180_out, OP2);
  not not_181 (not_181_out, OP1);
  not not_182 (not_182_out, OP0);
  not not_183 (not_183_out, F4);
  not not_184 (not_184_out, F3);
  not not_185 (not_185_out, F0);
  and and_1 (and_1_out, not_1_out, not_2_out, not_3_out, not_4_out, not_5_out, not_6_out, not_7_out, not_8_out, not_9_out, F5);
  and and_2 (and_2_out, not_10_out, not_11_out, not_12_out, not_13_out, not_14_out, not_15_out, F2, not_16_out, not_17_out, F5);
  and and_3 (and_3_out, not_18_out, not_19_out, not_20_out, not_21_out, not_22_out, not_23_out, F1, not_24_out, F3, not_25_out, F5);
  and and_4 (and_4_out, not_26_out, not_27_out, not_28_out, not_29_out, not_30_out, F0, F1, not_31_out, not_32_out, not_33_out, not_34_out);
  and and_5 (and_5_out, not_35_out, not_36_out, not_37_out, OP3, not_38_out);
  and and_6 (and_6_out, not_39_out, not_40_out, OP3, not_41_out, not_42_out);
  and and_7 (and_7_out, not_43_out, not_44_out, OP3, not_45_out, not_46_out);
  and and_8 (and_8_out, not_47_out, not_48_out, OP3, not_49_out, not_50_out);
  and and_9 (and_9_out, OP0, OP1, not_51_out, not_52_out, OP5);
  and and_10 (and_10_out, not_53_out, not_54_out, not_55_out, not_56_out, not_57_out, not_58_out, not_59_out, not_60_out, F2, not_61_out, not_62_out, F5);
  and and_11 (and_11_out, not_63_out, not_64_out, not_65_out, not_66_out, not_67_out, not_68_out, not_69_out, F1, not_70_out, not_71_out, not_72_out);
  and and_12 (and_12_out, not_73_out, not_74_out, not_75_out, not_76_out, not_77_out, not_78_out, not_79_out, F1, not_80_out, not_81_out, F5);
  and and_13 (and_13_out, not_82_out, not_83_out, not_84_out, not_85_out, not_86_out, not_87_out, F0, F1, not_88_out, not_89_out, F5);
  and and_14 (and_14_out, not_90_out, not_91_out, OP2, OP3, not_92_out, not_93_out);
  and and_15 (and_15_out, not_94_out, OP1, not_95_out, OP3, not_96_out, not_97_out);
  and and_16 (and_16_out, not_98_out, not_99_out, not_100_out, not_101_out, not_102_out, not_103_out, not_104_out, not_105_out, not_106_out, F5);
  and and_17 (and_17_out, not_107_out, not_108_out, not_109_out, not_110_out, not_111_out, not_112_out, not_113_out, not_114_out, F5);
  and and_18 (and_18_out, not_115_out, not_116_out, not_117_out, not_118_out, not_119_out, F0, F1, not_120_out, not_121_out, F5);
  and and_19 (and_19_out, not_122_out, not_123_out, not_124_out, OP3, not_125_out);
  and and_20 (and_20_out, not_126_out, not_127_out, OP3, not_128_out, not_129_out);
  and and_21 (and_21_out, not_130_out, not_131_out, OP3, not_132_out, not_133_out);
  and and_22 (and_22_out, OP0, OP1, not_134_out, not_135_out, OP5);
  and and_23 (and_23_out, not_136_out, not_137_out, not_138_out, not_139_out, not_140_out, not_141_out, F5, not_142_out, not_143_out, F2, not_144_out, F0);
  and and_24 (and_24_out, not_145_out, not_146_out, not_147_out, not_148_out, not_149_out, not_150_out, F5, not_151_out, not_152_out, F2, F1, F0);
  and and_25 (and_25_out, not_153_out, not_154_out, not_155_out, not_156_out, not_157_out, not_158_out, F5, not_159_out, F3, not_160_out, F1, not_161_out);
  and and_26 (and_26_out, not_162_out, not_163_out, not_164_out, not_165_out, not_166_out, not_167_out, F5, not_168_out, F3, not_169_out, F1, F0);
  and and_27 (and_27_out, not_170_out, not_171_out, OP3, not_172_out, OP1, not_173_out);
  and and_28 (and_28_out, not_174_out, not_175_out, OP3, OP2, not_176_out, OP0);
  and and_29 (and_29_out, not_177_out, not_178_out, not_179_out, not_180_out, not_181_out, not_182_out, F5, not_183_out, not_184_out, F2, F1, not_185_out);
  or or_1 (S0, and_1_out, and_2_out, and_3_out, and_4_out, and_5_out, and_6_out, and_7_out, and_8_out, and_9_out);
  or or_2 (S1, and_10_out, and_11_out, and_12_out, and_13_out, and_14_out, and_15_out);
  or or_3 (S2, and_16_out, and_17_out, and_18_out, and_19_out, and_20_out, and_21_out, and_22_out);
  or or_4 (S3, and_23_out, and_24_out, and_25_out, and_26_out, and_27_out, and_28_out, and_29_out);
endmodule

// 控制信号生成
module \控制信号自动生成  (
  input  OP0,
  input  OP1,
  input  OP2,
  input  OP3,
  input  OP4,
  input  OP5,
  input  F0,
  input  F1,
  input  F2,
  input  F3,
  input  F4,
  input  F5,
  output MemToReg,
  output MemWrite,
  output ALU_SRC,
  output ERET,
  output BLEZ,
  output SB,
  output RegWrite,
  output SysCALL,
  output SignedExt,
  output RegDst,
  output BEQ,
  output BNE,
  output JR,
  output JUMP,
  output JAL
);

  wire and_2_out, and_3_out, and_4_out, and_5_out, and_6_out, and_7_out, and_11_out, and_12_out, and_13_out,
       and_14_out, and_15_out, and_16_out, and_17_out, and_19_out, and_20_out, and_21_out, and_22_out,
       and_23_out, and_24_out, and_25_out, and_26_out, and_27_out, and_28_out, and_32_out, and_33_out,
       not_1_out, not_2_out, not_3_out, not_4_out, not_5_out, not_6_out, not_7_out, not_8_out, not_9_out,
       not_10_out, not_11_out, not_12_out, not_13_out, not_14_out, not_15_out, not_16_out, not_17_out,
       not_18_out, not_19_out, not_20_out, not_21_out, not_22_out, not_23_out, not_24_out, not_25_out,
       not_26_out, not_27_out, not_28_out, not_29_out, not_30_out, not_31_out, not_32_out, not_33_out,
       not_34_out, not_35_out, not_36_out, not_37_out, not_38_out, not_39_out, not_40_out, not_41_out,
       not_42_out, not_43_out, not_44_out, not_45_out, not_46_out, not_47_out, not_48_out, not_49_out,
       not_50_out, not_51_out, not_52_out, not_53_out, not_54_out, not_55_out, not_56_out, not_57_out,
       not_58_out, not_59_out, not_60_out, not_61_out, not_62_out, not_63_out, not_64_out, not_65_out,
       not_66_out, not_67_out, not_68_out, not_69_out, not_70_out, not_71_out, not_72_out, not_73_out,
       not_74_out, not_75_out, not_76_out, not_77_out, not_78_out, not_79_out, not_80_out, not_81_out,
       not_82_out, not_83_out, not_84_out, not_85_out, not_86_out, not_87_out, not_88_out, not_89_out,
       not_90_out, not_91_out, not_92_out, not_93_out, not_94_out, not_95_out, not_96_out, not_97_out,
       not_98_out, not_99_out, not_100_out, not_101_out, not_102_out, not_103_out, not_104_out, not_105_out,
       not_106_out, not_107_out, not_108_out, not_109_out, not_110_out, not_111_out, not_112_out,
       not_113_out, not_114_out, not_115_out, not_116_out, not_117_out, not_118_out, not_119_out,
       not_120_out, not_121_out, not_122_out, not_123_out, not_124_out, not_125_out, not_126_out,
       not_127_out, not_128_out, not_129_out, not_130_out, not_131_out, not_132_out, not_133_out,
       not_134_out, not_135_out, not_136_out, not_137_out, not_138_out, not_139_out, not_140_out,
       not_141_out, not_142_out, not_143_out, not_144_out, not_145_out, not_146_out, not_147_out,
       not_148_out, not_149_out, not_150_out, not_151_out, not_152_out, not_153_out, not_154_out,
       not_155_out, not_156_out, not_157_out, not_158_out, not_159_out, not_160_out, not_161_out,
       not_162_out, not_163_out, not_164_out, not_165_out, not_166_out, not_167_out, not_168_out,
       not_169_out, not_170_out, not_171_out, not_172_out, not_173_out, not_174_out, not_175_out,
       not_176_out, not_177_out, not_178_out, not_179_out, not_180_out, not_181_out, not_182_out,
       not_183_out, not_184_out, not_185_out;

  not not_1 (not_1_out, OP2);
  not not_2 (not_2_out, OP3);
  not not_3 (not_3_out, OP4);
  not not_4 (not_4_out, OP0);
  not not_5 (not_5_out, OP1);
  not not_6 (not_6_out, OP2);
  not not_7 (not_7_out, OP4);
  not not_8 (not_8_out, OP2);
  not not_9 (not_9_out, OP4);
  not not_10 (not_10_out, OP0);
  not not_11 (not_11_out, OP1);
  not not_12 (not_12_out, OP2);
  not not_13 (not_13_out, OP4);
  not not_14 (not_14_out, OP0);
  not not_15 (not_15_out, OP2);
  not not_16 (not_16_out, OP4);
  not not_17 (not_17_out, OP5);
  not not_18 (not_18_out, OP1);
  not not_19 (not_19_out, OP4);
  not not_20 (not_20_out, OP5);
  not not_21 (not_21_out, OP2);
  not not_22 (not_22_out, OP4);
  not not_23 (not_23_out, OP5);
  not not_24 (not_24_out, OP3);
  not not_25 (not_25_out, OP2);
  not not_26 (not_26_out, OP1);
  not not_27 (not_27_out, OP0);
  not not_28 (not_28_out, F5);
  not not_29 (not_29_out, F2);
  not not_30 (not_30_out, F1);
  not not_31 (not_31_out, F0);
  not not_32 (not_32_out, OP0);
  not not_33 (not_33_out, OP3);
  not not_34 (not_34_out, OP4);
  not not_35 (not_35_out, OP5);
  not not_36 (not_36_out, OP0);
  not not_37 (not_37_out, OP1);
  not not_38 (not_38_out, OP2);
  not not_39 (not_39_out, OP4);
  not not_40 (not_40_out, OP0);
  not not_41 (not_41_out, OP1);
  not not_42 (not_42_out, OP2);
  not not_43 (not_43_out, OP4);
  not not_44 (not_44_out, OP5);
  not not_45 (not_45_out, F0);
  not not_46 (not_46_out, F2);
  not not_47 (not_47_out, F3);
  not not_48 (not_48_out, F4);
  not not_49 (not_49_out, OP0);
  not not_50 (not_50_out, OP1);
  not not_51 (not_51_out, OP2);
  not not_52 (not_52_out, OP4);
  not not_53 (not_53_out, OP5);
  not not_54 (not_54_out, F3);
  not not_55 (not_55_out, F4);
  not not_56 (not_56_out, OP0);
  not not_57 (not_57_out, OP1);
  not not_58 (not_58_out, OP2);
  not not_59 (not_59_out, OP4);
  not not_60 (not_60_out, OP5);
  not not_61 (not_61_out, F2);
  not not_62 (not_62_out, F3);
  not not_63 (not_63_out, F4);
  not not_64 (not_64_out, OP0);
  not not_65 (not_65_out, OP1);
  not not_66 (not_66_out, OP2);
  not not_67 (not_67_out, OP4);
  not not_68 (not_68_out, OP5);
  not not_69 (not_69_out, F2);
  not not_70 (not_70_out, F4);
  not not_71 (not_71_out, OP0);
  not not_72 (not_72_out, OP2);
  not not_73 (not_73_out, OP4);
  not not_74 (not_74_out, OP5);
  not not_75 (not_75_out, OP1);
  not not_76 (not_76_out, OP4);
  not not_77 (not_77_out, OP5);
  not not_78 (not_78_out, OP2);
  not not_79 (not_79_out, OP3);
  not not_80 (not_80_out, OP4);
  not not_81 (not_81_out, OP0);
  not not_82 (not_82_out, OP1);
  not not_83 (not_83_out, OP2);
  not not_84 (not_84_out, OP3);
  not not_85 (not_85_out, OP4);
  not not_86 (not_86_out, OP5);
  not not_87 (not_87_out, F0);
  not not_88 (not_88_out, F1);
  not not_89 (not_89_out, F4);
  not not_90 (not_90_out, F5);
  not not_91 (not_91_out, OP0);
  not not_92 (not_92_out, OP1);
  not not_93 (not_93_out, OP2);
  not not_94 (not_94_out, OP4);
  not not_95 (not_95_out, OP0);
  not not_96 (not_96_out, OP2);
  not not_97 (not_97_out, OP4);
  not not_98 (not_98_out, OP5);
  not not_99 (not_99_out, OP1);
  not not_100 (not_100_out, OP2);
  not not_101 (not_101_out, OP4);
  not not_102 (not_102_out, OP5);
  not not_103 (not_103_out, OP0);
  not not_104 (not_104_out, OP3);
  not not_105 (not_105_out, OP4);
  not not_106 (not_106_out, OP5);
  not not_107 (not_107_out, OP1);
  not not_108 (not_108_out, OP3);
  not not_109 (not_109_out, OP4);
  not not_110 (not_110_out, OP5);
  not not_111 (not_111_out, OP2);
  not not_112 (not_112_out, OP4);
  not not_113 (not_113_out, OP0);
  not not_114 (not_114_out, OP1);
  not not_115 (not_115_out, OP2);
  not not_116 (not_116_out, OP3);
  not not_117 (not_117_out, OP4);
  not not_118 (not_118_out, OP5);
  not not_119 (not_119_out, F0);
  not not_120 (not_120_out, F2);
  not not_121 (not_121_out, F3);
  not not_122 (not_122_out, F4);
  not not_123 (not_123_out, OP0);
  not not_124 (not_124_out, OP1);
  not not_125 (not_125_out, OP2);
  not not_126 (not_126_out, OP3);
  not not_127 (not_127_out, OP4);
  not not_128 (not_128_out, OP5);
  not not_129 (not_129_out, F3);
  not not_130 (not_130_out, F4);
  not not_131 (not_131_out, OP0);
  not not_132 (not_132_out, OP1);
  not not_133 (not_133_out, OP2);
  not not_134 (not_134_out, OP3);
  not not_135 (not_135_out, OP4);
  not not_136 (not_136_out, OP5);
  not not_137 (not_137_out, F2);
  not not_138 (not_138_out, F3);
  not not_139 (not_139_out, F4);
  not not_140 (not_140_out, OP0);
  not not_141 (not_141_out, OP1);
  not not_142 (not_142_out, OP2);
  not not_143 (not_143_out, OP3);
  not not_144 (not_144_out, OP4);
  not not_145 (not_145_out, OP5);
  not not_146 (not_146_out, F2);
  not not_147 (not_147_out, F4);
  not not_148 (not_148_out, OP0);
  not not_149 (not_149_out, OP1);
  not not_150 (not_150_out, OP3);
  not not_151 (not_151_out, OP4);
  not not_152 (not_152_out, OP5);
  not not_153 (not_153_out, OP1);
  not not_154 (not_154_out, OP3);
  not not_155 (not_155_out, OP4);
  not not_156 (not_156_out, OP5);
  not not_157 (not_157_out, OP0);
  not not_158 (not_158_out, OP1);
  not not_159 (not_159_out, OP2);
  not not_160 (not_160_out, OP3);
  not not_161 (not_161_out, OP4);
  not not_162 (not_162_out, OP5);
  not not_163 (not_163_out, F0);
  not not_164 (not_164_out, F1);
  not not_165 (not_165_out, F2);
  not not_166 (not_166_out, F4);
  not not_167 (not_167_out, F5);
  not not_168 (not_168_out, OP0);
  not not_169 (not_169_out, OP2);
  not not_170 (not_170_out, OP3);
  not not_171 (not_171_out, OP4);
  not not_172 (not_172_out, OP5);
  not not_173 (not_173_out, F0);
  not not_174 (not_174_out, F1);
  not not_175 (not_175_out, F2);
  not not_176 (not_176_out, F4);
  not not_177 (not_177_out, F5);
  not not_178 (not_178_out, OP2);
  not not_179 (not_179_out, OP3);
  not not_180 (not_180_out, OP4);
  not not_181 (not_181_out, OP5);
  not not_182 (not_182_out, OP2);
  not not_183 (not_183_out, OP3);
  not not_184 (not_184_out, OP4);
  not not_185 (not_185_out, OP5);
  and and_1 (MemToReg, OP0, OP1, not_1_out, not_2_out, not_3_out, OP5);
  and and_2 (and_2_out, not_4_out, not_5_out, not_6_out, OP3, not_7_out, OP5);
  and and_3 (and_3_out, OP0, OP1, not_8_out, OP3, not_9_out, OP5);
  and and_4 (and_4_out, not_10_out, not_11_out, not_12_out, OP3, not_13_out);
  and and_5 (and_5_out, not_14_out, not_15_out, OP3, not_16_out, not_17_out);
  and and_6 (and_6_out, not_18_out, OP3, not_19_out, not_20_out);
  and and_7 (and_7_out, OP0, OP1, not_21_out, not_22_out, OP5);
  and and_8 (ERET, not_23_out, OP4, not_24_out, not_25_out, not_26_out, not_27_out, not_28_out, F4, F3, not_29_out, not_30_out, not_31_out);
  and and_9 (BLEZ, not_32_out, OP1, OP2, not_33_out, not_34_out, not_35_out);
  and and_10 (SB, not_36_out, not_37_out, not_38_out, OP3, not_39_out, OP5);
  and and_11 (and_11_out, not_40_out, not_41_out, not_42_out, not_43_out, not_44_out, not_45_out, not_46_out, not_47_out, not_48_out);
  and and_12 (and_12_out, not_49_out, not_50_out, not_51_out, not_52_out, not_53_out, not_54_out, not_55_out, F5);
  and and_13 (and_13_out, not_56_out, not_57_out, not_58_out, not_59_out, not_60_out, F1, not_61_out, not_62_out, not_63_out);
  and and_14 (and_14_out, not_64_out, not_65_out, not_66_out, not_67_out, not_68_out, F1, not_69_out, not_70_out, F5);
  and and_15 (and_15_out, not_71_out, not_72_out, OP3, not_73_out, not_74_out);
  and and_16 (and_16_out, not_75_out, OP3, not_76_out, not_77_out);
  and and_17 (and_17_out, OP0, OP1, not_78_out, not_79_out, not_80_out);
  and and_18 (SysCALL, not_81_out, not_82_out, not_83_out, not_84_out, not_85_out, not_86_out, not_87_out, not_88_out, F2, F3, not_89_out, not_90_out);
  and and_19 (and_19_out, not_91_out, not_92_out, not_93_out, OP3, not_94_out);
  and and_20 (and_20_out, not_95_out, not_96_out, OP3, not_97_out, not_98_out);
  and and_21 (and_21_out, not_99_out, not_100_out, OP3, not_101_out, not_102_out);
  and and_22 (and_22_out, not_103_out, OP2, not_104_out, not_105_out, not_106_out);
  and and_23 (and_23_out, not_107_out, OP2, not_108_out, not_109_out, not_110_out);
  and and_24 (and_24_out, OP0, OP1, not_111_out, not_112_out, OP5);
  and and_25 (and_25_out, not_113_out, not_114_out, not_115_out, not_116_out, not_117_out, not_118_out, not_119_out, not_120_out, not_121_out, not_122_out);
  and and_26 (and_26_out, not_123_out, not_124_out, not_125_out, not_126_out, not_127_out, not_128_out, not_129_out, not_130_out, F5);
  and and_27 (and_27_out, not_131_out, not_132_out, not_133_out, not_134_out, not_135_out, not_136_out, F1, not_137_out, not_138_out, not_139_out);
  and and_28 (and_28_out, not_140_out, not_141_out, not_142_out, not_143_out, not_144_out, not_145_out, F1, not_146_out, not_147_out, F5);
  and and_29 (BEQ, not_148_out, not_149_out, OP2, not_150_out, not_151_out, not_152_out);
  and and_30 (BNE, OP0, not_153_out, OP2, not_154_out, not_155_out, not_156_out);
  and and_31 (JR, not_157_out, not_158_out, not_159_out, not_160_out, not_161_out, not_162_out, not_163_out, not_164_out, not_165_out, F3, not_166_out, not_167_out);
  and and_32 (and_32_out, not_168_out, not_169_out, not_170_out, not_171_out, not_172_out, not_173_out, not_174_out, not_175_out, F3, not_176_out, not_177_out);
  and and_33 (and_33_out, OP1, not_178_out, not_179_out, not_180_out, not_181_out);
  and and_34 (JAL, OP0, OP1, not_182_out, not_183_out, not_184_out, not_185_out);
  or or_1 (MemWrite, and_2_out, and_3_out);
  or or_2 (ALU_SRC, and_4_out, and_5_out, and_6_out, and_7_out);
  or or_3 (RegWrite, and_11_out, and_12_out, and_13_out, and_14_out, and_15_out, and_16_out, and_17_out);
  or or_4 (SignedExt, and_19_out, and_20_out, and_21_out, and_22_out, and_23_out, and_24_out);
  or or_5 (RegDst, and_25_out, and_26_out, and_27_out, and_28_out);
  or or_6 (JUMP, and_32_out, and_33_out);
endmodule

// ALU
module MIPS_ALU (
  input  [4:0] shamt,
  input  [31:0] X,
  input  [31:0] Y,
  input  [3:0] AluOP,
  output Equal,
  output [31:0] Result,
  output [31:0] Result_2
);

  wire [0:0] comparator_1_lt, comparator_2_lt;
  wire [31:0] adder_1_out, AND_out, divider_1_out, divider_1_rem, multiplier_1_cout, multiplier_1_out,
       NOR_out, OR_out, shifter_1_out, shifter_2_out, shifter_3_out, subtractor_1_out, XOR_out;

  assign AND_out = X & Y;  // AND_Gate AND, 32 bits wide
  assign OR_out = X | Y;  // OR_Gate OR, 32 bits wide
  Shifter #(.width(32), .shift("ll")) shifter_1 (.in(Y), .\dist (shamt), .out(shifter_1_out));
  Shifter #(.width(32), .shift("ar")) shifter_2 (.in(Y), .\dist (shamt), .out(shifter_2_out));
  Shifter #(.width(32), .shift("lr")) shifter_3 (.in(Y), .\dist (shamt), .out(shifter_3_out));
  Multiplier #(.width(32)) multiplier_1 (.a(X), .b(Y), .out(multiplier_1_out), .cout(multiplier_1_cout));  // open: cin
  Divider #(.width(32)) divider_1 (.a(X), .b(Y), .out(divider_1_out), .rem(divider_1_rem));  // open: upper
  Adder #(.width(32)) adder_1 (.a(X), .b(Y), .out(adder_1_out));  // open: cin, cout
  Subtractor #(.width(32)) subtractor_1 (.a(X), .b(Y), .out(subtractor_1_out));  // open: bin, bout
  assign XOR_out = X ^ Y;  // XOR_Gate XOR, 32 bits wide
  assign NOR_out = ~(X | Y);  // NOR_Gate NOR, 32 bits wide
  Comparator #(.width(32), .mode("twosComplement")) comparator_1 (
    .a(X), .b(Y), .eq(Equal), .lt(comparator_1_lt[0]));  // open: gt
  Comparator #(.width(32), .mode("unsigned")) comparator_2 (.a(X), .b(Y), .lt(comparator_2_lt[0]));  // open: gt, eq
  Multiplexer #(.select(4), .width(32), .disabled("Z"), .enable("false")) multiplexer_1 (
    .in0(shifter_1_out), .in1(shifter_2_out), .in2(shifter_3_out), .in3(multiplier_1_out),
    .in4(divider_1_out), .in5(adder_1_out), .in6(subtractor_1_out), .in7(AND_out), .in8(OR_out),
    .in9(XOR_out), .in10(NOR_out), .in11({{31{1'b0}}, comparator_1_lt[0]}),
    .in12({{31{1'b0}}, comparator_2_lt[0]}), .in13({32{1'b0}}), .in14({32{1'b0}}), .in15({32{1'b0}}),
    .out(Result), .sel(AluOP));
  Multiplexer #(.select(4), .width(32), .disabled("Z"), .enable("false")) multiplexer_2 (
    .in0({32{1'b0}}), .in1({32{1'b0}}), .in2({32{1'b0}}), .in3(multiplier_1_cout), .in4(divider_1_rem),
    .in5({32{1'b0}}), .in6({32{1'b0}}), .in7({32{1'b0}}), .in8({32{1'b0}}), .in9({32{1'b0}}),
    .in10({32{1'b0}}), .in11({32{1'b0}}), .in12({32{1'b0}}), .in13({32{1'b0}}), .in14({32{1'b0}}),
    .in15({32{1'b0}}), .out(Result_2), .sel(AluOP));

  // Other names for the same wires on the sheet: Result2[31:0] = Result_2; S[3:0] = AluOP

  // Notes on the sheet:
  //   不要改变此引脚区域内容，也不要改变ALU封装形式
  //   输入引脚
  //   输出引脚
endmodule

module MIPS_Regifile (
  input  [31:0] Din,
  input  Clk,
  input  WE,
  input  [4:0] R1_num,
  input  [4:0] W_num,
  input  [4:0] R2_num,
  output [31:0] R1,
  output [31:0] R2
);

  // RegisterFile registerfile_1: pin names not known; wires that end beside it: Din, Clk, WE, W_num, R1_num, R2_num, R1, R2
endmodule

module \理想流水线  (
);

  wire and_2_out, and_3_out, and_4_out, and_5_out, and_6_out, and_7_out, CLK, comparator_1_eq,
       comparator_2_eq, comparator_2_lt, ex_mem_l_1_jal_2, ex_mem_l_1_memtoreg_2, ex_mem_l_1_memwrite_2,
       ex_mem_l_1_regdst_2, ex_mem_l_1_regwrite_2, ex_mem_l_1_sb_2, ex_mem_l_1_syscall_2, final_IsStop,
       final_IsStop_t, Go, id_ex_l_1_alusrcb_2, id_ex_l_1_beq_2, id_ex_l_1_blez_2, id_ex_l_1_bne_2,
       id_ex_l_1_jal_2, id_ex_l_1_jr_2, id_ex_l_1_memtoreg_2, id_ex_l_1_memwrite_2, id_ex_l_1_regdst_2,
       id_ex_l_1_regwrite_2, id_ex_l_1_sb_2, id_ex_l_1_syscall_2, IR1, IR2, IR3, IsStop, JAL,
       mem_wb_l_1_memtoreg_2, mips_alu_1_equal, multiplexer_4_out, multiplexer_11_out, not_1_out, not_2_out,
       not_3_out, not_4_out, not_5_out, or_1_out, or_2_out, or_3_out, or_5_out, or_6_out, RegDst,
       register_3_q, RegWrite, RST, RstFlow, SEL, SignedExt, stop, Syscall, W1, W2, W3,
       \单周期硬布线控制器_1_alu_src , \单周期硬布线控制器_1_beq , \单周期硬布线控制器_1_blez , \单周期硬布线控制器_1_bne , \单周期硬布线控制器_1_jal ,
       \单周期硬布线控制器_1_jmp , \单周期硬布线控制器_1_jr , \单周期硬布线控制器_1_memtoreg , \单周期硬布线控制器_1_memwrite ,
       \单周期硬布线控制器_1_regdst , \单周期硬布线控制器_1_regwrite , \单周期硬布线控制器_1_sb , \单周期硬布线控制器_1_signedext ,
       \点击此键_先设置同步清零信号_out ;
  wire [1:0] or_4_out;
  wire [3:0] id_ex_l_1_aluop_2, \单周期硬布线控制器_1_alu_op ;
  wire [4:0] multiplexer_6_out, multiplexer_7_out, multiplexer_8_out, multiplexer_9_out, WB_rd, WB_rt;
  wire [7:0] ram_1_data, ram_1_data_2, ram_1_data_3, ram_1_data_4;
  wire [11:0] EX_PC, ID_PC, IF_PC, MEM_PC, WB_PC;
  wire [15:0] \LoadUse次数 , \总周期数 , \插入气泡数 , \无条件分支数 , \条件分支成功数 ;
  wire [27:2] PC_no_condition;
  wire [31:0] a0, adder_1_out, bit_extender_1_out, bit_extender_2_out, ex_mem_l_1_alu_2, ex_mem_l_1_ir_2,
       ex_mem_l_1_pc_2, ex_mem_l_1_pc_4_2, ex_mem_l_1_r2_2, id_ex_l_1_ir_2, id_ex_l_1_pc_2, id_ex_l_1_r2_2,
       if_id_l_1_ir_2, if_id_l_1_pc_2, if_id_l_1_pc_4_2, Jal_PC_4, LedData, mem_wb_l_1_alu_2,
       mem_wb_l_1_ir_2, mem_wb_l_1_md_2, mips_alu_1_result, multiplexer_1_out, multiplexer_2_out,
       multiplexer_3_out, multiplexer_10_out, multiplexer_12_out, multiplexer_13_out, multiplexer_14_out,
       multiplexer_15_out, multiplexer_16_out, PC_4, PC_condition, PC_q, rom_1_data, RS, shifter_1_out, v0;

  Multiplexer #(.select(1), .width(32), .disabled("Z"), .enable("false")) multiplexer_1 (
    .in0({PC_4[31:28], PC_no_condition, 2'b00}), .in1(RS), .out(multiplexer_1_out), .sel(id_ex_l_1_jr_2));
  Button \u_点击此键_先设置同步清零信号  (.out(\点击此键_先设置同步清零信号_out ));
  Register #(.width(1), .trigger("falling"), .Select("low")) register_1 (
    .D(1'b0), .Q(RstFlow), .clk(RST), .preset(\点击此键_先设置同步清零信号_out ));  // open: en, clr, cs
  Multiplexer #(.select(2), .width(32), .disabled("Z"), .enable("false")) multiplexer_2 (
    .in0(adder_1_out), .in1(PC_condition), .in2(multiplexer_1_out), .out(multiplexer_2_out), .sel(or_4_out));  // open: in3
  Comparator #(.width(32), .mode("twosComplement")) comparator_1 (
    .a(v0), .b(32'h22), .eq(comparator_1_eq));  // open: gt, lt
  Multiplexer #(.select(1), .width(32), .disabled("Z"), .enable("false")) multiplexer_3 (
    .in0(multiplexer_2_out), .in1(PC_q), .out(multiplexer_3_out), .sel(stop));
  Register #(.width(32), .trigger("rising"), .Select("low")) PC (
    .D(multiplexer_3_out), .Q(PC_q), .clk(CLK), .clr(RST));  // open: en
  not not_1 (not_1_out, comparator_1_eq);
  and and_1 (IsStop, not_1_out, Syscall);
  xor xor_1 (stop, final_IsStop_t, register_3_q);
  Button \u_再总复位  (.out(RST));
  Button _1 (.out(IR1));
  Button _2 (.out(IR2));
  Button _3 (.out(IR3));
  Register #(.width(32), .trigger("rising"), .Select("low")) register_2 (
    .D(a0), .Q(LedData), .clk(and_2_out), .clr(RST));  // open: en
  and and_2 (and_2_out, Syscall, comparator_1_eq);
  and and_3 (and_3_out, final_IsStop_t, Go);
  Register #(.width(1), .trigger("rising"), .Select("low")) register_3 (
    .D(1'b0), .Q(register_3_q), .clk(CLK), .clr(RST), .preset(and_3_out));  // open: en, cs
  Button \u_继续运行  (.out(Go));
  LED #(.active("true")) led_1 (.in(W1));
  LED #(.active("true")) led_2 (.in(W2));
  LED #(.active("true")) led_3 (.in(W3));
  Multiplexer #(.select(1), .width(1), .disabled("Z"), .enable("false")) multiplexer_4 (
    .in0(final_IsStop_t), .in1(1'b0), .out(multiplexer_4_out), .sel(register_3_q));
  Hex_Digit_Display hex_digit_display_1 (.value(LedData[27:24]));  // open: dp
  Hex_Digit_Display hex_digit_display_2 (.value(LedData[31:28]));  // open: dp
  Adder #(.width(32)) adder_1 (.a(PC_q), .b(32'h4), .out(adder_1_out));  // open: cin, cout
  ROM #(.addrWidth(10), .dataWidth(32), .Select("high")) rom_1 (.addr(PC_q[11:2]), .data(rom_1_data));
  Multiplexer #(.select(1), .width(1), .disabled("Z"), .enable("false")) multiplexer_5 (
    .in0(multiplexer_4_out), .in1(1'b0), .out(SEL), .sel(RstFlow));
  Hex_Digit_Display hex_digit_display_3 (.value(LedData[23:20]));  // open: dp
  Hex_Digit_Display hex_digit_display_4 (.value(LedData[19:16]));  // open: dp
  or or_1 (or_1_out, RST, CLK);
  Hex_Digit_Display hex_digit_display_5 (.value(LedData[15:12]));  // open: dp
  Hex_Digit_Display hex_digit_display_6 (.value(LedData[11:8]));  // open: dp
  Clock #(.highDuration(1), .lowDuration(1)) clock_1 (.out(CLK));
  IF_ID_l if_id_l_1 (
    .CLK(or_1_out), .\同步清零_气泡_高电平有效 (RstFlow), .\使能端_低电平有效 (SEL), .PC(PC_q), .PC_2(if_id_l_1_pc_2),
    .IR(rom_1_data), .IR_2(if_id_l_1_ir_2), .PC_4(adder_1_out), .PC_4_2(if_id_l_1_pc_4_2));  // open: ERET, ERET_2
  Hex_Digit_Display hex_digit_display_7 (.value(LedData[3:0]));  // open: dp
  Hex_Digit_Display hex_digit_display_8 (.value(LedData[7:4]));  // open: dp
  Multiplexer #(.select(1), .width(5), .disabled("Z"), .enable("false")) multiplexer_6 (
    .in0(WB_rt), .in1(WB_rd), .out(multiplexer_6_out), .sel(RegDst));
  // Probe on \总周期数 
  // Probe on \无条件分支数 
  // Probe on \条件分支成功数 
  // Probe on \插入气泡数 
  // Probe on \LoadUse次数 
  \单周期硬布线控制器  \u_单周期硬布线控制器_1  (
    .OP(if_id_l_1_ir_2[31:26]), .Func(if_id_l_1_ir_2[5:0]), .ALU_OP(\单周期硬布线控制器_1_alu_op ),
    .MemToReg(\单周期硬布线控制器_1_memtoreg ), .MemWrite(\单周期硬布线控制器_1_memwrite ), .ALU_SRC(\单周期硬布线控制器_1_alu_src ),
    .RegWrite(\单周期硬布线控制器_1_regwrite ), .SysCALL(Syscall), .SignedExt(\单周期硬布线控制器_1_signedext ),
    .RegDst(\单周期硬布线控制器_1_regdst ), .Beq(\单周期硬布线控制器_1_beq ), .Bne(\单周期硬布线控制器_1_bne ), .JR(\单周期硬布线控制器_1_jr ),
    .JMP(\单周期硬布线控制器_1_jmp ), .JAL(\单周期硬布线控制器_1_jal ), .BLEZ(\单周期硬布线控制器_1_blez ), .SB(\单周期硬布线控制器_1_sb ));  // open: ERET
  Multiplexer #(.select(1), .width(5), .disabled("Z"), .enable("false")) multiplexer_7 (
    .in0(if_id_l_1_ir_2[25:21]), .in1(5'b00010), .out(multiplexer_7_out), .sel(Syscall));
  Multiplexer #(.select(1), .width(5), .disabled("Z"), .enable("false")) multiplexer_8 (
    .in0(if_id_l_1_ir_2[20:16]), .in1(5'b00100), .out(multiplexer_8_out), .sel(Syscall));
  Multiplexer #(.select(1), .width(5), .disabled("Z"), .enable("false")) multiplexer_9 (
    .in0(multiplexer_6_out), .in1({5{1'b1}}), .out(multiplexer_9_out), .sel(JAL));
  Multiplexer #(.select(1), .width(32), .disabled("Z"), .enable("false")) multiplexer_10 (
    .in0(multiplexer_16_out), .in1(Jal_PC_4), .out(multiplexer_10_out), .sel(JAL));
  // Probe on IF_PC
  MIPS_Regifile mips_regifile_1 (
    .Din(multiplexer_10_out), .Clk(CLK), .R1(v0), .R2(a0), .WE(RegWrite), .W_num(multiplexer_9_out),
    .R1_num(multiplexer_7_out), .R2_num(multiplexer_8_out));
  // Probe on EX_PC
  // Probe on ID_PC
  // Probe on MEM_PC
  // Probe on WB_PC
  or or_2 (or_2_out, RST, CLK);
  ID_EX_l id_ex_l_1 (
    .CLK(or_2_out), .\同步清零_气泡_高电平有效 (RstFlow), .\使能端_低电平有效 (SEL), .PC(if_id_l_1_pc_2), .R1(v0),
    .BLEZ(\单周期硬布线控制器_1_blez ), .SignedExt(\单周期硬布线控制器_1_signedext ), .MemToReg(\单周期硬布线控制器_1_memtoreg ),
    .MemWrite(\单周期硬布线控制器_1_memwrite ), .BEQ(\单周期硬布线控制器_1_beq ), .Syscall(IsStop),
    .RegWrite(\单周期硬布线控制器_1_regwrite ), .SB(\单周期硬布线控制器_1_sb ), .BNE(\单周期硬布线控制器_1_bne ),
    .RegDst(\单周期硬布线控制器_1_regdst ), .IR(if_id_l_1_ir_2), .R2(a0), .AluSrcB(\单周期硬布线控制器_1_alu_src ),
    .JR(\单周期硬布线控制器_1_jr ), .JAL(\单周期硬布线控制器_1_jal ), .AluOP(\单周期硬布线控制器_1_alu_op ),
    .Imm26(if_id_l_1_ir_2[25:0]), .JMP(\单周期硬布线控制器_1_jmp ), .PC_2(id_ex_l_1_pc_2), .R1_2(RS),
    .BLEZ_2(id_ex_l_1_blez_2), .SignedExt_2(SignedExt), .MemToReg_2(id_ex_l_1_memtoreg_2),
    .MemWrite_2(id_ex_l_1_memwrite_2), .BEQ_2(id_ex_l_1_beq_2), .Syscall_2(id_ex_l_1_syscall_2),
    .RegWrite_2(id_ex_l_1_regwrite_2), .SB_2(id_ex_l_1_sb_2), .BNE_2(id_ex_l_1_bne_2),
    .RegDst_2(id_ex_l_1_regdst_2), .IR_2(id_ex_l_1_ir_2), .R2_2(id_ex_l_1_r2_2),
    .AluSrcB_2(id_ex_l_1_alusrcb_2), .JR_2(id_ex_l_1_jr_2), .JAL_2(id_ex_l_1_jal_2),
    .AluOP_2(id_ex_l_1_aluop_2), .Imm26_2(PC_no_condition), .JMP_2(or_4_out[1]), .PC_4(if_id_l_1_pc_4_2),
    .PC_4_2(PC_4));  // open: Forwarding_R1, Forwarding_R1_2, Forwarding_R2, Forwarding_R2_2, ERET, ERET_2
  and and_4 (and_4_out, not_2_out, CLK);
  not not_2 (not_2_out, stop);
  Counter #(.width(16), .max('hffff), .ongoal("wrap"), .trigger("rising"), .behavior("old")) counter_1 (
    .count(1'b1), .Q(\总周期数 ), .clk(multiplexer_11_out), .clr(RST));  // open: load, D, carry, preset
  Multiplexer #(.select(1), .width(1), .disabled("Z"), .enable("false")) multiplexer_11 (
    .in0(and_4_out), .in1(1'b0), .out(multiplexer_11_out), .sel(not_4_out));
  not not_3 (not_3_out, CLK);
  not not_4 (not_4_out, not_3_out);
  Comparator #(.width(32), .mode("twosComplement")) comparator_2 (
    .a(RS), .b({32{1'b0}}), .eq(comparator_2_eq), .lt(comparator_2_lt));  // open: gt
  assign bit_extender_1_out = {{16{1'b0}}, PC_no_condition[17:2]};  // Bit_Extender bit_extender_1
  assign bit_extender_2_out = {{16{PC_no_condition[17]}}, PC_no_condition[17:2]};  // Bit_Extender bit_extender_2
  or or_3 (or_3_out, comparator_2_eq, comparator_2_lt);
  Multiplexer #(.select(1), .width(32), .disabled("Z"), .enable("false")) multiplexer_12 (
    .in0(bit_extender_1_out), .in1(bit_extender_2_out), .out(multiplexer_12_out), .sel(SignedExt));
  and and_5 (and_5_out, or_3_out, id_ex_l_1_blez_2);
  Multiplexer #(.select(1), .width(32), .disabled("Z"), .enable("false")) multiplexer_13 (
    .in0(id_ex_l_1_r2_2), .in1(multiplexer_12_out), .out(multiplexer_13_out), .sel(id_ex_l_1_alusrcb_2));
  Shifter #(.width(32), .shift("ll")) shifter_1 (.in(multiplexer_12_out), .\dist (5'b00010), .out(shifter_1_out));
  Adder #(.width(32)) adder_2 (.a(shifter_1_out), .b(PC_4), .out(PC_condition));  // open: cin, cout
  not not_5 (not_5_out, mips_alu_1_equal);
  MIPS_ALU mips_alu_1 (
    .X(RS), .Y(multiplexer_13_out), .AluOP(id_ex_l_1_aluop_2), .Equal(mips_alu_1_equal),
    .Result(mips_alu_1_result), .shamt(PC_no_condition[12:8]));  // open: Result_2
  and and_6 (and_6_out, mips_alu_1_equal, id_ex_l_1_beq_2);
  and and_7 (and_7_out, id_ex_l_1_bne_2, not_5_out);
  or or_4 (or_4_out[0], and_5_out, and_7_out, and_6_out);
  or or_5 (or_5_out, RST, CLK);
  EX_MEM_l ex_mem_l_1 (
    .CLK(or_5_out), .\同步清零_气泡_高电平有效 (RstFlow), .\使能端_低电平有效 (SEL), .PC(id_ex_l_1_pc_2),
    .MemToReg(id_ex_l_1_memtoreg_2), .MemWrite(id_ex_l_1_memwrite_2), .RegWrite(id_ex_l_1_regwrite_2),
    .SB(id_ex_l_1_sb_2), .RegDst(id_ex_l_1_regdst_2), .IR(id_ex_l_1_ir_2), .R2(id_ex_l_1_r2_2),
    .JAL(id_ex_l_1_jal_2), .PC_2(ex_mem_l_1_pc_2), .MemToReg_2(ex_mem_l_1_memtoreg_2),
    .MemWrite_2(ex_mem_l_1_memwrite_2), .RegWrite_2(ex_mem_l_1_regwrite_2), .SB_2(ex_mem_l_1_sb_2),
    .RegDst_2(ex_mem_l_1_regdst_2), .IR_2(ex_mem_l_1_ir_2), .R2_2(ex_mem_l_1_r2_2), .JAL_2(ex_mem_l_1_jal_2),
    .ALU(mips_alu_1_result), .ALU_2(ex_mem_l_1_alu_2), .PC_4(PC_4), .PC_4_2(ex_mem_l_1_pc_4_2),
    .Syscall(id_ex_l_1_syscall_2), .Syscall_2(ex_mem_l_1_syscall_2));
  Multiplexer #(.select(2), .width(32), .disabled("Z"), .enable("false")) multiplexer_14 (
    .in0({ram_1_data, ram_1_data_4, ram_1_data_3, ex_mem_l_1_r2_2[7:0]}),
    .in1({ram_1_data, ram_1_data_4, ex_mem_l_1_r2_2[7:0], ram_1_data_2}),
    .in2({ram_1_data, ex_mem_l_1_r2_2[7:0], ram_1_data_3, ram_1_data_2}),
    .in3({ex_mem_l_1_r2_2[7:0], ram_1_data_4, ram_1_data_3, ram_1_data_2}), .out(multiplexer_14_out),
    .sel(ex_mem_l_1_alu_2[1:0]));
  Multiplexer #(.select(1), .width(32), .disabled("Z"), .enable("false")) multiplexer_15 (
    .in0(ex_mem_l_1_r2_2), .in1(multiplexer_14_out), .out(multiplexer_15_out), .sel(ex_mem_l_1_sb_2));
  RAM #(.addrWidth(10), .dataWidth(32), .bus("separate"), .Select("high")) ram_1 (
    .addr(ex_mem_l_1_alu_2[11:2]), .din(multiplexer_15_out),
    .data({ram_1_data, ram_1_data_4, ram_1_data_3, ram_1_data_2}), .str(ex_mem_l_1_memwrite_2), .clk(CLK),
    .clr(RST));  // open: sel, ld
  or or_6 (or_6_out, RST, CLK);
  MEM_WB_l mem_wb_l_1 (
    .CLK(or_6_out), .\同步清零_气泡_高电平有效 (RstFlow), .\使能端_低电平有效 (SEL), .PC(ex_mem_l_1_pc_2),
    .MemToReg(ex_mem_l_1_memtoreg_2), .MemToReg_2(mem_wb_l_1_memtoreg_2), .RegWrite(ex_mem_l_1_regwrite_2),
    .RegWrite_2(RegWrite), .RegDst(ex_mem_l_1_regdst_2), .IR(ex_mem_l_1_ir_2),
    .MD({ram_1_data, ram_1_data_4, ram_1_data_3, ram_1_data_2}), .RegDst_2(RegDst),
    .IR_2({mem_wb_l_1_ir_2[31:21], WB_rt, WB_rd, mem_wb_l_1_ir_2[10:0]}), .MD_2(mem_wb_l_1_md_2),
    .JAL(ex_mem_l_1_jal_2), .JAL_2(JAL), .ALU(ex_mem_l_1_alu_2), .ALU_2(mem_wb_l_1_alu_2),
    .PC_4(ex_mem_l_1_pc_4_2), .PC_4_2(Jal_PC_4), .Syscall(ex_mem_l_1_syscall_2), .Syscall_2(final_IsStop));  // open: PC_2
  Multiplexer #(.select(1), .width(32), .disabled("Z"), .enable("false")) multiplexer_16 (
    .in0(mem_wb_l_1_alu_2), .in1(mem_wb_l_1_md_2), .out(multiplexer_16_out), .sel(mem_wb_l_1_memtoreg_2));

  // Other names for the same wires on the sheet: PC_no_condition[31:28] = PC_4[31:28]

  // Notes on the sheet:
  //   中断源
  //   中断等待指示
  //   指令存储器
  //   contents of rom_1 (hex, n*v repeats v):
  //   20100000 20110000 20120000 20130000 36100000 36310001 36520002 36730003 ae100000 ae110004 ae120008
  //   ae13000c 2002000a 20110000 20120000 20130000 c
  //   数码管输出
  //   PC+4
  //   IR
  //   PC
  //   指令字
  //   OP
  //   Func
  //   rs
  //   rt
  //   rd
  //   Imm26
  //   流水调试日志用
  //   IR
  //   PC
  //   MemWrite
  //   SB
  //   IR
  //   PC
  //   R2
  //   ALU
  //   MemToReg
  //   rt
  //   rd
endmodule

module \气泡流水线  (
);

  wire and_1_out, and_3_out, and_4_out, and_5_out, and_6_out, and_7_out, and_8_out, and_9_out, and_10_out,
       and_11_out, Bubble, CLK, comparator_1_eq, comparator_2_eq, comparator_2_lt, ex_mem_l_1_jal_2,
       ex_mem_l_1_memtoreg_2, ex_mem_l_1_memwrite_2, ex_mem_l_1_regdst_2, ex_mem_l_1_sb_2,
       ex_mem_l_1_syscall_2, EX_RegWrite, final_IsStop, final_IsStop_t, Go, id_ex_l_1_alusrcb_2,
       id_ex_l_1_beq_2, id_ex_l_1_blez_2, id_ex_l_1_bne_2, id_ex_l_1_jal_2, id_ex_l_1_jr_2,
       id_ex_l_1_memtoreg_2, id_ex_l_1_memwrite_2, id_ex_l_1_regdst_2, id_ex_l_1_sb_2, id_ex_l_1_syscall_2,
       IR1, IR2, IR3, IsRelated, IsStop, JAL, MEM_RegWrite, mem_wb_l_1_memtoreg_2, mips_alu_1_equal,
       multiplexer_4_out, multiplexer_11_out, multiplexer_14_out, multiplexer_15_out, multiplexer_20_out,
       not_1_out, not_2_out, not_3_out, not_4_out, not_5_out, not_6_out, not_7_out, not_8_out, not_9_out,
       not_10_out, not_11_out, not_12_out, not_13_out, or_1_out, or_2_out, or_3_out, or_4_out, or_5_out,
       or_6_out, or_9_out, or_10_out, RegDst, register_3_q, RegWrite, RST, RstFlow, SEL, SignedExt, stop,
       Syscall, W1, W2, W3, \单周期硬布线控制器_1_alu_src , \单周期硬布线控制器_1_beq , \单周期硬布线控制器_1_blez , \单周期硬布线控制器_1_bne ,
       \单周期硬布线控制器_1_jal , \单周期硬布线控制器_1_jmp , \单周期硬布线控制器_1_jr , \单周期硬布线控制器_1_memtoreg ,
       \单周期硬布线控制器_1_memwrite , \单周期硬布线控制器_1_regdst , \单周期硬布线控制器_1_regwrite , \单周期硬布线控制器_1_sb ,
       \单周期硬布线控制器_1_signedext , \无条件分支 , \条件分支 , \源寄存器使用情况_1_r1_used , \源寄存器使用情况_1_r2_used ,
       \点击此键_先设置同步清零信号_out ;
  wire [3:0] id_ex_l_1_aluop_2, \单周期硬布线控制器_1_alu_op ;
  wire [4:0] EX_WriteReg_num, MEM_WriteReg_num, multiplexer_8_out, multiplexer_9_out, multiplexer_16_out,
       multiplexer_21_out, R1_Relate, R2_Relate, WB_rd, WB_rt;
  wire [5:0] Func, OP;
  wire [15:0] \LoadUse次数 , \总周期数 , \插入气泡数 , \无条件分支数 , \条件分支成功数 ;
  wire [25:6] if_id_l_1_ir_2;
  wire [27:2] PC_no_condition;
  wire [31:0] a0, adder_1_out, bit_extender_1_out, bit_extender_2_out, ex_mem_l_1_alu_2, ex_mem_l_1_ir_2,
       ex_mem_l_1_pc_4_2, ex_mem_l_1_r2_2, EX_PC, id_ex_l_1_ir_2, id_ex_l_1_r2_2, ID_PC, if_id_l_1_pc_4_2,
       IF_PC, Jal_PC_4, LedData, MEM_PC, mem_wb_l_1_alu_2, mem_wb_l_1_ir_2, mem_wb_l_1_md_2,
       mips_alu_1_result, multiplexer_1_out, multiplexer_2_out, multiplexer_3_out, multiplexer_10_out,
       multiplexer_12_out, multiplexer_13_out, multiplexer_18_out, multiplexer_19_out, multiplexer_23_out,
       PC_4, PC_condition, ram_1_data, rom_1_data, RS, shifter_1_out, v0, WB_PC;

  Multiplexer #(.select(1), .width(32), .disabled("Z"), .enable("false")) multiplexer_1 (
    .in0({PC_4[31:28], PC_no_condition, 2'b00}), .in1(RS), .out(multiplexer_1_out), .sel(id_ex_l_1_jr_2));
  Button \u_点击此键_先设置同步清零信号  (.out(\点击此键_先设置同步清零信号_out ));
  Register #(.width(1), .trigger("falling"), .Select("low")) register_1 (
    .D(1'b0), .Q(RstFlow), .clk(RST), .preset(\点击此键_先设置同步清零信号_out ));  // open: en, clr, cs
  Multiplexer #(.select(2), .width(32), .disabled("Z"), .enable("false")) multiplexer_2 (
    .in0(adder_1_out), .in1(PC_condition), .in2(multiplexer_1_out), .out(multiplexer_2_out),
    .sel({\无条件分支 , \条件分支 }));  // open: in3
  Comparator #(.width(32), .mode("twosComplement")) comparator_1 (
    .a(v0), .b(32'h22), .eq(comparator_1_eq));  // open: gt, lt
  not not_1 (not_1_out, comparator_1_eq);
  Register #(.width(32), .trigger("rising"), .Select("low")) PC (
    .D(multiplexer_3_out), .en(not_2_out), .Q(IF_PC), .clk(CLK), .clr(RST));
  Multiplexer #(.select(1), .width(32), .disabled("Z"), .enable("false")) multiplexer_3 (
    .in0(multiplexer_2_out), .in1(IF_PC), .out(multiplexer_3_out), .sel(stop));
  not not_2 (not_2_out, IsRelated);
  and and_1 (and_1_out, Syscall, comparator_1_eq);
  and and_2 (IsStop, not_1_out, Syscall);
  xor xor_1 (stop, final_IsStop_t, register_3_q);
  Button \u_再总复位  (.out(RST));
  Button _1 (.out(IR1));
  Button _2 (.out(IR2));
  Button _3 (.out(IR3));
  Register #(.width(32), .trigger("rising"), .Select("low")) register_2 (
    .D(a0), .Q(LedData), .clk(and_1_out), .clr(RST));  // open: en
  and and_3 (and_3_out, final_IsStop_t, Go);
  Register #(.width(1), .trigger("rising"), .Select("low")) register_3 (
    .D(1'b0), .Q(register_3_q), .clk(CLK), .clr(RST), .preset(and_3_out));  // open: en, cs
  Button \u_继续运行  (.out(Go));
  LED #(.active("true")) led_1 (.in(W1));
  LED #(.active("true")) led_2 (.in(W2));
  LED #(.active("true")) led_3 (.in(W3));
  Adder #(.width(32)) adder_1 (.a(IF_PC), .b(32'h4), .out(adder_1_out));  // open: cin, cout
  Multiplexer #(.select(1), .width(1), .disabled("Z"), .enable("false")) multiplexer_4 (
    .in0(final_IsStop_t), .in1(1'b0), .out(multiplexer_4_out), .sel(register_3_q));
  Multiplexer #(.select(1), .width(1), .disabled("Z"), .enable("false")) multiplexer_5 (
    .in0(multiplexer_4_out), .in1(1'b0), .out(SEL), .sel(or_1_out));
  Hex_Digit_Display hex_digit_display_1 (.value(LedData[27:24]));  // open: dp
  Hex_Digit_Display hex_digit_display_2 (.value(LedData[31:28]));  // open: dp
  ROM #(.addrWidth(10), .dataWidth(32), .Select("high")) rom_1 (.addr(IF_PC[11:2]), .data(rom_1_data));
  or or_1 (or_1_out, Bubble, RstFlow);
  or or_2 (or_2_out, SEL, IsRelated);
  Hex_Digit_Display hex_digit_display_3 (.value(LedData[23:20]));  // open: dp
  Hex_Digit_Display hex_digit_display_4 (.value(LedData[19:16]));  // open: dp
  IF_ID_l if_id_l_1 (
    .CLK(or_3_out), .\同步清零_气泡_高电平有效 (or_1_out), .\使能端_低电平有效 (or_2_out), .PC(IF_PC), .PC_2(ID_PC),
    .IR(rom_1_data), .IR_2({OP, if_id_l_1_ir_2, Func}), .PC_4(adder_1_out), .PC_4_2(if_id_l_1_pc_4_2));  // open: ERET, ERET_2
  or or_3 (or_3_out, RST, CLK);
  Hex_Digit_Display hex_digit_display_5 (.value(LedData[15:12]));  // open: dp
  Hex_Digit_Display hex_digit_display_6 (.value(LedData[11:8]));  // open: dp
  Clock #(.highDuration(1), .lowDuration(1)) clock_1 (.out(CLK));
  Hex_Digit_Display hex_digit_display_7 (.value(LedData[3:0]));  // open: dp
  Hex_Digit_Display hex_digit_display_8 (.value(LedData[7:4]));  // open: dp
  \源寄存器使用情况  \u_源寄存器使用情况_1  (.OP(OP), .FUN(Func), .R1_Used(\源寄存器使用情况_1_r1_used ), .R2_Used(\源寄存器使用情况_1_r2_used ));
  \数据相关检测  \u_数据相关检测_1  (
    .R1_Used(\源寄存器使用情况_1_r1_used ), .R2_Used(\源寄存器使用情况_1_r2_used ), .R1_num(R1_Relate), .R2_num(R2_Relate),
    .EX_WriteReg_num(EX_WriteReg_num), .EX_RegWrite(EX_RegWrite), .MEM_WriteReg_num(MEM_WriteReg_num),
    .MEM_RegWrite(MEM_RegWrite), .Relate(IsRelated));  // open: EX_OP, Load_Use, R1_EX_Relate, R2_EX_Relate, R1_MEM_Relate, R2_MEM_Relate
  \单周期硬布线控制器  \u_单周期硬布线控制器_1  (
    .OP(OP), .Func(Func), .ALU_OP(\单周期硬布线控制器_1_alu_op ), .MemToReg(\单周期硬布线控制器_1_memtoreg ),
    .MemWrite(\单周期硬布线控制器_1_memwrite ), .ALU_SRC(\单周期硬布线控制器_1_alu_src ), .RegWrite(\单周期硬布线控制器_1_regwrite ),
    .SysCALL(Syscall), .SignedExt(\单周期硬布线控制器_1_signedext ), .RegDst(\单周期硬布线控制器_1_regdst ),
    .Beq(\单周期硬布线控制器_1_beq ), .Bne(\单周期硬布线控制器_1_bne ), .JR(\单周期硬布线控制器_1_jr ), .JMP(\单周期硬布线控制器_1_jmp ),
    .JAL(\单周期硬布线控制器_1_jal ), .BLEZ(\单周期硬布线控制器_1_blez ), .SB(\单周期硬布线控制器_1_sb ));  // open: ERET
  Multiplexer #(.select(1), .width(5), .disabled("Z"), .enable("false")) multiplexer_6 (
    .in0(if_id_l_1_ir_2[25:21]), .in1(5'b00010), .out(R1_Relate), .sel(Syscall));
  Multiplexer #(.select(1), .width(5), .disabled("Z"), .enable("false")) multiplexer_7 (
    .in0(if_id_l_1_ir_2[20:16]), .in1(5'b00100), .out(R2_Relate), .sel(Syscall));
  Multiplexer #(.select(1), .width(5), .disabled("Z"), .enable("false")) multiplexer_8 (
    .in0(WB_rt), .in1(WB_rd), .out(multiplexer_8_out), .sel(RegDst));
  Multiplexer #(.select(1), .width(5), .disabled("Z"), .enable("false")) multiplexer_9 (
    .in0(multiplexer_8_out), .in1({5{1'b1}}), .out(multiplexer_9_out), .sel(JAL));
  Multiplexer #(.select(1), .width(32), .disabled("Z"), .enable("false")) multiplexer_10 (
    .in0(multiplexer_23_out), .in1(Jal_PC_4), .out(multiplexer_10_out), .sel(JAL));
  // Probe on \总周期数 
  // Probe on \无条件分支数 
  // Probe on \条件分支成功数 
  // Probe on \插入气泡数 
  // Probe on \LoadUse次数 
  // Probe on IF_PC[11:0]
  MIPS_Regifile mips_regifile_1 (
    .Din(multiplexer_10_out), .Clk(CLK), .R1(v0), .R2(a0), .WE(RegWrite), .W_num(multiplexer_9_out),
    .R1_num(R1_Relate), .R2_num(R2_Relate));
  // Probe on EX_PC[11:0]
  // Probe on ID_PC[11:0]
  or or_4 (or_4_out, Bubble, IsRelated, RstFlow);
  // Probe on MEM_PC[11:0]
  // Probe on WB_PC[11:0]
  or or_5 (or_5_out, RST, CLK);
  ID_EX_l id_ex_l_1 (
    .CLK(or_5_out), .\同步清零_气泡_高电平有效 (or_4_out), .\使能端_低电平有效 (SEL), .PC(ID_PC), .R1(v0),
    .BLEZ(\单周期硬布线控制器_1_blez ), .SignedExt(\单周期硬布线控制器_1_signedext ), .MemToReg(\单周期硬布线控制器_1_memtoreg ),
    .MemWrite(\单周期硬布线控制器_1_memwrite ), .BEQ(\单周期硬布线控制器_1_beq ), .Syscall(IsStop),
    .RegWrite(\单周期硬布线控制器_1_regwrite ), .SB(\单周期硬布线控制器_1_sb ), .BNE(\单周期硬布线控制器_1_bne ),
    .RegDst(\单周期硬布线控制器_1_regdst ), .IR({OP, if_id_l_1_ir_2, Func}), .R2(a0), .AluSrcB(\单周期硬布线控制器_1_alu_src ),
    .JR(\单周期硬布线控制器_1_jr ), .JAL(\单周期硬布线控制器_1_jal ), .AluOP(\单周期硬布线控制器_1_alu_op ),
    .Imm26({if_id_l_1_ir_2, Func}), .JMP(\单周期硬布线控制器_1_jmp ), .PC_2(EX_PC), .R1_2(RS),
    .BLEZ_2(id_ex_l_1_blez_2), .SignedExt_2(SignedExt), .MemToReg_2(id_ex_l_1_memtoreg_2),
    .MemWrite_2(id_ex_l_1_memwrite_2), .BEQ_2(id_ex_l_1_beq_2), .Syscall_2(id_ex_l_1_syscall_2),
    .RegWrite_2(EX_RegWrite), .SB_2(id_ex_l_1_sb_2), .BNE_2(id_ex_l_1_bne_2), .RegDst_2(id_ex_l_1_regdst_2),
    .IR_2(id_ex_l_1_ir_2), .R2_2(id_ex_l_1_r2_2), .AluSrcB_2(id_ex_l_1_alusrcb_2), .JR_2(id_ex_l_1_jr_2),
    .JAL_2(id_ex_l_1_jal_2), .AluOP_2(id_ex_l_1_aluop_2), .Imm26_2(PC_no_condition), .JMP_2(\无条件分支 ),
    .PC_4(if_id_l_1_pc_4_2), .PC_4_2(PC_4));  // open: Forwarding_R1, Forwarding_R1_2, Forwarding_R2, Forwarding_R2_2, ERET, ERET_2
  and and_4 (and_4_out, not_3_out, CLK);
  not not_3 (not_3_out, stop);
  assign bit_extender_1_out = {{16{1'b0}}, PC_no_condition[17:2]};  // Bit_Extender bit_extender_1
  assign bit_extender_2_out = {{16{PC_no_condition[17]}}, PC_no_condition[17:2]};  // Bit_Extender bit_extender_2
  Counter #(.width(16), .max('hffff), .ongoal("wrap"), .trigger("rising"), .behavior("old")) counter_1 (
    .count(1'b1), .Q(\总周期数 ), .clk(multiplexer_11_out), .clr(RST));  // open: load, D, carry, preset
  Multiplexer #(.select(1), .width(1), .disabled("Z"), .enable("false")) multiplexer_11 (
    .in0(and_4_out), .in1(1'b0), .out(multiplexer_11_out), .sel(not_5_out));
  not not_4 (not_4_out, CLK);
  not not_5 (not_5_out, not_4_out);
  Comparator #(.width(32), .mode("twosComplement")) comparator_2 (
    .a(RS), .b({32{1'b0}}), .eq(comparator_2_eq), .lt(comparator_2_lt));  // open: gt
  Multiplexer #(.select(1), .width(32), .disabled("Z"), .enable("false")) multiplexer_12 (
    .in0(bit_extender_1_out), .in1(bit_extender_2_out), .out(multiplexer_12_out), .sel(SignedExt));
  or or_6 (or_6_out, comparator_2_eq, comparator_2_lt);
  Multiplexer #(.select(1), .width(32), .disabled("Z"), .enable("false")) multiplexer_13 (
    .in0(id_ex_l_1_r2_2), .in1(multiplexer_12_out), .out(multiplexer_13_out), .sel(id_ex_l_1_alusrcb_2));
  Shifter #(.width(32), .shift("ll")) shifter_1 (.in(multiplexer_12_out), .\dist (5'b00010), .out(shifter_1_out));
  and and_5 (and_5_out, or_6_out, id_ex_l_1_blez_2);
  MIPS_ALU mips_alu_1 (
    .X(RS), .Y(multiplexer_13_out), .AluOP(id_ex_l_1_aluop_2), .Equal(mips_alu_1_equal),
    .Result(mips_alu_1_result), .shamt(PC_no_condition[12:8]));  // open: Result_2
  Adder #(.width(32)) adder_2 (.a(shifter_1_out), .b(PC_4), .out(PC_condition));  // open: cin, cout
  Multiplexer #(.select(1), .width(1), .disabled("Z"), .enable("false")) multiplexer_14 (
    .in0(and_6_out), .in1(1'b0), .out(multiplexer_14_out), .sel(not_7_out));
  and and_6 (and_6_out, \无条件分支 , CLK);
  not not_6 (not_6_out, mips_alu_1_equal);
  Counter #(.width(16), .max('hffff), .ongoal("wrap"), .trigger("rising"), .behavior("old")) counter_2 (
    .count(1'b1), .Q(\无条件分支数 ), .clk(multiplexer_14_out), .clr(RST));  // open: load, D, carry, preset
  not not_7 (not_7_out, not_8_out);
  not not_8 (not_8_out, CLK);
  or or_7 (\条件分支 , and_5_out, and_8_out, and_7_out);
  and and_7 (and_7_out, mips_alu_1_equal, id_ex_l_1_beq_2);
  and and_8 (and_8_out, id_ex_l_1_bne_2, not_6_out);
  or or_8 (Bubble, \无条件分支 , \条件分支 );
  or or_9 (or_9_out, RST, CLK);
  Counter #(.width(16), .max('hffff), .ongoal("wrap"), .trigger("rising"), .behavior("old")) counter_3 (
    .count(1'b1), .Q(\条件分支成功数 ), .clk(multiplexer_15_out), .clr(RST));  // open: load, D, carry, preset
  Multiplexer #(.select(1), .width(1), .disabled("Z"), .enable("false")) multiplexer_15 (
    .in0(and_9_out), .in1(1'b0), .out(multiplexer_15_out), .sel(not_9_out));
  and and_9 (and_9_out, \条件分支 , CLK);
  Multiplexer #(.select(1), .width(5), .disabled("Z"), .enable("false")) multiplexer_16 (
    .in0(id_ex_l_1_ir_2[20:16]), .in1(id_ex_l_1_ir_2[15:11]), .out(multiplexer_16_out),
    .sel(id_ex_l_1_regdst_2));
  Multiplexer #(.select(1), .width(5), .disabled("Z"), .enable("false")) multiplexer_17 (
    .in0(multiplexer_16_out), .in1({5{1'b1}}), .out(EX_WriteReg_num), .sel(id_ex_l_1_jal_2));
  EX_MEM_l ex_mem_l_1 (
    .CLK(or_9_out), .\同步清零_气泡_高电平有效 (RstFlow), .\使能端_低电平有效 (SEL), .PC(EX_PC),
    .MemToReg(id_ex_l_1_memtoreg_2), .MemWrite(id_ex_l_1_memwrite_2), .RegWrite(EX_RegWrite),
    .SB(id_ex_l_1_sb_2), .RegDst(id_ex_l_1_regdst_2), .IR(id_ex_l_1_ir_2), .R2(id_ex_l_1_r2_2),
    .JAL(id_ex_l_1_jal_2), .PC_2(MEM_PC), .MemToReg_2(ex_mem_l_1_memtoreg_2),
    .MemWrite_2(ex_mem_l_1_memwrite_2), .RegWrite_2(MEM_RegWrite), .SB_2(ex_mem_l_1_sb_2),
    .RegDst_2(ex_mem_l_1_regdst_2), .IR_2(ex_mem_l_1_ir_2), .R2_2(ex_mem_l_1_r2_2), .JAL_2(ex_mem_l_1_jal_2),
    .ALU(mips_alu_1_result), .ALU_2(ex_mem_l_1_alu_2), .PC_4(PC_4), .PC_4_2(ex_mem_l_1_pc_4_2),
    .Syscall(id_ex_l_1_syscall_2), .Syscall_2(ex_mem_l_1_syscall_2));
  not not_9 (not_9_out, not_10_out);
  not not_10 (not_10_out, CLK);
  Multiplexer #(.select(1), .width(32), .disabled("Z"), .enable("false")) multiplexer_18 (
    .in0(ex_mem_l_1_r2_2), .in1(multiplexer_19_out), .out(multiplexer_18_out), .sel(ex_mem_l_1_sb_2));
  Multiplexer #(.select(2), .width(32), .disabled("Z"), .enable("false")) multiplexer_19 (
    .in0({ram_1_data[31:8], ex_mem_l_1_r2_2[7:0]}),
    .in1({ram_1_data[31:16], ex_mem_l_1_r2_2[7:0], ram_1_data[7:0]}),
    .in2({ram_1_data[31:24], ex_mem_l_1_r2_2[7:0], ram_1_data[15:0]}),
    .in3({ex_mem_l_1_r2_2[7:0], ram_1_data[23:0]}), .out(multiplexer_19_out), .sel(ex_mem_l_1_alu_2[1:0]));
  not not_11 (not_11_out, final_IsStop);
  Multiplexer #(.select(1), .width(1), .disabled("Z"), .enable("false")) multiplexer_20 (
    .in0(and_11_out), .in1(1'b0), .out(multiplexer_20_out), .sel(not_13_out));
  and and_10 (and_10_out, not_11_out, IsRelated);
  and and_11 (and_11_out, and_10_out, CLK);
  Multiplexer #(.select(1), .width(5), .disabled("Z"), .enable("false")) multiplexer_21 (
    .in0(ex_mem_l_1_ir_2[20:16]), .in1(ex_mem_l_1_ir_2[15:11]), .out(multiplexer_21_out),
    .sel(ex_mem_l_1_regdst_2));
  RAM #(.addrWidth(10), .dataWidth(32), .bus("separate"), .Select("high")) ram_1 (
    .addr(ex_mem_l_1_alu_2[11:2]), .din(multiplexer_18_out), .data(ram_1_data), .str(ex_mem_l_1_memwrite_2),
    .clk(CLK), .clr(RST));  // open: sel, ld
  Counter #(.width(16), .max('hffff), .ongoal("wrap"), .trigger("rising"), .behavior("old")) counter_4 (
    .count(1'b1), .Q(\插入气泡数 ), .clk(multiplexer_20_out), .clr(RST));  // open: load, D, carry, preset
  not not_12 (not_12_out, CLK);
  not not_13 (not_13_out, not_12_out);
  Multiplexer #(.select(1), .width(5), .disabled("Z"), .enable("false")) multiplexer_22 (
    .in0(multiplexer_21_out), .in1({5{1'b1}}), .out(MEM_WriteReg_num), .sel(ex_mem_l_1_jal_2));
  or or_10 (or_10_out, RST, CLK);
  MEM_WB_l mem_wb_l_1 (
    .CLK(or_10_out), .\同步清零_气泡_高电平有效 (RstFlow), .\使能端_低电平有效 (SEL), .PC(MEM_PC),
    .MemToReg(ex_mem_l_1_memtoreg_2), .PC_2(WB_PC), .MemToReg_2(mem_wb_l_1_memtoreg_2),
    .RegWrite(MEM_RegWrite), .RegWrite_2(RegWrite), .RegDst(ex_mem_l_1_regdst_2), .IR(ex_mem_l_1_ir_2),
    .MD(ram_1_data), .RegDst_2(RegDst), .IR_2({mem_wb_l_1_ir_2[31:21], WB_rt, WB_rd, mem_wb_l_1_ir_2[10:0]}),
    .MD_2(mem_wb_l_1_md_2), .JAL(ex_mem_l_1_jal_2), .JAL_2(JAL), .ALU(ex_mem_l_1_alu_2),
    .ALU_2(mem_wb_l_1_alu_2), .PC_4(ex_mem_l_1_pc_4_2), .PC_4_2(Jal_PC_4), .Syscall(ex_mem_l_1_syscall_2),
    .Syscall_2(final_IsStop));
  Multiplexer #(.select(1), .width(32), .disabled("Z"), .enable("false")) multiplexer_23 (
    .in0(mem_wb_l_1_alu_2), .in1(mem_wb_l_1_md_2), .out(multiplexer_23_out), .sel(mem_wb_l_1_memtoreg_2));

  // Other names for the same wires on the sheet: PC_no_condition[31:28] = PC_4[31:28]; stall = IsRelated

  // Notes on the sheet:
  //   中断源
  //   中断等待指示
  //   指令存储器
  //   contents of rom_1 (hex, n*v repeats v):
  //   20100001 109fc0 139fc3 8021 2012000c 24160003 26100001 3210000f 20080008 20090001 139900 2709825
  //   132020 20020022 c 1094022 1500fff9 22100001 2018000f 2188024 108700 20080008 20090001 139902 2709825
  //   132021 20020022 c 1094022 1500fff9 108702 2c9b022 12c00001 8000c06 4020 1084027 84400 3508ffff
  //   132021 20020022 c 2002000a c
  //   数码管输出
  //   PC+4
  //   IR
  //   PC
  //   指令字
  //   OP
  //   Func
  //   rs
  //   rt
  //   rd
  //   R1_Used
  //   R2_Used
  //   Imm26
  //   Bubble统计的是分支相关数，IsRelated统计的是数据相关数，即插入的气泡数
  //   流水调试日志用
  //   IR
  //   PC
  //   rt
  //   rd
  //   MemWrite
  //   SB
  //   IR
  //   PC
  //   R2
  //   ALU
  //   rt
  //   rd
  //   MemToReg
  //   rt
  //   rd
endmodule

module \重定向流水线  (
  output RegWrite,
  output MemWrite,
  output [31:0] IF_PC,
  output [31:0] ID_PC,
  output [31:0] EX_PC,
  output [31:0] MEM_PC,
  output [31:0] WB_PC,
  output [31:0] RDin,
  output [31:0] MDin
);

  wire and_1_out, and_3_out, and_4_out, and_5_out, and_6_out, and_7_out, and_8_out, and_9_out, and_10_out,
       and_11_out, and_12_out, Bubble, CLK, comparator_1_eq, comparator_2_eq, comparator_2_lt,
       ex_mem_l_1_jal_2, ex_mem_l_1_memtoreg_2, ex_mem_l_1_regdst_2, ex_mem_l_1_sb_2, ex_mem_l_1_syscall_2,
       EX_RegWrite, EX_Syscall, final_IsStop, final_IsStop_t, Go, id_ex_l_1_alusrcb_2, id_ex_l_1_beq_2,
       id_ex_l_1_blez_2, id_ex_l_1_bne_2, id_ex_l_1_jal_2, id_ex_l_1_jr_2, id_ex_l_1_memtoreg_2,
       id_ex_l_1_memwrite_2, id_ex_l_1_regdst_2, id_ex_l_1_sb_2, IR1, IR2, IR3, IsRelated, IsStop, JAL,
       Load_Use, MEM_RegWrite, mips_alu_1_equal, multiplexer_4_out, multiplexer_17_out, multiplexer_20_out,
       multiplexer_21_out, multiplexer_26_out, multiplexer_30_out, not_1_out, not_2_out, not_3_out,
       not_4_out, not_5_out, not_6_out, not_7_out, not_8_out, not_9_out, not_10_out, not_11_out, not_12_out,
       not_13_out, not_14_out, not_15_out, or_1_out, or_2_out, or_3_out, or_4_out, or_5_out, or_6_out,
       or_9_out, or_10_out, or_11_out, RegDst, register_3_q, RST, RstFlow, SEL, SignedExt, stop, Syscall, W1,
       W2, W3, WB_MemToReg, \单周期硬布线控制器_1_alu_src , \单周期硬布线控制器_1_beq , \单周期硬布线控制器_1_blez , \单周期硬布线控制器_1_bne ,
       \单周期硬布线控制器_1_jal , \单周期硬布线控制器_1_jmp , \单周期硬布线控制器_1_jr , \单周期硬布线控制器_1_memtoreg ,
       \单周期硬布线控制器_1_memwrite , \单周期硬布线控制器_1_regdst , \单周期硬布线控制器_1_regwrite , \单周期硬布线控制器_1_sb ,
       \单周期硬布线控制器_1_signedext , \无条件分支 , \条件分支 , \源寄存器使用情况_1_r1_used , \源寄存器使用情况_1_r2_used ,
       \点击此键_先设置同步清零信号_out ;
  wire [1:0] EX_Forward_R1, EX_Forward_R2, ID_Forward_R1, ID_Forward_R2, \数据相关检测_1_r1_ex_relate ,
       \数据相关检测_1_r2_ex_relate ;
  wire [3:0] id_ex_l_1_aluop_2, \单周期硬布线控制器_1_alu_op ;
  wire [4:0] EX_WriteReg_num, MEM_WriteReg_num, multiplexer_11_out, multiplexer_12_out, multiplexer_22_out,
       multiplexer_27_out, R1_Relate, R2_Relate, WB_rd, WB_rt;
  wire [5:0] EX_OP, Func, OP;
  wire [15:0] \LoadUse次数 , \总周期数 , \插入气泡数 , \无条件分支数 , \条件分支成功数 ;
  wire [25:0] id_ex_l_1_ir_2;
  wire [25:6] if_id_l_1_ir_2;
  wire [27:2] PC_no_condition;
  wire [31:0] a0, adder_1_out, bit_extender_1_out, bit_extender_2_out, ex_mem_l_1_ir_2, ex_mem_l_1_pc_4_2,
       ex_mem_l_1_r2_2, if_id_l_1_pc_4_2, Jal_PC_4, LedData, MEM_ALU, mem_wb_l_1_ir_2, mips_alu_1_result,
       multiplexer_1_out, multiplexer_2_out, multiplexer_3_out, multiplexer_6_out, multiplexer_15_out,
       multiplexer_18_out, multiplexer_19_out, multiplexer_25_out, multiplexer_29_out, PC_4, PC_condition,
       R1_Old, R1_Redirect, R2_Old, R2_Redirect, ram_1_data, rom_1_data, shifter_1_out, v0, WB_ALU,
       WB_ReadData;

  Multiplexer #(.select(1), .width(32), .disabled("Z"), .enable("false")) multiplexer_1 (
    .in0({PC_4[31:28], PC_no_condition, 2'b00}), .in1(R1_Redirect), .out(multiplexer_1_out),
    .sel(id_ex_l_1_jr_2));
  Button \u_点击此键_先设置同步清零信号  (.out(\点击此键_先设置同步清零信号_out ));
  Register #(.width(1), .trigger("falling"), .Select("low")) register_1 (
    .D(1'b0), .Q(RstFlow), .clk(RST), .preset(\点击此键_先设置同步清零信号_out ));  // open: en, clr, cs
  Multiplexer #(.select(2), .width(32), .disabled("Z"), .enable("false")) multiplexer_2 (
    .in0(adder_1_out), .in1(PC_condition), .in2(multiplexer_1_out), .out(multiplexer_2_out),
    .sel({\无条件分支 , \条件分支 }));  // open: in3
  Comparator #(.width(32), .mode("twosComplement")) comparator_1 (
    .a(R1_Redirect), .b(32'h22), .eq(comparator_1_eq));  // open: gt, lt
  not not_1 (not_1_out, comparator_1_eq);
  Register #(.width(32), .trigger("rising"), .Select("low")) PC (
    .D(multiplexer_3_out), .en(not_2_out), .Q(IF_PC), .clk(CLK), .clr(RST));
  Multiplexer #(.select(1), .width(32), .disabled("Z"), .enable("false")) multiplexer_3 (
    .in0(multiplexer_2_out), .in1(IF_PC), .out(multiplexer_3_out), .sel(stop));
  not not_2 (not_2_out, Load_Use);
  and and_1 (and_1_out, EX_Syscall, comparator_1_eq);
  and and_2 (IsStop, not_1_out, EX_Syscall);
  xor xor_1 (stop, final_IsStop_t, register_3_q);
  Button \u_再总复位  (.out(RST));
  Button _1 (.out(IR1));
  Button _2 (.out(IR2));
  Button _3 (.out(IR3));
  Register #(.width(32), .trigger("rising"), .Select("low")) register_2 (
    .D(R2_Redirect), .Q(LedData), .clk(and_1_out), .clr(RST));  // open: en
  and and_3 (and_3_out, final_IsStop_t, Go);
  Register #(.width(1), .trigger("rising"), .Select("low")) register_3 (
    .D(1'b0), .Q(register_3_q), .clk(CLK), .clr(RST), .preset(and_3_out));  // open: en, cs
  Button \u_继续运行  (.out(Go));
  LED #(.active("true")) led_1 (.in(W1));
  LED #(.active("true")) led_2 (.in(W2));
  LED #(.active("true")) led_3 (.in(W3));
  Adder #(.width(32)) adder_1 (.a(IF_PC), .b(32'h4), .out(adder_1_out));  // open: cin, cout
  Multiplexer #(.select(1), .width(1), .disabled("Z"), .enable("false")) multiplexer_4 (
    .in0(final_IsStop_t), .in1(1'b0), .out(multiplexer_4_out), .sel(register_3_q));
  Multiplexer #(.select(1), .width(1), .disabled("Z"), .enable("false")) multiplexer_5 (
    .in0(multiplexer_4_out), .in1(1'b0), .out(SEL), .sel(or_1_out));
  Hex_Digit_Display hex_digit_display_1 (.value(LedData[31:28]));  // open: dp
  Hex_Digit_Display hex_digit_display_2 (.value(LedData[27:24]));  // open: dp
  \源寄存器使用情况  \u_源寄存器使用情况_1  (.OP(OP), .FUN(Func), .R1_Used(\源寄存器使用情况_1_r1_used ), .R2_Used(\源寄存器使用情况_1_r2_used ));
  ROM #(.addrWidth(10), .dataWidth(32), .Select("high")) rom_1 (.addr(IF_PC[11:2]), .data(rom_1_data));
  or or_1 (or_1_out, Bubble, RstFlow);
  or or_2 (or_2_out, SEL, Load_Use);
  Hex_Digit_Display hex_digit_display_3 (.value(LedData[23:20]));  // open: dp
  Hex_Digit_Display hex_digit_display_4 (.value(LedData[19:16]));  // open: dp
  IF_ID_l if_id_l_1 (
    .CLK(or_3_out), .\同步清零_气泡_高电平有效 (or_1_out), .\使能端_低电平有效 (or_2_out), .PC(IF_PC), .PC_2(ID_PC),
    .IR(rom_1_data), .IR_2({OP, if_id_l_1_ir_2, Func}), .PC_4(adder_1_out), .PC_4_2(if_id_l_1_pc_4_2));  // open: ERET, ERET_2
  or or_3 (or_3_out, RST, CLK);
  Hex_Digit_Display hex_digit_display_5 (.value(LedData[15:12]));  // open: dp
  Hex_Digit_Display hex_digit_display_6 (.value(LedData[11:8]));  // open: dp
  Clock #(.highDuration(1), .lowDuration(1)) clock_1 (.out(CLK));
  \数据相关检测  \u_数据相关检测_1  (
    .R1_Used(\源寄存器使用情况_1_r1_used ), .R2_Used(\源寄存器使用情况_1_r2_used ), .R1_num(R1_Relate), .R2_num(R2_Relate),
    .EX_WriteReg_num(EX_WriteReg_num), .EX_RegWrite(EX_RegWrite), .MEM_WriteReg_num(MEM_WriteReg_num),
    .MEM_RegWrite(MEM_RegWrite), .Relate(IsRelated), .EX_OP(EX_OP), .Load_Use(Load_Use),
    .R1_EX_Relate(\数据相关检测_1_r1_ex_relate [0]), .R2_EX_Relate(\数据相关检测_1_r2_ex_relate [0]),
    .R1_MEM_Relate(\数据相关检测_1_r1_ex_relate [1]), .R2_MEM_Relate(\数据相关检测_1_r2_ex_relate [1]));
  Hex_Digit_Display hex_digit_display_7 (.value(LedData[3:0]));  // open: dp
  Hex_Digit_Display hex_digit_display_8 (.value(LedData[7:4]));  // open: dp
  Multiplexer #(.select(1), .width(32), .disabled("Z"), .enable("false")) multiplexer_6 (
    .in0(WB_ALU), .in1(WB_ReadData), .out(multiplexer_6_out), .sel(WB_MemToReg));
  Multiplexer #(.select(2), .width(32), .disabled("Z"), .enable("false")) multiplexer_7 (
    .in0(R1_Old), .in1(MEM_ALU), .in2(multiplexer_6_out), .in3(MEM_ALU), .out(R1_Redirect),
    .sel(EX_Forward_R1));
  Multiplexer #(.select(1), .width(2), .disabled("Z"), .enable("false")) multiplexer_8 (
    .in0(\数据相关检测_1_r2_ex_relate ), .in1(2'b00), .out(ID_Forward_R2), .sel(Load_Use));
  \单周期硬布线控制器  \u_单周期硬布线控制器_1  (
    .OP(OP), .Func(Func), .ALU_OP(\单周期硬布线控制器_1_alu_op ), .MemToReg(\单周期硬布线控制器_1_memtoreg ),
    .MemWrite(\单周期硬布线控制器_1_memwrite ), .ALU_SRC(\单周期硬布线控制器_1_alu_src ), .RegWrite(\单周期硬布线控制器_1_regwrite ),
    .SysCALL(Syscall), .SignedExt(\单周期硬布线控制器_1_signedext ), .RegDst(\单周期硬布线控制器_1_regdst ),
    .Beq(\单周期硬布线控制器_1_beq ), .Bne(\单周期硬布线控制器_1_bne ), .JR(\单周期硬布线控制器_1_jr ), .JMP(\单周期硬布线控制器_1_jmp ),
    .JAL(\单周期硬布线控制器_1_jal ), .BLEZ(\单周期硬布线控制器_1_blez ), .SB(\单周期硬布线控制器_1_sb ));  // open: ERET
  Multiplexer #(.select(1), .width(5), .disabled("Z"), .enable("false")) multiplexer_9 (
    .in0(if_id_l_1_ir_2[25:21]), .in1(5'b00010), .out(R1_Relate), .sel(Syscall));
  Multiplexer #(.select(1), .width(5), .disabled("Z"), .enable("false")) multiplexer_10 (
    .in0(if_id_l_1_ir_2[20:16]), .in1(5'b00100), .out(R2_Relate), .sel(Syscall));
  Multiplexer #(.select(1), .width(5), .disabled("Z"), .enable("false")) multiplexer_11 (
    .in0(WB_rt), .in1(WB_rd), .out(multiplexer_11_out), .sel(RegDst));
  Multiplexer #(.select(1), .width(5), .disabled("Z"), .enable("false")) multiplexer_12 (
    .in0(multiplexer_11_out), .in1({5{1'b1}}), .out(multiplexer_12_out), .sel(JAL));
  Multiplexer #(.select(1), .width(32), .disabled("Z"), .enable("false")) multiplexer_13 (
    .in0(multiplexer_29_out), .in1(Jal_PC_4), .out(RDin), .sel(JAL));
  // Probe on \总周期数 
  // Probe on \无条件分支数 
  // Probe on \条件分支成功数 
  // Probe on \插入气泡数 
  // Probe on \LoadUse次数 
  // Probe on IF_PC[11:0]
  MIPS_Regifile mips_regifile_1 (
    .Din(RDin), .Clk(CLK), .R1(v0), .R2(a0), .WE(RegWrite), .W_num(multiplexer_12_out), .R1_num(R1_Relate),
    .R2_num(R2_Relate));
  // Probe on ID_PC[11:0]
  // Probe on EX_PC[11:0]
  Multiplexer #(.select(1), .width(2), .disabled("Z"), .enable("false")) multiplexer_14 (
    .in0(\数据相关检测_1_r1_ex_relate ), .in1(2'b00), .out(ID_Forward_R1), .sel(Load_Use));
  or or_4 (or_4_out, Bubble, Load_Use, RstFlow);
  // Probe on MEM_PC[11:0]
  // Probe on WB_PC[11:0]
  or or_5 (or_5_out, RST, CLK);
  Multiplexer #(.select(1), .width(32), .disabled("Z"), .enable("false")) multiplexer_15 (
    .in0(WB_ALU), .in1(WB_ReadData), .out(multiplexer_15_out), .sel(WB_MemToReg));
  ID_EX_l id_ex_l_1 (
    .CLK(or_5_out), .\同步清零_气泡_高电平有效 (or_4_out), .\使能端_低电平有效 (SEL), .PC(ID_PC), .R1(v0),
    .BLEZ(\单周期硬布线控制器_1_blez ), .SignedExt(\单周期硬布线控制器_1_signedext ), .MemToReg(\单周期硬布线控制器_1_memtoreg ),
    .MemWrite(\单周期硬布线控制器_1_memwrite ), .BEQ(\单周期硬布线控制器_1_beq ), .Syscall(Syscall),
    .RegWrite(\单周期硬布线控制器_1_regwrite ), .SB(\单周期硬布线控制器_1_sb ), .BNE(\单周期硬布线控制器_1_bne ),
    .RegDst(\单周期硬布线控制器_1_regdst ), .IR({OP, if_id_l_1_ir_2, Func}), .R2(a0), .AluSrcB(\单周期硬布线控制器_1_alu_src ),
    .JR(\单周期硬布线控制器_1_jr ), .JAL(\单周期硬布线控制器_1_jal ), .AluOP(\单周期硬布线控制器_1_alu_op ),
    .Imm26({if_id_l_1_ir_2, Func}), .JMP(\单周期硬布线控制器_1_jmp ), .PC_2(EX_PC), .R1_2(R1_Old),
    .BLEZ_2(id_ex_l_1_blez_2), .SignedExt_2(SignedExt), .MemToReg_2(id_ex_l_1_memtoreg_2),
    .MemWrite_2(id_ex_l_1_memwrite_2), .BEQ_2(id_ex_l_1_beq_2), .Syscall_2(EX_Syscall),
    .RegWrite_2(EX_RegWrite), .SB_2(id_ex_l_1_sb_2), .BNE_2(id_ex_l_1_bne_2), .RegDst_2(id_ex_l_1_regdst_2),
    .IR_2({EX_OP, id_ex_l_1_ir_2}), .R2_2(R2_Old), .AluSrcB_2(id_ex_l_1_alusrcb_2), .JR_2(id_ex_l_1_jr_2),
    .JAL_2(id_ex_l_1_jal_2), .AluOP_2(id_ex_l_1_aluop_2), .Imm26_2(PC_no_condition), .JMP_2(\无条件分支 ),
    .PC_4(if_id_l_1_pc_4_2), .PC_4_2(PC_4), .Forwarding_R1(ID_Forward_R1), .Forwarding_R1_2(EX_Forward_R1),
    .Forwarding_R2(ID_Forward_R2), .Forwarding_R2_2(EX_Forward_R2));  // open: ERET, ERET_2
  and and_4 (and_4_out, not_3_out, CLK);
  not not_3 (not_3_out, stop);
  Multiplexer #(.select(2), .width(32), .disabled("Z"), .enable("false")) multiplexer_16 (
    .in0(R2_Old), .in1(MEM_ALU), .in2(multiplexer_15_out), .in3(MEM_ALU), .out(R2_Redirect),
    .sel(EX_Forward_R2));
  assign bit_extender_1_out = {{16{1'b0}}, PC_no_condition[17:2]};  // Bit_Extender bit_extender_1
  assign bit_extender_2_out = {{16{PC_no_condition[17]}}, PC_no_condition[17:2]};  // Bit_Extender bit_extender_2
  Counter #(.width(16), .max('hffff), .ongoal("wrap"), .trigger("rising"), .behavior("old")) counter_1 (
    .count(1'b1), .Q(\总周期数 ), .clk(multiplexer_17_out), .clr(RST));  // open: load, D, carry, preset
  Multiplexer #(.select(1), .width(1), .disabled("Z"), .enable("false")) multiplexer_17 (
    .in0(and_4_out), .in1(1'b0), .out(multiplexer_17_out), .sel(not_4_out));
  not not_4 (not_4_out, not_5_out);
  not not_5 (not_5_out, CLK);
  Comparator #(.width(32), .mode("twosComplement")) comparator_2 (
    .a(R1_Redirect), .b({32{1'b0}}), .eq(comparator_2_eq), .lt(comparator_2_lt));  // open: gt
  Multiplexer #(.select(1), .width(32), .disabled("Z"), .enable("false")) multiplexer_18 (
    .in0(bit_extender_1_out), .in1(bit_extender_2_out), .out(multiplexer_18_out), .sel(SignedExt));
  or or_6 (or_6_out, comparator_2_eq, comparator_2_lt);
  Multiplexer #(.select(1), .width(32), .disabled("Z"), .enable("false")) multiplexer_19 (
    .in0(R2_Redirect), .in1(multiplexer_18_out), .out(multiplexer_19_out), .sel(id_ex_l_1_alusrcb_2));
  Shifter #(.width(32), .shift("ll")) shifter_1 (.in(multiplexer_18_out), .\dist (5'b00010), .out(shifter_1_out));
  and and_5 (and_5_out, or_6_out, id_ex_l_1_blez_2);
  MIPS_ALU mips_alu_1 (
    .X(R1_Redirect), .Y(multiplexer_19_out), .AluOP(id_ex_l_1_aluop_2), .Equal(mips_alu_1_equal),
    .Result(mips_alu_1_result), .shamt(PC_no_condition[12:8]));  // open: Result_2
  Adder #(.width(32)) adder_2 (.a(shifter_1_out), .b(PC_4), .out(PC_condition));  // open: cin, cout
  Multiplexer #(.select(1), .width(1), .disabled("Z"), .enable("false")) multiplexer_20 (
    .in0(and_6_out), .in1(1'b0), .out(multiplexer_20_out), .sel(not_8_out));
  and and_6 (and_6_out, \无条件分支 , CLK);
  not not_6 (not_6_out, mips_alu_1_equal);
  Counter #(.width(16), .max('hffff), .ongoal("wrap"), .trigger("rising"), .behavior("old")) counter_2 (
    .count(1'b1), .Q(\无条件分支数 ), .clk(multiplexer_20_out), .clr(RST));  // open: load, D, carry, preset
  not not_7 (not_7_out, CLK);
  not not_8 (not_8_out, not_7_out);
  or or_7 (\条件分支 , and_5_out, and_8_out, and_7_out);
  and and_7 (and_7_out, mips_alu_1_equal, id_ex_l_1_beq_2);
  and and_8 (and_8_out, id_ex_l_1_bne_2, not_6_out);
  or or_8 (Bubble, \无条件分支 , \条件分支 );
  or or_9 (or_9_out, RST, CLK);
  Counter #(.width(16), .max('hffff), .ongoal("wrap"), .trigger("rising"), .behavior("old")) counter_3 (
    .count(1'b1), .Q(\条件分支成功数 ), .clk(multiplexer_21_out), .clr(RST));  // open: load, D, carry, preset
  Multiplexer #(.select(1), .width(1), .disabled("Z"), .enable("false")) multiplexer_21 (
    .in0(and_9_out), .in1(1'b0), .out(multiplexer_21_out), .sel(not_10_out));
  and and_9 (and_9_out, \条件分支 , CLK);
  Multiplexer #(.select(1), .width(5), .disabled("Z"), .enable("false")) multiplexer_22 (
    .in0(id_ex_l_1_ir_2[20:16]), .in1(id_ex_l_1_ir_2[15:11]), .out(multiplexer_22_out),
    .sel(id_ex_l_1_regdst_2));
  Multiplexer #(.select(1), .width(5), .disabled("Z"), .enable("false")) multiplexer_23 (
    .in0(multiplexer_22_out), .in1({5{1'b1}}), .out(EX_WriteReg_num), .sel(id_ex_l_1_jal_2));
  EX_MEM_l ex_mem_l_1 (
    .CLK(or_9_out), .\同步清零_气泡_高电平有效 (RstFlow), .\使能端_低电平有效 (SEL), .PC(EX_PC),
    .MemToReg(id_ex_l_1_memtoreg_2), .MemWrite(id_ex_l_1_memwrite_2), .RegWrite(EX_RegWrite),
    .SB(id_ex_l_1_sb_2), .RegDst(id_ex_l_1_regdst_2), .IR({EX_OP, id_ex_l_1_ir_2}), .R2(R2_Redirect),
    .JAL(id_ex_l_1_jal_2), .PC_2(MEM_PC), .MemToReg_2(ex_mem_l_1_memtoreg_2), .MemWrite_2(MemWrite),
    .RegWrite_2(MEM_RegWrite), .SB_2(ex_mem_l_1_sb_2), .RegDst_2(ex_mem_l_1_regdst_2),
    .IR_2(ex_mem_l_1_ir_2), .R2_2(ex_mem_l_1_r2_2), .JAL_2(ex_mem_l_1_jal_2), .ALU(mips_alu_1_result),
    .ALU_2(MEM_ALU), .PC_4(PC_4), .PC_4_2(ex_mem_l_1_pc_4_2), .Syscall(IsStop),
    .Syscall_2(ex_mem_l_1_syscall_2));
  not not_9 (not_9_out, CLK);
  not not_10 (not_10_out, not_9_out);
  Multiplexer #(.select(1), .width(32), .disabled("Z"), .enable("false")) multiplexer_24 (
    .in0(ex_mem_l_1_r2_2), .in1(multiplexer_25_out), .out(MDin), .sel(ex_mem_l_1_sb_2));
  Multiplexer #(.select(2), .width(32), .disabled("Z"), .enable("false")) multiplexer_25 (
    .in0({ram_1_data[31:8], ex_mem_l_1_r2_2[7:0]}),
    .in1({ram_1_data[31:16], ex_mem_l_1_r2_2[7:0], ram_1_data[7:0]}),
    .in2({ram_1_data[31:24], ex_mem_l_1_r2_2[7:0], ram_1_data[15:0]}),
    .in3({ex_mem_l_1_r2_2[7:0], ram_1_data[23:0]}), .out(multiplexer_25_out), .sel(MEM_ALU[1:0]));
  not not_11 (not_11_out, final_IsStop);
  or or_10 (or_10_out, Bubble, Load_Use);
  Multiplexer #(.select(1), .width(1), .disabled("Z"), .enable("false")) multiplexer_26 (
    .in0(and_11_out), .in1(1'b0), .out(multiplexer_26_out), .sel(not_12_out));
  and and_10 (and_10_out, not_11_out, or_10_out);
  and and_11 (and_11_out, and_10_out, CLK);
  Multiplexer #(.select(1), .width(5), .disabled("Z"), .enable("false")) multiplexer_27 (
    .in0(ex_mem_l_1_ir_2[20:16]), .in1(ex_mem_l_1_ir_2[15:11]), .out(multiplexer_27_out),
    .sel(ex_mem_l_1_regdst_2));
  RAM #(.addrWidth(10), .dataWidth(32), .bus("separate"), .Select("high")) ram_1 (
    .addr(MEM_ALU[11:2]), .din(MDin), .data(ram_1_data), .str(MemWrite), .clk(CLK), .clr(RST));  // open: sel, ld
  Counter #(.width(16), .max('hffff), .ongoal("wrap"), .trigger("rising"), .behavior("old")) counter_4 (
    .count(1'b1), .Q(\插入气泡数 ), .clk(multiplexer_26_out), .clr(RST));  // open: load, D, carry, preset
  not not_12 (not_12_out, not_13_out);
  not not_13 (not_13_out, CLK);
  Multiplexer #(.select(1), .width(5), .disabled("Z"), .enable("false")) multiplexer_28 (
    .in0(multiplexer_27_out), .in1({5{1'b1}}), .out(MEM_WriteReg_num), .sel(ex_mem_l_1_jal_2));
  or or_11 (or_11_out, RST, CLK);
  MEM_WB_l mem_wb_l_1 (
    .CLK(or_11_out), .\同步清零_气泡_高电平有效 (RstFlow), .\使能端_低电平有效 (SEL), .PC(MEM_PC),
    .MemToReg(ex_mem_l_1_memtoreg_2), .PC_2(WB_PC), .MemToReg_2(WB_MemToReg), .RegWrite(MEM_RegWrite),
    .RegWrite_2(RegWrite), .RegDst(ex_mem_l_1_regdst_2), .IR(ex_mem_l_1_ir_2), .MD(ram_1_data),
    .RegDst_2(RegDst), .IR_2({mem_wb_l_1_ir_2[31:21], WB_rt, WB_rd, mem_wb_l_1_ir_2[10:0]}),
    .MD_2(WB_ReadData), .JAL(ex_mem_l_1_jal_2), .JAL_2(JAL), .ALU(MEM_ALU), .ALU_2(WB_ALU),
    .PC_4(ex_mem_l_1_pc_4_2), .PC_4_2(Jal_PC_4), .Syscall(ex_mem_l_1_syscall_2), .Syscall_2(final_IsStop));
  and and_12 (and_12_out, Load_Use, CLK);
  Multiplexer #(.select(1), .width(32), .disabled("Z"), .enable("false")) multiplexer_29 (
    .in0(WB_ALU), .in1(WB_ReadData), .out(multiplexer_29_out), .sel(WB_MemToReg));
  Counter #(.width(16), .max('hffff), .ongoal("wrap"), .trigger("rising"), .behavior("old")) counter_5 (
    .count(1'b1), .Q(\LoadUse次数 ), .clk(multiplexer_30_out), .clr(RST));  // open: load, D, carry, preset
  Multiplexer #(.select(1), .width(1), .disabled("Z"), .enable("false")) multiplexer_30 (
    .in0(and_12_out), .in1(1'b0), .out(multiplexer_30_out), .sel(not_14_out));
  not not_14 (not_14_out, not_15_out);
  not not_15 (not_15_out, CLK);

  // Other names for the same wires on the sheet: PC_no_condition[31:28] = PC_4[31:28]; RS[31:0] = R1_Redirect

  // Notes on the sheet:
  //   中断源
  //   中断等待指示
  //   指令存储器
  //   R1_Used
  //   R2_Used
  //   contents of rom_1 (hex, n*v repeats v):
  //   20110001 8000c05 20110001 20120002 20130003 8000c09 20110001 20120002 20130003 8000c0d 20110001
  //   20120002 20130003 8000c11 20110001 20120002 20130003 c000cb8 20100001 20110001 118fc0 112020
  //   20020022 c 118882 12200001 8000c15 112020 20020022 c 20110001 118880 112020 20020022 c 12200001
  //   8000c1f 20110001 118fc0 112020 20020022 c 1188c3 112020 20020022 c 118903 112020 20020022 c 118903
  //   112020 20020022 c 118903 112020 20020022 c 118903 112020 20020022 c 118903 112020 20020022 c 118903
  //   112020 20020022 c 118903 112020 20020022 c 20100001 109fc0 139fc3 8021 2012000c 24160003 26100001
  //   3210000f 20080008 20090001 139900 2709825 132020 20020022 c 1094022 1500fff9 22100001 2018000f
  //   2188024 108700 20080008 20090001 139902 2709825 132021 20020022 c 1094022 1500fff9 108702 2c9b022
  //   12c00001 8000c50 4020 1084027 84400 3508ffff 82021 20020022 c 2010ffff 20110000 ae300000 22100001
  //   22310004 ae300000 22100001 22310004 ae300000 22100001 22310004 ae300000 22100001 22310004 ae300000
  //   22100001 22310004 ae300000 22100001 22310004 ae300000 22100001 22310004 ae300000 22100001 22310004
  //   ae300000 22100001 22310004 ae300000 22100001 22310004 ae300000 22100001 22310004 ae300000 22100001
  //   22310004 ae300000 22100001 22310004 ae300000 22100001 22310004 ae300000 22100001 22310004 ae300000
  //   22100001 22310004 22100001 8020 2011003c 8e130000 8e340000 274402a 11000002 ae330000 ae140000
  //   2231fffc 1611fff8 102020 20020022 c 22100004 2011003c 1611fff2 20020032 c 20100000 22100001 102020
  //   20020022 c 22100002 102020 20020022 c 22100003 102020 20020022 c 22100004 102020 20020022 c 22100005
  //   102020 20020022 c 22100006 102020 20020022 c 22100007 102020 20020022 c 22100008 102020 20020022
  //   20020022 c 3e00008
  //   数码管输出
  //   PC+4
  //   IR
  //   PC
  //   指令字
  //   OP
  //   Func
  //   rs
  //   rt
  //   rd
  //   Imm26
  //   Bubble统计的是分支相关数，load_use是数据相关时处理的气泡数
  //   流水调试日志用
  //   IR
  //   PC
  //   rt
  //   rd
  //   MemWrite
  //   SB
  //   IR
  //   PC
  //   R2
  //   ALU
  //   rt
  //   rd
  //   MemToReg
  //   rt
  //   rd
endmodule

module \中断按键参考电路  (
  input  \同步清零信号 ,
  output \与中断屏蔽位与 
);

  wire \_1号中断_out , and_1_out, clock_1_out, d_ff_1_q, or_1_out, or_2_out;

  Clock #(.highDuration(1), .lowDuration(1)) clock_1 (.out(clock_1_out));
  Button \_1号中断  (.out(\_1号中断_out ));
  LED #(.active("true")) \_1号中断等待指示灯  (.in(or_1_out));
  or or_1 (or_1_out, \与中断屏蔽位与 , d_ff_1_q);
  D_Flip_Flop #(.trigger("rising"), .Pre_Clr_Positions("LEGACY"), .NegatePresetClear("false"), .enable("true"), .NewFFLayout("false")) d_ff_1 (
    .clk(\_1号中断_out ), .D(1'b1), .Q(d_ff_1_q), .reset(\与中断屏蔽位与 ));  // open: Qn, preset, en
  or or_2 (or_2_out, d_ff_1_q, \与中断屏蔽位与 );
  and and_1 (and_1_out, or_2_out, ~\同步清零信号 );  // AND_Gate
  D_Flip_Flop #(.trigger("rising"), .Pre_Clr_Positions("LEGACY"), .NegatePresetClear("false"), .enable("true"), .NewFFLayout("false")) IR1 (
    .clk(clock_1_out), .D(and_1_out), .Q(\与中断屏蔽位与 ));  // open: Qn, preset, en, reset
  \单周期硬布线控制器  \u_单周期硬布线控制器_1  ();  // open: OP, Func, ALU_OP, MemToReg, MemWrite, ALU_SRC, RegWrite, SysCALL, SignedExt, RegDst, Beq, Bne, JR, JMP, JAL, BLEZ, SB, ERET

  // Notes on the sheet:
  //   中断信号采样参考电路
  //   Reset 
endmodule
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module \单级中断  (
);

  wire and_1_out, and_2_out, and_4_out, and_5_out, and_6_out, and_7_out, and_8_out, and_9_out, and_11_out,
       and_12_out, and_16_out, Clear1, Clear2, Clear3, CLK, comparator_1_eq, comparator_2_eq,
       comparator_2_lt, decoder_1_out0, decoder_1_out1, decoder_1_out2, ERET, Go, IE, IE_q, INT, IR1, IR2,
       IR3, MemWrite, mips_alu_1_equal, multiplexer_1_out, multiplexer_4_out, multiplexer_7_out,
       multiplexer_8_out, not_1_out, not_2_out, not_3_out, not_4_out, not_5_out, not_6_out, not_7_out,
       not_8_out, not_9_out, not_10_out, not_11_out, not_12_out, not_13_out, not_15_out, or_1_out, or_2_out,
       or_6_out, or_7_out, or_8_out, or_9_out, or_10_out, or_11_out, or_12_out, priority_encoder_1_gs,
       register_1_q, register_2_q, register_3_q, register_5_q, register_6_q, register_7_q, register_8_q,
       register_9_q, register_10_q, RegWrite, RST, SignedExt, stop, Syscall, W1, W2, W3, xor_1_out,
       \单周期硬布线控制器_1_alu_src , \单周期硬布线控制器_1_beq , \单周期硬布线控制器_1_blez , \单周期硬布线控制器_1_bne , \单周期硬布线控制器_1_jal ,
       \单周期硬布线控制器_1_jr , \单周期硬布线控制器_1_memtoreg , \单周期硬布线控制器_1_regdst , \单周期硬布线控制器_1_sb , \无条件分支 , \条件分支成功 ;
  wire [1:0] priority_encoder_1_out, \锁存当前中断号_q ;
  wire [3:0] \单周期硬布线控制器_1_alu_op ;
  wire [4:0] multiplexer_10_out, multiplexer_11_out, multiplexer_12_out, multiplexer_13_out;
  wire [7:0] ram_1_data, ram_1_data_2, ram_1_data_3, ram_1_data_4;
  wire [15:0] \总周期数 , \无条件分支数 , \条件分支成功数 ;
  wire [31:0] a0, adder_1_out, adder_2_out, bit_extender_1_out, bit_extender_2_out, INT_PC, IR, LedData,
       MDin, mips_alu_1_result, multiplexer_2_out, multiplexer_3_out, multiplexer_5_out, multiplexer_9_out,
       multiplexer_15_out, multiplexer_17_out, multiplexer_19_out, multiplexer_20_out, Next_PC, PC, RDin,
       Ret_PC, shifter_1_out, v0;

  Button \u_总复位  (.out(RST));
  not not_1 (not_1_out, stop);
  // Probe on \总周期数 
  // Probe on \无条件分支数 
  // Probe on \条件分支成功数 
  Counter #(.width(16), .max('hffff), .ongoal("wrap"), .trigger("rising"), .behavior("old")) counter_1 (
    .count(1'b1), .Q(\总周期数 ), .clk(multiplexer_1_out), .clr(RST));  // open: load, D, carry, preset
  Multiplexer #(.select(1), .width(1), .disabled("Z"), .enable("false")) multiplexer_1 (
    .in0(and_1_out), .in1(1'b0), .out(multiplexer_1_out), .sel(not_2_out));
  not not_2 (not_2_out, not_3_out);
  and and_1 (and_1_out, not_1_out, CLK);
  Multiplexer #(.select(2), .width(32), .disabled("Z"), .enable("false")) multiplexer_2 (
    .in0(adder_1_out), .in1(adder_2_out), .in2(multiplexer_3_out), .out(multiplexer_2_out),
    .sel({\无条件分支 , \条件分支成功 }));  // open: in3
  Multiplexer #(.select(1), .width(32), .disabled("Z"), .enable("false")) multiplexer_3 (
    .in0({adder_1_out[31:28], IR[25:0], 2'b00}), .in1(v0), .out(multiplexer_3_out), .sel(\单周期硬布线控制器_1_jr ));
  Clock #(.highDuration(1), .lowDuration(1)) clock_1 (.out(CLK));
  Button _1 (.out(IR1));
  Button _2 (.out(IR2));
  Button _3 (.out(IR3));
  not not_3 (not_3_out, CLK);
  Button \u_继续运行  (.out(Go));
  LED #(.active("true")) led_1 (.in(W1));
  LED #(.active("true")) led_2 (.in(W2));
  LED #(.active("true")) led_3 (.in(W3));
  Multiplexer #(.select(1), .width(1), .disabled("Z"), .enable("false")) multiplexer_4 (
    .in0(and_2_out), .in1(1'b0), .out(multiplexer_4_out), .sel(not_4_out));
  and and_2 (and_2_out, \条件分支成功 , CLK);
  Comparator #(.width(32), .mode("twosComplement")) comparator_1 (
    .a(v0), .b(32'h22), .eq(comparator_1_eq));  // open: gt, lt
  xor xor_1 (xor_1_out, stop, register_1_q);
  Multiplexer #(.select(1), .width(32), .disabled("Z"), .enable("false")) multiplexer_5 (
    .in0(multiplexer_2_out), .in1(Ret_PC), .out(multiplexer_5_out), .sel(ERET));
  Hex_Digit_Display hex_digit_display_1 (.value(LedData[31:28]));  // open: dp
  Hex_Digit_Display hex_digit_display_2 (.value(LedData[27:24]));  // open: dp
  Counter #(.width(16), .max('hffff), .ongoal("wrap"), .trigger("rising"), .behavior("old")) counter_2 (
    .count(1'b1), .Q(\条件分支成功数 ), .clk(multiplexer_4_out), .clr(RST));  // open: load, D, carry, preset
  not not_4 (not_4_out, not_5_out);
  not not_5 (not_5_out, CLK);
  not not_6 (not_6_out, comparator_1_eq);
  and and_3 (stop, not_6_out, Syscall);
  Multiplexer #(.select(1), .width(32), .disabled("Z"), .enable("false")) multiplexer_6 (
    .in0(multiplexer_5_out), .in1(PC), .out(Next_PC), .sel(xor_1_out));
  Hex_Digit_Display hex_digit_display_3 (.value(LedData[19:16]));  // open: dp
  Hex_Digit_Display hex_digit_display_4 (.value(LedData[23:20]));  // open: dp
  and and_4 (and_4_out, Syscall, comparator_1_eq);
  and and_5 (and_5_out, stop, Go);
  Register #(.width(1), .trigger("rising"), .Select("low")) register_1 (
    .D(1'b0), .Q(register_1_q), .clk(CLK), .clr(RST), .preset(and_5_out));  // open: en, cs
  Register #(.width(32), .trigger("rising"), .Select("low")) u_PC (
    .D(Next_PC), .Q(PC), .clk(CLK), .clr(RST));  // open: en
  Register #(.width(1), .trigger("rising"), .Select("low")) register_2 (
    .D(1'b1), .Q(register_2_q), .clk(INT), .clr(or_1_out));  // open: en
  or or_1 (or_1_out, RST, register_3_q);
  Register #(.width(1), .trigger("rising"), .Select("low")) register_3 (
    .D(1'b1), .Q(register_3_q), .clk(multiplexer_7_out), .clr(or_2_out));  // open: en
  or or_2 (or_2_out, register_3_q, RST);
  Multiplexer #(.select(1), .width(1), .disabled("Z"), .enable("false")) multiplexer_7 (
    .in0(1'b1), .in1(CLK), .out(multiplexer_7_out), .sel(register_2_q));
  Hex_Digit_Display hex_digit_display_5 (.value(LedData[15:12]));  // open: dp
  Hex_Digit_Display hex_digit_display_6 (.value(LedData[11:8]));  // open: dp
  Multiplexer #(.select(1), .width(1), .disabled("Z"), .enable("false")) multiplexer_8 (
    .in0(and_6_out), .in1(1'b0), .out(multiplexer_8_out), .sel(not_8_out));
  and and_6 (and_6_out, \无条件分支 , CLK);
  Register #(.width(32), .trigger("rising"), .Select("low")) register_4 (
    .D(a0), .Q(LedData), .clk(and_4_out), .clr(RST));  // open: en
  Multiplexer #(.select(1), .width(32), .disabled("Z"), .enable("false")) multiplexer_9 (
    .in0(PC), .in1(INT_PC), .out(multiplexer_9_out), .sel(register_2_q));
  Hex_Digit_Display hex_digit_display_7 (.value(LedData[7:4]));  // open: dp
  Hex_Digit_Display hex_digit_display_8 (.value(LedData[3:0]));  // open: dp
  // Probe on \总周期数 
  Counter #(.width(16), .max('hffff), .ongoal("wrap"), .trigger("rising"), .behavior("old")) counter_3 (
    .count(1'b1), .Q(\无条件分支数 ), .clk(multiplexer_8_out), .clr(RST));  // open: load, D, carry, preset
  not not_7 (not_7_out, CLK);
  not not_8 (not_8_out, not_7_out);
  ROM #(.addrWidth(10), .dataWidth(32), .Select("high")) rom_1 (.addr(multiplexer_9_out[11:2]), .data(IR));
  Adder #(.width(32)) adder_1 (.a(multiplexer_9_out), .b(32'h4), .out(adder_1_out));  // open: cin, cout
  or or_3 (W1, register_8_q, register_5_q);
  or or_4 (W2, register_9_q, register_6_q);
  or or_5 (W3, register_10_q, register_7_q);
  Register #(.width(1), .trigger("rising"), .Select("low")) register_5 (
    .D(1'b1), .Q(register_5_q), .clk(IR1), .clr(or_6_out));  // open: en
  or or_6 (or_6_out, register_8_q, RST);
  Register #(.width(1), .trigger("rising"), .Select("low")) register_6 (
    .D(1'b1), .Q(register_6_q), .clk(IR2), .clr(or_7_out));  // open: en
  or or_7 (or_7_out, register_9_q, RST);
  Register #(.width(1), .trigger("rising"), .Select("low")) register_7 (
    .D(1'b1), .Q(register_7_q), .clk(IR3), .clr(or_8_out));  // open: en
  or or_8 (or_8_out, register_10_q, RST);
  or or_9 (or_9_out, register_5_q, register_8_q);
  or or_10 (or_10_out, register_6_q, register_9_q);
  or or_11 (or_11_out, register_7_q, register_10_q);
  \单周期硬布线控制器  \u_单周期硬布线控制器_1  (
    .OP(IR[31:26]), .Func(IR[5:0]), .ALU_OP(\单周期硬布线控制器_1_alu_op ), .MemToReg(\单周期硬布线控制器_1_memtoreg ),
    .MemWrite(MemWrite), .ALU_SRC(\单周期硬布线控制器_1_alu_src ), .RegWrite(RegWrite), .SysCALL(Syscall),
    .SignedExt(SignedExt), .RegDst(\单周期硬布线控制器_1_regdst ), .Beq(\单周期硬布线控制器_1_beq ), .Bne(\单周期硬布线控制器_1_bne ),
    .JR(\单周期硬布线控制器_1_jr ), .JMP(\无条件分支 ), .JAL(\单周期硬布线控制器_1_jal ), .BLEZ(\单周期硬布线控制器_1_blez ),
    .SB(\单周期硬布线控制器_1_sb ), .ERET(ERET));
  and and_7 (and_7_out, or_9_out, not_9_out);
  not not_9 (not_9_out, Clear1);
  and and_8 (and_8_out, or_10_out, not_10_out);
  not not_10 (not_10_out, Clear2);
  and and_9 (and_9_out, or_11_out, not_11_out);
  not not_11 (not_11_out, Clear3);
  Multiplexer #(.select(1), .width(5), .disabled("Z"), .enable("false")) multiplexer_10 (
    .in0(IR[20:16]), .in1(IR[15:11]), .out(multiplexer_10_out), .sel(\单周期硬布线控制器_1_regdst ));
  Register #(.width(1), .trigger("rising"), .Select("low")) register_8 (
    .D(and_7_out), .Q(register_8_q), .clk(CLK), .clr(RST));  // open: en
  Register #(.width(1), .trigger("rising"), .Select("low")) register_9 (
    .D(and_8_out), .Q(register_9_q), .clk(CLK), .clr(RST));  // open: en
  Register #(.width(1), .trigger("rising"), .Select("low")) register_10 (
    .D(and_9_out), .Q(register_10_q), .clk(CLK), .clr(RST));  // open: en
  Multiplexer #(.select(1), .width(5), .disabled("Z"), .enable("false")) multiplexer_11 (
    .in0(IR[25:21]), .in1(5'b00010), .out(multiplexer_11_out), .sel(Syscall));
  Multiplexer #(.select(1), .width(5), .disabled("Z"), .enable("false")) multiplexer_12 (
    .in0(IR[20:16]), .in1(5'b00100), .out(multiplexer_12_out), .sel(Syscall));
  Multiplexer #(.select(1), .width(5), .disabled("Z"), .enable("false")) multiplexer_13 (
    .in0(multiplexer_10_out), .in1({5{1'b1}}), .out(multiplexer_13_out), .sel(\单周期硬布线控制器_1_jal ));
  Multiplexer #(.select(1), .width(32), .disabled("Z"), .enable("false")) multiplexer_14 (
    .in0(multiplexer_20_out), .in1(adder_1_out), .out(RDin), .sel(\单周期硬布线控制器_1_jal ));
  assign bit_extender_1_out = {{16{1'b0}}, IR[15:0]};  // Bit_Extender bit_extender_1
  assign bit_extender_2_out = {{16{IR[15]}}, IR[15:0]};  // Bit_Extender bit_extender_2
  MIPS_Regifile mips_regifile_1 (
    .Din(RDin), .Clk(CLK), .R1(v0), .R2(a0), .WE(RegWrite), .W_num(multiplexer_13_out),
    .R1_num(multiplexer_11_out), .R2_num(multiplexer_12_out));
  Multiplexer #(.select(1), .width(32), .disabled("Z"), .enable("false")) multiplexer_15 (
    .in0(bit_extender_1_out), .in1(bit_extender_2_out), .out(multiplexer_15_out), .sel(SignedExt));
  not not_12 (not_12_out, 1'b0);
  not not_13 (not_13_out, ERET);
  Priority_Encoder #(.select(2), .disabled("Z")) priority_encoder_1 (
    .in0(register_8_q), .in1(register_9_q), .in2(register_10_q), .in3(1'b0), .out(priority_encoder_1_out),
    .gs(priority_encoder_1_gs), .en_in(not_12_out));  // open: en_out
  and and_10 (INT, priority_encoder_1_gs, IE);
  Multiplexer #(.select(2), .width(32), .disabled("Z"), .enable("false")) multiplexer_16 (
    .in0(32'h3488), .in1(32'h34f4), .in2(32'h3560), .out(INT_PC), .sel(priority_encoder_1_out));  // open: in3
  Register #(.width(32), .trigger("rising"), .Select("low")) EPC (
    .D(PC), .Q(Ret_PC), .clk(INT), .clr(RST));  // open: en
  not not_14 (IE, IE_q);
  Register #(.width(1), .trigger("rising"), .Select("low")) u_IE (
    .D(1'b0), .Q(IE_q), .clk(not_13_out), .clr(RST), .preset(INT));  // open: en, cs
  or or_12 (or_12_out, comparator_2_eq, comparator_2_lt);
  Comparator #(.width(32), .mode("twosComplement")) comparator_2 (
    .a(v0), .b({32{1'b0}}), .eq(comparator_2_eq), .lt(comparator_2_lt));  // open: gt
  Shifter #(.width(32), .shift("ll")) shifter_1 (.in(multiplexer_15_out), .\dist (5'b00010), .out(shifter_1_out));
  // Probe on priority_encoder_1_out
  and and_11 (and_11_out, or_12_out, \单周期硬布线控制器_1_blez );
  Multiplexer #(.select(1), .width(32), .disabled("Z"), .enable("false")) multiplexer_17 (
    .in0(a0), .in1(multiplexer_15_out), .out(multiplexer_17_out), .sel(\单周期硬布线控制器_1_alu_src ));
  Adder #(.width(32)) adder_2 (.a(shifter_1_out), .b(adder_1_out), .out(adder_2_out));  // open: cin, cout
  Register #(.width(2), .trigger("rising"), .Select("low")) \u_锁存当前中断号  (
    .D(priority_encoder_1_out), .Q(\锁存当前中断号_q ), .clk(INT), .clr(RST));  // open: en
  MIPS_ALU mips_alu_1 (
    .X(v0), .Y(multiplexer_17_out), .AluOP(\单周期硬布线控制器_1_alu_op ), .Equal(mips_alu_1_equal),
    .Result(mips_alu_1_result), .shamt(IR[10:6]));  // open: Result_2
  Decoder #(.select(2), .tristate("false"), .disabled("Z"), .enable("false")) decoder_1 (
    .out0(decoder_1_out0), .out1(decoder_1_out1), .out2(decoder_1_out2), .sel(\锁存当前中断号_q ));  // open: out3
  and and_12 (and_12_out, mips_alu_1_equal, \单周期硬布线控制器_1_beq );
  and and_13 (Clear1, decoder_1_out0, ERET);
  and and_14 (Clear2, decoder_1_out1, ERET);
  and and_15 (Clear3, decoder_1_out2, ERET);
  not not_15 (not_15_out, mips_alu_1_equal);
  Multiplexer #(.select(1), .width(32), .disabled("Z"), .enable("false")) multiplexer_18 (
    .in0(a0), .in1(multiplexer_19_out), .out(MDin), .sel(\单周期硬布线控制器_1_sb ));
  Multiplexer #(.select(2), .width(32), .disabled("Z"), .enable("false")) multiplexer_19 (
    .in0({ram_1_data, ram_1_data_4, ram_1_data_3, a0[7:0]}),
    .in1({ram_1_data, ram_1_data_4, a0[7:0], ram_1_data_2}),
    .in2({ram_1_data, a0[7:0], ram_1_data_3, ram_1_data_2}),
    .in3({a0[7:0], ram_1_data_4, ram_1_data_3, ram_1_data_2}), .out(multiplexer_19_out),
    .sel(mips_alu_1_result[1:0]));
  and and_16 (and_16_out, not_15_out, \单周期硬布线控制器_1_bne );
  or or_13 (\条件分支成功 , and_11_out, and_16_out, and_12_out);
  RAM #(.addrWidth(10), .dataWidth(32), .bus("separate"), .Select("high")) ram_1 (
    .addr(mips_alu_1_result[11:2]), .din(MDin),
    .data({ram_1_data, ram_1_data_4, ram_1_data_3, ram_1_data_2}), .str(MemWrite), .clk(CLK));  // open: sel, ld, clr
  Multiplexer #(.select(1), .width(32), .disabled("Z"), .enable("false")) multiplexer_20 (
    .in0(mips_alu_1_result), .in1({ram_1_data, ram_1_data_4, ram_1_data_3, ram_1_data_2}),
    .out(multiplexer_20_out), .sel(\单周期硬布线控制器_1_memtoreg ));

  // Notes on the sheet:
  //   总复位信号应将除ROM以外所有存储组件全部清零
  //   中断源
  //   中断等待指示
  //   数码管输出应该用寄存器锁存，否则显示数据只能一闪而过
  //   数码管输出
  //   指令存储器
  //   contents of rom_1 (hex, n*v repeats v):
  //   201d0100 20110200 20020022 112020 20020022 c 2231ffff 1620fffb 20020032 c 20110001 8000c0f 20110001
  //   20120002 20130003 8000c13 20110001 20120002 20130003 8000c17 20110001 20120002 20130003 8000c1b
  //   20110001 20120002 20130003 c000cff 20100001 20110001 118fc0 112020 20020022 c 118882 12200001
  //   8000c1f 112020 20020022 c 20110001 118880 112020 20020022 c 12200001 8000c29 20110001 118fc0 112020
  //   20020022 c 1188c3 112020 20020022 c 118903 112020 20020022 c 118903 112020 20020022 c 118903 112020
  //   20020022 c 118903 112020 20020022 c 118903 112020 20020022 c 118903 112020 20020022 c 118903 112020
  //   20020022 c 20100001 109fc0 139fc3 8021 2012000c 24160003 26100001 3210000f 20080008 20090001 139900
  //   2709825 132020 20020022 c 1094022 1500fff9 22100001 2018000f 2188024 108700 20080008 20090001 139902
  //   2709825 132021 20020022 c 1094022 1500fff9 108702 2c9b022 12c00001 8000c5a 4020 1084027 84400
  //   3508ffff 82021 20020022 c 2010ffff 20110000 ae300000 22100001 22310004 ae300000 22100001 22310004
  //   ae300000 22100001 22310004 ae300000 22100001 22310004 ae300000 22100001 22310004 ae300000 22100001
  //   22310004 ae300000 22100001 22310004 ae300000 22100001 22310004 ae300000 22100001 22310004 ae300000
  //   22100001 22310004 ae300000 22100001 22310004 ae300000 22100001 22310004 ae300000 22100001 22310004
  //   ae300000 22100001 22310004 ae300000 22100001 22310004 ae300000 22100001 22310004 22100001 8020
  //   2011003c 8e130000 8e340000 274402a 11000002 ae330000 ae140000 2231fffc 1611fff8 102020 20020022 c
  //   22100004 2011003c 1611fff2 20020032 c 20080001 20110010 112020 20020022 c 200b0020 2288823 112020
  //   20020022 c 216bffff 1560fffa 2002000a c 2008ffff 20117777 112020 20020022 c 200b0010 2288826 112020
  //   20020022 c 216bffff 1560fffa 2002000a c 20090000 200b0020 20110000 20120001 a1310000 112020 20020022
  //   c 2328820 21290001 216bffff 1560fff8 200b0008 20090000 8d310000 112020 20020022 c 21290004 216bffff
  //   1560fff9 2002000a c 2011fff1 112020 20020022 c 22310001 1a20fffb 2002000a c 2002000a c 20100000
  //   22100001 102020 20020022 c 22100002 102020 20020022 c 22100003 102020 20020022 c 22100004 102020
  //   20020022 c 22100005 102020 20020022 c 22100006 102020 20020022 c 22100007 102020 20020022 c 22100008
  //   102020 20020022 20020022 c 3e00008 afb00000 afb30004 afb40008 afb5000c afb60010 afa40014 afa20018
  //   20160001 20140006 20150001 168020 108100 2149825 132020 20020022 c 1600fffa 295a022 1680fff7
  //   8fa20018 8fa40014 8fb60010 8fb5000c 8fb40008 8fb30004 8fb00000 42000018 afb00000 afb30004 afb40008
  //   afb5000c afb60010 afa40014 afa20018 20160002 20140006 20150001 168020 108100 2149825 132020 20020022
  //   c 1600fffa 295a022 1680fff7 8fa20018 8fa40014 8fb60010 8fb5000c 8fb40008 8fb30004 8fb00000 42000018
  //   afb00000 afb30004 afb40008 afb5000c afb60010 afa40014 afa20018 20160003 20140006 20150001 168020
  //   108100 2149825 132020 20020022 c 1600fffa 295a022 1680fff7 8fa20018 8fa40014 8fb60010 8fb5000c
  //   8fb40008 8fb30004 8fb00000 42000018
  //   OP
  //   Func
  //   rs
  //   指令字
  //   rt
  //   rd
  //   JMP
  //   JR
  //   OP
  //   Func
  //   BLEZ
  //   Beq
  //   Bne
  //   SB
  //   AluOP
  //   AluSrcB
  //   RegWrite
  //   JAL
  //   RegDst
  //   Syscall
  //   MemToReg
  //   MemWrite
  //   INT： 每个中断来临时，提供一个上升沿
endmodule
